// Logisim project ALU.circ as structural Verilog: 4 circuits, main circuit ALU
module ALU (
  input  [15:0] AX,
  input  [15:0] BX,
  input  [15:0] CX,
  input  [15:0] DX,
  input  [15:0] EX,
  input  [15:0] DR,
  input  [15:0] IR,
  input  AX__DR,
  input  BX__DR,
  input  CX__DR,
  input  DX__DR,
  input  EX__DR,
  input  AX__IR,
  input  BX__IR,
  input  CX__IR,
  input  DX__IR,
  input  EX__IR,
  input  AX__BX,
  input  AX__CX,
  input  AX__DX,
  input  AX__EX,
  input  BX_AX,
  input  BX__CX,
  input  BX__DX,
  input  BX__EX,
  input  CX__AX,
  input  CX__BX,
  input  CX__DX,
  input  CX__EX,
  input  DX__AX,
  input  DX__BX,
  input  DX__CX,
  input  DX__EX,
  input  EX__AX,
  input  EX__BX,
  input  EX__CX,
  input  EX__DX,
  input  Cin,
  input  AND,
  input  OR,
  input  XOR,
  input  ADD,
  input  ADC,
  input  SUB,
  input  SBB,
  input  MUL,
  input  DIV,
  input  CMP,
  output Zero,
  output [15:0] MAIN_OUT,
  output [15:0] SECOND_OUT,
  output Cout
);

  wire add_adc_1_cout, and_1_out, and_3_out, cmp_1_a___b, cmp_1_a___b_2, cmp_1_a___b_3, or_2_out, or_3_out,
       sub_sbb_1_bout;
  wire [15:0] add_adc_1_output, and_2_output, div_1_quotient, div_1_remainder, mul_1_high_16, mul_1_low_16,
       or_1_output, sub_sbb_1_output, xor_1_output;
  wire [19:0] alu_register_adjuster_1__20;
  wire [29:0] alu_register_adjuster_1__30;

  and and_1 (and_1_out, Cin, ADC);
  ALU_REGISTER_ADJUSTER alu_register_adjuster_1 (
    .AX__DR(AX__DR), .BX__DR(BX__DR), .CX__DR(CX__DR), .DX__DR(DX__DR), .EX__DR(EX__DR), .AX__IR(AX__IR),
    .BX__IR(BX__IR), .CX__IR(CX__IR), .DX__IR(DX__IR), .EX__IR(EX__IR), .AX__BX(AX__BX), .AX__CX(AX__CX),
    .AX__DX(AX__DX), .AX__EX(AX__EX), .BX__AX(BX_AX), .BX__CX(BX__CX), .BX__DX(BX__DX), .BX__EX(BX__EX),
    .CX__AX(CX__AX), .CX__BX(CX__BX), .CX__DX(CX__DX), .CX__EX(CX__EX), .DX__AX(DX__AX), .DX__BX(DX__BX),
    .DX__CX(DX__CX), .DX__EX(DX__EX), .EX__AX(EX__AX), .EX__BX(EX__BX), .EX__CX(EX__CX), .EX__DX(EX__DX),
    ._30(alu_register_adjuster_1__30), ._20(alu_register_adjuster_1__20));
  AND and_2 (
    .AX(AX), .BX(BX), .CX(CX), .DX(DX), .EX(EX), .DR(DR), .IR(IR), .AX__DR(alu_register_adjuster_1__20[19]),
    .BX__DR(alu_register_adjuster_1__20[18]), .CX__DR(alu_register_adjuster_1__20[17]),
    .DX__DR(alu_register_adjuster_1__20[16]), .EX__DR(alu_register_adjuster_1__20[15]),
    .AX__IR(alu_register_adjuster_1__20[14]), .BX__IR(alu_register_adjuster_1__20[13]),
    .CX__IR(alu_register_adjuster_1__20[12]), .DX__IR(alu_register_adjuster_1__20[11]),
    .EX__IR(alu_register_adjuster_1__20[10]), .AX__BX(alu_register_adjuster_1__20[9]),
    .AX__CX(alu_register_adjuster_1__20[8]), .AX__DX(alu_register_adjuster_1__20[7]),
    .AX__EX(alu_register_adjuster_1__20[6]), .BX__CX(alu_register_adjuster_1__20[5]),
    .BX__DX(alu_register_adjuster_1__20[4]), .BX__EX(alu_register_adjuster_1__20[3]),
    .CX__DX(alu_register_adjuster_1__20[2]), .CX__EX(alu_register_adjuster_1__20[1]),
    .DX__EX(alu_register_adjuster_1__20[0]), .OUTPUT(and_2_output));
  OR or_1 (
    .AX(AX), .BX(BX), .CX(CX), .DX(DX), .EX(EX), .DR(DR), .IR(IR), .AX__DR(alu_register_adjuster_1__20[19]),
    .BX__DR(alu_register_adjuster_1__20[18]), .CX__DR(alu_register_adjuster_1__20[17]),
    .DX__DR(alu_register_adjuster_1__20[16]), .EX__DR(alu_register_adjuster_1__20[15]),
    .AX__IR(alu_register_adjuster_1__20[14]), .BX__IR(alu_register_adjuster_1__20[13]),
    .CX__IR(alu_register_adjuster_1__20[12]), .DX__IR(alu_register_adjuster_1__20[11]),
    .EX__IR(alu_register_adjuster_1__20[10]), .AX__BX(alu_register_adjuster_1__20[9]),
    .AX__CX(alu_register_adjuster_1__20[8]), .AX__DX(alu_register_adjuster_1__20[7]),
    .AX__EX(alu_register_adjuster_1__20[6]), .BX__CX(alu_register_adjuster_1__20[5]),
    .BX__DX(alu_register_adjuster_1__20[4]), .BX__EX(alu_register_adjuster_1__20[3]),
    .CX__DX(alu_register_adjuster_1__20[2]), .CX__EX(alu_register_adjuster_1__20[1]),
    .DX__EX(alu_register_adjuster_1__20[0]), .OUTPUT(or_1_output));
  XOR xor_1 (
    .AX(AX), .BX(BX), .CX(CX), .DX(DX), .EX(EX), .DR(DR), .IR(IR), .AX__DR(alu_register_adjuster_1__20[19]),
    .BX__DR(alu_register_adjuster_1__20[18]), .CX__DR(alu_register_adjuster_1__20[17]),
    .DX__DR(alu_register_adjuster_1__20[16]), .EX__DR(alu_register_adjuster_1__20[15]),
    .AX__IR(alu_register_adjuster_1__20[14]), .BX__IR(alu_register_adjuster_1__20[13]),
    .CX__IR(alu_register_adjuster_1__20[12]), .DX__IR(alu_register_adjuster_1__20[11]),
    .EX__IR(alu_register_adjuster_1__20[10]), .AX__BX(alu_register_adjuster_1__20[9]),
    .AX__CX(alu_register_adjuster_1__20[8]), .AX__DX(alu_register_adjuster_1__20[7]),
    .AX__EX(alu_register_adjuster_1__20[6]), .BX__CX(alu_register_adjuster_1__20[5]),
    .BX__DX(alu_register_adjuster_1__20[4]), .BX__EX(alu_register_adjuster_1__20[3]),
    .CX__DX(alu_register_adjuster_1__20[2]), .CX__EX(alu_register_adjuster_1__20[1]),
    .DX__EX(alu_register_adjuster_1__20[0]), .OUTPUT(xor_1_output));
  ADD_ADC add_adc_1 (
    .AX(AX), .BX(BX), .CX(CX), .DX(DX), .EX(EX), .DR(DR), .IR(IR), .Cin(and_1_out),
    .AX__DR(alu_register_adjuster_1__20[19]), .BX__DR(alu_register_adjuster_1__20[18]),
    .CX__DR(alu_register_adjuster_1__20[17]), .DX__DR(alu_register_adjuster_1__20[16]),
    .EX__DR(alu_register_adjuster_1__20[15]), .AX__IR(alu_register_adjuster_1__20[14]),
    .BX__IR(alu_register_adjuster_1__20[13]), .CX__IR(alu_register_adjuster_1__20[12]),
    .DX__IR(alu_register_adjuster_1__20[11]), .EX__IR(alu_register_adjuster_1__20[10]),
    .AX__BX(alu_register_adjuster_1__20[9]), .AX__CX(alu_register_adjuster_1__20[8]),
    .AX__DX(alu_register_adjuster_1__20[7]), .AX__EX(alu_register_adjuster_1__20[6]),
    .BX__CX(alu_register_adjuster_1__20[5]), .BX__DX(alu_register_adjuster_1__20[4]),
    .BX__EX(alu_register_adjuster_1__20[3]), .CX__DX(alu_register_adjuster_1__20[2]),
    .CX__EX(alu_register_adjuster_1__20[1]), .DX__EX(alu_register_adjuster_1__20[0]),
    .OUTPUT(add_adc_1_output), .Cout(add_adc_1_cout));
  MUL mul_1 (
    .AX(AX), .BX(BX), .CX(CX), .DX(DX), .EX(EX), .DR(DR), .IR(IR), .AX__DR(alu_register_adjuster_1__20[19]),
    .BX__DR(alu_register_adjuster_1__20[18]), .CX__DR(alu_register_adjuster_1__20[17]),
    .DX__DR(alu_register_adjuster_1__20[16]), .EX__DR(alu_register_adjuster_1__20[15]),
    .AX__IR(alu_register_adjuster_1__20[14]), .BX__IR(alu_register_adjuster_1__20[13]),
    .CX__IR(alu_register_adjuster_1__20[12]), .DX__IR(alu_register_adjuster_1__20[11]),
    .EX__IR(alu_register_adjuster_1__20[10]), .AX__BX(alu_register_adjuster_1__20[9]),
    .AX__CX(alu_register_adjuster_1__20[8]), .AX__DX(alu_register_adjuster_1__20[7]),
    .AX__EX(alu_register_adjuster_1__20[6]), .BX__CX(alu_register_adjuster_1__20[5]),
    .BX__DX(alu_register_adjuster_1__20[4]), .BX__EX(alu_register_adjuster_1__20[3]),
    .CX__DX(alu_register_adjuster_1__20[2]), .CX__EX(alu_register_adjuster_1__20[1]),
    .DX__EX(alu_register_adjuster_1__20[0]), .LOW_16(mul_1_low_16), .HIGH_16(mul_1_high_16));
  and and_3 (and_3_out, SBB, Cin);
  assign MAIN_OUT = or_2_out ? add_adc_1_output : 16'bz;  // Controlled_Buffer controlled_buffer_1
  assign SECOND_OUT = MUL ? mul_1_low_16 : 16'bz;  // Controlled_Buffer controlled_buffer_2
  assign MAIN_OUT = MUL ? mul_1_high_16 : 16'bz;  // Controlled_Buffer controlled_buffer_3
  or or_2 (or_2_out, ADD, ADC);
  assign SECOND_OUT = DIV ? div_1_remainder : 16'bz;  // Controlled_Buffer controlled_buffer_4
  assign MAIN_OUT = AND ? and_2_output : 16'bz;  // Controlled_Buffer controlled_buffer_5
  assign MAIN_OUT = OR ? or_1_output : 16'bz;  // Controlled_Buffer controlled_buffer_6
  assign MAIN_OUT = XOR ? xor_1_output : 16'bz;  // Controlled_Buffer controlled_buffer_7
  assign MAIN_OUT = or_3_out ? sub_sbb_1_output : 16'bz;  // Controlled_Buffer controlled_buffer_8
  assign MAIN_OUT = DIV ? div_1_quotient : 16'bz;  // Controlled_Buffer controlled_buffer_9
  or or_3 (or_3_out, SUB, SBB);
  SUB_SBB sub_sbb_1 (
    .AX(AX), .BX(BX), .CX(CX), .DX(DX), .EX(EX), .DR(DR), .IR(IR), .Bin(and_3_out),
    .AX__DR(alu_register_adjuster_1__30[29]), .BX__DR(alu_register_adjuster_1__30[28]),
    .CX__DR(alu_register_adjuster_1__30[27]), .DX__DR(alu_register_adjuster_1__30[26]),
    .EX__DR(alu_register_adjuster_1__30[25]), .AX__IR(alu_register_adjuster_1__30[24]),
    .BX__IR(alu_register_adjuster_1__30[23]), .CX__IR(alu_register_adjuster_1__30[22]),
    .DX__IR(alu_register_adjuster_1__30[21]), .EX__IR(alu_register_adjuster_1__30[20]),
    .AX__BX(alu_register_adjuster_1__30[19]), .AX__CX(alu_register_adjuster_1__30[18]),
    .AX__DX(alu_register_adjuster_1__30[17]), .AX__EX(alu_register_adjuster_1__30[16]),
    .BX__AX(alu_register_adjuster_1__30[15]), .BX__CX(alu_register_adjuster_1__30[14]),
    .BX__DX(alu_register_adjuster_1__30[13]), .BX__EX(alu_register_adjuster_1__30[12]),
    .CX__AX(alu_register_adjuster_1__30[11]), .CX__BX(alu_register_adjuster_1__30[10]),
    .CX__DX(alu_register_adjuster_1__30[9]), .CX__EX(alu_register_adjuster_1__30[8]),
    .DX__AX(alu_register_adjuster_1__30[7]), .DX__BX(alu_register_adjuster_1__30[6]),
    .DX__CX(alu_register_adjuster_1__30[5]), .DX__EX(alu_register_adjuster_1__30[4]),
    .EX__AX(alu_register_adjuster_1__30[3]), .EX__BX(alu_register_adjuster_1__30[2]),
    .EX__CX(alu_register_adjuster_1__30[1]), .EX__DX(alu_register_adjuster_1__30[0]),
    .OUTPUT(sub_sbb_1_output), .Bout(sub_sbb_1_bout));
  DIV div_1 (
    .AX(AX), .BX(BX), .CX(CX), .DX(DX), .EX(EX), .DR(DR), .IR(IR), .AX__DR(alu_register_adjuster_1__30[29]),
    .BX__DR(alu_register_adjuster_1__30[28]), .CX__DR(alu_register_adjuster_1__30[27]),
    .DX__DR(alu_register_adjuster_1__30[26]), .EX__DR(alu_register_adjuster_1__30[25]),
    .AX__IR(alu_register_adjuster_1__30[24]), .BX__IR(alu_register_adjuster_1__30[23]),
    .CX__IR(alu_register_adjuster_1__30[22]), .DX__IR(alu_register_adjuster_1__30[21]),
    .EX__IR(alu_register_adjuster_1__30[20]), .AX__BX(alu_register_adjuster_1__30[19]),
    .AX__CX(alu_register_adjuster_1__30[18]), .AX__DX(alu_register_adjuster_1__30[17]),
    .AX__EX(alu_register_adjuster_1__30[16]), .BX__AX(alu_register_adjuster_1__30[15]),
    .BX__CX(alu_register_adjuster_1__30[14]), .BX__DX(alu_register_adjuster_1__30[13]),
    .BX__EX(alu_register_adjuster_1__30[12]), .CX__AX(alu_register_adjuster_1__30[11]),
    .CX__BX(alu_register_adjuster_1__30[10]), .CX__DX(alu_register_adjuster_1__30[9]),
    .CX__EX(alu_register_adjuster_1__30[8]), .DX__AX(alu_register_adjuster_1__30[7]),
    .DX__BX(alu_register_adjuster_1__30[6]), .DX__CX(alu_register_adjuster_1__30[5]),
    .DX__EX(alu_register_adjuster_1__30[4]), .EX__AX(alu_register_adjuster_1__30[3]),
    .EX__BX(alu_register_adjuster_1__30[2]), .EX__CX(alu_register_adjuster_1__30[1]),
    .EX__DX(alu_register_adjuster_1__30[0]), .QUOTIENT(div_1_quotient), .REMAINDER(div_1_remainder));
  CMP cmp_1 (
    .AX(AX), .BX(BX), .CX(CX), .DX(DX), .EX(EX), .DR(DR), .IR(IR), .AX__DR(alu_register_adjuster_1__30[29]),
    .BX__DR(alu_register_adjuster_1__30[28]), .CX__DR(alu_register_adjuster_1__30[27]),
    .DX__DR(alu_register_adjuster_1__30[26]), .EX__DR(alu_register_adjuster_1__30[25]),
    .AX__IR(alu_register_adjuster_1__30[24]), .BX__IR(alu_register_adjuster_1__30[23]),
    .CX__IR(alu_register_adjuster_1__30[22]), .DX__IR(alu_register_adjuster_1__30[21]),
    .EX__IR(alu_register_adjuster_1__30[20]), .AX__BX(alu_register_adjuster_1__30[19]),
    .AX__CX(alu_register_adjuster_1__30[18]), .AX__DX(alu_register_adjuster_1__30[17]),
    .AX__EX(alu_register_adjuster_1__30[16]), .BX__AX(alu_register_adjuster_1__30[15]),
    .BX__CX(alu_register_adjuster_1__30[14]), .BX__DX(alu_register_adjuster_1__30[13]),
    .BX__EX(alu_register_adjuster_1__30[12]), .CX__AX(alu_register_adjuster_1__30[11]),
    .CX__BX(alu_register_adjuster_1__30[10]), .CX__DX(alu_register_adjuster_1__30[9]),
    .CX__EX(alu_register_adjuster_1__30[8]), .DX__AX(alu_register_adjuster_1__30[7]),
    .DX__BX(alu_register_adjuster_1__30[6]), .DX__CX(alu_register_adjuster_1__30[5]),
    .DX__EX(alu_register_adjuster_1__30[4]), .EX__AX(alu_register_adjuster_1__30[3]),
    .EX__BX(alu_register_adjuster_1__30[2]), .EX__CX(alu_register_adjuster_1__30[1]),
    .EX__DX(alu_register_adjuster_1__30[0]), .A___B(cmp_1_a___b), .A___B_2(cmp_1_a___b_2),
    .A___B_3(cmp_1_a___b_3));
  ALU_Zero alu_zero_1 (
    .MAIN_OUT(MAIN_OUT), .CMP(CMP), .A___B(cmp_1_a___b_3), .A___B_2(cmp_1_a___b_2), .A___B_3(cmp_1_a___b),
    .Zero(Zero));
  ALU_Cout alu_cout_1 (
    .ADD(ADD), .ADC(ADC), .Cout_from_add(add_adc_1_cout), .SUB(SUB), .SBB(SBB),
    .Bout_from_sub(sub_sbb_1_bout), .A___B(cmp_1_a___b_3), .A___B_2(cmp_1_a___b_2), .A___B_3(cmp_1_a___b),
    .CMP(CMP), .OUT(Cout));
endmodule

// REGISTER_ADJUSTER
module ALU_REGISTER_ADJUSTER (
  input  AX__DR,
  input  BX__DR,
  input  CX__DR,
  input  DX__DR,
  input  EX__DR,
  input  AX__IR,
  input  BX__IR,
  input  CX__IR,
  input  DX__IR,
  input  EX__IR,
  input  AX__BX,
  input  AX__CX,
  input  AX__DX,
  input  AX__EX,
  input  BX__AX,
  input  BX__CX,
  input  BX__DX,
  input  BX__EX,
  input  CX__AX,
  input  CX__BX,
  input  CX__DX,
  input  CX__EX,
  input  DX__AX,
  input  DX__BX,
  input  DX__CX,
  input  DX__EX,
  input  EX__AX,
  input  EX__BX,
  input  EX__CX,
  input  EX__DX,
  output [29:0] _30,
  output [19:0] _20
);

  or or_1 (_20[9], AX__BX, BX__AX);
  or or_2 (_20[8], AX__CX, CX__AX);
  or or_3 (_20[7], BX__CX, CX__BX);
  or or_4 (_20[6], AX__DX, DX__AX);
  or or_5 (_20[5], BX__DX, DX__BX);
  or or_6 (_20[4], CX__DX, DX__CX);
  or or_7 (_20[3], AX__EX, EX__AX);
  or or_8 (_20[2], BX__EX, EX__BX);
  or or_9 (_20[1], CX__EX, EX__CX);
  or or_10 (_20[0], DX__EX, EX__DX);

  assign _20[19:10] = {AX__DR, BX__DR, CX__DR, DX__DR, EX__DR, AX__IR, BX__IR, CX__IR, DX__IR, EX__IR};
  assign _30 = {AX__DR, BX__DR, CX__DR, DX__DR, EX__DR, AX__IR, BX__IR, CX__IR, DX__IR, EX__IR, AX__BX, AX__CX, AX__DX, AX__EX, BX__AX, BX__CX, BX__DX, BX__EX, CX__AX, CX__BX, CX__DX, CX__EX, DX__AX, DX__BX, DX__CX, DX__EX, EX__AX, EX__BX, EX__CX, EX__DX};
endmodule

module ALU_Cout (
  input  ADD,
  input  ADC,
  input  Cout_from_add,
  input  SUB,
  input  SBB,
  input  Bout_from_sub,
  input  A___B,
  input  A___B_2,
  input  A___B_3,
  input  CMP,
  output OUT
);

  wire and_1_out, and_2_out, and_3_out, and_4_out, and_5_out, nand_1_out, not_1_out, or_1_out, or_2_out,
       or_3_out, or_4_out, or_5_out;

  or or_1 (or_1_out, ADD, ADC);
  or or_2 (or_2_out, SUB, SBB);
  or or_3 (or_3_out, A___B, A___B_2);
  and and_1 (and_1_out, or_1_out, Cout_from_add);
  and and_2 (and_2_out, or_2_out, Bout_from_sub);
  and and_3 (and_3_out, or_3_out, CMP);
  nand nand_1 (nand_1_out, A___B_3, CMP);
  or or_4 (or_4_out, and_1_out, and_2_out);
  or or_5 (or_5_out, and_3_out, nand_1_out);
  and and_4 (and_4_out, or_4_out, not_1_out);
  not not_1 (not_1_out, CMP);
  and and_5 (and_5_out, or_5_out, CMP);
  or or_6 (OUT, and_4_out, and_5_out);
endmodule

module ALU_Zero (
  input  [15:0] MAIN_OUT,
  input  CMP,
  input  A___B,
  input  A___B_2,
  input  A___B_3,
  output Zero
);

  wire and_1_out, and_2_out, not_1_out, not_2_out, not_3_out, or_1_out, or_2_out;

  not not_1 (not_1_out, A___B);
  or or_1 (or_1_out, A___B_2, A___B_3);
  and and_1 (and_1_out, CMP, not_1_out, or_1_out);
  not not_2 (not_2_out, CMP);
  or or_2 (or_2_out, MAIN_OUT[0], MAIN_OUT[1], MAIN_OUT[2], MAIN_OUT[3], MAIN_OUT[4], MAIN_OUT[5], MAIN_OUT[6], MAIN_OUT[7], MAIN_OUT[8], MAIN_OUT[9], MAIN_OUT[10], MAIN_OUT[11], MAIN_OUT[12], MAIN_OUT[13], MAIN_OUT[14], MAIN_OUT[15], 1'b0);
  not not_3 (not_3_out, or_2_out);
  and and_2 (and_2_out, not_3_out, not_2_out);
  or or_3 (Zero, and_2_out, and_1_out);
endmodule
