// Logisim project LOGIC UNITS.circ as structural Verilog: 3 circuits, main circuit AND
module AND (
  input  AX__DR,
  input  BX__DR,
  input  CX__DR,
  input  DX__DR,
  input  EX__DR,
  input  AX__IR,
  input  BX__IR,
  input  CX__IR,
  input  DX__IR,
  input  EX__IR,
  input  AX__AX,
  input  AX__BX,
  input  AX__CX,
  input  AX__DX,
  input  AX__EX,
  input  BX__BX,
  input  BX__CX,
  input  BX__DX,
  input  BX__EX,
  input  CX__CX,
  input  CX__DX,
  input  CX__EX,
  input  DX__DX,
  input  DX__EX,
  input  EX__EX,
  input  [15:0] AX,
  input  [15:0] BX,
  input  [15:0] CX,
  input  [15:0] DX,
  input  [15:0] EX,
  input  [15:0] DR,
  input  [15:0] IR,
  output [15:0] OUTPUT
);

  wire [3:0] input_16to4_1_ax_0_3, input_16to4_1_ax_4_7, input_16to4_1_ax_8_11, input_16to4_1_ax_12_15,
       input_16to4_1_bx_0_3, input_16to4_1_bx_4_7, input_16to4_1_bx_8_11, input_16to4_1_bx_12_15,
       input_16to4_1_cx_0_3, input_16to4_1_cx_4_7, input_16to4_1_cx_8_11, input_16to4_1_cx_12_15,
       input_16to4_1_dr_0_3, input_16to4_1_dr_4_7, input_16to4_1_dr_8_11, input_16to4_1_dr_12_15,
       input_16to4_1_dx_0_3, input_16to4_1_dx_4_7, input_16to4_1_dx_8_11, input_16to4_1_dx_12_15,
       input_16to4_1_ex_0_3, input_16to4_1_ex_4_7, input_16to4_1_ex_8_11, input_16to4_1_ex_12_15,
       input_16to4_1_ir_0_3, input_16to4_1_ir_0_3_2, input_16to4_1_ir_4_7, input_16to4_1_ir_12_15;

  INPUT_16to4 input_16to4_1 (
    .AX(AX), .BX(BX), .CX(CX), .DX(DX), .EX(EX), .DR(DR), .IR(IR), .AX_0_3(input_16to4_1_ax_0_3),
    .BX_0_3(input_16to4_1_bx_0_3), .CX_0_3(input_16to4_1_cx_0_3), .DX_0_3(input_16to4_1_dx_0_3),
    .EX_0_3(input_16to4_1_ex_0_3), .DR_0_3(input_16to4_1_dr_0_3), .IR_0_3(input_16to4_1_ir_0_3),
    .AX_4_7(input_16to4_1_ax_4_7), .BX_4_7(input_16to4_1_bx_4_7), .CX_4_7(input_16to4_1_cx_4_7),
    .DX_4_7(input_16to4_1_dx_4_7), .EX_4_7(input_16to4_1_ex_4_7), .DR_4_7(input_16to4_1_dr_4_7),
    .IR_4_7(input_16to4_1_ir_4_7), .AX_8_11(input_16to4_1_ax_8_11), .BX_8_11(input_16to4_1_bx_8_11),
    .CX_8_11(input_16to4_1_cx_8_11), .DX_8_11(input_16to4_1_dx_8_11), .EX_8_11(input_16to4_1_ex_8_11),
    .DR_8_11(input_16to4_1_dr_8_11), .IR_0_3_2(input_16to4_1_ir_0_3_2), .AX_12_15(input_16to4_1_ax_12_15),
    .BX_12_15(input_16to4_1_bx_12_15), .CX_12_15(input_16to4_1_cx_12_15), .DX_12_15(input_16to4_1_dx_12_15),
    .EX_12_15(input_16to4_1_ex_12_15), .DR_12_15(input_16to4_1_dr_12_15), .IR_12_15(input_16to4_1_ir_12_15));
  // AND_4 and_4_1: pin names not known; wires that end beside it: OUTPUT[3:0]
  // AND_4 and_4_2: pin names not known; wires that end beside it: OUTPUT[7:4]
  // AND_4 and_4_3: pin names not known; wires that end beside it: OUTPUT[11:8]
  // AND_4 and_4_4: pin names not known; wires that end beside it: OUTPUT[15:12]
endmodule

module OR (
  input  AX__DR,
  input  BX__DR,
  input  CX__DR,
  input  DX__DR,
  input  EX__DR,
  input  AX__IR,
  input  BX__IR,
  input  CX__IR,
  input  DX__IR,
  input  EX__IR,
  input  AX__AX,
  input  AX__BX,
  input  AX__CX,
  input  AX__DX,
  input  AX__EX,
  input  BX__BX,
  input  BX__CX,
  input  BX__DX,
  input  BX__EX,
  input  CX__CX,
  input  CX__DX,
  input  CX__EX,
  input  DX__DX,
  input  DX__EX,
  input  EX__EX,
  input  [15:0] AX,
  input  [15:0] BX,
  input  [15:0] CX,
  input  [15:0] DX,
  input  [15:0] EX,
  input  [15:0] DR,
  input  [15:0] IR,
  output [15:0] OUTPUT
);

  wire [3:0] input_16to4_1_ax_0_3, input_16to4_1_ax_4_7, input_16to4_1_ax_8_11, input_16to4_1_ax_12_15,
       input_16to4_1_bx_0_3, input_16to4_1_bx_4_7, input_16to4_1_bx_8_11, input_16to4_1_bx_12_15,
       input_16to4_1_cx_0_3, input_16to4_1_cx_4_7, input_16to4_1_cx_8_11, input_16to4_1_cx_12_15,
       input_16to4_1_dr_0_3, input_16to4_1_dr_4_7, input_16to4_1_dr_8_11, input_16to4_1_dr_12_15,
       input_16to4_1_dx_0_3, input_16to4_1_dx_4_7, input_16to4_1_dx_8_11, input_16to4_1_dx_12_15,
       input_16to4_1_ex_0_3, input_16to4_1_ex_4_7, input_16to4_1_ex_8_11, input_16to4_1_ex_12_15,
       input_16to4_1_ir_0_3, input_16to4_1_ir_0_3_2, input_16to4_1_ir_4_7, input_16to4_1_ir_12_15;

  INPUT_16to4 input_16to4_1 (
    .AX(AX), .BX(BX), .CX(CX), .DX(DX), .EX(EX), .DR(DR), .IR(IR), .AX_0_3(input_16to4_1_ax_0_3),
    .BX_0_3(input_16to4_1_bx_0_3), .CX_0_3(input_16to4_1_cx_0_3), .DX_0_3(input_16to4_1_dx_0_3),
    .EX_0_3(input_16to4_1_ex_0_3), .DR_0_3(input_16to4_1_dr_0_3), .IR_0_3(input_16to4_1_ir_0_3),
    .AX_4_7(input_16to4_1_ax_4_7), .BX_4_7(input_16to4_1_bx_4_7), .CX_4_7(input_16to4_1_cx_4_7),
    .DX_4_7(input_16to4_1_dx_4_7), .EX_4_7(input_16to4_1_ex_4_7), .DR_4_7(input_16to4_1_dr_4_7),
    .IR_4_7(input_16to4_1_ir_4_7), .AX_8_11(input_16to4_1_ax_8_11), .BX_8_11(input_16to4_1_bx_8_11),
    .CX_8_11(input_16to4_1_cx_8_11), .DX_8_11(input_16to4_1_dx_8_11), .EX_8_11(input_16to4_1_ex_8_11),
    .DR_8_11(input_16to4_1_dr_8_11), .IR_0_3_2(input_16to4_1_ir_0_3_2), .AX_12_15(input_16to4_1_ax_12_15),
    .BX_12_15(input_16to4_1_bx_12_15), .CX_12_15(input_16to4_1_cx_12_15), .DX_12_15(input_16to4_1_dx_12_15),
    .EX_12_15(input_16to4_1_ex_12_15), .DR_12_15(input_16to4_1_dr_12_15), .IR_12_15(input_16to4_1_ir_12_15));
  // OR_4 or_4_1: pin names not known; wires that end beside it: OUTPUT[3:0]
  // OR_4 or_4_2: pin names not known; wires that end beside it: OUTPUT[7:4]
  // OR_4 or_4_3: pin names not known; wires that end beside it: OUTPUT[11:8]
  // OR_4 or_4_4: pin names not known; wires that end beside it: OUTPUT[15:12]
endmodule

module XOR (
  input  AX__DR,
  input  BX__DR,
  input  CX__DR,
  input  DX__DR,
  input  EX__DR,
  input  AX__IR,
  input  BX__IR,
  input  CX__IR,
  input  DX__IR,
  input  EX__IR,
  input  AX__AX,
  input  AX__BX,
  input  AX__CX,
  input  AX__DX,
  input  AX__EX,
  input  BX__BX,
  input  BX__CX,
  input  BX__DX,
  input  BX__EX,
  input  CX__CX,
  input  CX__DX,
  input  CX__EX,
  input  DX__DX,
  input  DX__EX,
  input  EX__EX,
  input  [15:0] AX,
  input  [15:0] BX,
  input  [15:0] CX,
  input  [15:0] DX,
  input  [15:0] EX,
  input  [15:0] DR,
  input  [15:0] IR,
  output [15:0] OUTPUT
);

  wire [3:0] input_16to4_1_ax_0_3, input_16to4_1_ax_4_7, input_16to4_1_ax_8_11, input_16to4_1_ax_12_15,
       input_16to4_1_bx_0_3, input_16to4_1_bx_4_7, input_16to4_1_bx_8_11, input_16to4_1_bx_12_15,
       input_16to4_1_cx_0_3, input_16to4_1_cx_4_7, input_16to4_1_cx_8_11, input_16to4_1_cx_12_15,
       input_16to4_1_dr_0_3, input_16to4_1_dr_4_7, input_16to4_1_dr_8_11, input_16to4_1_dr_12_15,
       input_16to4_1_dx_0_3, input_16to4_1_dx_4_7, input_16to4_1_dx_8_11, input_16to4_1_dx_12_15,
       input_16to4_1_ex_0_3, input_16to4_1_ex_4_7, input_16to4_1_ex_8_11, input_16to4_1_ex_12_15,
       input_16to4_1_ir_0_3, input_16to4_1_ir_0_3_2, input_16to4_1_ir_4_7, input_16to4_1_ir_12_15;

  INPUT_16to4 input_16to4_1 (
    .AX(AX), .BX(BX), .CX(CX), .DX(DX), .EX(EX), .DR(DR), .IR(IR), .AX_0_3(input_16to4_1_ax_0_3),
    .BX_0_3(input_16to4_1_bx_0_3), .CX_0_3(input_16to4_1_cx_0_3), .DX_0_3(input_16to4_1_dx_0_3),
    .EX_0_3(input_16to4_1_ex_0_3), .DR_0_3(input_16to4_1_dr_0_3), .IR_0_3(input_16to4_1_ir_0_3),
    .AX_4_7(input_16to4_1_ax_4_7), .BX_4_7(input_16to4_1_bx_4_7), .CX_4_7(input_16to4_1_cx_4_7),
    .DX_4_7(input_16to4_1_dx_4_7), .EX_4_7(input_16to4_1_ex_4_7), .DR_4_7(input_16to4_1_dr_4_7),
    .IR_4_7(input_16to4_1_ir_4_7), .AX_8_11(input_16to4_1_ax_8_11), .BX_8_11(input_16to4_1_bx_8_11),
    .CX_8_11(input_16to4_1_cx_8_11), .DX_8_11(input_16to4_1_dx_8_11), .EX_8_11(input_16to4_1_ex_8_11),
    .DR_8_11(input_16to4_1_dr_8_11), .IR_0_3_2(input_16to4_1_ir_0_3_2), .AX_12_15(input_16to4_1_ax_12_15),
    .BX_12_15(input_16to4_1_bx_12_15), .CX_12_15(input_16to4_1_cx_12_15), .DX_12_15(input_16to4_1_dx_12_15),
    .EX_12_15(input_16to4_1_ex_12_15), .DR_12_15(input_16to4_1_dr_12_15), .IR_12_15(input_16to4_1_ir_12_15));
  // XOR_4 xor_4_1: pin names not known; wires that end beside it: OUTPUT[3:0]
  // XOR_4 xor_4_2: pin names not known; wires that end beside it: OUTPUT[7:4]
  // XOR_4 xor_4_3: pin names not known; wires that end beside it: OUTPUT[11:8]
  // XOR_4 xor_4_4: pin names not known; wires that end beside it: OUTPUT[15:12]
endmodule
