// Logisim project ARITHMETIC UNITS.circ as structural Verilog: 5 circuits, main circuit MUL
module MUL (
  input  AX__DR,
  input  BX__DR,
  input  CX__DR,
  input  DX__DR,
  input  EX__DR,
  input  AX__IR,
  input  BX__IR,
  input  CX__IR,
  input  DX__IR,
  input  EX__IR,
  input  AX__BX,
  input  AX__CX,
  input  AX__DX,
  input  AX__EX,
  input  BX__CX,
  input  BX__DX,
  input  BX__EX,
  input  CX__DX,
  input  CX__EX,
  input  DX__EX,
  input  [15:0] AX,
  input  [15:0] BX,
  input  [15:0] CX,
  input  [15:0] DX,
  input  [15:0] EX,
  input  [15:0] DR,
  input  [15:0] IR,
  output [15:0] LOW_16,
  output [15:0] HIGH_16
);

  wire [15:0] mul_input_adjuster_1_multiplied, mul_input_adjuster_1_multiplier;
  wire [19:0] mul_4_line_adder_1_output, mul_4_line_adder_3_output, mul_4_line_adder_4_output;
  wire [19:4] adder_1_out, adder_2_out, mul_4_line_adder_2_output;

  MUL_INPUT_ADJUSTER mul_input_adjuster_1 (
    .AX(AX), .BX(BX), .CX(CX), .DX(DX), .EX(EX), .DR(DR), .IR(IR), .AX__DR(AX__DR), .BX__DR(BX__DR),
    .CX__DR(CX__DR), .DX__DR(DX__DR), .EX__DR(EX__DR), .AX__IR(AX__IR), .BX__IR(BX__IR), .CX__IR(CX__IR),
    .DX__IR(DX__IR), .EX__IR(EX__IR), .AX__BX(AX__BX), .AX__CX(AX__CX), .AX__DX(AX__DX), .AX__EX(AX__EX),
    .BX__CX(BX__CX), .BX__DX(BX__DX), .BX__EX(BX__EX), .CX__DX(CX__DX), .CX__EX(CX__EX), .DX__EX(DX__EX),
    .MULTIPLIER(mul_input_adjuster_1_multiplier), .MULTIPLIED(mul_input_adjuster_1_multiplied));
  MUL_4_LINE_ADDER mul_4_line_adder_1 (
    .MULTIPLIED(mul_input_adjuster_1_multiplied), .MULTIPLIER(mul_input_adjuster_1_multiplier[7:4]),
    .OUTPUT(mul_4_line_adder_1_output));
  MUL_4_LINE_ADDER mul_4_line_adder_2 (
    .MULTIPLIED(mul_input_adjuster_1_multiplied), .MULTIPLIER(mul_input_adjuster_1_multiplier[3:0]),
    .OUTPUT({mul_4_line_adder_2_output, LOW_16[3:0]}));
  MUL_4_LINE_ADDER mul_4_line_adder_3 (
    .MULTIPLIED(mul_input_adjuster_1_multiplied), .MULTIPLIER(mul_input_adjuster_1_multiplier[11:8]),
    .OUTPUT(mul_4_line_adder_3_output));
  Adder #(.width(20)) adder_1 (
    .a(mul_4_line_adder_1_output), .b({4'b0000, mul_4_line_adder_2_output}), .out({adder_1_out, LOW_16[7:4]}));  // open: cin, cout
  MUL_4_LINE_ADDER mul_4_line_adder_4 (
    .MULTIPLIED(mul_input_adjuster_1_multiplied), .MULTIPLIER(mul_input_adjuster_1_multiplier[15:12]),
    .OUTPUT(mul_4_line_adder_4_output));
  Adder #(.width(20)) adder_2 (
    .a(mul_4_line_adder_3_output), .b({4'b0000, adder_1_out}), .out({adder_2_out, LOW_16[11:8]}));  // open: cin, cout
  Adder #(.width(20)) adder_3 (
    .a(mul_4_line_adder_4_output), .b({4'b0000, adder_2_out}), .out({HIGH_16, LOW_16[15:12]}));  // open: cin, cout
endmodule

module DIV (
  input  AX__DR,
  input  BX__DR,
  input  CX__DR,
  input  DX__DR,
  input  EX__DR,
  input  AX__IR,
  input  BX__IR,
  input  CX__IR,
  input  DX__IR,
  input  EX__IR,
  input  AX__BX,
  input  AX__CX,
  input  AX__DX,
  input  AX__EX,
  input  BX__AX,
  input  BX__CX,
  input  BX__DX,
  input  BX__EX,
  input  CX__AX,
  input  CX__BX,
  input  CX__DX,
  input  CX__EX,
  input  DX__AX,
  input  DX__BX,
  input  DX__CX,
  input  DX__EX,
  input  EX__AX,
  input  EX__BX,
  input  EX__CX,
  input  EX__DX,
  input  [15:0] AX,
  input  [15:0] BX,
  input  [15:0] CX,
  input  [15:0] DX,
  input  [15:0] EX,
  input  [15:0] DR,
  input  [15:0] IR,
  output [15:0] QUOTIENT,
  output [15:0] REMAINDER
);

  wire [15:0] div_4_line_1_r, div_4_line_2_r, div_4_line_3_r, div_input_adjuster_1_dividend,
       div_input_adjuster_1_divisor;

  DIV_INPUT_ADJUSTER div_input_adjuster_1 (
    .AX(AX), .BX(BX), .CX(CX), .DX(DX), .EX(EX), .DR(DR), .IR(IR), .AX__DR(AX__DR), .BX__DR(BX__DR),
    .CX__DR(CX__DR), .DX__DR(DX__DR), .EX__DR(EX__DR), .AX__IR(AX__IR), .BX__IR(BX__IR), .CX__IR(CX__IR),
    .DX__IR(DX__IR), .EX__IR(EX__IR), .AX__BX(AX__BX), .AX__CX(AX__CX), .AX__DX(AX__DX), .AX__EX(AX__EX),
    .BX__AX(BX__AX), .BX__CX(BX__CX), .BX__DX(BX__DX), .BX__EX(BX__EX), .CX__AX(CX__AX), .CX__BX(CX__BX),
    .CX__DX(CX__DX), .CX__EX(CX__EX), .DX__AX(DX__AX), .DX__BX(DX__BX), .DX__CX(DX__CX), .DX__EX(DX__EX),
    .EX__AX(EX__AX), .EX__BX(EX__BX), .EX__CX(EX__CX), .EX__DX(EX__DX),
    .DIVIDEND(div_input_adjuster_1_dividend), .DIVISOR(div_input_adjuster_1_divisor));
  DIV_4_LINE div_4_line_1 (
    .DIVIDEND_4(div_input_adjuster_1_dividend[15:12]), .R_FROM_UP_LINE({16{1'b0}}),
    .DIVISOR(div_input_adjuster_1_divisor), .Q(QUOTIENT[15:12]), .R(div_4_line_1_r));
  DIV_4_LINE div_4_line_2 (
    .DIVIDEND_4(div_input_adjuster_1_dividend[11:8]), .R_FROM_UP_LINE(div_4_line_1_r),
    .DIVISOR(div_input_adjuster_1_divisor), .Q(QUOTIENT[11:8]), .R(div_4_line_2_r));
  DIV_4_LINE div_4_line_3 (
    .DIVIDEND_4(div_input_adjuster_1_dividend[7:4]), .R_FROM_UP_LINE(div_4_line_2_r),
    .DIVISOR(div_input_adjuster_1_divisor), .Q(QUOTIENT[7:4]), .R(div_4_line_3_r));
  DIV_4_LINE div_4_line_4 (
    .DIVIDEND_4(div_input_adjuster_1_dividend[3:0]), .R_FROM_UP_LINE(div_4_line_3_r),
    .DIVISOR(div_input_adjuster_1_divisor), .Q(QUOTIENT[3:0]), .R(REMAINDER));
endmodule

module CMP (
  input  AX__DR,
  input  BX__DR,
  input  CX__DR,
  input  DX__DR,
  input  EX__DR,
  input  AX__IR,
  input  BX__IR,
  input  CX__IR,
  input  DX__IR,
  input  EX__IR,
  input  AX__BX,
  input  AX__CX,
  input  AX__DX,
  input  AX__EX,
  input  BX__AX,
  input  BX__CX,
  input  BX__DX,
  input  BX__EX,
  input  CX__AX,
  input  CX__BX,
  input  CX__DX,
  input  CX__EX,
  input  DX__AX,
  input  DX__BX,
  input  DX__CX,
  input  DX__EX,
  input  EX__AX,
  input  EX__BX,
  input  EX__CX,
  input  EX__DX,
  input  [15:0] AX,
  input  [15:0] BX,
  input  [15:0] CX,
  input  [15:0] DX,
  input  [15:0] EX,
  input  [15:0] DR,
  input  [15:0] IR,
  output A___B,
  output A___B_2,
  output A___B_3
);

  wire and_1_out, and_2_out, and_3_out, and_4_out, and_5_out, and_6_out, cmp_4_1_a___b, cmp_4_1_a___b_2,
       cmp_4_1_a___b_3, cmp_4_2_a___b, cmp_4_2_a___b_2, cmp_4_2_a___b_3, cmp_4_3_a___b, cmp_4_3_a___b_2,
       cmp_4_3_a___b_3, cmp_4_4_a___b, cmp_4_4_a___b_2, cmp_4_4_a___b_3;
  wire [15:0] cmp_input_adjuster_1_a, cmp_input_adjuster_1_b;

  CMP_INPUT_ADJUSTER cmp_input_adjuster_1 (
    .AX(AX), .BX(BX), .CX(CX), .DX(DX), .EX(EX), .DR(DR), .IR(IR), .AX__DR(AX__DR), .BX__DR(BX__DR),
    .CX__DR(CX__DR), .DX__DR(DX__DR), .EX__DR(EX__DR), .AX__IR(AX__IR), .BX__IR(BX__IR), .CX__IR(CX__IR),
    .DX__IR(DX__IR), .EX__IR(EX__IR), .AX__BX(AX__BX), .AX__CX(AX__CX), .AX__DX(AX__DX), .AX__EX(AX__EX),
    .BX__AX(BX__AX), .BX__CX(BX__CX), .BX__DX(BX__DX), .BX__EX(BX__EX), .CX__AX(CX__AX), .CX__BX(CX__BX),
    .CX__DX(CX__DX), .CX__EX(CX__EX), .DX__AX(DX__AX), .DX__BX(DX__BX), .DX__CX(DX__CX), .DX__EX(DX__EX),
    .EX__AX(EX__AX), .EX__BX(EX__BX), .EX__CX(EX__CX), .EX__DX(EX__DX), .A(cmp_input_adjuster_1_a),
    .B(cmp_input_adjuster_1_b));
  CMP_4 cmp_4_1 (
    .A(cmp_input_adjuster_1_a[3:0]), .B(cmp_input_adjuster_1_b[3:0]), .A___B(cmp_4_1_a___b),
    .A___B_2(cmp_4_1_a___b_2), .A___B_3(cmp_4_1_a___b_3));
  CMP_4 cmp_4_2 (
    .A(cmp_input_adjuster_1_a[7:4]), .B(cmp_input_adjuster_1_b[7:4]), .A___B(cmp_4_2_a___b),
    .A___B_2(cmp_4_2_a___b_2), .A___B_3(cmp_4_2_a___b_3));
  CMP_4 cmp_4_3 (
    .A(cmp_input_adjuster_1_a[11:8]), .B(cmp_input_adjuster_1_b[11:8]), .A___B(cmp_4_3_a___b),
    .A___B_2(cmp_4_3_a___b_2), .A___B_3(cmp_4_3_a___b_3));
  CMP_4 cmp_4_4 (
    .A(cmp_input_adjuster_1_a[15:12]), .B(cmp_input_adjuster_1_b[15:12]), .A___B(cmp_4_4_a___b),
    .A___B_2(cmp_4_4_a___b_2), .A___B_3(cmp_4_4_a___b_3));
  and and_1 (and_1_out, cmp_4_4_a___b_2, cmp_4_3_a___b);
  and and_2 (and_2_out, cmp_4_4_a___b_2, cmp_4_3_a___b_2, cmp_4_2_a___b);
  and and_3 (and_3_out, cmp_4_4_a___b_2, cmp_4_3_a___b_2, cmp_4_2_a___b_2, cmp_4_1_a___b);
  and and_4 (and_4_out, cmp_4_1_a___b_3, cmp_4_2_a___b_2, cmp_4_3_a___b_2, cmp_4_4_a___b_2);
  and and_5 (and_5_out, cmp_4_2_a___b_3, cmp_4_3_a___b_2, cmp_4_4_a___b_2);
  and and_6 (and_6_out, cmp_4_3_a___b_3, cmp_4_4_a___b_2);
  or or_1 (A___B, cmp_4_4_a___b, and_1_out, and_2_out, and_3_out);
  and and_7 (A___B_2, cmp_4_1_a___b_2, cmp_4_2_a___b_2, cmp_4_3_a___b_2, cmp_4_4_a___b_2);
  or or_2 (A___B_3, and_4_out, and_5_out, and_6_out, cmp_4_4_a___b_3);
endmodule

module ADD_ADC (
  input  AX__DR,
  input  BX__DR,
  input  CX__DR,
  input  DX__DR,
  input  EX__DR,
  input  AX__IR,
  input  BX__IR,
  input  CX__IR,
  input  DX__IR,
  input  EX__IR,
  input  AX__BX,
  input  AX__CX,
  input  AX__DX,
  input  AX__EX,
  input  BX__CX,
  input  BX__DX,
  input  BX__EX,
  input  CX__DX,
  input  CX__EX,
  input  DX__EX,
  input  [15:0] AX,
  input  [15:0] BX,
  input  [15:0] CX,
  input  [15:0] DX,
  input  [15:0] EX,
  input  [15:0] DR,
  input  [15:0] IR,
  input  Cin,
  output [15:0] OUTPUT,
  output Cout
);

  wire add_adc_4_1_cout, add_adc_4_2_cout, add_adc_4_3_cout;
  wire [3:0] input_16to4_1_ax_0_3, input_16to4_1_ax_4_7, input_16to4_1_ax_8_11, input_16to4_1_ax_12_15,
       input_16to4_1_bx_0_3, input_16to4_1_bx_4_7, input_16to4_1_bx_8_11, input_16to4_1_bx_12_15,
       input_16to4_1_cx_0_3, input_16to4_1_cx_4_7, input_16to4_1_cx_8_11, input_16to4_1_cx_12_15,
       input_16to4_1_dr_0_3, input_16to4_1_dr_4_7, input_16to4_1_dr_8_11, input_16to4_1_dr_12_15,
       input_16to4_1_dx_0_3, input_16to4_1_dx_4_7, input_16to4_1_dx_8_11, input_16to4_1_dx_12_15,
       input_16to4_1_ex_0_3, input_16to4_1_ex_4_7, input_16to4_1_ex_8_11, input_16to4_1_ex_12_15,
       input_16to4_1_ir_0_3, input_16to4_1_ir_0_3_2, input_16to4_1_ir_4_7, input_16to4_1_ir_12_15;

  INPUT_16to4 input_16to4_1 (
    .AX(AX), .BX(BX), .CX(CX), .DX(DX), .EX(EX), .DR(DR), .IR(IR), .AX_0_3(input_16to4_1_ax_0_3),
    .BX_0_3(input_16to4_1_bx_0_3), .CX_0_3(input_16to4_1_cx_0_3), .DX_0_3(input_16to4_1_dx_0_3),
    .EX_0_3(input_16to4_1_ex_0_3), .DR_0_3(input_16to4_1_dr_0_3), .IR_0_3(input_16to4_1_ir_0_3),
    .AX_4_7(input_16to4_1_ax_4_7), .BX_4_7(input_16to4_1_bx_4_7), .CX_4_7(input_16to4_1_cx_4_7),
    .DX_4_7(input_16to4_1_dx_4_7), .EX_4_7(input_16to4_1_ex_4_7), .DR_4_7(input_16to4_1_dr_4_7),
    .IR_4_7(input_16to4_1_ir_4_7), .AX_8_11(input_16to4_1_ax_8_11), .BX_8_11(input_16to4_1_bx_8_11),
    .CX_8_11(input_16to4_1_cx_8_11), .DX_8_11(input_16to4_1_dx_8_11), .EX_8_11(input_16to4_1_ex_8_11),
    .DR_8_11(input_16to4_1_dr_8_11), .IR_0_3_2(input_16to4_1_ir_0_3_2), .AX_12_15(input_16to4_1_ax_12_15),
    .BX_12_15(input_16to4_1_bx_12_15), .CX_12_15(input_16to4_1_cx_12_15), .DX_12_15(input_16to4_1_dx_12_15),
    .EX_12_15(input_16to4_1_ex_12_15), .DR_12_15(input_16to4_1_dr_12_15), .IR_12_15(input_16to4_1_ir_12_15));
  ADD_ADC_4 add_adc_4_1 (
    .AX(input_16to4_1_ax_0_3), .BX(input_16to4_1_bx_0_3), .CX(input_16to4_1_cx_0_3),
    .DX(input_16to4_1_dx_0_3), .EX(input_16to4_1_ex_0_3), .DR(input_16to4_1_dr_0_3),
    .IR(input_16to4_1_ir_0_3), .Cin(Cin), .AX__DR(AX__DR), .BX__DR(BX__DR), .CX__DR(CX__DR), .DX__DR(DX__DR),
    .EX__DR(EX__DR), .AX__IR(AX__IR), .BX__IR(BX__IR), .CX__IR(CX__IR), .DX__IR(DX__IR), .EX__IR(EX__IR),
    .AX__BX(AX__BX), .AX__CX(AX__CX), .AX__DX(AX__DX), .AX__EX(AX__EX), .BX__CX(BX__CX), .BX__DX(BX__DX),
    .BX__EX(BX__EX), .CX__DX(CX__DX), .CX__EX(CX__EX), .DX__EX(DX__EX), .OUTPUT(OUTPUT[3:0]),
    .Cout(add_adc_4_1_cout));
  ADD_ADC_4 add_adc_4_2 (
    .AX(input_16to4_1_ax_4_7), .BX(input_16to4_1_bx_4_7), .CX(input_16to4_1_cx_4_7),
    .DX(input_16to4_1_dx_4_7), .EX(input_16to4_1_ex_4_7), .DR(input_16to4_1_dr_4_7),
    .IR(input_16to4_1_ir_4_7), .Cin(add_adc_4_1_cout), .AX__DR(AX__DR), .BX__DR(BX__DR), .CX__DR(CX__DR),
    .DX__DR(DX__DR), .EX__DR(EX__DR), .AX__IR(AX__IR), .BX__IR(BX__IR), .CX__IR(CX__IR), .DX__IR(DX__IR),
    .EX__IR(EX__IR), .AX__BX(AX__BX), .AX__CX(AX__CX), .AX__DX(AX__DX), .AX__EX(AX__EX), .BX__CX(BX__CX),
    .BX__DX(BX__DX), .BX__EX(BX__EX), .CX__DX(CX__DX), .CX__EX(CX__EX), .DX__EX(DX__EX),
    .OUTPUT(OUTPUT[7:4]), .Cout(add_adc_4_2_cout));
  ADD_ADC_4 add_adc_4_3 (
    .AX(input_16to4_1_ax_8_11), .BX(input_16to4_1_bx_8_11), .CX(input_16to4_1_cx_8_11),
    .DX(input_16to4_1_dx_8_11), .EX(input_16to4_1_ex_8_11), .DR(input_16to4_1_dr_8_11),
    .IR(input_16to4_1_ir_0_3_2), .Cin(add_adc_4_2_cout), .AX__DR(AX__DR), .BX__DR(BX__DR), .CX__DR(CX__DR),
    .DX__DR(DX__DR), .EX__DR(EX__DR), .AX__IR(AX__IR), .BX__IR(BX__IR), .CX__IR(CX__IR), .DX__IR(DX__IR),
    .EX__IR(EX__IR), .AX__BX(AX__BX), .AX__CX(AX__CX), .AX__DX(AX__DX), .AX__EX(AX__EX), .BX__CX(BX__CX),
    .BX__DX(BX__DX), .BX__EX(BX__EX), .CX__DX(CX__DX), .CX__EX(CX__EX), .DX__EX(DX__EX),
    .OUTPUT(OUTPUT[11:8]), .Cout(add_adc_4_3_cout));
  ADD_ADC_4 add_adc_4_4 (
    .AX(input_16to4_1_ax_12_15), .BX(input_16to4_1_bx_12_15), .CX(input_16to4_1_cx_12_15),
    .DX(input_16to4_1_dx_12_15), .EX(input_16to4_1_ex_12_15), .DR(input_16to4_1_dr_12_15),
    .IR(input_16to4_1_ir_12_15), .Cin(add_adc_4_3_cout), .AX__DR(AX__DR), .BX__DR(BX__DR), .CX__DR(CX__DR),
    .DX__DR(DX__DR), .EX__DR(EX__DR), .AX__IR(AX__IR), .BX__IR(BX__IR), .CX__IR(CX__IR), .DX__IR(DX__IR),
    .EX__IR(EX__IR), .AX__BX(AX__BX), .AX__CX(AX__CX), .AX__DX(AX__DX), .AX__EX(AX__EX), .BX__CX(BX__CX),
    .BX__DX(BX__DX), .BX__EX(BX__EX), .CX__DX(CX__DX), .CX__EX(CX__EX), .DX__EX(DX__EX),
    .OUTPUT(OUTPUT[15:12]), .Cout(Cout));
endmodule

module SUB_SBB (
  input  AX__DR,
  input  BX__DR,
  input  CX__DR,
  input  DX__DR,
  input  EX__DR,
  input  AX__IR,
  input  BX__IR,
  input  CX__IR,
  input  DX__IR,
  input  EX__IR,
  input  AX__BX,
  input  AX__CX,
  input  AX__DX,
  input  AX__EX,
  input  BX__AX,
  input  BX__CX,
  input  BX__DX,
  input  BX__EX,
  input  CX__AX,
  input  CX__BX,
  input  CX__DX,
  input  CX__EX,
  input  DX__AX,
  input  DX__BX,
  input  DX__CX,
  input  DX__EX,
  input  EX__AX,
  input  EX__BX,
  input  EX__CX,
  input  EX__DX,
  input  [15:0] AX,
  input  [15:0] BX,
  input  [15:0] CX,
  input  [15:0] DX,
  input  [15:0] EX,
  input  [15:0] DR,
  input  [15:0] IR,
  input  Bin,
  output [15:0] OUTPUT,
  output Bout
);

  wire sub_sbb_4_1_bout, sub_sbb_4_2_bout, sub_sbb_4_3_bout;
  wire [3:0] input_16to4_1_ax_0_3, input_16to4_1_ax_4_7, input_16to4_1_ax_8_11, input_16to4_1_ax_12_15,
       input_16to4_1_bx_0_3, input_16to4_1_bx_4_7, input_16to4_1_bx_8_11, input_16to4_1_bx_12_15,
       input_16to4_1_cx_0_3, input_16to4_1_cx_4_7, input_16to4_1_cx_8_11, input_16to4_1_cx_12_15,
       input_16to4_1_dr_0_3, input_16to4_1_dr_4_7, input_16to4_1_dr_8_11, input_16to4_1_dr_12_15,
       input_16to4_1_dx_0_3, input_16to4_1_dx_4_7, input_16to4_1_dx_8_11, input_16to4_1_dx_12_15,
       input_16to4_1_ex_0_3, input_16to4_1_ex_4_7, input_16to4_1_ex_8_11, input_16to4_1_ex_12_15,
       input_16to4_1_ir_0_3, input_16to4_1_ir_0_3_2, input_16to4_1_ir_4_7, input_16to4_1_ir_12_15;

  INPUT_16to4 input_16to4_1 (
    .AX(AX), .BX(BX), .CX(CX), .DX(DX), .EX(EX), .DR(DR), .IR(IR), .AX_0_3(input_16to4_1_ax_0_3),
    .BX_0_3(input_16to4_1_bx_0_3), .CX_0_3(input_16to4_1_cx_0_3), .DX_0_3(input_16to4_1_dx_0_3),
    .EX_0_3(input_16to4_1_ex_0_3), .DR_0_3(input_16to4_1_dr_0_3), .IR_0_3(input_16to4_1_ir_0_3),
    .AX_4_7(input_16to4_1_ax_4_7), .BX_4_7(input_16to4_1_bx_4_7), .CX_4_7(input_16to4_1_cx_4_7),
    .DX_4_7(input_16to4_1_dx_4_7), .EX_4_7(input_16to4_1_ex_4_7), .DR_4_7(input_16to4_1_dr_4_7),
    .IR_4_7(input_16to4_1_ir_4_7), .AX_8_11(input_16to4_1_ax_8_11), .BX_8_11(input_16to4_1_bx_8_11),
    .CX_8_11(input_16to4_1_cx_8_11), .DX_8_11(input_16to4_1_dx_8_11), .EX_8_11(input_16to4_1_ex_8_11),
    .DR_8_11(input_16to4_1_dr_8_11), .IR_0_3_2(input_16to4_1_ir_0_3_2), .AX_12_15(input_16to4_1_ax_12_15),
    .BX_12_15(input_16to4_1_bx_12_15), .CX_12_15(input_16to4_1_cx_12_15), .DX_12_15(input_16to4_1_dx_12_15),
    .EX_12_15(input_16to4_1_ex_12_15), .DR_12_15(input_16to4_1_dr_12_15), .IR_12_15(input_16to4_1_ir_12_15));
  SUB_SBB_4 sub_sbb_4_1 (
    .AX(input_16to4_1_ax_0_3), .BX(input_16to4_1_bx_0_3), .CX(input_16to4_1_cx_0_3),
    .DX(input_16to4_1_dx_0_3), .EX(input_16to4_1_ex_0_3), .DR(input_16to4_1_dr_0_3),
    .IR(input_16to4_1_ir_0_3), .Bin(Bin), .AX__DR(AX__DR), .BX__DR(BX__DR), .CX__DR(CX__DR), .DX__DR(DX__DR),
    .EX__DR(EX__DR), .AX__IR(AX__IR), .BX__IR(BX__IR), .CX__IR(CX__IR), .DX__IR(DX__IR), .EX__IR(EX__IR),
    .AX__BX(AX__BX), .AX__CX(AX__CX), .AX__DX(AX__DX), .AX__EX(AX__EX), .BX__AX(BX__AX), .BX__CX(BX__CX),
    .BX__DX(BX__DX), .BX__EX(BX__EX), .CX__AX(CX__AX), .CX__BX(CX__BX), .CX__DX(CX__DX), .CX__EX(CX__EX),
    .DX__AX(DX__AX), .DX__BX(DX__BX), .DX__CX(DX__CX), .DX__EX(DX__EX), .EX__AX(EX__AX), .EX__BX(EX__BX),
    .EX__CX(EX__CX), .EX__DX(EX__DX), .OUTPUT(OUTPUT[3:0]), .Bout(sub_sbb_4_1_bout));
  SUB_SBB_4 sub_sbb_4_2 (
    .AX(input_16to4_1_ax_4_7), .BX(input_16to4_1_bx_4_7), .CX(input_16to4_1_cx_4_7),
    .DX(input_16to4_1_dx_4_7), .EX(input_16to4_1_ex_4_7), .DR(input_16to4_1_dr_4_7),
    .IR(input_16to4_1_ir_4_7), .Bin(sub_sbb_4_1_bout), .AX__DR(AX__DR), .BX__DR(BX__DR), .CX__DR(CX__DR),
    .DX__DR(DX__DR), .EX__DR(EX__DR), .AX__IR(AX__IR), .BX__IR(BX__IR), .CX__IR(CX__IR), .DX__IR(DX__IR),
    .EX__IR(EX__IR), .AX__BX(AX__BX), .AX__CX(AX__CX), .AX__DX(AX__DX), .AX__EX(AX__EX), .BX__AX(BX__AX),
    .BX__CX(BX__CX), .BX__DX(BX__DX), .BX__EX(BX__EX), .CX__AX(CX__AX), .CX__BX(CX__BX), .CX__DX(CX__DX),
    .CX__EX(CX__EX), .DX__AX(DX__AX), .DX__BX(DX__BX), .DX__CX(DX__CX), .DX__EX(DX__EX), .EX__AX(EX__AX),
    .EX__BX(EX__BX), .EX__CX(EX__CX), .EX__DX(EX__DX), .OUTPUT(OUTPUT[7:4]), .Bout(sub_sbb_4_2_bout));
  SUB_SBB_4 sub_sbb_4_3 (
    .AX(input_16to4_1_ax_8_11), .BX(input_16to4_1_bx_8_11), .CX(input_16to4_1_cx_8_11),
    .DX(input_16to4_1_dx_8_11), .EX(input_16to4_1_ex_8_11), .DR(input_16to4_1_dr_8_11),
    .IR(input_16to4_1_ir_0_3_2), .Bin(sub_sbb_4_2_bout), .AX__DR(AX__DR), .BX__DR(BX__DR), .CX__DR(CX__DR),
    .DX__DR(DX__DR), .EX__DR(EX__DR), .AX__IR(AX__IR), .BX__IR(BX__IR), .CX__IR(CX__IR), .DX__IR(DX__IR),
    .EX__IR(EX__IR), .AX__BX(AX__BX), .AX__CX(AX__CX), .AX__DX(AX__DX), .AX__EX(AX__EX), .BX__AX(BX__AX),
    .BX__CX(BX__CX), .BX__DX(BX__DX), .BX__EX(BX__EX), .CX__AX(CX__AX), .CX__BX(CX__BX), .CX__DX(CX__DX),
    .CX__EX(CX__EX), .DX__AX(DX__AX), .DX__BX(DX__BX), .DX__CX(DX__CX), .DX__EX(DX__EX), .EX__AX(EX__AX),
    .EX__BX(EX__BX), .EX__CX(EX__CX), .EX__DX(EX__DX), .OUTPUT(OUTPUT[11:8]), .Bout(sub_sbb_4_3_bout));
  SUB_SBB_4 sub_sbb_4_4 (
    .AX(input_16to4_1_ax_12_15), .BX(input_16to4_1_bx_12_15), .CX(input_16to4_1_cx_12_15),
    .DX(input_16to4_1_dx_12_15), .EX(input_16to4_1_ex_12_15), .DR(input_16to4_1_dr_12_15),
    .IR(input_16to4_1_ir_12_15), .Bin(sub_sbb_4_3_bout), .AX__DR(AX__DR), .BX__DR(BX__DR), .CX__DR(CX__DR),
    .DX__DR(DX__DR), .EX__DR(EX__DR), .AX__IR(AX__IR), .BX__IR(BX__IR), .CX__IR(CX__IR), .DX__IR(DX__IR),
    .EX__IR(EX__IR), .AX__BX(AX__BX), .AX__CX(AX__CX), .AX__DX(AX__DX), .AX__EX(AX__EX), .BX__AX(BX__AX),
    .BX__CX(BX__CX), .BX__DX(BX__DX), .BX__EX(BX__EX), .CX__AX(CX__AX), .CX__BX(CX__BX), .CX__DX(CX__DX),
    .CX__EX(CX__EX), .DX__AX(DX__AX), .DX__BX(DX__BX), .DX__CX(DX__CX), .DX__EX(DX__EX), .EX__AX(EX__AX),
    .EX__BX(EX__BX), .EX__CX(EX__CX), .EX__DX(EX__DX), .OUTPUT(OUTPUT[15:12]), .Bout(Bout));
endmodule
