// Logisim project ARITHMETIC_UNITS.circ as structural Verilog: 5 circuits, main circuit ADD_ADC
module ADD_ADC (
  input  [15:0] AX,
  input  [15:0] BX,
  input  [15:0] CX,
  input  [15:0] DX,
  input  [15:0] EX,
  input  [15:0] DR,
  input  [15:0] IR,
  input  Cin,
  input  AX_2,
  input  BX_2,
  input  CX_2,
  input  DX_2,
  input  EX_2,
  input  DR_2,
  input  IR_2,
  output [15:0] OUTPUT,
  output Cout
);

  wire add_adc_4_2_cout, add_adc_4_3_cout, add_adc_4_4_cout;
  wire [3:0] input_16to4_1_ax_0_3, input_16to4_1_ax_4_7, input_16to4_1_bx_0_3, input_16to4_1_bx_4_7,
       input_16to4_1_cx_0_3, input_16to4_1_cx_4_7, input_16to4_1_dr_0_3, input_16to4_1_dr_4_7,
       input_16to4_1_dx_0_3, input_16to4_1_dx_4_7, input_16to4_1_ex_0_3, input_16to4_1_ex_4_7,
       input_16to4_1_ir_0_3, input_16to4_1_ir_4_7;
  wire [27:0] input_16to4_1_ir_8_11, input_16to4_1_ir_15_12;

  ADD_ADC_4 add_adc_4_1 (
    .AX_2(AX_2), .BX_2(BX_2), .CX_2(CX_2), .DX_2(DX_2), .EX_2(EX_2), .DR_2(DR_2), .IR_2(IR_2),
    .AX(input_16to4_1_ir_15_12[27:24]), .BX(input_16to4_1_ir_15_12[23:20]),
    .CX(input_16to4_1_ir_15_12[19:16]), .DX(input_16to4_1_ir_15_12[15:12]),
    .EX(input_16to4_1_ir_15_12[11:8]), .DR(input_16to4_1_ir_15_12[7:4]), .IR(input_16to4_1_ir_15_12[3:0]),
    .Cin(add_adc_4_2_cout), .Cout(Cout), .OUTPUT(OUTPUT[15:12]));
  INPUT_16to4 input_16to4_1 (
    .AX(AX), .BX(BX), .CX(CX), .DX(DX), .EX(EX), .DR(DR), .IR(IR), .AX_15_12(input_16to4_1_ir_15_12[27:24]),
    .BX_15_12(input_16to4_1_ir_15_12[23:20]), .CX_15_12(input_16to4_1_ir_15_12[19:16]),
    .DX_15_12(input_16to4_1_ir_15_12[15:12]), .EX_15_12(input_16to4_1_ir_15_12[11:8]),
    .DR_15_12(input_16to4_1_ir_15_12[7:4]), .IR_15_12(input_16to4_1_ir_15_12[3:0]),
    .AX_8_11(input_16to4_1_ir_8_11[27:24]), .BX_8_11(input_16to4_1_ir_8_11[23:20]),
    .CX_8_11(input_16to4_1_ir_8_11[19:16]), .DX_8_11(input_16to4_1_ir_8_11[15:12]),
    .EX_8_11(input_16to4_1_ir_8_11[11:8]), .DR_2(input_16to4_1_ir_8_11[7:4]),
    .IR_8_11(input_16to4_1_ir_8_11[3:0]), .AX_4_7(input_16to4_1_ax_4_7), .BX_4_7(input_16to4_1_bx_4_7),
    .CX_4_7(input_16to4_1_cx_4_7), .DX_4_7(input_16to4_1_dx_4_7), .EX_4_7(input_16to4_1_ex_4_7),
    .DR_4_7(input_16to4_1_dr_4_7), .IR_4_7(input_16to4_1_ir_4_7), .AX_0_3(input_16to4_1_ax_0_3),
    .BX_0_3(input_16to4_1_bx_0_3), .CX_0_3(input_16to4_1_cx_0_3), .DX_0_3(input_16to4_1_dx_0_3),
    .EX_0_3(input_16to4_1_ex_0_3), .DR_0_3(input_16to4_1_dr_0_3), .IR_0_3(input_16to4_1_ir_0_3));
  ADD_ADC_4 add_adc_4_2 (
    .AX_2(AX_2), .BX_2(BX_2), .CX_2(CX_2), .DX_2(DX_2), .EX_2(EX_2), .DR_2(DR_2), .IR_2(IR_2),
    .AX(input_16to4_1_ir_8_11[27:24]), .BX(input_16to4_1_ir_8_11[23:20]), .CX(input_16to4_1_ir_8_11[19:16]),
    .DX(input_16to4_1_ir_8_11[15:12]), .EX(input_16to4_1_ir_8_11[11:8]), .DR(input_16to4_1_ir_8_11[7:4]),
    .IR(input_16to4_1_ir_8_11[3:0]), .Cin(add_adc_4_3_cout), .Cout(add_adc_4_2_cout), .OUTPUT(OUTPUT[11:8]));
  ADD_ADC_4 add_adc_4_3 (
    .AX_2(AX_2), .BX_2(BX_2), .CX_2(CX_2), .DX_2(DX_2), .EX_2(EX_2), .DR_2(DR_2), .IR_2(IR_2),
    .AX(input_16to4_1_ax_4_7), .BX(input_16to4_1_bx_4_7), .CX(input_16to4_1_cx_4_7),
    .DX(input_16to4_1_dx_4_7), .EX(input_16to4_1_ex_4_7), .DR(input_16to4_1_dr_4_7),
    .IR(input_16to4_1_ir_4_7), .Cin(add_adc_4_4_cout), .Cout(add_adc_4_3_cout), .OUTPUT(OUTPUT[7:4]));
  ADD_ADC_4 add_adc_4_4 (
    .AX_2(AX_2), .BX_2(BX_2), .CX_2(CX_2), .DX_2(DX_2), .EX_2(EX_2), .DR_2(DR_2), .IR_2(IR_2),
    .AX(input_16to4_1_ax_0_3), .BX(input_16to4_1_bx_0_3), .CX(input_16to4_1_cx_0_3),
    .DX(input_16to4_1_dx_0_3), .EX(input_16to4_1_ex_0_3), .DR(input_16to4_1_dr_0_3),
    .IR(input_16to4_1_ir_0_3), .Cin(Cin), .Cout(add_adc_4_4_cout), .OUTPUT(OUTPUT[3:0]));
endmodule

module SUB_SBB (
  input  [15:0] AX,
  input  [15:0] BX,
  input  [15:0] CX,
  input  [15:0] DX,
  input  [15:0] EX,
  input  [15:0] DR,
  input  [15:0] IR,
  input  Bin,
  input  AX_2,
  input  BX_2,
  input  CX_2,
  input  DX_2,
  input  EX_2,
  input  DR_2,
  input  IR_2,
  input  AX_3,
  input  BX_3,
  input  CX_3,
  input  DX_3,
  input  EX_3,
  input  DR_3,
  input  IR_3,
  output [15:0] OUTPUT,
  output Bout
);

  wire sub_sbb_4_2_bout, sub_sbb_4_3_bout, sub_sbb_4_4_bout;
  wire [3:0] input_16to4_1_ax_0_3, input_16to4_1_ax_4_7, input_16to4_1_bx_0_3, input_16to4_1_bx_4_7,
       input_16to4_1_cx_0_3, input_16to4_1_cx_4_7, input_16to4_1_dr_0_3, input_16to4_1_dr_4_7,
       input_16to4_1_dx_0_3, input_16to4_1_dx_4_7, input_16to4_1_ex_0_3, input_16to4_1_ex_4_7,
       input_16to4_1_ir_0_3, input_16to4_1_ir_4_7;
  wire [27:0] input_16to4_1_ir_8_11, input_16to4_1_ir_15_12;

  SUB_SBB_4 sub_sbb_4_1 (
    .AX_2(AX_2), .BX_2(BX_2), .CX_2(CX_2), .DX_2(DX_2), .EX_2(EX_2), .DR_2(DR_2), .IR_2(IR_2), .AX_3(AX_3),
    .BX_3(BX_3), .CX_3(CX_3), .DX_3(DX_3), .EX_3(EX_3), .DR_3(DR_3), .IR_3(IR_3),
    .AX(input_16to4_1_ir_15_12[27:24]), .BX(input_16to4_1_ir_15_12[23:20]),
    .CX(input_16to4_1_ir_15_12[19:16]), .DX(input_16to4_1_ir_15_12[15:12]),
    .EX(input_16to4_1_ir_15_12[11:8]), .DR(input_16to4_1_ir_15_12[7:4]), .IR(input_16to4_1_ir_15_12[3:0]),
    .Bin(sub_sbb_4_2_bout), .Bout(Bout), .OUTPUT(OUTPUT[15:12]));
  INPUT_16to4 input_16to4_1 (
    .AX(AX), .BX(BX), .CX(CX), .DX(DX), .EX(EX), .DR(DR), .IR(IR), .AX_15_12(input_16to4_1_ir_15_12[27:24]),
    .BX_15_12(input_16to4_1_ir_15_12[23:20]), .CX_15_12(input_16to4_1_ir_15_12[19:16]),
    .DX_15_12(input_16to4_1_ir_15_12[15:12]), .EX_15_12(input_16to4_1_ir_15_12[11:8]),
    .DR_15_12(input_16to4_1_ir_15_12[7:4]), .IR_15_12(input_16to4_1_ir_15_12[3:0]),
    .AX_8_11(input_16to4_1_ir_8_11[27:24]), .BX_8_11(input_16to4_1_ir_8_11[23:20]),
    .CX_8_11(input_16to4_1_ir_8_11[19:16]), .DX_8_11(input_16to4_1_ir_8_11[15:12]),
    .EX_8_11(input_16to4_1_ir_8_11[11:8]), .DR_2(input_16to4_1_ir_8_11[7:4]),
    .IR_8_11(input_16to4_1_ir_8_11[3:0]), .AX_4_7(input_16to4_1_ax_4_7), .BX_4_7(input_16to4_1_bx_4_7),
    .CX_4_7(input_16to4_1_cx_4_7), .DX_4_7(input_16to4_1_dx_4_7), .EX_4_7(input_16to4_1_ex_4_7),
    .DR_4_7(input_16to4_1_dr_4_7), .IR_4_7(input_16to4_1_ir_4_7), .AX_0_3(input_16to4_1_ax_0_3),
    .BX_0_3(input_16to4_1_bx_0_3), .CX_0_3(input_16to4_1_cx_0_3), .DX_0_3(input_16to4_1_dx_0_3),
    .EX_0_3(input_16to4_1_ex_0_3), .DR_0_3(input_16to4_1_dr_0_3), .IR_0_3(input_16to4_1_ir_0_3));
  SUB_SBB_4 sub_sbb_4_2 (
    .AX_2(AX_2), .BX_2(BX_2), .CX_2(CX_2), .DX_2(DX_2), .EX_2(EX_2), .DR_2(DR_2), .IR_2(IR_2), .AX_3(AX_3),
    .BX_3(BX_3), .CX_3(CX_3), .DX_3(DX_3), .EX_3(EX_3), .DR_3(DR_3), .IR_3(IR_3),
    .AX(input_16to4_1_ir_8_11[27:24]), .BX(input_16to4_1_ir_8_11[23:20]), .CX(input_16to4_1_ir_8_11[19:16]),
    .DX(input_16to4_1_ir_8_11[15:12]), .EX(input_16to4_1_ir_8_11[11:8]), .DR(input_16to4_1_ir_8_11[7:4]),
    .IR(input_16to4_1_ir_8_11[3:0]), .Bin(sub_sbb_4_3_bout), .Bout(sub_sbb_4_2_bout), .OUTPUT(OUTPUT[11:8]));
  SUB_SBB_4 sub_sbb_4_3 (
    .AX_2(AX_2), .BX_2(BX_2), .CX_2(CX_2), .DX_2(DX_2), .EX_2(EX_2), .DR_2(DR_2), .IR_2(IR_2), .AX_3(AX_3),
    .BX_3(BX_3), .CX_3(CX_3), .DX_3(DX_3), .EX_3(EX_3), .DR_3(DR_3), .IR_3(IR_3), .AX(input_16to4_1_ax_4_7),
    .BX(input_16to4_1_bx_4_7), .CX(input_16to4_1_cx_4_7), .DX(input_16to4_1_dx_4_7),
    .EX(input_16to4_1_ex_4_7), .DR(input_16to4_1_dr_4_7), .IR(input_16to4_1_ir_4_7), .Bin(sub_sbb_4_4_bout),
    .Bout(sub_sbb_4_3_bout), .OUTPUT(OUTPUT[7:4]));
  SUB_SBB_4 sub_sbb_4_4 (
    .AX_2(AX_2), .BX_2(BX_2), .CX_2(CX_2), .DX_2(DX_2), .EX_2(EX_2), .DR_2(DR_2), .IR_2(IR_2), .AX_3(AX_3),
    .BX_3(BX_3), .CX_3(CX_3), .DX_3(DX_3), .EX_3(EX_3), .DR_3(DR_3), .IR_3(IR_3), .AX(input_16to4_1_ax_0_3),
    .BX(input_16to4_1_bx_0_3), .CX(input_16to4_1_cx_0_3), .DX(input_16to4_1_dx_0_3),
    .EX(input_16to4_1_ex_0_3), .DR(input_16to4_1_dr_0_3), .IR(input_16to4_1_ir_0_3), .Bin(Bin),
    .Bout(sub_sbb_4_4_bout), .OUTPUT(OUTPUT[3:0]));
endmodule

module MUL (
  input  [15:0] AX,
  input  AX_2,
  input  BX,
  input  CX,
  input  DX,
  input  EX,
  input  DR,
  input  IR,
  input  [15:0] BX_2,
  input  [15:0] CX_2,
  input  [15:0] DX_2,
  input  [15:0] EX_2,
  input  [15:0] DR_2,
  input  [15:0] IR_2,
  output [15:0] LOW_16,
  output [15:0] HIGH_16
);

  wire [15:0] mul_input_adjuster_1_multiplied, mul_input_adjuster_1_multiplier;
  wire [19:0] mul_4_line_adder_2_output, mul_4_line_adder_3_output, mul_4_line_adder_4_output;
  wire [19:4] adder_1_out, adder_2_out, mul_4_line_adder_1_output;

  MUL_INPUT_ADJUSTER mul_input_adjuster_1 (
    .AX_2(AX), .BX_2(BX_2), .CX_2(CX_2), .DX_2(DX_2), .EX_2(EX_2), .DR_2(DR_2), .IR_2(IR_2), .AX(AX_2),
    .BX(BX), .CX(CX), .DX(DX), .EX(EX), .DR(DR), .IR(IR), .MULTIPLIER(mul_input_adjuster_1_multiplier),
    .MULTIPLIED(mul_input_adjuster_1_multiplied));
  MUL_4_LINE_ADDER mul_4_line_adder_1 (
    .MULTIPLIED(mul_input_adjuster_1_multiplied), .MULTIPLIER(mul_input_adjuster_1_multiplier[3:0]),
    .OUTPUT({mul_4_line_adder_1_output, LOW_16[3:0]}));
  MUL_4_LINE_ADDER mul_4_line_adder_2 (
    .MULTIPLIED(mul_input_adjuster_1_multiplied), .MULTIPLIER(mul_input_adjuster_1_multiplier[7:4]),
    .OUTPUT(mul_4_line_adder_2_output));
  MUL_4_LINE_ADDER mul_4_line_adder_3 (
    .MULTIPLIED(mul_input_adjuster_1_multiplied), .MULTIPLIER(mul_input_adjuster_1_multiplier[11:8]),
    .OUTPUT(mul_4_line_adder_3_output));
  Adder #(.width(20)) adder_1 (
    .a(mul_4_line_adder_2_output), .b({4'b0000, mul_4_line_adder_1_output}), .out({adder_1_out, LOW_16[7:4]}));  // open: cin, cout
  MUL_4_LINE_ADDER mul_4_line_adder_4 (
    .MULTIPLIED(mul_input_adjuster_1_multiplied), .MULTIPLIER(mul_input_adjuster_1_multiplier[15:12]),
    .OUTPUT(mul_4_line_adder_4_output));
  Adder #(.width(20)) adder_2 (
    .a(mul_4_line_adder_3_output), .b({4'b0000, adder_1_out}), .out({adder_2_out, LOW_16[11:8]}));  // open: cin, cout
  Adder #(.width(20)) adder_3 (
    .a(mul_4_line_adder_4_output), .b({4'b0000, adder_2_out}), .out({HIGH_16, LOW_16[15:12]}));  // open: cin, cout
endmodule

module DIV (
  input  AX,
  input  BX,
  input  CX,
  input  DX,
  input  EX,
  input  DR,
  input  IR,
  input  AX_2,
  input  BX_2,
  input  CX_2,
  input  DX_2,
  input  EX_2,
  input  DR_2,
  input  IR_2,
  input  [15:0] AX_3,
  input  [15:0] BX_3,
  input  [15:0] CX_3,
  input  [15:0] DX_3,
  input  [15:0] EX_3,
  input  [15:0] DR_3,
  input  [15:0] IR_3,
  output [15:0] QUOTIENT,
  output [15:0] REMAINDER
);

  wire [15:0] div_4_line_1_r, div_4_line_2_r, div_4_line_3_r, div_input_adjuster_1_dividend,
       div_input_adjuster_1_divisor;

  DIV_INPUT_ADJUSTER div_input_adjuster_1 (
    .AX_3(AX_3), .BX_3(BX_3), .CX_3(CX_3), .DX_3(DX_3), .EX_3(EX_3), .DR_3(DR_3), .IR_3(IR_3), .AX(AX),
    .BX(BX), .CX(CX), .DX(DX), .EX(EX), .DR(DR), .IR(IR), .AX_2(AX_2), .BX_2(BX_2), .CX_2(CX_2), .DX_2(DX_2),
    .EX_2(EX_2), .DR_2(DR_2), .IR_2(IR_2), .DIVIDEND(div_input_adjuster_1_dividend),
    .DIVISOR(div_input_adjuster_1_divisor));
  DIV_4_LINE div_4_line_1 (
    .DIVIDEND_4(div_input_adjuster_1_dividend[15:12]), .R_FROM_UP_LINE({16{1'b0}}),
    .DIVISOR(div_input_adjuster_1_divisor), .Q(QUOTIENT[15:12]), .R(div_4_line_1_r));
  DIV_4_LINE div_4_line_2 (
    .DIVIDEND_4(div_input_adjuster_1_dividend[11:8]), .R_FROM_UP_LINE(div_4_line_1_r),
    .DIVISOR(div_input_adjuster_1_divisor), .Q(QUOTIENT[11:8]), .R(div_4_line_2_r));
  DIV_4_LINE div_4_line_3 (
    .DIVIDEND_4(div_input_adjuster_1_dividend[7:4]), .R_FROM_UP_LINE(div_4_line_2_r),
    .DIVISOR(div_input_adjuster_1_divisor), .Q(QUOTIENT[7:4]), .R(div_4_line_3_r));
  DIV_4_LINE div_4_line_4 (
    .DIVIDEND_4(div_input_adjuster_1_dividend[3:0]), .R_FROM_UP_LINE(div_4_line_3_r),
    .DIVISOR(div_input_adjuster_1_divisor), .Q(QUOTIENT[3:0]), .R(REMAINDER));
endmodule

module CMP (
  input  AX,
  input  BX,
  input  CX,
  input  DX,
  input  EX,
  input  DR,
  input  IR,
  input  AX_2,
  input  BX_2,
  input  CX_2,
  input  DX_2,
  input  EX_2,
  input  DR_2,
  input  IR_2,
  input  [15:0] AX_3,
  input  [15:0] BX_3,
  input  [15:0] CX_3,
  input  [15:0] DX_3,
  input  [15:0] EX_3,
  input  [15:0] DR_3,
  input  [15:0] IR_3,
  output A___B,
  output A___B_2,
  output A___B_3
);

  wire and_1_out, and_2_out, and_3_out, and_5_out, and_6_out, and_7_out, cmp_4_1_a___b, cmp_4_1_a___b_2,
       cmp_4_1_a___b_3, cmp_4_2_a___b, cmp_4_2_a___b_2, cmp_4_2_a___b_3, cmp_4_3_a___b, cmp_4_3_a___b_2,
       cmp_4_3_a___b_3, cmp_4_4_a___b, cmp_4_4_a___b_2, cmp_4_4_a___b_3;
  wire [15:0] cmp_input_adjuster_1_a, cmp_input_adjuster_1_b;

  CMP_INPUT_ADJUSTER cmp_input_adjuster_1 (
    .AX_3(AX_3), .BX_3(BX_3), .CX_3(CX_3), .DX_3(DX_3), .EX_3(EX_3), .DR_3(DR_3), .IR_3(IR_3), .AX(AX),
    .BX(BX), .CX(CX), .DX(DX), .EX(EX), .DR(DR), .IR(IR), .AX_2(AX_2), .BX_2(BX_2), .CX_2(CX_2), .DX_2(DX_2),
    .EX_2(EX_2), .DR_2(DR_2), .IR_2(IR_2), .A(cmp_input_adjuster_1_a), .B(cmp_input_adjuster_1_b));
  CMP_4 cmp_4_1 (
    .A(cmp_input_adjuster_1_a[3:0]), .B(cmp_input_adjuster_1_b[3:0]), .A___B(cmp_4_1_a___b),
    .A___B_2(cmp_4_1_a___b_2), .A___B_3(cmp_4_1_a___b_3));
  CMP_4 cmp_4_2 (
    .A(cmp_input_adjuster_1_a[7:4]), .B(cmp_input_adjuster_1_b[7:4]), .A___B(cmp_4_2_a___b),
    .A___B_2(cmp_4_2_a___b_2), .A___B_3(cmp_4_2_a___b_3));
  CMP_4 cmp_4_3 (
    .A(cmp_input_adjuster_1_a[11:8]), .B(cmp_input_adjuster_1_b[11:8]), .A___B(cmp_4_3_a___b),
    .A___B_2(cmp_4_3_a___b_2), .A___B_3(cmp_4_3_a___b_3));
  CMP_4 cmp_4_4 (
    .A(cmp_input_adjuster_1_a[15:12]), .B(cmp_input_adjuster_1_b[15:12]), .A___B(cmp_4_4_a___b),
    .A___B_2(cmp_4_4_a___b_2), .A___B_3(cmp_4_4_a___b_3));
  and and_1 (and_1_out, cmp_4_4_a___b_2, cmp_4_3_a___b);
  and and_2 (and_2_out, cmp_4_4_a___b_2, cmp_4_3_a___b_2, cmp_4_2_a___b);
  and and_3 (and_3_out, cmp_4_4_a___b_2, cmp_4_3_a___b_2, cmp_4_2_a___b_2, cmp_4_1_a___b);
  and and_4 (A___B_2, cmp_4_1_a___b_2, cmp_4_2_a___b_2, cmp_4_3_a___b_2, cmp_4_4_a___b_2);
  and and_5 (and_5_out, cmp_4_1_a___b_3, cmp_4_2_a___b_2, cmp_4_3_a___b_2, cmp_4_4_a___b_2);
  and and_6 (and_6_out, cmp_4_2_a___b_3, cmp_4_3_a___b_2, cmp_4_4_a___b_2);
  and and_7 (and_7_out, cmp_4_3_a___b_3, cmp_4_4_a___b_2);
  or or_1 (A___B, cmp_4_4_a___b, and_1_out, and_2_out, and_3_out);
  or or_2 (A___B_3, and_5_out, and_6_out, and_7_out, cmp_4_4_a___b_3);
endmodule
