// Logisim project Sub_Circuits.circ as structural Verilog: 16 circuits, main circuit INPUT_4to1
// 4to1_ADJUSTER
module INPUT_4to1 (
  input  [3:0] AX,
  input  [3:0] BX,
  input  [3:0] CX,
  input  [3:0] DX,
  input  [3:0] EX,
  input  [3:0] DR,
  input  [3:0] IR,
  output AX3,
  output BX3,
  output CX3,
  output DX3,
  output EX3,
  output DR3,
  output IR3,
  output AX2,
  output BX2,
  output CX2,
  output DX2,
  output EX2,
  output DR2,
  output IR2,
  output AX1,
  output BX1,
  output CX1,
  output DX1,
  output EX1,
  output DR1,
  output IR1,
  output AX0,
  output BX0,
  output CX0,
  output DX0,
  output EX0,
  output DR0,
  output IR0
);


  assign AX0 = AX[0];
  assign AX1 = AX[1];
  assign AX2 = AX[2];
  assign AX3 = AX[3];
  assign BX0 = BX[0];
  assign BX1 = BX[1];
  assign BX2 = BX[2];
  assign BX3 = BX[3];
  assign CX0 = CX[0];
  assign CX1 = CX[1];
  assign CX2 = CX[2];
  assign CX3 = CX[3];
  assign DR0 = DR[0];
  assign DR1 = DR[1];
  assign DR2 = DR[2];
  assign DR3 = DR[3];
  assign DX0 = DX[0];
  assign DX1 = DX[1];
  assign DX2 = DX[2];
  assign DX3 = DX[3];
  assign EX0 = EX[0];
  assign EX1 = EX[1];
  assign EX2 = EX[2];
  assign EX3 = EX[3];
  assign IR0 = IR[0];
  assign IR1 = IR[1];
  assign IR2 = IR[2];
  assign IR3 = IR[3];
endmodule

// 16to4_ADJUSTER
module INPUT_16to4 (
  input  [15:0] AX,
  input  [15:0] BX,
  input  [15:0] CX,
  input  [15:0] DX,
  input  [15:0] EX,
  input  [15:0] DR,
  input  [15:0] IR,
  output [3:0] AX_15_12,
  output [3:0] BX_15_12,
  output [3:0] CX_15_12,
  output [3:0] DX_15_12,
  output [3:0] EX_15_12,
  output [3:0] DR_15_12,
  output [3:0] IR_15_12,
  output [3:0] AX_8_11,
  output [3:0] BX_8_11,
  output [3:0] CX_8_11,
  output [3:0] DX_8_11,
  output [3:0] EX_8_11,
  output [3:0] DR_2,
  output [3:0] IR_8_11,
  output [3:0] AX_4_7,
  output [3:0] BX_4_7,
  output [3:0] CX_4_7,
  output [3:0] DX_4_7,
  output [3:0] EX_4_7,
  output [3:0] DR_4_7,
  output [3:0] IR_4_7,
  output [3:0] AX_0_3,
  output [3:0] BX_0_3,
  output [3:0] CX_0_3,
  output [3:0] DX_0_3,
  output [3:0] EX_0_3,
  output [3:0] DR_0_3,
  output [3:0] IR_0_3
);


  assign AX_0_3 = AX[3:0];
  assign AX_4_7 = AX[7:4];
  assign AX_8_11 = AX[11:8];
  assign AX_15_12 = AX[15:12];
  assign BX_0_3 = BX[3:0];
  assign BX_4_7 = BX[7:4];
  assign BX_8_11 = BX[11:8];
  assign BX_15_12 = BX[15:12];
  assign CX_0_3 = CX[3:0];
  assign CX_4_7 = CX[7:4];
  assign CX_8_11 = CX[11:8];
  assign CX_15_12 = CX[15:12];
  assign DR_0_3 = DR[3:0];
  assign DR_2 = DR[11:8];
  assign DR_4_7 = DR[7:4];
  assign DR_15_12 = DR[15:12];
  assign DX_0_3 = DX[3:0];
  assign DX_4_7 = DX[7:4];
  assign DX_8_11 = DX[11:8];
  assign DX_15_12 = DX[15:12];
  assign EX_0_3 = EX[3:0];
  assign EX_4_7 = EX[7:4];
  assign EX_8_11 = EX[11:8];
  assign EX_15_12 = EX[15:12];
  assign IR_0_3 = IR[3:0];
  assign IR_4_7 = IR[7:4];
  assign IR_8_11 = IR[11:8];
  assign IR_15_12 = IR[15:12];
endmodule

module ADD_ADC_1 (
  input  AX,
  input  BX,
  input  CX,
  input  DX,
  input  EX,
  input  DR,
  input  IR,
  input  AX_2,
  input  BX_2,
  input  CX_2,
  input  DX_2,
  input  EX_2,
  input  DR_2,
  input  IR_2,
  input  Cin,
  output OUTPUT,
  output Cout
);

  wire AX_2_out, AX_out, BX_2_out, BX_out, CX_2_out, CX_out, DR_2_out, DR_out, DX_2_out, DX_out, EX_2_out,
       EX_out, IR_2_out, IR_out, or_1_out, or_2_out;

  and u_AX (AX_out, AX_2, AX);
  and u_BX (BX_out, BX, ~AX_2, BX_2);  // AND_Gate
  and u_CX (CX_out, CX, ~AX_2, ~BX_2, CX_2);  // AND_Gate
  and u_DX (DX_out, DX, ~AX_2, ~BX_2, ~CX_2, DX_2);  // AND_Gate
  or or_1 (or_1_out, AX_out, BX_out, CX_out, DX_out, EX_out, DR_out, IR_out);
  and u_EX (EX_out, EX, ~AX_2, ~BX_2, ~CX_2, ~DX_2, EX_2);  // AND_Gate
  and u_DR (DR_out, DR, ~AX_2, ~BX_2, ~CX_2, ~DX_2, ~EX_2, DR_2);  // AND_Gate
  and u_IR (IR_out, IR, ~AX_2, ~BX_2, ~CX_2, ~DX_2, ~EX_2, ~DR_2, IR_2);  // AND_Gate
  and u_IR_2 (IR_2_out, IR, IR_2);
  and u_DR_2 (DR_2_out, DR, ~IR_2, DR_2);  // AND_Gate
  and u_EX_2 (EX_2_out, EX, ~IR_2, ~DR_2, EX_2);  // AND_Gate
  and u_DX_2 (DX_2_out, DX, ~IR_2, ~DR_2, ~EX_2, DX_2);  // AND_Gate
  or or_2 (or_2_out, IR_2_out, DR_2_out, EX_2_out, DX_2_out, CX_2_out, BX_2_out, AX_2_out);
  and u_CX_2 (CX_2_out, CX, ~IR_2, ~DR_2, ~EX_2, ~DX_2, CX_2);  // AND_Gate
  Adder #(.width(1)) adder_1 (.a(or_2_out), .b(or_1_out), .out(OUTPUT), .cin(Cin), .cout(Cout));
  and u_BX_2 (BX_2_out, BX, ~IR_2, ~DR_2, ~EX_2, ~DX_2, ~CX_2, BX_2);  // AND_Gate
  and u_AX_2 (AX_2_out, AX, ~IR_2, ~DR_2, ~EX_2, ~DX_2, ~CX_2, ~BX_2, AX_2);  // AND_Gate

  // Notes on the sheet:
  //   Değerler
  //   Sinyaller
endmodule

module ADD_ADC_4 (
  input  [3:0] AX,
  input  [3:0] BX,
  input  [3:0] CX,
  input  [3:0] DX,
  input  [3:0] EX,
  input  [3:0] DR,
  input  [3:0] IR,
  input  Cin,
  input  AX_2,
  input  BX_2,
  input  CX_2,
  input  DX_2,
  input  EX_2,
  input  DR_2,
  input  IR_2,
  output [3:0] OUTPUT,
  output Cout
);

  wire add_adc_1_2_cout, add_adc_1_3_cout, add_adc_1_4_cout;
  wire [6:0] input_4to1_1_ir0, input_4to1_1_ir1, input_4to1_1_ir2, input_4to1_1_ir3;

  ADD_ADC_1 add_adc_1_1 (
    .AX_2(AX_2), .BX_2(BX_2), .CX_2(CX_2), .DX_2(DX_2), .EX_2(EX_2), .DR_2(DR_2), .IR_2(IR_2),
    .AX(input_4to1_1_ir3[6]), .BX(input_4to1_1_ir3[5]), .CX(input_4to1_1_ir3[4]), .DX(input_4to1_1_ir3[3]),
    .EX(input_4to1_1_ir3[2]), .DR(input_4to1_1_ir3[1]), .IR(input_4to1_1_ir3[0]), .Cin(add_adc_1_2_cout),
    .Cout(Cout), .OUTPUT(OUTPUT[3]));
  INPUT_4to1 input_4to1_1 (
    .AX(AX), .BX(BX), .CX(CX), .DX(DX), .EX(EX), .DR(DR), .IR(IR), .AX3(input_4to1_1_ir3[6]),
    .BX3(input_4to1_1_ir3[5]), .CX3(input_4to1_1_ir3[4]), .DX3(input_4to1_1_ir3[3]),
    .EX3(input_4to1_1_ir3[2]), .DR3(input_4to1_1_ir3[1]), .IR3(input_4to1_1_ir3[0]),
    .AX2(input_4to1_1_ir2[6]), .BX2(input_4to1_1_ir2[5]), .CX2(input_4to1_1_ir2[4]),
    .DX2(input_4to1_1_ir2[3]), .EX2(input_4to1_1_ir2[2]), .DR2(input_4to1_1_ir2[1]),
    .IR2(input_4to1_1_ir2[0]), .AX1(input_4to1_1_ir1[6]), .BX1(input_4to1_1_ir1[5]),
    .CX1(input_4to1_1_ir1[4]), .DX1(input_4to1_1_ir1[3]), .EX1(input_4to1_1_ir1[2]),
    .DR1(input_4to1_1_ir1[1]), .IR1(input_4to1_1_ir1[0]), .AX0(input_4to1_1_ir0[6]),
    .BX0(input_4to1_1_ir0[5]), .CX0(input_4to1_1_ir0[4]), .DX0(input_4to1_1_ir0[3]),
    .EX0(input_4to1_1_ir0[2]), .DR0(input_4to1_1_ir0[1]), .IR0(input_4to1_1_ir0[0]));
  ADD_ADC_1 add_adc_1_2 (
    .AX_2(AX_2), .BX_2(BX_2), .CX_2(CX_2), .DX_2(DX_2), .EX_2(EX_2), .DR_2(DR_2), .IR_2(IR_2),
    .AX(input_4to1_1_ir2[6]), .BX(input_4to1_1_ir2[5]), .CX(input_4to1_1_ir2[4]), .DX(input_4to1_1_ir2[3]),
    .EX(input_4to1_1_ir2[2]), .DR(input_4to1_1_ir2[1]), .IR(input_4to1_1_ir2[0]), .Cin(add_adc_1_3_cout),
    .Cout(add_adc_1_2_cout), .OUTPUT(OUTPUT[2]));
  ADD_ADC_1 add_adc_1_3 (
    .AX_2(AX_2), .BX_2(BX_2), .CX_2(CX_2), .DX_2(DX_2), .EX_2(EX_2), .DR_2(DR_2), .IR_2(IR_2),
    .AX(input_4to1_1_ir1[6]), .BX(input_4to1_1_ir1[5]), .CX(input_4to1_1_ir1[4]), .DX(input_4to1_1_ir1[3]),
    .EX(input_4to1_1_ir1[2]), .DR(input_4to1_1_ir1[1]), .IR(input_4to1_1_ir1[0]), .Cin(add_adc_1_4_cout),
    .Cout(add_adc_1_3_cout), .OUTPUT(OUTPUT[1]));
  ADD_ADC_1 add_adc_1_4 (
    .AX_2(AX_2), .BX_2(BX_2), .CX_2(CX_2), .DX_2(DX_2), .EX_2(EX_2), .DR_2(DR_2), .IR_2(IR_2),
    .AX(input_4to1_1_ir0[6]), .BX(input_4to1_1_ir0[5]), .CX(input_4to1_1_ir0[4]), .DX(input_4to1_1_ir0[3]),
    .EX(input_4to1_1_ir0[2]), .DR(input_4to1_1_ir0[1]), .IR(input_4to1_1_ir0[0]), .Cin(Cin),
    .Cout(add_adc_1_4_cout), .OUTPUT(OUTPUT[0]));
endmodule

module SUB_SBB_1 (
  input  AX,
  input  BX,
  input  CX,
  input  DX,
  input  EX,
  input  DR,
  input  IR,
  input  AX_2,
  input  BX_2,
  input  CX_2,
  input  DX_2,
  input  EX_2,
  input  DR_2,
  input  IR_2,
  input  AX_3,
  input  BX_3,
  input  CX_3,
  input  DX_3,
  input  EX_3,
  input  DR_3,
  input  IR_3,
  input  Bin,
  output OUTPUT,
  output Bout
);

  wire AX_2_out, AX_out, BX_2_out, BX_out, CX_2_out, CX_out, DR_2_out, DR_out, DX_2_out, DX_out, EX_2_out,
       EX_out, IR_2_out, IR_out, or_1_out, or_2_out;

  and u_AX (AX_out, AX_2, AX);
  and u_BX (BX_out, BX, ~AX_2, BX_2);  // AND_Gate
  and u_CX (CX_out, CX, ~AX_2, ~BX_2, CX_2);  // AND_Gate
  and u_DX (DX_out, DX, ~AX_2, ~BX_2, ~CX_2, DX_2);  // AND_Gate
  or or_1 (or_1_out, AX_out, BX_out, CX_out, DX_out, EX_out, DR_out, IR_out);
  and u_EX (EX_out, EX, ~AX_2, ~BX_2, ~CX_2, ~DX_2, EX_2);  // AND_Gate
  and u_DR (DR_out, DR, ~AX_2, ~BX_2, ~CX_2, ~DX_2, ~EX_2, DR_2);  // AND_Gate
  and u_IR (IR_out, IR, ~AX_2, ~BX_2, ~CX_2, ~DX_2, ~EX_2, ~DR_2, IR_2);  // AND_Gate
  and u_AX_2 (AX_2_out, AX, AX_3);
  and u_CX_2 (CX_2_out, CX, ~AX_3, ~BX_3, CX_3);  // AND_Gate
  and u_BX_2 (BX_2_out, BX, ~AX_3, BX_3);  // AND_Gate
  and u_DX_2 (DX_2_out, DX, ~AX_3, ~BX_3, ~CX_3, DX_3);  // AND_Gate
  or or_2 (or_2_out, AX_2_out, BX_2_out, CX_2_out, DX_2_out, EX_2_out, DR_2_out, IR_2_out);
  and u_EX_2 (EX_2_out, EX, ~AX_3, ~BX_3, ~CX_3, ~DX_3, EX_3);  // AND_Gate
  Subtractor #(.width(1)) subtractor_1 (.a(or_1_out), .b(or_2_out), .out(OUTPUT), .bin(Bin), .bout(Bout));
  and u_DR_2 (DR_2_out, DR, ~AX_3, ~BX_3, ~CX_3, ~DX_3, ~EX_3, DR_3);  // AND_Gate
  and u_IR_2 (IR_2_out, IR, ~AX_3, ~BX_3, ~CX_3, ~DX_3, ~EX_3, ~DR_3, IR_3);  // AND_Gate

  // Notes on the sheet:
  //   Değerler
  //   Sinyaller
endmodule

module SUB_SBB_4 (
  input  [3:0] AX,
  input  [3:0] BX,
  input  [3:0] CX,
  input  [3:0] DX,
  input  [3:0] EX,
  input  [3:0] DR,
  input  [3:0] IR,
  input  Bin,
  input  AX_2,
  input  BX_2,
  input  CX_2,
  input  DX_2,
  input  EX_2,
  input  DR_2,
  input  IR_2,
  input  AX_3,
  input  BX_3,
  input  CX_3,
  input  DX_3,
  input  EX_3,
  input  DR_3,
  input  IR_3,
  output [3:0] OUTPUT,
  output Bout
);

  wire sub_sbb_1_2_bout, sub_sbb_1_3_bout, sub_sbb_1_4_bout;
  wire [6:0] input_4to1_1_ir0, input_4to1_1_ir1, input_4to1_1_ir2, input_4to1_1_ir3;

  SUB_SBB_1 sub_sbb_1_1 (
    .AX_2(AX_2), .BX_2(BX_2), .CX_2(CX_2), .DX_2(DX_2), .EX_2(EX_2), .DR_2(DR_2), .IR_2(IR_2), .AX_3(AX_3),
    .BX_3(BX_3), .CX_3(CX_3), .DX_3(DX_3), .EX_3(EX_3), .DR_3(DR_3), .IR_3(IR_3), .AX(input_4to1_1_ir3[6]),
    .BX(input_4to1_1_ir3[5]), .CX(input_4to1_1_ir3[4]), .DX(input_4to1_1_ir3[3]), .EX(input_4to1_1_ir3[2]),
    .DR(input_4to1_1_ir3[1]), .IR(input_4to1_1_ir3[0]), .Bin(sub_sbb_1_2_bout), .Bout(Bout),
    .OUTPUT(OUTPUT[3]));
  INPUT_4to1 input_4to1_1 (
    .AX(AX), .BX(BX), .CX(CX), .DX(DX), .EX(EX), .DR(DR), .IR(IR), .AX3(input_4to1_1_ir3[6]),
    .BX3(input_4to1_1_ir3[5]), .CX3(input_4to1_1_ir3[4]), .DX3(input_4to1_1_ir3[3]),
    .EX3(input_4to1_1_ir3[2]), .DR3(input_4to1_1_ir3[1]), .IR3(input_4to1_1_ir3[0]),
    .AX2(input_4to1_1_ir2[6]), .BX2(input_4to1_1_ir2[5]), .CX2(input_4to1_1_ir2[4]),
    .DX2(input_4to1_1_ir2[3]), .EX2(input_4to1_1_ir2[2]), .DR2(input_4to1_1_ir2[1]),
    .IR2(input_4to1_1_ir2[0]), .AX1(input_4to1_1_ir1[6]), .BX1(input_4to1_1_ir1[5]),
    .CX1(input_4to1_1_ir1[4]), .DX1(input_4to1_1_ir1[3]), .EX1(input_4to1_1_ir1[2]),
    .DR1(input_4to1_1_ir1[1]), .IR1(input_4to1_1_ir1[0]), .AX0(input_4to1_1_ir0[6]),
    .BX0(input_4to1_1_ir0[5]), .CX0(input_4to1_1_ir0[4]), .DX0(input_4to1_1_ir0[3]),
    .EX0(input_4to1_1_ir0[2]), .DR0(input_4to1_1_ir0[1]), .IR0(input_4to1_1_ir0[0]));
  SUB_SBB_1 sub_sbb_1_2 (
    .AX_2(AX_2), .BX_2(BX_2), .CX_2(CX_2), .DX_2(DX_2), .EX_2(EX_2), .DR_2(DR_2), .IR_2(IR_2), .AX_3(AX_3),
    .BX_3(BX_3), .CX_3(CX_3), .DX_3(DX_3), .EX_3(EX_3), .DR_3(DR_3), .IR_3(IR_3), .AX(input_4to1_1_ir2[6]),
    .BX(input_4to1_1_ir2[5]), .CX(input_4to1_1_ir2[4]), .DX(input_4to1_1_ir2[3]), .EX(input_4to1_1_ir2[2]),
    .DR(input_4to1_1_ir2[1]), .IR(input_4to1_1_ir2[0]), .Bin(sub_sbb_1_3_bout), .Bout(sub_sbb_1_2_bout),
    .OUTPUT(OUTPUT[2]));
  SUB_SBB_1 sub_sbb_1_3 (
    .AX_2(AX_2), .BX_2(BX_2), .CX_2(CX_2), .DX_2(DX_2), .EX_2(EX_2), .DR_2(DR_2), .IR_2(IR_2), .AX_3(AX_3),
    .BX_3(BX_3), .CX_3(CX_3), .DX_3(DX_3), .EX_3(EX_3), .DR_3(DR_3), .IR_3(IR_3), .AX(input_4to1_1_ir1[6]),
    .BX(input_4to1_1_ir1[5]), .CX(input_4to1_1_ir1[4]), .DX(input_4to1_1_ir1[3]), .EX(input_4to1_1_ir1[2]),
    .DR(input_4to1_1_ir1[1]), .IR(input_4to1_1_ir1[0]), .Bin(sub_sbb_1_4_bout), .Bout(sub_sbb_1_3_bout),
    .OUTPUT(OUTPUT[1]));
  SUB_SBB_1 sub_sbb_1_4 (
    .AX_2(AX_2), .BX_2(BX_2), .CX_2(CX_2), .DX_2(DX_2), .EX_2(EX_2), .DR_2(DR_2), .IR_2(IR_2), .AX_3(AX_3),
    .BX_3(BX_3), .CX_3(CX_3), .DX_3(DX_3), .EX_3(EX_3), .DR_3(DR_3), .IR_3(IR_3), .AX(input_4to1_1_ir0[6]),
    .BX(input_4to1_1_ir0[5]), .CX(input_4to1_1_ir0[4]), .DX(input_4to1_1_ir0[3]), .EX(input_4to1_1_ir0[2]),
    .DR(input_4to1_1_ir0[1]), .IR(input_4to1_1_ir0[0]), .Bin(Bin), .Bout(sub_sbb_1_4_bout), .OUTPUT(OUTPUT[0]));
endmodule

// LINE_SPLIT
module MUL_LINE_SPLIT (
  input  MULTIPLIER_1,
  input  [15:0] MULTIPLIED,
  output _0,
  output _1,
  output _2,
  output _3,
  output _4,
  output _5,
  output _6,
  output _7,
  output _8,
  output _9,
  output _10,
  output _11,
  output _12,
  output _13,
  output _14,
  output _15
);

  and and_1 (_0, MULTIPLIER_1, MULTIPLIED[0]);
  and and_2 (_1, MULTIPLIER_1, MULTIPLIED[1]);
  and and_3 (_2, MULTIPLIER_1, MULTIPLIED[2]);
  and and_4 (_3, MULTIPLIER_1, MULTIPLIED[3]);
  and and_5 (_4, MULTIPLIER_1, MULTIPLIED[4]);
  and and_6 (_5, MULTIPLIER_1, MULTIPLIED[5]);
  and and_7 (_6, MULTIPLIER_1, MULTIPLIED[6]);
  and and_8 (_7, MULTIPLIER_1, MULTIPLIED[7]);
  and and_9 (_8, MULTIPLIER_1, MULTIPLIED[8]);
  and and_10 (_9, MULTIPLIER_1, MULTIPLIED[9]);
  and and_11 (_10, MULTIPLIER_1, MULTIPLIED[10]);
  and and_12 (_11, MULTIPLIER_1, MULTIPLIED[11]);
  and and_13 (_12, MULTIPLIER_1, MULTIPLIED[12]);
  and and_14 (_13, MULTIPLIER_1, MULTIPLIED[13]);
  and and_15 (_14, MULTIPLIER_1, MULTIPLIED[14]);
  and and_16 (_15, MULTIPLIER_1, MULTIPLIED[15]);
endmodule

module MUL_4_LINE_ADDER (
  input  [3:0] MULTIPLIER,
  input  [15:0] MULTIPLIED,
  output [19:0] OUTPUT
);

  wire [14:0] mul_line_split_1__1;
  wire [15:0] mul_line_split_2__0, mul_line_split_3__0, mul_line_split_4__0;
  wire [15:1] adder_1_out, adder_2_out;
  wire [15:15] adder_1_cout, adder_2_cout;

  MUL_LINE_SPLIT mul_line_split_1 (
    .MULTIPLIED(MULTIPLIED), .MULTIPLIER_1(MULTIPLIER[0]), ._0(OUTPUT[0]), ._1(mul_line_split_1__1[0]),
    ._2(mul_line_split_1__1[1]), ._3(mul_line_split_1__1[2]), ._4(mul_line_split_1__1[3]),
    ._5(mul_line_split_1__1[4]), ._6(mul_line_split_1__1[5]), ._7(mul_line_split_1__1[6]),
    ._8(mul_line_split_1__1[7]), ._9(mul_line_split_1__1[8]), ._10(mul_line_split_1__1[9]),
    ._11(mul_line_split_1__1[10]), ._12(mul_line_split_1__1[11]), ._13(mul_line_split_1__1[12]),
    ._14(mul_line_split_1__1[13]), ._15(mul_line_split_1__1[14]));
  MUL_LINE_SPLIT mul_line_split_2 (
    .MULTIPLIED(MULTIPLIED), .MULTIPLIER_1(MULTIPLIER[1]), ._0(mul_line_split_2__0[0]),
    ._1(mul_line_split_2__0[1]), ._2(mul_line_split_2__0[2]), ._3(mul_line_split_2__0[3]),
    ._4(mul_line_split_2__0[4]), ._5(mul_line_split_2__0[5]), ._6(mul_line_split_2__0[6]),
    ._7(mul_line_split_2__0[7]), ._8(mul_line_split_2__0[8]), ._9(mul_line_split_2__0[9]),
    ._10(mul_line_split_2__0[10]), ._11(mul_line_split_2__0[11]), ._12(mul_line_split_2__0[12]),
    ._13(mul_line_split_2__0[13]), ._14(mul_line_split_2__0[14]), ._15(mul_line_split_2__0[15]));
  MUL_LINE_SPLIT mul_line_split_3 (
    .MULTIPLIED(MULTIPLIED), .MULTIPLIER_1(MULTIPLIER[2]), ._0(mul_line_split_3__0[0]),
    ._1(mul_line_split_3__0[1]), ._2(mul_line_split_3__0[2]), ._3(mul_line_split_3__0[3]),
    ._4(mul_line_split_3__0[4]), ._5(mul_line_split_3__0[5]), ._6(mul_line_split_3__0[6]),
    ._7(mul_line_split_3__0[7]), ._8(mul_line_split_3__0[8]), ._9(mul_line_split_3__0[9]),
    ._10(mul_line_split_3__0[10]), ._11(mul_line_split_3__0[11]), ._12(mul_line_split_3__0[12]),
    ._13(mul_line_split_3__0[13]), ._14(mul_line_split_3__0[14]), ._15(mul_line_split_3__0[15]));
  Adder #(.width(16)) adder_1 (
    .a(mul_line_split_2__0), .b({1'b0, mul_line_split_1__1}), .out({adder_1_out, OUTPUT[1]}),
    .cout(adder_1_cout[15]));  // open: cin
  Adder #(.width(16)) adder_2 (
    .a(mul_line_split_3__0), .b({adder_1_cout[15], adder_1_out}), .out({adder_2_out, OUTPUT[2]}),
    .cout(adder_2_cout[15]));  // open: cin
  MUL_LINE_SPLIT mul_line_split_4 (
    .MULTIPLIED(MULTIPLIED), .MULTIPLIER_1(MULTIPLIER[3]), ._0(mul_line_split_4__0[0]),
    ._1(mul_line_split_4__0[1]), ._2(mul_line_split_4__0[2]), ._3(mul_line_split_4__0[3]),
    ._4(mul_line_split_4__0[4]), ._5(mul_line_split_4__0[5]), ._6(mul_line_split_4__0[6]),
    ._7(mul_line_split_4__0[7]), ._8(mul_line_split_4__0[8]), ._9(mul_line_split_4__0[9]),
    ._10(mul_line_split_4__0[10]), ._11(mul_line_split_4__0[11]), ._12(mul_line_split_4__0[12]),
    ._13(mul_line_split_4__0[13]), ._14(mul_line_split_4__0[14]), ._15(mul_line_split_4__0[15]));
  Adder #(.width(16)) adder_3 (
    .a(mul_line_split_4__0), .b({adder_2_cout[15], adder_2_out}), .out(OUTPUT[18:3]), .cout(OUTPUT[19]));  // open: cin
endmodule

module MUL_INPUT_ADJUSTER (
  input  AX,
  input  BX,
  input  CX,
  input  DX,
  input  EX,
  input  DR,
  input  IR,
  input  [15:0] AX_2,
  input  [15:0] BX_2,
  input  [15:0] CX_2,
  input  [15:0] DX_2,
  input  [15:0] EX_2,
  input  [15:0] DR_2,
  input  [15:0] IR_2,
  output [15:0] MULTIPLIER,
  output [15:0] MULTIPLIED
);

  wire AX_out, BX_2_out, BX_out, CX_2_out, CX_out, DR_out, DX_2_out, DX_out, EX_2_out, EX_out;

  and u_BX (BX_out, ~AX, BX);  // AND_Gate
  assign MULTIPLIER = AX ? AX_2 : 16'bz;  // Controlled_Buffer controlled_buffer_1
  assign MULTIPLIED = AX_out ? AX_2 : 16'bz;  // Controlled_Buffer controlled_buffer_2
  assign MULTIPLIER = BX_out ? BX_2 : 16'bz;  // Controlled_Buffer controlled_buffer_3
  assign MULTIPLIED = BX_2_out ? BX_2 : 16'bz;  // Controlled_Buffer controlled_buffer_4
  assign MULTIPLIER = CX_out ? CX_2 : 16'bz;  // Controlled_Buffer controlled_buffer_5
  assign MULTIPLIED = CX_2_out ? CX_2 : 16'bz;  // Controlled_Buffer controlled_buffer_6
  assign MULTIPLIER = DX_out ? DX_2 : 16'bz;  // Controlled_Buffer controlled_buffer_7
  assign MULTIPLIED = DX_2_out ? DX_2 : 16'bz;  // Controlled_Buffer controlled_buffer_8
  assign MULTIPLIER = EX_out ? EX_2 : 16'bz;  // Controlled_Buffer controlled_buffer_9
  assign MULTIPLIED = EX_2_out ? EX_2 : 16'bz;  // Controlled_Buffer controlled_buffer_10
  assign MULTIPLIED = DR_out ? DR_2 : 16'bz;  // Controlled_Buffer controlled_buffer_11
  assign MULTIPLIED = IR ? IR_2 : 16'bz;  // Controlled_Buffer controlled_buffer_12
  and u_CX (CX_out, ~AX, ~BX, CX);  // AND_Gate
  and u_DX (DX_out, ~AX, ~BX, ~CX, DX);  // AND_Gate
  and u_EX (EX_out, ~AX, ~BX, ~CX, ~DX, EX);  // AND_Gate
  and u_DR (DR_out, ~IR, DR);  // AND_Gate
  and u_DX_2 (DX_2_out, ~IR, ~DR, ~EX, DX);  // AND_Gate
  and u_EX_2 (EX_2_out, ~IR, ~DR, EX);  // AND_Gate
  and u_CX_2 (CX_2_out, ~IR, ~DR, ~EX, ~DX, CX);  // AND_Gate
  and u_BX_2 (BX_2_out, ~IR, ~DR, ~EX, ~DX, ~CX, BX);  // AND_Gate
  and u_AX (AX_out, ~IR, ~DR, ~EX, ~DX, ~CX, ~BX, AX);  // AND_Gate
endmodule

module DIV_1 (
  input  A,
  input  Cin,
  input  B,
  input  C_Mux,
  output Q,
  output C_Mux_2,
  output OUT
);

  wire and_1_out, and_2_out, and_3_out, and_4_out, not_1_out, not_2_out, xor_1_out, xor_2_out, xor_3_out;

  not not_1 (not_1_out, B);
  xor xor_1 (xor_1_out, A, not_1_out);
  xor xor_2 (xor_2_out, Cin, xor_1_out);
  and and_1 (and_1_out, Cin, not_1_out);
  xor xor_3 (xor_3_out, Cin, not_1_out);
  and and_2 (and_2_out, xor_3_out, A);
  or or_1 (Q, and_1_out, and_2_out);
  not not_2 (not_2_out, C_Mux);
  and and_3 (and_3_out, xor_2_out, C_Mux);
  or or_2 (OUT, and_3_out, and_4_out);
  and and_4 (and_4_out, A, not_2_out);

  assign C_Mux_2 = C_Mux;
endmodule

module DIV_LINE_PROCESS_UNIT (
  input  A15,
  input  A14,
  input  A13,
  input  A12,
  input  A11,
  input  A10,
  input  A9,
  input  A8,
  input  A7,
  input  A6,
  input  A5,
  input  A4,
  input  A3,
  input  A2,
  input  A1,
  input  A0,
  input  B15,
  input  B14,
  input  B13,
  input  B12,
  input  B11,
  input  B10,
  input  B9,
  input  B8,
  input  B7,
  input  B6,
  input  B5,
  input  B4,
  input  B3,
  input  B2,
  input  B1,
  input  B0,
  output out_33,
  output _0,
  output _1,
  output _2,
  output _3,
  output _4,
  output _5,
  output _6,
  output _7,
  output _8,
  output _9,
  output _10,
  output _11,
  output _12,
  output _13,
  output _14,
  output _15
);

  wire div_1_1_c_mux_2, div_1_2_c_mux_2, div_1_2_q, div_1_3_c_mux_2, div_1_3_q, div_1_4_c_mux_2, div_1_4_q,
       div_1_5_c_mux_2, div_1_5_q, div_1_6_c_mux_2, div_1_6_q, div_1_7_c_mux_2, div_1_7_q, div_1_8_c_mux_2,
       div_1_8_q, div_1_9_c_mux_2, div_1_9_q, div_1_10_c_mux_2, div_1_10_q, div_1_11_c_mux_2, div_1_11_q,
       div_1_12_c_mux_2, div_1_12_q, div_1_13_c_mux_2, div_1_13_q, div_1_14_c_mux_2, div_1_14_q,
       div_1_15_c_mux_2, div_1_15_q, div_1_16_q;

  DIV_1 div_1_1 (.Q(out_33), .C_Mux(out_33), .A(A15), .B(B15), .Cin(div_1_2_q), .C_Mux_2(div_1_1_c_mux_2), .OUT(_15));
  DIV_1 div_1_2 (
    .Q(div_1_2_q), .C_Mux(div_1_1_c_mux_2), .A(A14), .B(B14), .Cin(div_1_4_q), .C_Mux_2(div_1_2_c_mux_2),
    .OUT(_14));
  DIV_1 div_1_3 (
    .Q(div_1_3_q), .C_Mux(div_1_4_c_mux_2), .A(A12), .B(B12), .Cin(div_1_5_q), .C_Mux_2(div_1_3_c_mux_2),
    .OUT(_12));
  DIV_1 div_1_4 (
    .Q(div_1_4_q), .C_Mux(div_1_2_c_mux_2), .A(A13), .B(B13), .Cin(div_1_3_q), .C_Mux_2(div_1_4_c_mux_2),
    .OUT(_13));
  DIV_1 div_1_5 (
    .Q(div_1_5_q), .C_Mux(div_1_3_c_mux_2), .A(A11), .B(B11), .Cin(div_1_7_q), .C_Mux_2(div_1_5_c_mux_2),
    .OUT(_11));
  DIV_1 div_1_6 (
    .Q(div_1_6_q), .C_Mux(div_1_7_c_mux_2), .A(A9), .B(B9), .Cin(div_1_8_q), .C_Mux_2(div_1_6_c_mux_2),
    .OUT(_9));
  DIV_1 div_1_7 (
    .Q(div_1_7_q), .C_Mux(div_1_5_c_mux_2), .A(A10), .B(B10), .Cin(div_1_6_q), .C_Mux_2(div_1_7_c_mux_2),
    .OUT(_10));
  DIV_1 div_1_8 (
    .Q(div_1_8_q), .C_Mux(div_1_6_c_mux_2), .A(A8), .B(B8), .Cin(div_1_10_q), .C_Mux_2(div_1_8_c_mux_2),
    .OUT(_8));
  DIV_1 div_1_9 (
    .Q(div_1_9_q), .C_Mux(div_1_10_c_mux_2), .A(A6), .B(B6), .Cin(div_1_12_q), .C_Mux_2(div_1_9_c_mux_2),
    .OUT(_6));
  DIV_1 div_1_10 (
    .Q(div_1_10_q), .C_Mux(div_1_8_c_mux_2), .A(A7), .B(B7), .Cin(div_1_9_q), .C_Mux_2(div_1_10_c_mux_2),
    .OUT(_7));
  DIV_1 div_1_11 (
    .Q(div_1_11_q), .C_Mux(div_1_12_c_mux_2), .A(A4), .B(B4), .Cin(div_1_13_q), .C_Mux_2(div_1_11_c_mux_2),
    .OUT(_4));
  DIV_1 div_1_12 (
    .Q(div_1_12_q), .C_Mux(div_1_9_c_mux_2), .A(A5), .B(B5), .Cin(div_1_11_q), .C_Mux_2(div_1_12_c_mux_2),
    .OUT(_5));
  DIV_1 div_1_13 (
    .Q(div_1_13_q), .C_Mux(div_1_11_c_mux_2), .A(A3), .B(B3), .Cin(div_1_15_q), .C_Mux_2(div_1_13_c_mux_2),
    .OUT(_3));
  DIV_1 div_1_14 (
    .Q(div_1_14_q), .C_Mux(div_1_15_c_mux_2), .A(A1), .B(B1), .Cin(div_1_16_q), .C_Mux_2(div_1_14_c_mux_2),
    .OUT(_1));
  DIV_1 div_1_15 (
    .Q(div_1_15_q), .C_Mux(div_1_13_c_mux_2), .A(A2), .B(B2), .Cin(div_1_14_q), .C_Mux_2(div_1_15_c_mux_2),
    .OUT(_2));
  DIV_1 div_1_16 (.Q(div_1_16_q), .C_Mux(div_1_14_c_mux_2), .A(A0), .B(B0), .Cin(1'b1), .OUT(_0));  // open: C_Mux_2
endmodule

module DIV_4_LINE (
  input  [3:0] DIVIDEND_4,
  input  [15:0] R_FROM_UP_LINE,
  input  [15:0] DIVISOR,
  output [3:0] Q,
  output [15:0] R
);

  wire [15:0] div_line_process_unit_1__0, div_line_process_unit_2__0, div_line_process_unit_3__0;

  DIV_LINE_PROCESS_UNIT div_line_process_unit_1 (
    .A15(R_FROM_UP_LINE[14]), .A14(R_FROM_UP_LINE[13]), .A13(R_FROM_UP_LINE[12]), .A12(R_FROM_UP_LINE[11]),
    .A11(R_FROM_UP_LINE[10]), .A10(R_FROM_UP_LINE[9]), .A9(R_FROM_UP_LINE[8]), .A8(R_FROM_UP_LINE[7]),
    .A7(R_FROM_UP_LINE[6]), .A6(R_FROM_UP_LINE[5]), .A5(R_FROM_UP_LINE[4]), .A4(R_FROM_UP_LINE[3]),
    .A3(R_FROM_UP_LINE[2]), .A2(R_FROM_UP_LINE[1]), .A1(R_FROM_UP_LINE[0]), .A0(DIVIDEND_4[3]),
    .B15(DIVISOR[15]), .B14(DIVISOR[14]), .B13(DIVISOR[13]), .B12(DIVISOR[12]), .B11(DIVISOR[11]),
    .B10(DIVISOR[10]), .B9(DIVISOR[9]), .B8(DIVISOR[8]), .B7(DIVISOR[7]), .B6(DIVISOR[6]), .B5(DIVISOR[5]),
    .B4(DIVISOR[4]), .B3(DIVISOR[3]), .B2(DIVISOR[2]), .B1(DIVISOR[1]), .B0(DIVISOR[0]), .out_33(Q[3]),
    ._0(div_line_process_unit_1__0[0]), ._1(div_line_process_unit_1__0[1]),
    ._2(div_line_process_unit_1__0[2]), ._3(div_line_process_unit_1__0[3]),
    ._4(div_line_process_unit_1__0[4]), ._5(div_line_process_unit_1__0[5]),
    ._6(div_line_process_unit_1__0[6]), ._7(div_line_process_unit_1__0[7]),
    ._8(div_line_process_unit_1__0[8]), ._9(div_line_process_unit_1__0[9]),
    ._10(div_line_process_unit_1__0[10]), ._11(div_line_process_unit_1__0[11]),
    ._12(div_line_process_unit_1__0[12]), ._13(div_line_process_unit_1__0[13]),
    ._14(div_line_process_unit_1__0[14]), ._15(div_line_process_unit_1__0[15]));
  DIV_LINE_PROCESS_UNIT div_line_process_unit_2 (
    .A15(div_line_process_unit_1__0[14]), .A14(div_line_process_unit_1__0[13]),
    .A13(div_line_process_unit_1__0[12]), .A12(div_line_process_unit_1__0[11]),
    .A11(div_line_process_unit_1__0[10]), .A10(div_line_process_unit_1__0[9]),
    .A9(div_line_process_unit_1__0[8]), .A8(div_line_process_unit_1__0[7]),
    .A7(div_line_process_unit_1__0[6]), .A6(div_line_process_unit_1__0[5]),
    .A5(div_line_process_unit_1__0[4]), .A4(div_line_process_unit_1__0[3]),
    .A3(div_line_process_unit_1__0[2]), .A2(div_line_process_unit_1__0[1]),
    .A1(div_line_process_unit_1__0[0]), .A0(DIVIDEND_4[2]), .B15(DIVISOR[15]), .B14(DIVISOR[14]),
    .B13(DIVISOR[13]), .B12(DIVISOR[12]), .B11(DIVISOR[11]), .B10(DIVISOR[10]), .B9(DIVISOR[9]),
    .B8(DIVISOR[8]), .B7(DIVISOR[7]), .B6(DIVISOR[6]), .B5(DIVISOR[5]), .B4(DIVISOR[4]), .B3(DIVISOR[3]),
    .B2(DIVISOR[2]), .B1(DIVISOR[1]), .B0(DIVISOR[0]), .out_33(Q[2]), ._0(div_line_process_unit_2__0[0]),
    ._1(div_line_process_unit_2__0[1]), ._2(div_line_process_unit_2__0[2]),
    ._3(div_line_process_unit_2__0[3]), ._4(div_line_process_unit_2__0[4]),
    ._5(div_line_process_unit_2__0[5]), ._6(div_line_process_unit_2__0[6]),
    ._7(div_line_process_unit_2__0[7]), ._8(div_line_process_unit_2__0[8]),
    ._9(div_line_process_unit_2__0[9]), ._10(div_line_process_unit_2__0[10]),
    ._11(div_line_process_unit_2__0[11]), ._12(div_line_process_unit_2__0[12]),
    ._13(div_line_process_unit_2__0[13]), ._14(div_line_process_unit_2__0[14]),
    ._15(div_line_process_unit_2__0[15]));
  DIV_LINE_PROCESS_UNIT div_line_process_unit_3 (
    .A15(div_line_process_unit_2__0[14]), .A14(div_line_process_unit_2__0[13]),
    .A13(div_line_process_unit_2__0[12]), .A12(div_line_process_unit_2__0[11]),
    .A11(div_line_process_unit_2__0[10]), .A10(div_line_process_unit_2__0[9]),
    .A9(div_line_process_unit_2__0[8]), .A8(div_line_process_unit_2__0[7]),
    .A7(div_line_process_unit_2__0[6]), .A6(div_line_process_unit_2__0[5]),
    .A5(div_line_process_unit_2__0[4]), .A4(div_line_process_unit_2__0[3]),
    .A3(div_line_process_unit_2__0[2]), .A2(div_line_process_unit_2__0[1]),
    .A1(div_line_process_unit_2__0[0]), .A0(DIVIDEND_4[1]), .B15(DIVISOR[15]), .B14(DIVISOR[14]),
    .B13(DIVISOR[13]), .B12(DIVISOR[12]), .B11(DIVISOR[11]), .B10(DIVISOR[10]), .B9(DIVISOR[9]),
    .B8(DIVISOR[8]), .B7(DIVISOR[7]), .B6(DIVISOR[6]), .B5(DIVISOR[5]), .B4(DIVISOR[4]), .B3(DIVISOR[3]),
    .B2(DIVISOR[2]), .B1(DIVISOR[1]), .B0(DIVISOR[0]), .out_33(Q[1]), ._0(div_line_process_unit_3__0[0]),
    ._1(div_line_process_unit_3__0[1]), ._2(div_line_process_unit_3__0[2]),
    ._3(div_line_process_unit_3__0[3]), ._4(div_line_process_unit_3__0[4]),
    ._5(div_line_process_unit_3__0[5]), ._6(div_line_process_unit_3__0[6]),
    ._7(div_line_process_unit_3__0[7]), ._8(div_line_process_unit_3__0[8]),
    ._9(div_line_process_unit_3__0[9]), ._10(div_line_process_unit_3__0[10]),
    ._11(div_line_process_unit_3__0[11]), ._12(div_line_process_unit_3__0[12]),
    ._13(div_line_process_unit_3__0[13]), ._14(div_line_process_unit_3__0[14]),
    ._15(div_line_process_unit_3__0[15]));
  DIV_LINE_PROCESS_UNIT div_line_process_unit_4 (
    .A15(div_line_process_unit_3__0[14]), .A14(div_line_process_unit_3__0[13]),
    .A13(div_line_process_unit_3__0[12]), .A12(div_line_process_unit_3__0[11]),
    .A11(div_line_process_unit_3__0[10]), .A10(div_line_process_unit_3__0[9]),
    .A9(div_line_process_unit_3__0[8]), .A8(div_line_process_unit_3__0[7]),
    .A7(div_line_process_unit_3__0[6]), .A6(div_line_process_unit_3__0[5]),
    .A5(div_line_process_unit_3__0[4]), .A4(div_line_process_unit_3__0[3]),
    .A3(div_line_process_unit_3__0[2]), .A2(div_line_process_unit_3__0[1]),
    .A1(div_line_process_unit_3__0[0]), .A0(DIVIDEND_4[0]), .B15(DIVISOR[15]), .B14(DIVISOR[14]),
    .B13(DIVISOR[13]), .B12(DIVISOR[12]), .B11(DIVISOR[11]), .B10(DIVISOR[10]), .B9(DIVISOR[9]),
    .B8(DIVISOR[8]), .B7(DIVISOR[7]), .B6(DIVISOR[6]), .B5(DIVISOR[5]), .B4(DIVISOR[4]), .B3(DIVISOR[3]),
    .B2(DIVISOR[2]), .B1(DIVISOR[1]), .B0(DIVISOR[0]), .out_33(Q[0]), ._0(R[0]), ._1(R[1]), ._2(R[2]),
    ._3(R[3]), ._4(R[4]), ._5(R[5]), ._6(R[6]), ._7(R[7]), ._8(R[8]), ._9(R[9]), ._10(R[10]), ._11(R[11]),
    ._12(R[12]), ._13(R[13]), ._14(R[14]), ._15(R[15]));
endmodule

module DIV_INPUT_ADJUSTER (
  input  AX,
  input  BX,
  input  CX,
  input  DX,
  input  EX,
  input  DR,
  input  IR,
  input  AX_2,
  input  BX_2,
  input  CX_2,
  input  DX_2,
  input  EX_2,
  input  DR_2,
  input  IR_2,
  input  [15:0] AX_3,
  input  [15:0] BX_3,
  input  [15:0] CX_3,
  input  [15:0] DX_3,
  input  [15:0] EX_3,
  input  [15:0] DR_3,
  input  [15:0] IR_3,
  output [15:0] DIVIDEND,
  output [15:0] DIVISOR
);

  wire AX_out, BX_2_out, BX_out, CX_2_out, CX_out, DR_2_out, DR_out, DX_2_out, DX_out, EX_2_out, EX_out,
       IR_out;

  assign DIVIDEND = AX ? AX_3 : 16'bz;  // Controlled_Buffer controlled_buffer_1
  assign DIVISOR = AX_out ? AX_3 : 16'bz;  // Controlled_Buffer controlled_buffer_2
  assign DIVIDEND = BX_out ? BX_3 : 16'bz;  // Controlled_Buffer controlled_buffer_3
  assign DIVISOR = BX_2_out ? BX_3 : 16'bz;  // Controlled_Buffer controlled_buffer_4
  assign DIVIDEND = CX_out ? CX_3 : 16'bz;  // Controlled_Buffer controlled_buffer_5
  assign DIVISOR = CX_2_out ? CX_3 : 16'bz;  // Controlled_Buffer controlled_buffer_6
  assign DIVIDEND = DX_out ? DX_3 : 16'bz;  // Controlled_Buffer controlled_buffer_7
  assign DIVISOR = DX_2_out ? DX_3 : 16'bz;  // Controlled_Buffer controlled_buffer_8
  assign DIVIDEND = EX_out ? EX_3 : 16'bz;  // Controlled_Buffer controlled_buffer_9
  assign DIVISOR = EX_2_out ? EX_3 : 16'bz;  // Controlled_Buffer controlled_buffer_10
  assign DIVIDEND = DR_out ? DR_3 : 16'bz;  // Controlled_Buffer controlled_buffer_11
  assign DIVISOR = DR_2_out ? DR_3 : 16'bz;  // Controlled_Buffer controlled_buffer_12
  assign DIVIDEND = IR_out ? IR_3 : 16'bz;  // Controlled_Buffer controlled_buffer_13
  assign DIVISOR = IR_2 ? IR_3 : 16'bz;  // Controlled_Buffer controlled_buffer_14
  and u_CX (CX_out, ~AX, ~BX, CX);  // AND_Gate
  and u_BX (BX_out, ~AX, BX);  // AND_Gate
  and u_DX (DX_out, ~AX, ~BX, ~CX, DX);  // AND_Gate
  and u_EX (EX_out, ~AX, ~BX, ~CX, ~DX, EX);  // AND_Gate
  and u_DR (DR_out, ~AX, ~BX, ~CX, ~DX, ~EX, DR);  // AND_Gate
  and u_IR (IR_out, ~AX, ~BX, ~CX, ~DX, ~EX, ~DR, IR);  // AND_Gate
  and u_EX_2 (EX_2_out, ~IR_2, ~DR_2, EX_2);  // AND_Gate
  and u_DR_2 (DR_2_out, ~IR_2, DR_2);  // AND_Gate
  and u_DX_2 (DX_2_out, ~IR_2, ~DR_2, ~EX_2, DX_2);  // AND_Gate
  and u_CX_2 (CX_2_out, ~IR_2, ~DR_2, ~EX_2, ~DX_2, CX_2);  // AND_Gate
  and u_BX_2 (BX_2_out, ~IR_2, ~DR_2, ~EX_2, ~DX_2, ~CX_2, BX_2);  // AND_Gate
  and u_AX (AX_out, ~IR_2, ~DR_2, ~EX_2, ~DX_2, ~CX_2, ~BX_2, AX_2);  // AND_Gate
endmodule

module CMP_1 (
  input  A,
  input  B,
  output A___B,
  output A___B_2,
  output A___B_3
);

  wire not_1_out, not_2_out;

  not not_1 (not_1_out, A);
  not not_2 (not_2_out, B);
  and and_1 (A___B, not_1_out, B);
  xnor xnor_1 (A___B_2, A, B);
  and and_2 (A___B_3, A, not_2_out);
endmodule

module CMP_4 (
  input  [3:0] A,
  input  [3:0] B,
  output A___B,
  output A___B_2,
  output A___B_3
);

  wire and_1_out, and_2_out, and_3_out, and_5_out, and_6_out, and_7_out, cmp_1_1_a___b, cmp_1_1_a___b_2,
       cmp_1_1_a___b_3, cmp_1_2_a___b, cmp_1_2_a___b_2, cmp_1_2_a___b_3, cmp_1_3_a___b, cmp_1_3_a___b_2,
       cmp_1_3_a___b_3, cmp_1_4_a___b, cmp_1_4_a___b_2, cmp_1_4_a___b_3;

  CMP_1 cmp_1_1 (.A(A[0]), .B(B[0]), .A___B(cmp_1_1_a___b), .A___B_2(cmp_1_1_a___b_2), .A___B_3(cmp_1_1_a___b_3));
  CMP_1 cmp_1_2 (.A(A[1]), .B(B[1]), .A___B(cmp_1_2_a___b), .A___B_2(cmp_1_2_a___b_2), .A___B_3(cmp_1_2_a___b_3));
  CMP_1 cmp_1_3 (.A(A[2]), .B(B[2]), .A___B(cmp_1_3_a___b), .A___B_2(cmp_1_3_a___b_2), .A___B_3(cmp_1_3_a___b_3));
  CMP_1 cmp_1_4 (.A(A[3]), .B(B[3]), .A___B(cmp_1_4_a___b), .A___B_2(cmp_1_4_a___b_2), .A___B_3(cmp_1_4_a___b_3));
  and and_1 (and_1_out, cmp_1_4_a___b_2, cmp_1_3_a___b);
  and and_2 (and_2_out, cmp_1_4_a___b_2, cmp_1_3_a___b_2, cmp_1_2_a___b);
  and and_3 (and_3_out, cmp_1_4_a___b_2, cmp_1_3_a___b_2, cmp_1_2_a___b_2, cmp_1_1_a___b);
  and and_4 (A___B_2, cmp_1_1_a___b_2, cmp_1_2_a___b_2, cmp_1_3_a___b_2, cmp_1_4_a___b_2);
  and and_5 (and_5_out, cmp_1_1_a___b_3, cmp_1_2_a___b_2, cmp_1_3_a___b_2, cmp_1_4_a___b_2);
  and and_6 (and_6_out, cmp_1_2_a___b_3, cmp_1_3_a___b_2, cmp_1_4_a___b_2);
  and and_7 (and_7_out, cmp_1_3_a___b_3, cmp_1_4_a___b_2);
  or or_1 (A___B, cmp_1_4_a___b, and_1_out, and_2_out, and_3_out);
  or or_2 (A___B_3, and_5_out, and_6_out, and_7_out, cmp_1_4_a___b_3);
endmodule

module CMP_INPUT_ADJUSTER (
  input  AX,
  input  BX,
  input  CX,
  input  DX,
  input  EX,
  input  DR,
  input  IR,
  input  AX_2,
  input  BX_2,
  input  CX_2,
  input  DX_2,
  input  EX_2,
  input  DR_2,
  input  IR_2,
  input  [15:0] AX_3,
  input  [15:0] BX_3,
  input  [15:0] CX_3,
  input  [15:0] DX_3,
  input  [15:0] EX_3,
  input  [15:0] DR_3,
  input  [15:0] IR_3,
  output [15:0] A,
  output [15:0] B
);

  wire AX_out, BX_2_out, BX_out, CX_2_out, CX_out, DR_2_out, DR_out, DX_2_out, DX_out, EX_2_out, EX_out,
       IR_out;

  assign A = AX ? AX_3 : 16'bz;  // Controlled_Buffer controlled_buffer_1
  assign B = AX_out ? AX_3 : 16'bz;  // Controlled_Buffer controlled_buffer_2
  assign A = BX_out ? BX_3 : 16'bz;  // Controlled_Buffer controlled_buffer_3
  assign B = BX_2_out ? BX_3 : 16'bz;  // Controlled_Buffer controlled_buffer_4
  assign A = CX_out ? CX_3 : 16'bz;  // Controlled_Buffer controlled_buffer_5
  assign B = CX_2_out ? CX_3 : 16'bz;  // Controlled_Buffer controlled_buffer_6
  assign A = DX_out ? DX_3 : 16'bz;  // Controlled_Buffer controlled_buffer_7
  assign B = DX_2_out ? DX_3 : 16'bz;  // Controlled_Buffer controlled_buffer_8
  assign A = EX_out ? EX_3 : 16'bz;  // Controlled_Buffer controlled_buffer_9
  assign B = EX_2_out ? EX_3 : 16'bz;  // Controlled_Buffer controlled_buffer_10
  assign A = DR_out ? DR_3 : 16'bz;  // Controlled_Buffer controlled_buffer_11
  assign B = DR_2_out ? DR_3 : 16'bz;  // Controlled_Buffer controlled_buffer_12
  assign A = IR_out ? IR_3 : 16'bz;  // Controlled_Buffer controlled_buffer_13
  assign B = IR_2 ? IR_3 : 16'bz;  // Controlled_Buffer controlled_buffer_14
  and u_BX (BX_out, ~AX, BX);  // AND_Gate
  and u_CX (CX_out, ~AX, ~BX, CX);  // AND_Gate
  and u_DX (DX_out, ~AX, ~BX, ~CX, DX);  // AND_Gate
  and u_EX (EX_out, ~AX, ~BX, ~CX, ~DX, EX);  // AND_Gate
  and u_DR (DR_out, ~AX, ~BX, ~CX, ~DX, ~EX, DR);  // AND_Gate
  and u_IR (IR_out, ~AX, ~BX, ~CX, ~DX, ~EX, ~DR, IR);  // AND_Gate
  and u_EX_2 (EX_2_out, ~IR_2, ~DR_2, EX_2);  // AND_Gate
  and u_DR_2 (DR_2_out, ~IR_2, DR_2);  // AND_Gate
  and u_DX_2 (DX_2_out, ~IR_2, ~DR_2, ~EX_2, DX_2);  // AND_Gate
  and u_CX_2 (CX_2_out, ~IR_2, ~DR_2, ~EX_2, ~DX_2, CX_2);  // AND_Gate
  and u_BX_2 (BX_2_out, ~IR_2, ~DR_2, ~EX_2, ~DX_2, ~CX_2, BX_2);  // AND_Gate
  and u_AX (AX_out, ~IR_2, ~DR_2, ~EX_2, ~DX_2, ~CX_2, ~BX_2, AX_2);  // AND_Gate
endmodule
