// Logisim project Sub Circuits.circ as structural Verilog: 8 circuits, main circuit AND_1
module AND_1 (
  input  AX,
  input  BX,
  input  CX,
  input  DX,
  input  EX,
  input  DR,
  input  IR,
  input  AX__DR,
  input  BX__DR,
  input  CX__DR,
  input  DX__DR,
  input  EX__DR,
  input  AX__IR,
  input  BX__IR,
  input  CX__IR,
  input  DX__IR,
  input  EX__IR,
  input  AX__AX,
  input  AX__BX,
  input  AX__CX,
  input  AX__DX,
  input  AX__EX,
  input  BX__BX,
  input  BX__CX,
  input  BX__DX,
  input  BX__EX,
  input  CX__CX,
  input  CX__DX,
  input  CX__EX,
  input  DX__DX,
  input  DX__EX,
  input  EX__EX,
  output OUTPUT
);

  wire and_1_out, and_2_out, and_3_out, and_4_out, and_5_out, and_6_out, and_7_out, and_8_out, and_9_out,
       and_10_out, and_11_out, and_12_out, and_13_out, and_14_out, and_15_out, and_16_out, and_17_out,
       and_18_out, and_19_out, and_20_out, and_21_out, and_22_out, and_23_out, and_24_out, and_25_out;

  and and_1 (and_1_out, AX__DR, DR, AX);
  and and_2 (and_2_out, BX__DR, DR, BX);
  and and_3 (and_3_out, CX__DR, DR, CX);
  and and_4 (and_4_out, DX__DR, DR, DX);
  and and_5 (and_5_out, EX__DR, DR, EX);
  and and_6 (and_6_out, AX__IR, IR, AX);
  and and_7 (and_7_out, BX__IR, IR, BX);
  and and_8 (and_8_out, CX__IR, IR, CX);
  and and_9 (and_9_out, DX__IR, IR, DX);
  and and_10 (and_10_out, EX__IR, IR, EX);
  and and_11 (and_11_out, AX__AX, AX, AX);
  and and_12 (and_12_out, AX__BX, BX, AX);
  and and_13 (and_13_out, AX__CX, CX, AX);
  and and_14 (and_14_out, AX__DX, DX, AX);
  and and_15 (and_15_out, AX__EX, EX, AX);
  and and_16 (and_16_out, BX__BX, BX, BX);
  and and_17 (and_17_out, BX__CX, CX, BX);
  and and_18 (and_18_out, BX__DX, DX, BX);
  and and_19 (and_19_out, BX__EX, EX, BX);
  and and_20 (and_20_out, CX__CX, CX, CX);
  and and_21 (and_21_out, CX__DX, DX, CX);
  and and_22 (and_22_out, CX__EX, EX, CX);
  and and_23 (and_23_out, DX__DX, DX, DX);
  and and_24 (and_24_out, DX__EX, EX, DX);
  and and_25 (and_25_out, EX__EX, EX, EX);
  or or_1 (OUTPUT, and_1_out, and_2_out, and_3_out, and_4_out, and_5_out, and_6_out, and_7_out, and_8_out, and_9_out, and_10_out, and_11_out, and_12_out, and_13_out, and_14_out, and_15_out, and_16_out, and_17_out, and_18_out, and_19_out, and_20_out, and_21_out, and_22_out, and_23_out, and_24_out, and_25_out);
endmodule

module OR_1 (
  input  AX,
  input  BX,
  input  CX,
  input  DX,
  input  EX,
  input  DR,
  input  IR,
  input  AX__DR,
  input  BX__DR,
  input  CX__DR,
  input  DX__DR,
  input  EX__DR,
  input  AX__IR,
  input  BX__IR,
  input  CX__IR,
  input  DX__IR,
  input  EX__IR,
  input  AX__AX,
  input  AX__BX,
  input  AX__CX,
  input  AX__DX,
  input  AX__EX,
  input  BX__BX,
  input  BX__CX,
  input  BX__DX,
  input  BX__EX,
  input  CX__CX,
  input  CX__DX,
  input  CX__EX,
  input  DX__DX,
  input  DX__EX,
  input  EX__EX,
  output OUTPUT
);

  wire and_1_out, and_2_out, and_3_out, and_4_out, and_5_out, and_6_out, and_7_out, and_8_out, and_9_out,
       and_10_out, and_11_out, and_12_out, and_13_out, and_14_out, and_15_out, and_16_out, and_17_out,
       and_18_out, and_19_out, and_20_out, and_21_out, and_22_out, and_23_out, and_24_out, and_25_out,
       or_1_out, or_2_out, or_3_out, or_4_out, or_5_out, or_6_out, or_7_out, or_8_out, or_9_out, or_10_out,
       or_11_out, or_12_out, or_13_out, or_14_out, or_15_out, or_16_out, or_17_out, or_18_out, or_19_out,
       or_20_out, or_21_out, or_22_out, or_23_out, or_24_out, or_25_out;

  or or_1 (or_1_out, DR, AX);
  or or_2 (or_2_out, DR, BX);
  or or_3 (or_3_out, DR, CX);
  or or_4 (or_4_out, DR, DX);
  or or_5 (or_5_out, DR, EX);
  or or_6 (or_6_out, IR, AX);
  or or_7 (or_7_out, IR, BX);
  or or_8 (or_8_out, IR, CX);
  or or_9 (or_9_out, IR, DX);
  or or_10 (or_10_out, IR, EX);
  or or_11 (or_11_out, AX, AX);
  or or_12 (or_12_out, AX, BX);
  or or_13 (or_13_out, AX, CX);
  or or_14 (or_14_out, AX, DX);
  or or_15 (or_15_out, AX, EX);
  or or_16 (or_16_out, BX, BX);
  or or_17 (or_17_out, BX, CX);
  or or_18 (or_18_out, DX, BX);
  or or_19 (or_19_out, EX, BX);
  or or_20 (or_20_out, CX, CX);
  or or_21 (or_21_out, DX, CX);
  or or_22 (or_22_out, EX, CX);
  or or_23 (or_23_out, DX, DX);
  or or_24 (or_24_out, EX, DX);
  or or_25 (or_25_out, EX, EX);
  and and_1 (and_1_out, AX__DR, or_1_out);
  and and_2 (and_2_out, BX__DR, or_2_out);
  and and_3 (and_3_out, CX__DR, or_3_out);
  and and_4 (and_4_out, DX__DR, or_4_out);
  and and_5 (and_5_out, EX__DR, or_5_out);
  and and_6 (and_6_out, AX__IR, or_6_out);
  and and_7 (and_7_out, BX__IR, or_7_out);
  and and_8 (and_8_out, CX__IR, or_8_out);
  and and_9 (and_9_out, DX__IR, or_9_out);
  and and_10 (and_10_out, EX__IR, or_10_out);
  and and_11 (and_11_out, AX__AX, or_11_out);
  and and_12 (and_12_out, AX__BX, or_12_out);
  and and_13 (and_13_out, AX__CX, or_13_out);
  and and_14 (and_14_out, AX__DX, or_14_out);
  and and_15 (and_15_out, AX__EX, or_15_out);
  and and_16 (and_16_out, BX__BX, or_16_out);
  and and_17 (and_17_out, BX__CX, or_17_out);
  and and_18 (and_18_out, BX__DX, or_18_out);
  and and_19 (and_19_out, BX__EX, or_19_out);
  and and_20 (and_20_out, CX__CX, or_20_out);
  and and_21 (and_21_out, CX__DX, or_21_out);
  and and_22 (and_22_out, CX__EX, or_22_out);
  and and_23 (and_23_out, DX__DX, or_23_out);
  and and_24 (and_24_out, DX__EX, or_24_out);
  and and_25 (and_25_out, EX__EX, or_25_out);
  or or_26 (OUTPUT, and_1_out, and_2_out, and_3_out, and_4_out, and_5_out, and_6_out, and_7_out, and_8_out, and_9_out, and_10_out, and_11_out, and_12_out, and_13_out, and_14_out, and_15_out, and_16_out, and_17_out, and_18_out, and_19_out, and_20_out, and_21_out, and_22_out, and_23_out, and_24_out, and_25_out);
endmodule

module XOR_1 (
  input  AX,
  input  BX,
  input  CX,
  input  DX,
  input  EX,
  input  DR,
  input  IR,
  input  AX__DR,
  input  BX__DR,
  input  CX__DR,
  input  DX__DR,
  input  EX__DR,
  input  AX__IR,
  input  BX__IR,
  input  CX__IR,
  input  DX__IR,
  input  EX__IR,
  input  AX__AX,
  input  AX__BX,
  input  AX__CX,
  input  AX__DX,
  input  AX__EX,
  input  BX__BX,
  input  BX__CX,
  input  BX__DX,
  input  BX__EX,
  input  CX__CX,
  input  CX__DX,
  input  CX__EX,
  input  DX__DX,
  input  DX__EX,
  input  EX__EX,
  output OUTPUT
);

  wire and_1_out, and_2_out, and_3_out, and_4_out, and_5_out, and_6_out, and_7_out, and_8_out, and_9_out,
       and_10_out, and_11_out, and_12_out, and_13_out, and_14_out, and_15_out, and_16_out, and_17_out,
       and_18_out, and_19_out, and_20_out, and_21_out, and_22_out, and_23_out, and_24_out, and_25_out,
       xor_1_out, xor_2_out, xor_3_out, xor_4_out, xor_5_out, xor_6_out, xor_7_out, xor_8_out, xor_9_out,
       xor_10_out, xor_11_out, xor_12_out, xor_13_out, xor_14_out, xor_15_out, xor_16_out, xor_17_out,
       xor_18_out, xor_19_out, xor_20_out, xor_21_out, xor_22_out, xor_23_out, xor_24_out, xor_25_out;

  xor xor_1 (xor_1_out, DR, AX);
  xor xor_2 (xor_2_out, DR, BX);
  xor xor_3 (xor_3_out, DR, CX);
  xor xor_4 (xor_4_out, DR, DX);
  xor xor_5 (xor_5_out, DR, EX);
  xor xor_6 (xor_6_out, IR, AX);
  xor xor_7 (xor_7_out, IR, BX);
  xor xor_8 (xor_8_out, IR, CX);
  xor xor_9 (xor_9_out, IR, DX);
  xor xor_10 (xor_10_out, IR, EX);
  xor xor_11 (xor_11_out, AX, AX);
  xor xor_12 (xor_12_out, BX, AX);
  xor xor_13 (xor_13_out, CX, AX);
  xor xor_14 (xor_14_out, DX, AX);
  xor xor_15 (xor_15_out, EX, AX);
  xor xor_16 (xor_16_out, BX, BX);
  xor xor_17 (xor_17_out, CX, BX);
  xor xor_18 (xor_18_out, DX, BX);
  xor xor_19 (xor_19_out, EX, BX);
  xor xor_20 (xor_20_out, CX, CX);
  xor xor_21 (xor_21_out, DX, CX);
  xor xor_22 (xor_22_out, EX, CX);
  xor xor_23 (xor_23_out, DX, DX);
  xor xor_24 (xor_24_out, EX, DX);
  xor xor_25 (xor_25_out, EX, EX);
  and and_1 (and_1_out, AX__DR, xor_1_out);
  and and_2 (and_2_out, BX__DR, xor_2_out);
  and and_3 (and_3_out, CX__DR, xor_3_out);
  and and_4 (and_4_out, DX__DR, xor_4_out);
  and and_5 (and_5_out, EX__DR, xor_5_out);
  and and_6 (and_6_out, AX__IR, xor_6_out);
  and and_7 (and_7_out, BX__IR, xor_7_out);
  and and_8 (and_8_out, CX__IR, xor_8_out);
  and and_9 (and_9_out, DX__IR, xor_9_out);
  and and_10 (and_10_out, EX__IR, xor_10_out);
  and and_11 (and_11_out, AX__AX, xor_11_out);
  and and_12 (and_12_out, AX__BX, xor_12_out);
  and and_13 (and_13_out, AX__CX, xor_13_out);
  and and_14 (and_14_out, AX__DX, xor_14_out);
  and and_15 (and_15_out, AX__EX, xor_15_out);
  and and_16 (and_16_out, BX__BX, xor_16_out);
  and and_17 (and_17_out, BX__CX, xor_17_out);
  and and_18 (and_18_out, BX__DX, xor_18_out);
  and and_19 (and_19_out, BX__EX, xor_19_out);
  and and_20 (and_20_out, CX__CX, xor_20_out);
  and and_21 (and_21_out, CX__DX, xor_21_out);
  and and_22 (and_22_out, CX__EX, xor_22_out);
  and and_23 (and_23_out, DX__DX, xor_23_out);
  and and_24 (and_24_out, DX__EX, xor_24_out);
  and and_25 (and_25_out, EX__EX, xor_25_out);
  or or_1 (OUTPUT, and_1_out, and_2_out, and_3_out, and_4_out, and_5_out, and_6_out, and_7_out, and_8_out, and_9_out, and_10_out, and_11_out, and_12_out, and_13_out, and_14_out, and_15_out, and_16_out, and_17_out, and_18_out, and_19_out, and_20_out, and_21_out, and_22_out, and_23_out, and_24_out, and_25_out);
endmodule

// INPUT ADJUSTER
module INPUT_4to1 (
  input  [3:0] AX,
  input  [3:0] BX,
  input  [3:0] CX,
  input  [3:0] DX,
  input  [3:0] EX,
  input  [3:0] DR,
  input  [3:0] IR,
  output AX3,
  output BX3,
  output CX3,
  output DX3,
  output EX3,
  output DR3,
  output IR3,
  output AX2,
  output BX2,
  output CX2,
  output DX2,
  output EX2,
  output DR2,
  output IR2,
  output AX1,
  output BX1,
  output CX1,
  output DX1,
  output EX1,
  output DR1,
  output IR1,
  output AX0,
  output BX0,
  output CX0,
  output DX0,
  output EX0,
  output DR0,
  output IR0
);


  assign AX0 = AX[0];
  assign AX1 = AX[1];
  assign AX2 = AX[2];
  assign AX3 = AX[3];
  assign BX0 = BX[0];
  assign BX1 = BX[1];
  assign BX2 = BX[2];
  assign BX3 = BX[3];
  assign CX0 = CX[0];
  assign CX1 = CX[1];
  assign CX2 = CX[2];
  assign CX3 = CX[3];
  assign DR0 = DR[0];
  assign DR1 = DR[1];
  assign DR2 = DR[2];
  assign DR3 = DR[3];
  assign DX0 = DX[0];
  assign DX1 = DX[1];
  assign DX2 = DX[2];
  assign DX3 = DX[3];
  assign EX0 = EX[0];
  assign EX1 = EX[1];
  assign EX2 = EX[2];
  assign EX3 = EX[3];
  assign IR0 = IR[0];
  assign IR1 = IR[1];
  assign IR2 = IR[2];
  assign IR3 = IR[3];
endmodule

module AND_4 (
  input  AX__DR,
  input  BX__DR,
  input  CX__DR,
  input  DX__DR,
  input  EX__DR,
  input  AX__IR,
  input  BX__IR,
  input  CX__IR,
  input  DX__IR,
  input  EX__IR,
  input  AX__AX,
  input  AX__BX,
  input  AX__CX,
  input  AX__DX,
  input  AX__EX,
  input  BX__BX,
  input  BX__CX,
  input  BX__DX,
  input  BX__EX,
  input  CX__CX,
  input  CX__DX,
  input  CX__EX,
  input  DX__DX,
  input  DX__EX,
  input  EX__EX,
  input  [3:0] AX,
  input  [3:0] BX,
  input  [3:0] CX,
  input  [3:0] DX,
  input  [3:0] EX,
  input  [3:0] DR,
  input  [3:0] IR,
  output [3:0] OUTPUT
);

  wire [6:0] input_4to1_1_ir0, input_4to1_1_ir1, input_4to1_1_ir2, input_4to1_1_ir3;

  INPUT_4to1 input_4to1_1 (
    .AX(AX), .BX(BX), .CX(CX), .DX(DX), .EX(EX), .DR(DR), .IR(IR), .AX3(input_4to1_1_ir3[6]),
    .BX3(input_4to1_1_ir3[5]), .CX3(input_4to1_1_ir3[4]), .DX3(input_4to1_1_ir3[3]),
    .EX3(input_4to1_1_ir3[2]), .DR3(input_4to1_1_ir3[1]), .IR3(input_4to1_1_ir3[0]),
    .AX2(input_4to1_1_ir2[6]), .BX2(input_4to1_1_ir2[5]), .CX2(input_4to1_1_ir2[4]),
    .DX2(input_4to1_1_ir2[3]), .EX2(input_4to1_1_ir2[2]), .DR2(input_4to1_1_ir2[1]),
    .IR2(input_4to1_1_ir2[0]), .AX1(input_4to1_1_ir1[6]), .BX1(input_4to1_1_ir1[5]),
    .CX1(input_4to1_1_ir1[4]), .DX1(input_4to1_1_ir1[3]), .EX1(input_4to1_1_ir1[2]),
    .DR1(input_4to1_1_ir1[1]), .IR1(input_4to1_1_ir1[0]), .AX0(input_4to1_1_ir0[6]),
    .BX0(input_4to1_1_ir0[5]), .CX0(input_4to1_1_ir0[4]), .DX0(input_4to1_1_ir0[3]),
    .EX0(input_4to1_1_ir0[2]), .DR0(input_4to1_1_ir0[1]), .IR0(input_4to1_1_ir0[0]));
  AND_1 and_1_1 (
    .AX__DR(AX__DR), .BX__DR(BX__DR), .CX__DR(CX__DR), .DX__DR(DX__DR), .EX__DR(EX__DR), .AX__IR(AX__IR),
    .BX__IR(BX__IR), .CX__IR(CX__IR), .DX__IR(DX__IR), .EX__IR(EX__IR), .AX__AX(AX__AX), .AX__BX(AX__BX),
    .AX__CX(AX__CX), .AX__DX(AX__DX), .AX__EX(AX__EX), .BX__BX(BX__BX), .BX__CX(BX__CX), .BX__DX(BX__DX),
    .BX__EX(BX__EX), .CX__CX(CX__CX), .CX__DX(CX__DX), .CX__EX(CX__EX), .DX__DX(DX__DX), .DX__EX(DX__EX),
    .EX__EX(EX__EX), .AX(input_4to1_1_ir3[6]), .BX(input_4to1_1_ir3[5]), .CX(input_4to1_1_ir3[4]),
    .DX(input_4to1_1_ir3[3]), .EX(input_4to1_1_ir3[2]), .DR(input_4to1_1_ir3[1]), .IR(input_4to1_1_ir3[0]),
    .OUTPUT(OUTPUT[3]));
  AND_1 and_1_2 (
    .AX__DR(AX__DR), .BX__DR(BX__DR), .CX__DR(CX__DR), .DX__DR(DX__DR), .EX__DR(EX__DR), .AX__IR(AX__IR),
    .BX__IR(BX__IR), .CX__IR(CX__IR), .DX__IR(DX__IR), .EX__IR(EX__IR), .AX__AX(AX__AX), .AX__BX(AX__BX),
    .AX__CX(AX__CX), .AX__DX(AX__DX), .AX__EX(AX__EX), .BX__BX(BX__BX), .BX__CX(BX__CX), .BX__DX(BX__DX),
    .BX__EX(BX__EX), .CX__CX(CX__CX), .CX__DX(CX__DX), .CX__EX(CX__EX), .DX__DX(DX__DX), .DX__EX(DX__EX),
    .EX__EX(EX__EX), .AX(input_4to1_1_ir2[6]), .BX(input_4to1_1_ir2[5]), .CX(input_4to1_1_ir2[4]),
    .DX(input_4to1_1_ir2[3]), .EX(input_4to1_1_ir2[2]), .DR(input_4to1_1_ir2[1]), .IR(input_4to1_1_ir2[0]),
    .OUTPUT(OUTPUT[2]));
  AND_1 and_1_3 (
    .AX__DR(AX__DR), .BX__DR(BX__DR), .CX__DR(CX__DR), .DX__DR(DX__DR), .EX__DR(EX__DR), .AX__IR(AX__IR),
    .BX__IR(BX__IR), .CX__IR(CX__IR), .DX__IR(DX__IR), .EX__IR(EX__IR), .AX__AX(AX__AX), .AX__BX(AX__BX),
    .AX__CX(AX__CX), .AX__DX(AX__DX), .AX__EX(AX__EX), .BX__BX(BX__BX), .BX__CX(BX__CX), .BX__DX(BX__DX),
    .BX__EX(BX__EX), .CX__CX(CX__CX), .CX__DX(CX__DX), .CX__EX(CX__EX), .DX__DX(DX__DX), .DX__EX(DX__EX),
    .EX__EX(EX__EX), .AX(input_4to1_1_ir1[6]), .BX(input_4to1_1_ir1[5]), .CX(input_4to1_1_ir1[4]),
    .DX(input_4to1_1_ir1[3]), .EX(input_4to1_1_ir1[2]), .DR(input_4to1_1_ir1[1]), .IR(input_4to1_1_ir1[0]),
    .OUTPUT(OUTPUT[1]));
  AND_1 and_1_4 (
    .AX__DR(AX__DR), .BX__DR(BX__DR), .CX__DR(CX__DR), .DX__DR(DX__DR), .EX__DR(EX__DR), .AX__IR(AX__IR),
    .BX__IR(BX__IR), .CX__IR(CX__IR), .DX__IR(DX__IR), .EX__IR(EX__IR), .AX__AX(AX__AX), .AX__BX(AX__BX),
    .AX__CX(AX__CX), .AX__DX(AX__DX), .AX__EX(AX__EX), .BX__BX(BX__BX), .BX__CX(BX__CX), .BX__DX(BX__DX),
    .BX__EX(BX__EX), .CX__CX(CX__CX), .CX__DX(CX__DX), .CX__EX(CX__EX), .DX__DX(DX__DX), .DX__EX(DX__EX),
    .EX__EX(EX__EX), .AX(input_4to1_1_ir0[6]), .BX(input_4to1_1_ir0[5]), .CX(input_4to1_1_ir0[4]),
    .DX(input_4to1_1_ir0[3]), .EX(input_4to1_1_ir0[2]), .DR(input_4to1_1_ir0[1]), .IR(input_4to1_1_ir0[0]),
    .OUTPUT(OUTPUT[0]));
endmodule

module OR_4 (
  input  AX__DR,
  input  BX__DR,
  input  CX__DR,
  input  DX__DR,
  input  EX__DR,
  input  AX__IR,
  input  BX__IR,
  input  CX__IR,
  input  DX__IR,
  input  EX__IR,
  input  AX__AX,
  input  AX__BX,
  input  AX__CX,
  input  AX__DX,
  input  AX__EX,
  input  BX__BX,
  input  BX__CX,
  input  BX__DX,
  input  BX__EX,
  input  CX__CX,
  input  CX__DX,
  input  CX__EX,
  input  DX__DX,
  input  DX__EX,
  input  EX__EX,
  input  [3:0] AX,
  input  [3:0] BX,
  input  [3:0] CX,
  input  [3:0] DX,
  input  [3:0] EX,
  input  [3:0] DR,
  input  [3:0] IR,
  output [3:0] OUTPUT
);

  wire [6:0] input_4to1_1_ir0, input_4to1_1_ir1, input_4to1_1_ir2, input_4to1_1_ir3;

  INPUT_4to1 input_4to1_1 (
    .AX(AX), .BX(BX), .CX(CX), .DX(DX), .EX(EX), .DR(DR), .IR(IR), .AX3(input_4to1_1_ir3[6]),
    .BX3(input_4to1_1_ir3[5]), .CX3(input_4to1_1_ir3[4]), .DX3(input_4to1_1_ir3[3]),
    .EX3(input_4to1_1_ir3[2]), .DR3(input_4to1_1_ir3[1]), .IR3(input_4to1_1_ir3[0]),
    .AX2(input_4to1_1_ir2[6]), .BX2(input_4to1_1_ir2[5]), .CX2(input_4to1_1_ir2[4]),
    .DX2(input_4to1_1_ir2[3]), .EX2(input_4to1_1_ir2[2]), .DR2(input_4to1_1_ir2[1]),
    .IR2(input_4to1_1_ir2[0]), .AX1(input_4to1_1_ir1[6]), .BX1(input_4to1_1_ir1[5]),
    .CX1(input_4to1_1_ir1[4]), .DX1(input_4to1_1_ir1[3]), .EX1(input_4to1_1_ir1[2]),
    .DR1(input_4to1_1_ir1[1]), .IR1(input_4to1_1_ir1[0]), .AX0(input_4to1_1_ir0[6]),
    .BX0(input_4to1_1_ir0[5]), .CX0(input_4to1_1_ir0[4]), .DX0(input_4to1_1_ir0[3]),
    .EX0(input_4to1_1_ir0[2]), .DR0(input_4to1_1_ir0[1]), .IR0(input_4to1_1_ir0[0]));
  OR_1 or_1_1 (
    .AX__DR(AX__DR), .BX__DR(BX__DR), .CX__DR(CX__DR), .DX__DR(DX__DR), .EX__DR(EX__DR), .AX__IR(AX__IR),
    .BX__IR(BX__IR), .CX__IR(CX__IR), .DX__IR(DX__IR), .EX__IR(EX__IR), .AX__AX(AX__AX), .AX__BX(AX__BX),
    .AX__CX(AX__CX), .AX__DX(AX__DX), .AX__EX(AX__EX), .BX__BX(BX__BX), .BX__CX(BX__CX), .BX__DX(BX__DX),
    .BX__EX(BX__EX), .CX__CX(CX__CX), .CX__DX(CX__DX), .CX__EX(CX__EX), .DX__DX(DX__DX), .DX__EX(DX__EX),
    .EX__EX(EX__EX), .AX(input_4to1_1_ir3[6]), .BX(input_4to1_1_ir3[5]), .CX(input_4to1_1_ir3[4]),
    .DX(input_4to1_1_ir3[3]), .EX(input_4to1_1_ir3[2]), .DR(input_4to1_1_ir3[1]), .IR(input_4to1_1_ir3[0]),
    .OUTPUT(OUTPUT[3]));
  OR_1 or_1_2 (
    .AX__DR(AX__DR), .BX__DR(BX__DR), .CX__DR(CX__DR), .DX__DR(DX__DR), .EX__DR(EX__DR), .AX__IR(AX__IR),
    .BX__IR(BX__IR), .CX__IR(CX__IR), .DX__IR(DX__IR), .EX__IR(EX__IR), .AX__AX(AX__AX), .AX__BX(AX__BX),
    .AX__CX(AX__CX), .AX__DX(AX__DX), .AX__EX(AX__EX), .BX__BX(BX__BX), .BX__CX(BX__CX), .BX__DX(BX__DX),
    .BX__EX(BX__EX), .CX__CX(CX__CX), .CX__DX(CX__DX), .CX__EX(CX__EX), .DX__DX(DX__DX), .DX__EX(DX__EX),
    .EX__EX(EX__EX), .AX(input_4to1_1_ir2[6]), .BX(input_4to1_1_ir2[5]), .CX(input_4to1_1_ir2[4]),
    .DX(input_4to1_1_ir2[3]), .EX(input_4to1_1_ir2[2]), .DR(input_4to1_1_ir2[1]), .IR(input_4to1_1_ir2[0]),
    .OUTPUT(OUTPUT[2]));
  OR_1 or_1_3 (
    .AX__DR(AX__DR), .BX__DR(BX__DR), .CX__DR(CX__DR), .DX__DR(DX__DR), .EX__DR(EX__DR), .AX__IR(AX__IR),
    .BX__IR(BX__IR), .CX__IR(CX__IR), .DX__IR(DX__IR), .EX__IR(EX__IR), .AX__AX(AX__AX), .AX__BX(AX__BX),
    .AX__CX(AX__CX), .AX__DX(AX__DX), .AX__EX(AX__EX), .BX__BX(BX__BX), .BX__CX(BX__CX), .BX__DX(BX__DX),
    .BX__EX(BX__EX), .CX__CX(CX__CX), .CX__DX(CX__DX), .CX__EX(CX__EX), .DX__DX(DX__DX), .DX__EX(DX__EX),
    .EX__EX(EX__EX), .AX(input_4to1_1_ir1[6]), .BX(input_4to1_1_ir1[5]), .CX(input_4to1_1_ir1[4]),
    .DX(input_4to1_1_ir1[3]), .EX(input_4to1_1_ir1[2]), .DR(input_4to1_1_ir1[1]), .IR(input_4to1_1_ir1[0]),
    .OUTPUT(OUTPUT[1]));
  OR_1 or_1_4 (
    .AX__DR(AX__DR), .BX__DR(BX__DR), .CX__DR(CX__DR), .DX__DR(DX__DR), .EX__DR(EX__DR), .AX__IR(AX__IR),
    .BX__IR(BX__IR), .CX__IR(CX__IR), .DX__IR(DX__IR), .EX__IR(EX__IR), .AX__AX(AX__AX), .AX__BX(AX__BX),
    .AX__CX(AX__CX), .AX__DX(AX__DX), .AX__EX(AX__EX), .BX__BX(BX__BX), .BX__CX(BX__CX), .BX__DX(BX__DX),
    .BX__EX(BX__EX), .CX__CX(CX__CX), .CX__DX(CX__DX), .CX__EX(CX__EX), .DX__DX(DX__DX), .DX__EX(DX__EX),
    .EX__EX(EX__EX), .AX(input_4to1_1_ir0[6]), .BX(input_4to1_1_ir0[5]), .CX(input_4to1_1_ir0[4]),
    .DX(input_4to1_1_ir0[3]), .EX(input_4to1_1_ir0[2]), .DR(input_4to1_1_ir0[1]), .IR(input_4to1_1_ir0[0]),
    .OUTPUT(OUTPUT[0]));
endmodule

module XOR_4 (
  input  AX__DR,
  input  BX__DR,
  input  CX__DR,
  input  DX__DR,
  input  EX__DR,
  input  AX__IR,
  input  BX__IR,
  input  CX__IR,
  input  DX__IR,
  input  EX__IR,
  input  AX__AX,
  input  AX__BX,
  input  AX__CX,
  input  AX__DX,
  input  AX__EX,
  input  BX__BX,
  input  BX__CX,
  input  BX__DX,
  input  BX__EX,
  input  CX__CX,
  input  CX__DX,
  input  CX__EX,
  input  DX__DX,
  input  DX__EX,
  input  EX__EX,
  input  [3:0] AX,
  input  [3:0] BX,
  input  [3:0] CX,
  input  [3:0] DX,
  input  [3:0] EX,
  input  [3:0] DR,
  input  [3:0] IR,
  output [3:0] OUTPUT
);

  wire [6:0] input_4to1_1_ir0, input_4to1_1_ir1, input_4to1_1_ir2, input_4to1_1_ir3;

  INPUT_4to1 input_4to1_1 (
    .AX(AX), .BX(BX), .CX(CX), .DX(DX), .EX(EX), .DR(DR), .IR(IR), .AX3(input_4to1_1_ir3[6]),
    .BX3(input_4to1_1_ir3[5]), .CX3(input_4to1_1_ir3[4]), .DX3(input_4to1_1_ir3[3]),
    .EX3(input_4to1_1_ir3[2]), .DR3(input_4to1_1_ir3[1]), .IR3(input_4to1_1_ir3[0]),
    .AX2(input_4to1_1_ir2[6]), .BX2(input_4to1_1_ir2[5]), .CX2(input_4to1_1_ir2[4]),
    .DX2(input_4to1_1_ir2[3]), .EX2(input_4to1_1_ir2[2]), .DR2(input_4to1_1_ir2[1]),
    .IR2(input_4to1_1_ir2[0]), .AX1(input_4to1_1_ir1[6]), .BX1(input_4to1_1_ir1[5]),
    .CX1(input_4to1_1_ir1[4]), .DX1(input_4to1_1_ir1[3]), .EX1(input_4to1_1_ir1[2]),
    .DR1(input_4to1_1_ir1[1]), .IR1(input_4to1_1_ir1[0]), .AX0(input_4to1_1_ir0[6]),
    .BX0(input_4to1_1_ir0[5]), .CX0(input_4to1_1_ir0[4]), .DX0(input_4to1_1_ir0[3]),
    .EX0(input_4to1_1_ir0[2]), .DR0(input_4to1_1_ir0[1]), .IR0(input_4to1_1_ir0[0]));
  XOR_1 xor_1_1 (
    .AX__DR(AX__DR), .BX__DR(BX__DR), .CX__DR(CX__DR), .DX__DR(DX__DR), .EX__DR(EX__DR), .AX__IR(AX__IR),
    .BX__IR(BX__IR), .CX__IR(CX__IR), .DX__IR(DX__IR), .EX__IR(EX__IR), .AX__AX(AX__AX), .AX__BX(AX__BX),
    .AX__CX(AX__CX), .AX__DX(AX__DX), .AX__EX(AX__EX), .BX__BX(BX__BX), .BX__CX(BX__CX), .BX__DX(BX__DX),
    .BX__EX(BX__EX), .CX__CX(CX__CX), .CX__DX(CX__DX), .CX__EX(CX__EX), .DX__DX(DX__DX), .DX__EX(DX__EX),
    .EX__EX(EX__EX), .AX(input_4to1_1_ir3[6]), .BX(input_4to1_1_ir3[5]), .CX(input_4to1_1_ir3[4]),
    .DX(input_4to1_1_ir3[3]), .EX(input_4to1_1_ir3[2]), .DR(input_4to1_1_ir3[1]), .IR(input_4to1_1_ir3[0]),
    .OUTPUT(OUTPUT[3]));
  XOR_1 xor_1_2 (
    .AX__DR(AX__DR), .BX__DR(BX__DR), .CX__DR(CX__DR), .DX__DR(DX__DR), .EX__DR(EX__DR), .AX__IR(AX__IR),
    .BX__IR(BX__IR), .CX__IR(CX__IR), .DX__IR(DX__IR), .EX__IR(EX__IR), .AX__AX(AX__AX), .AX__BX(AX__BX),
    .AX__CX(AX__CX), .AX__DX(AX__DX), .AX__EX(AX__EX), .BX__BX(BX__BX), .BX__CX(BX__CX), .BX__DX(BX__DX),
    .BX__EX(BX__EX), .CX__CX(CX__CX), .CX__DX(CX__DX), .CX__EX(CX__EX), .DX__DX(DX__DX), .DX__EX(DX__EX),
    .EX__EX(EX__EX), .AX(input_4to1_1_ir2[6]), .BX(input_4to1_1_ir2[5]), .CX(input_4to1_1_ir2[4]),
    .DX(input_4to1_1_ir2[3]), .EX(input_4to1_1_ir2[2]), .DR(input_4to1_1_ir2[1]), .IR(input_4to1_1_ir2[0]),
    .OUTPUT(OUTPUT[2]));
  XOR_1 xor_1_3 (
    .AX__DR(AX__DR), .BX__DR(BX__DR), .CX__DR(CX__DR), .DX__DR(DX__DR), .EX__DR(EX__DR), .AX__IR(AX__IR),
    .BX__IR(BX__IR), .CX__IR(CX__IR), .DX__IR(DX__IR), .EX__IR(EX__IR), .AX__AX(AX__AX), .AX__BX(AX__BX),
    .AX__CX(AX__CX), .AX__DX(AX__DX), .AX__EX(AX__EX), .BX__BX(BX__BX), .BX__CX(BX__CX), .BX__DX(BX__DX),
    .BX__EX(BX__EX), .CX__CX(CX__CX), .CX__DX(CX__DX), .CX__EX(CX__EX), .DX__DX(DX__DX), .DX__EX(DX__EX),
    .EX__EX(EX__EX), .AX(input_4to1_1_ir1[6]), .BX(input_4to1_1_ir1[5]), .CX(input_4to1_1_ir1[4]),
    .DX(input_4to1_1_ir1[3]), .EX(input_4to1_1_ir1[2]), .DR(input_4to1_1_ir1[1]), .IR(input_4to1_1_ir1[0]),
    .OUTPUT(OUTPUT[1]));
  XOR_1 xor_1_4 (
    .AX__DR(AX__DR), .BX__DR(BX__DR), .CX__DR(CX__DR), .DX__DR(DX__DR), .EX__DR(EX__DR), .AX__IR(AX__IR),
    .BX__IR(BX__IR), .CX__IR(CX__IR), .DX__IR(DX__IR), .EX__IR(EX__IR), .AX__AX(AX__AX), .AX__BX(AX__BX),
    .AX__CX(AX__CX), .AX__DX(AX__DX), .AX__EX(AX__EX), .BX__BX(BX__BX), .BX__CX(BX__CX), .BX__DX(BX__DX),
    .BX__EX(BX__EX), .CX__CX(CX__CX), .CX__DX(CX__DX), .CX__EX(CX__EX), .DX__DX(DX__DX), .DX__EX(DX__EX),
    .EX__EX(EX__EX), .AX(input_4to1_1_ir0[6]), .BX(input_4to1_1_ir0[5]), .CX(input_4to1_1_ir0[4]),
    .DX(input_4to1_1_ir0[3]), .EX(input_4to1_1_ir0[2]), .DR(input_4to1_1_ir0[1]), .IR(input_4to1_1_ir0[0]),
    .OUTPUT(OUTPUT[0]));
endmodule

// INPUT ADJUSTER
module INPUT_16to4 (
  input  [15:0] AX,
  input  [15:0] BX,
  input  [15:0] CX,
  input  [15:0] DX,
  input  [15:0] EX,
  input  [15:0] DR,
  input  [15:0] IR,
  output [3:0] AX_0_3,
  output [3:0] BX_0_3,
  output [3:0] CX_0_3,
  output [3:0] DX_0_3,
  output [3:0] EX_0_3,
  output [3:0] DR_0_3,
  output [3:0] IR_0_3,
  output [3:0] AX_4_7,
  output [3:0] BX_4_7,
  output [3:0] CX_4_7,
  output [3:0] DX_4_7,
  output [3:0] EX_4_7,
  output [3:0] DR_4_7,
  output [3:0] IR_4_7,
  output [3:0] AX_8_11,
  output [3:0] BX_8_11,
  output [3:0] CX_8_11,
  output [3:0] DX_8_11,
  output [3:0] EX_8_11,
  output [3:0] DR_8_11,
  output [3:0] IR_0_3_2,
  output [3:0] AX_12_15,
  output [3:0] BX_12_15,
  output [3:0] CX_12_15,
  output [3:0] DX_12_15,
  output [3:0] EX_12_15,
  output [3:0] DR_12_15,
  output [3:0] IR_12_15
);


  assign AX_0_3 = AX[3:0];
  assign AX_4_7 = AX[7:4];
  assign AX_8_11 = AX[11:8];
  assign AX_12_15 = AX[15:12];
  assign BX_0_3 = BX[3:0];
  assign BX_4_7 = BX[7:4];
  assign BX_8_11 = BX[11:8];
  assign BX_12_15 = BX[15:12];
  assign CX_0_3 = CX[3:0];
  assign CX_4_7 = CX[7:4];
  assign CX_8_11 = CX[11:8];
  assign CX_12_15 = CX[15:12];
  assign DR_0_3 = DR[3:0];
  assign DR_4_7 = DR[7:4];
  assign DR_8_11 = DR[11:8];
  assign DR_12_15 = DR[15:12];
  assign DX_0_3 = DX[3:0];
  assign DX_4_7 = DX[7:4];
  assign DX_8_11 = DX[11:8];
  assign DX_12_15 = DX[15:12];
  assign EX_0_3 = EX[3:0];
  assign EX_4_7 = EX[7:4];
  assign EX_8_11 = EX[11:8];
  assign EX_12_15 = EX[15:12];
  assign IR_0_3 = IR[3:0];
  assign IR_0_3_2 = IR[11:8];
  assign IR_4_7 = IR[7:4];
  assign IR_12_15 = IR[15:12];
endmodule
