// Logisim project LOGIC_UNITS.circ as structural Verilog: 4 circuits, main circuit AND
module AND (
  input  [15:0] AX,
  input  [15:0] BX,
  input  [15:0] CX,
  input  [15:0] DX,
  input  [15:0] EX,
  input  [15:0] DR,
  input  [15:0] IR,
  input  AX_2,
  input  BX_2,
  input  CX_2,
  input  DX_2,
  input  EX_2,
  input  DR_2,
  input  IR_2,
  output [15:0] out_15
);

  wire [3:0] input_16to4_1_ax_0_3, input_16to4_1_ax_4_7, input_16to4_1_ax_15_12, input_16to4_1_bx_0_3,
       input_16to4_1_bx_4_7, input_16to4_1_bx_15_12, input_16to4_1_cx_0_3, input_16to4_1_cx_4_7,
       input_16to4_1_cx_15_12, input_16to4_1_dr_0_3, input_16to4_1_dr_15_12, input_16to4_1_dx_0_3,
       input_16to4_1_dx_4_7, input_16to4_1_dx_15_12, input_16to4_1_ex_0_3, input_16to4_1_ex_15_12,
       input_16to4_1_ir_0_3, input_16to4_1_ir_15_12;
  wire [11:0] input_16to4_1_ir_4_7;
  wire [27:0] input_16to4_1_ir_8_11;

  AND_4 and_4_1 (
    .AX_2(AX_2), .BX_2(BX_2), .CX_2(CX_2), .DX_2(DX_2), .EX_2(EX_2), .DR_2(DR_2), .IR_2(IR_2),
    .AX(input_16to4_1_ax_15_12), .BX(input_16to4_1_bx_15_12), .CX(input_16to4_1_cx_15_12),
    .DX(input_16to4_1_dx_15_12), .EX(input_16to4_1_ex_15_12), .DR(input_16to4_1_dr_15_12),
    .IR(input_16to4_1_ir_15_12), .out_15(out_15[15:12]));
  INPUT_16to4 input_16to4_1 (
    .AX(AX), .BX(BX), .CX(CX), .DX(DX), .EX(EX), .DR(DR), .IR(IR), .AX_15_12(input_16to4_1_ax_15_12),
    .BX_15_12(input_16to4_1_bx_15_12), .CX_15_12(input_16to4_1_cx_15_12), .DX_15_12(input_16to4_1_dx_15_12),
    .EX_15_12(input_16to4_1_ex_15_12), .DR_15_12(input_16to4_1_dr_15_12), .IR_15_12(input_16to4_1_ir_15_12),
    .AX_8_11(input_16to4_1_ir_8_11[27:24]), .BX_8_11(input_16to4_1_ir_8_11[23:20]),
    .CX_8_11(input_16to4_1_ir_8_11[19:16]), .DX_8_11(input_16to4_1_ir_8_11[15:12]),
    .EX_8_11(input_16to4_1_ir_8_11[11:8]), .DR_2(input_16to4_1_ir_8_11[7:4]),
    .IR_8_11(input_16to4_1_ir_8_11[3:0]), .AX_4_7(input_16to4_1_ax_4_7), .BX_4_7(input_16to4_1_bx_4_7),
    .CX_4_7(input_16to4_1_cx_4_7), .DX_4_7(input_16to4_1_dx_4_7), .EX_4_7(input_16to4_1_ir_4_7[11:8]),
    .DR_4_7(input_16to4_1_ir_4_7[7:4]), .IR_4_7(input_16to4_1_ir_4_7[3:0]), .AX_0_3(input_16to4_1_ax_0_3),
    .BX_0_3(input_16to4_1_bx_0_3), .CX_0_3(input_16to4_1_cx_0_3), .DX_0_3(input_16to4_1_dx_0_3),
    .EX_0_3(input_16to4_1_ex_0_3), .DR_0_3(input_16to4_1_dr_0_3), .IR_0_3(input_16to4_1_ir_0_3));
  AND_4 and_4_2 (
    .AX_2(AX_2), .BX_2(BX_2), .CX_2(CX_2), .DX_2(DX_2), .EX_2(EX_2), .DR_2(DR_2), .IR_2(IR_2),
    .AX(input_16to4_1_ir_8_11[27:24]), .BX(input_16to4_1_ir_8_11[23:20]), .CX(input_16to4_1_ir_8_11[19:16]),
    .DX(input_16to4_1_ir_8_11[15:12]), .EX(input_16to4_1_ir_8_11[11:8]), .DR(input_16to4_1_ir_8_11[7:4]),
    .IR(input_16to4_1_ir_8_11[3:0]), .out_15(out_15[11:8]));
  AND_4 and_4_3 (
    .AX_2(AX_2), .BX_2(BX_2), .CX_2(CX_2), .DX_2(DX_2), .EX_2(EX_2), .DR_2(DR_2), .IR_2(IR_2),
    .AX(input_16to4_1_ax_4_7), .BX(input_16to4_1_bx_4_7), .CX(input_16to4_1_cx_4_7),
    .DX(input_16to4_1_dx_4_7), .EX(input_16to4_1_ir_4_7[11:8]), .DR(input_16to4_1_ir_4_7[7:4]),
    .IR(input_16to4_1_ir_4_7[3:0]), .out_15(out_15[7:4]));
  AND_4 and_4_4 (
    .AX_2(AX_2), .BX_2(BX_2), .CX_2(CX_2), .DX_2(DX_2), .EX_2(EX_2), .DR_2(DR_2), .IR_2(IR_2),
    .AX(input_16to4_1_ax_0_3), .BX(input_16to4_1_bx_0_3), .CX(input_16to4_1_cx_0_3),
    .DX(input_16to4_1_dx_0_3), .EX(input_16to4_1_ex_0_3), .DR(input_16to4_1_dr_0_3),
    .IR(input_16to4_1_ir_0_3), .out_15(out_15[3:0]));
endmodule

module OR (
  input  [15:0] AX,
  input  [15:0] BX,
  input  [15:0] CX,
  input  [15:0] DX,
  input  [15:0] EX,
  input  [15:0] DR,
  input  [15:0] IR,
  input  AX_2,
  input  BX_2,
  input  CX_2,
  input  DX_2,
  input  EX_2,
  input  DR_2,
  input  IR_2,
  output [15:0] out_15
);

  wire [3:0] input_16to4_1_ax_0_3, input_16to4_1_ax_4_7, input_16to4_1_ax_15_12, input_16to4_1_bx_0_3,
       input_16to4_1_bx_4_7, input_16to4_1_bx_15_12, input_16to4_1_cx_0_3, input_16to4_1_cx_4_7,
       input_16to4_1_cx_15_12, input_16to4_1_dr_0_3, input_16to4_1_dr_15_12, input_16to4_1_dx_0_3,
       input_16to4_1_dx_4_7, input_16to4_1_dx_15_12, input_16to4_1_ex_0_3, input_16to4_1_ex_15_12,
       input_16to4_1_ir_0_3, input_16to4_1_ir_15_12;
  wire [11:0] input_16to4_1_ir_4_7;
  wire [27:0] input_16to4_1_ir_8_11;

  OR_4 or_4_1 (
    .AX_2(AX_2), .BX_2(BX_2), .CX_2(CX_2), .DX_2(DX_2), .EX_2(EX_2), .DR_2(DR_2), .IR_2(IR_2),
    .AX(input_16to4_1_ax_15_12), .BX(input_16to4_1_bx_15_12), .CX(input_16to4_1_cx_15_12),
    .DX(input_16to4_1_dx_15_12), .EX(input_16to4_1_ex_15_12), .DR(input_16to4_1_dr_15_12),
    .IR(input_16to4_1_ir_15_12), .out_15(out_15[15:12]));
  INPUT_16to4 input_16to4_1 (
    .AX(AX), .BX(BX), .CX(CX), .DX(DX), .EX(EX), .DR(DR), .IR(IR), .AX_15_12(input_16to4_1_ax_15_12),
    .BX_15_12(input_16to4_1_bx_15_12), .CX_15_12(input_16to4_1_cx_15_12), .DX_15_12(input_16to4_1_dx_15_12),
    .EX_15_12(input_16to4_1_ex_15_12), .DR_15_12(input_16to4_1_dr_15_12), .IR_15_12(input_16to4_1_ir_15_12),
    .AX_8_11(input_16to4_1_ir_8_11[27:24]), .BX_8_11(input_16to4_1_ir_8_11[23:20]),
    .CX_8_11(input_16to4_1_ir_8_11[19:16]), .DX_8_11(input_16to4_1_ir_8_11[15:12]),
    .EX_8_11(input_16to4_1_ir_8_11[11:8]), .DR_2(input_16to4_1_ir_8_11[7:4]),
    .IR_8_11(input_16to4_1_ir_8_11[3:0]), .AX_4_7(input_16to4_1_ax_4_7), .BX_4_7(input_16to4_1_bx_4_7),
    .CX_4_7(input_16to4_1_cx_4_7), .DX_4_7(input_16to4_1_dx_4_7), .EX_4_7(input_16to4_1_ir_4_7[11:8]),
    .DR_4_7(input_16to4_1_ir_4_7[7:4]), .IR_4_7(input_16to4_1_ir_4_7[3:0]), .AX_0_3(input_16to4_1_ax_0_3),
    .BX_0_3(input_16to4_1_bx_0_3), .CX_0_3(input_16to4_1_cx_0_3), .DX_0_3(input_16to4_1_dx_0_3),
    .EX_0_3(input_16to4_1_ex_0_3), .DR_0_3(input_16to4_1_dr_0_3), .IR_0_3(input_16to4_1_ir_0_3));
  OR_4 or_4_2 (
    .AX_2(AX_2), .BX_2(BX_2), .CX_2(CX_2), .DX_2(DX_2), .EX_2(EX_2), .DR_2(DR_2), .IR_2(IR_2),
    .AX(input_16to4_1_ir_8_11[27:24]), .BX(input_16to4_1_ir_8_11[23:20]), .CX(input_16to4_1_ir_8_11[19:16]),
    .DX(input_16to4_1_ir_8_11[15:12]), .EX(input_16to4_1_ir_8_11[11:8]), .DR(input_16to4_1_ir_8_11[7:4]),
    .IR(input_16to4_1_ir_8_11[3:0]), .out_15(out_15[11:8]));
  OR_4 or_4_3 (
    .AX_2(AX_2), .BX_2(BX_2), .CX_2(CX_2), .DX_2(DX_2), .EX_2(EX_2), .DR_2(DR_2), .IR_2(IR_2),
    .AX(input_16to4_1_ax_4_7), .BX(input_16to4_1_bx_4_7), .CX(input_16to4_1_cx_4_7),
    .DX(input_16to4_1_dx_4_7), .EX(input_16to4_1_ir_4_7[11:8]), .DR(input_16to4_1_ir_4_7[7:4]),
    .IR(input_16to4_1_ir_4_7[3:0]), .out_15(out_15[7:4]));
  OR_4 or_4_4 (
    .AX_2(AX_2), .BX_2(BX_2), .CX_2(CX_2), .DX_2(DX_2), .EX_2(EX_2), .DR_2(DR_2), .IR_2(IR_2),
    .AX(input_16to4_1_ax_0_3), .BX(input_16to4_1_bx_0_3), .CX(input_16to4_1_cx_0_3),
    .DX(input_16to4_1_dx_0_3), .EX(input_16to4_1_ex_0_3), .DR(input_16to4_1_dr_0_3),
    .IR(input_16to4_1_ir_0_3), .out_15(out_15[3:0]));
endmodule

module XOR (
  input  [15:0] AX,
  input  [15:0] BX,
  input  [15:0] CX,
  input  [15:0] DX,
  input  [15:0] EX,
  input  [15:0] DR,
  input  [15:0] IR,
  input  AX_2,
  input  BX_2,
  input  CX_2,
  input  DX_2,
  input  EX_2,
  input  DR_2,
  input  IR_2,
  output [15:0] out_15
);

  wire [3:0] input_16to4_1_ax_0_3, input_16to4_1_ax_4_7, input_16to4_1_ax_15_12, input_16to4_1_bx_0_3,
       input_16to4_1_bx_4_7, input_16to4_1_bx_15_12, input_16to4_1_cx_0_3, input_16to4_1_cx_4_7,
       input_16to4_1_cx_15_12, input_16to4_1_dr_0_3, input_16to4_1_dr_15_12, input_16to4_1_dx_0_3,
       input_16to4_1_dx_4_7, input_16to4_1_dx_15_12, input_16to4_1_ex_0_3, input_16to4_1_ex_15_12,
       input_16to4_1_ir_0_3, input_16to4_1_ir_15_12;
  wire [11:0] input_16to4_1_ir_4_7;
  wire [27:0] input_16to4_1_ir_8_11;

  XOR_4 xor_4_1 (
    .AX_2(AX_2), .BX_2(BX_2), .CX_2(CX_2), .DX_2(DX_2), .EX_2(EX_2), .DR_2(DR_2), .IR_2(IR_2),
    .AX(input_16to4_1_ax_15_12), .BX(input_16to4_1_bx_15_12), .CX(input_16to4_1_cx_15_12),
    .DX(input_16to4_1_dx_15_12), .EX(input_16to4_1_ex_15_12), .DR(input_16to4_1_dr_15_12),
    .IR(input_16to4_1_ir_15_12), .out_15(out_15[15:12]));
  INPUT_16to4 input_16to4_1 (
    .AX(AX), .BX(BX), .CX(CX), .DX(DX), .EX(EX), .DR(DR), .IR(IR), .AX_15_12(input_16to4_1_ax_15_12),
    .BX_15_12(input_16to4_1_bx_15_12), .CX_15_12(input_16to4_1_cx_15_12), .DX_15_12(input_16to4_1_dx_15_12),
    .EX_15_12(input_16to4_1_ex_15_12), .DR_15_12(input_16to4_1_dr_15_12), .IR_15_12(input_16to4_1_ir_15_12),
    .AX_8_11(input_16to4_1_ir_8_11[27:24]), .BX_8_11(input_16to4_1_ir_8_11[23:20]),
    .CX_8_11(input_16to4_1_ir_8_11[19:16]), .DX_8_11(input_16to4_1_ir_8_11[15:12]),
    .EX_8_11(input_16to4_1_ir_8_11[11:8]), .DR_2(input_16to4_1_ir_8_11[7:4]),
    .IR_8_11(input_16to4_1_ir_8_11[3:0]), .AX_4_7(input_16to4_1_ax_4_7), .BX_4_7(input_16to4_1_bx_4_7),
    .CX_4_7(input_16to4_1_cx_4_7), .DX_4_7(input_16to4_1_dx_4_7), .EX_4_7(input_16to4_1_ir_4_7[11:8]),
    .DR_4_7(input_16to4_1_ir_4_7[7:4]), .IR_4_7(input_16to4_1_ir_4_7[3:0]), .AX_0_3(input_16to4_1_ax_0_3),
    .BX_0_3(input_16to4_1_bx_0_3), .CX_0_3(input_16to4_1_cx_0_3), .DX_0_3(input_16to4_1_dx_0_3),
    .EX_0_3(input_16to4_1_ex_0_3), .DR_0_3(input_16to4_1_dr_0_3), .IR_0_3(input_16to4_1_ir_0_3));
  XOR_4 xor_4_2 (
    .AX_2(AX_2), .BX_2(BX_2), .CX_2(CX_2), .DX_2(DX_2), .EX_2(EX_2), .DR_2(DR_2), .IR_2(IR_2),
    .AX(input_16to4_1_ir_8_11[27:24]), .BX(input_16to4_1_ir_8_11[23:20]), .CX(input_16to4_1_ir_8_11[19:16]),
    .DX(input_16to4_1_ir_8_11[15:12]), .EX(input_16to4_1_ir_8_11[11:8]), .DR(input_16to4_1_ir_8_11[7:4]),
    .IR(input_16to4_1_ir_8_11[3:0]), .out_15(out_15[11:8]));
  XOR_4 xor_4_3 (
    .AX_2(AX_2), .BX_2(BX_2), .CX_2(CX_2), .DX_2(DX_2), .EX_2(EX_2), .DR_2(DR_2), .IR_2(IR_2),
    .AX(input_16to4_1_ax_4_7), .BX(input_16to4_1_bx_4_7), .CX(input_16to4_1_cx_4_7),
    .DX(input_16to4_1_dx_4_7), .EX(input_16to4_1_ir_4_7[11:8]), .DR(input_16to4_1_ir_4_7[7:4]),
    .IR(input_16to4_1_ir_4_7[3:0]), .out_15(out_15[7:4]));
  XOR_4 xor_4_4 (
    .AX_2(AX_2), .BX_2(BX_2), .CX_2(CX_2), .DX_2(DX_2), .EX_2(EX_2), .DR_2(DR_2), .IR_2(IR_2),
    .AX(input_16to4_1_ax_0_3), .BX(input_16to4_1_bx_0_3), .CX(input_16to4_1_cx_0_3),
    .DX(input_16to4_1_dx_0_3), .EX(input_16to4_1_ex_0_3), .DR(input_16to4_1_dr_0_3),
    .IR(input_16to4_1_ir_0_3), .out_15(out_15[3:0]));
endmodule

module LOAD (
  input  [15:0] AX,
  input  [15:0] BX,
  input  [15:0] CX,
  input  [15:0] DX,
  input  [15:0] EX,
  input  [15:0] DR,
  input  [15:0] IR,
  input  AX_2,
  input  BX_2,
  input  CX_2,
  input  DX_2,
  input  EX_2,
  input  DR_2,
  input  IR_2,
  output [15:0] OUTPUT
);

  assign OUTPUT = AX_2 ? AX : 16'bz;  // Controlled_Buffer controlled_buffer_1
  assign OUTPUT = BX_2 ? BX : 16'bz;  // Controlled_Buffer controlled_buffer_2
  assign OUTPUT = CX_2 ? CX : 16'bz;  // Controlled_Buffer controlled_buffer_3
  assign OUTPUT = DX_2 ? DX : 16'bz;  // Controlled_Buffer controlled_buffer_4
  assign OUTPUT = EX_2 ? EX : 16'bz;  // Controlled_Buffer controlled_buffer_5
  assign OUTPUT = DR_2 ? DR : 16'bz;  // Controlled_Buffer controlled_buffer_6
  assign OUTPUT = IR_2 ? IR : 16'bz;  // Controlled_Buffer controlled_buffer_7
endmodule
