// Logisim project Sub_Circuits.circ as structural Verilog: 8 circuits, main circuit AND_1
module AND_1 (
  input  AX,
  input  BX,
  input  CX,
  input  DX,
  input  EX,
  input  DR,
  input  IR,
  input  AX_2,
  input  BX_2,
  input  CX_2,
  input  DX_2,
  input  EX_2,
  input  DR_2,
  input  IR_2,
  output OUTPUT
);

  wire AX_2_out, AX_out, BX_2_out, BX_out, CX_2_out, CX_out, DR_2_out, DR_out, DX_2_out, DX_out, EX_2_out,
       EX_out, IR_2_out, IR_out, or_1_out, or_2_out;

  and u_AX (AX_out, AX_2, AX);
  and u_CX (CX_out, CX, ~AX_2, ~BX_2, CX_2);  // AND_Gate
  and u_BX (BX_out, BX, ~AX_2, BX_2);  // AND_Gate
  and u_DX (DX_out, DX, ~AX_2, ~BX_2, ~CX_2, DX_2);  // AND_Gate
  or or_1 (or_1_out, AX_out, BX_out, CX_out, DX_out, EX_out, DR_out, IR_out);
  and u_EX (EX_out, EX, ~AX_2, ~BX_2, ~CX_2, ~DX_2, EX_2);  // AND_Gate
  and u_DR (DR_out, DR, ~AX_2, ~BX_2, ~CX_2, ~DX_2, ~EX_2, DR_2);  // AND_Gate
  and u_IR (IR_out, IR, ~AX_2, ~BX_2, ~CX_2, ~DX_2, ~EX_2, ~DR_2, IR_2);  // AND_Gate
  and u_IR_2 (IR_2_out, IR, IR_2);
  and u_EX_2 (EX_2_out, EX, ~IR_2, ~DR_2, EX_2);  // AND_Gate
  and u_DR_2 (DR_2_out, DR, ~IR_2, DR_2);  // AND_Gate
  and u_DX_2 (DX_2_out, DX, ~IR_2, ~DR_2, ~EX_2, DX_2);  // AND_Gate
  or or_2 (or_2_out, IR_2_out, DR_2_out, EX_2_out, DX_2_out, CX_2_out, BX_2_out, AX_2_out);
  and u_CX_2 (CX_2_out, CX, ~IR_2, ~DR_2, ~EX_2, ~DX_2, CX_2);  // AND_Gate
  and and_1 (OUTPUT, or_2_out, or_1_out);
  and u_BX_2 (BX_2_out, BX, ~IR_2, ~DR_2, ~EX_2, ~DX_2, ~CX_2, BX_2);  // AND_Gate
  and u_AX_2 (AX_2_out, AX, ~IR_2, ~DR_2, ~EX_2, ~DX_2, ~CX_2, ~BX_2, AX_2);  // AND_Gate

  // Notes on the sheet:
  //   Değerler
  //   Sinyaller
endmodule

module OR_1 (
  input  AX,
  input  BX,
  input  CX,
  input  DX,
  input  EX,
  input  DR,
  input  IR,
  input  AX_2,
  input  BX_2,
  input  CX_2,
  input  DX_2,
  input  EX_2,
  input  DR_2,
  input  IR_2,
  output OUTPUT
);

  wire AX_2_out, AX_out, BX_2_out, BX_out, CX_2_out, CX_out, DR_2_out, DR_out, DX_2_out, DX_out, EX_2_out,
       EX_out, IR_2_out, IR_out, or_1_out, or_2_out;

  and u_AX (AX_out, AX_2, AX);
  and u_CX (CX_out, CX, ~AX_2, ~BX_2, CX_2);  // AND_Gate
  and u_BX (BX_out, BX, ~AX_2, BX_2);  // AND_Gate
  and u_DX (DX_out, DX, ~AX_2, ~BX_2, ~CX_2, DX_2);  // AND_Gate
  or or_1 (or_1_out, AX_out, BX_out, CX_out, DX_out, EX_out, DR_out, IR_out);
  and u_EX (EX_out, EX, ~AX_2, ~BX_2, ~CX_2, ~DX_2, EX_2);  // AND_Gate
  and u_DR (DR_out, DR, ~AX_2, ~BX_2, ~CX_2, ~DX_2, ~EX_2, DR_2);  // AND_Gate
  and u_IR (IR_out, IR, ~AX_2, ~BX_2, ~CX_2, ~DX_2, ~EX_2, ~DR_2, IR_2);  // AND_Gate
  and u_IR_2 (IR_2_out, IR, IR_2);
  and u_DR_2 (DR_2_out, DR, ~IR_2, DR_2);  // AND_Gate
  and u_EX_2 (EX_2_out, EX, ~IR_2, ~DR_2, EX_2);  // AND_Gate
  and u_DX_2 (DX_2_out, DX, ~IR_2, ~DR_2, ~EX_2, DX_2);  // AND_Gate
  or or_2 (or_2_out, IR_2_out, DR_2_out, EX_2_out, DX_2_out, CX_2_out, BX_2_out, AX_2_out);
  and u_CX_2 (CX_2_out, CX, ~IR_2, ~DR_2, ~EX_2, ~DX_2, CX_2);  // AND_Gate
  or or_3 (OUTPUT, or_2_out, or_1_out);
  and u_BX_2 (BX_2_out, BX, ~IR_2, ~DR_2, ~EX_2, ~DX_2, ~CX_2, BX_2);  // AND_Gate
  and u_AX_2 (AX_2_out, AX, ~IR_2, ~DR_2, ~EX_2, ~DX_2, ~CX_2, ~BX_2, AX_2);  // AND_Gate

  // Notes on the sheet:
  //   Değerler
  //   Sinyaller
endmodule

module XOR_1 (
  input  AX,
  input  BX,
  input  CX,
  input  DX,
  input  EX,
  input  DR,
  input  IR,
  input  AX_2,
  input  BX_2,
  input  CX_2,
  input  DX_2,
  input  EX_2,
  input  DR_2,
  input  IR_2,
  output OUTPUT
);

  wire AX_2_out, AX_out, BX_2_out, BX_out, CX_2_out, CX_out, DR_2_out, DR_out, DX_2_out, DX_out, EX_2_out,
       EX_out, IR_2_out, IR_out, or_1_out, or_2_out;

  and u_AX (AX_out, AX_2, AX);
  and u_CX (CX_out, CX, ~AX_2, ~BX_2, CX_2);  // AND_Gate
  and u_BX (BX_out, BX, ~AX_2, BX_2);  // AND_Gate
  and u_DX (DX_out, DX, ~AX_2, ~BX_2, ~CX_2, DX_2);  // AND_Gate
  or or_1 (or_1_out, AX_out, BX_out, CX_out, DX_out, EX_out, DR_out, IR_out);
  and u_EX (EX_out, EX, ~AX_2, ~BX_2, ~CX_2, ~DX_2, EX_2);  // AND_Gate
  and u_DR (DR_out, DR, ~AX_2, ~BX_2, ~CX_2, ~DX_2, ~EX_2, DR_2);  // AND_Gate
  and u_IR (IR_out, IR, ~AX_2, ~BX_2, ~CX_2, ~DX_2, ~EX_2, ~DR_2, IR_2);  // AND_Gate
  and u_IR_2 (IR_2_out, IR, IR_2);
  and u_DR_2 (DR_2_out, DR, ~IR_2, DR_2);  // AND_Gate
  and u_EX_2 (EX_2_out, EX, ~IR_2, ~DR_2, EX_2);  // AND_Gate
  and u_DX_2 (DX_2_out, DX, ~IR_2, ~DR_2, ~EX_2, DX_2);  // AND_Gate
  or or_2 (or_2_out, IR_2_out, DR_2_out, EX_2_out, DX_2_out, CX_2_out, BX_2_out, AX_2_out);
  and u_CX_2 (CX_2_out, CX, ~IR_2, ~DR_2, ~EX_2, ~DX_2, CX_2);  // AND_Gate
  and u_BX_2 (BX_2_out, BX, ~IR_2, ~DR_2, ~EX_2, ~DX_2, ~CX_2, BX_2);  // AND_Gate
  xor xor_1 (OUTPUT, or_2_out, or_1_out);
  and u_AX_2 (AX_2_out, AX, ~IR_2, ~DR_2, ~EX_2, ~DX_2, ~CX_2, ~BX_2, AX_2);  // AND_Gate

  // Notes on the sheet:
  //   Değerler
  //   Sinyaller
endmodule

module AND_4 (
  input  [3:0] AX,
  input  [3:0] BX,
  input  [3:0] CX,
  input  [3:0] DX,
  input  [3:0] EX,
  input  [3:0] DR,
  input  [3:0] IR,
  input  AX_2,
  input  BX_2,
  input  CX_2,
  input  DX_2,
  input  EX_2,
  input  DR_2,
  input  IR_2,
  output [3:0] out_15
);

  wire [6:0] input_4to1_1_ir0, input_4to1_1_ir1, input_4to1_1_ir2, input_4to1_1_ir3;

  AND_1 and_1_1 (
    .AX_2(AX_2), .BX_2(BX_2), .CX_2(CX_2), .DX_2(DX_2), .EX_2(EX_2), .DR_2(DR_2), .IR_2(IR_2),
    .AX(input_4to1_1_ir3[6]), .BX(input_4to1_1_ir3[5]), .CX(input_4to1_1_ir3[4]), .DX(input_4to1_1_ir3[3]),
    .EX(input_4to1_1_ir3[2]), .DR(input_4to1_1_ir3[1]), .IR(input_4to1_1_ir3[0]), .OUTPUT(out_15[3]));
  INPUT_4to1 input_4to1_1 (
    .AX(AX), .BX(BX), .CX(CX), .DX(DX), .EX(EX), .DR(DR), .IR(IR), .AX3(input_4to1_1_ir3[6]),
    .BX3(input_4to1_1_ir3[5]), .CX3(input_4to1_1_ir3[4]), .DX3(input_4to1_1_ir3[3]),
    .EX3(input_4to1_1_ir3[2]), .DR3(input_4to1_1_ir3[1]), .IR3(input_4to1_1_ir3[0]),
    .AX2(input_4to1_1_ir2[6]), .BX2(input_4to1_1_ir2[5]), .CX2(input_4to1_1_ir2[4]),
    .DX2(input_4to1_1_ir2[3]), .EX2(input_4to1_1_ir2[2]), .DR2(input_4to1_1_ir2[1]),
    .IR2(input_4to1_1_ir2[0]), .AX1(input_4to1_1_ir1[6]), .BX1(input_4to1_1_ir1[5]),
    .CX1(input_4to1_1_ir1[4]), .DX1(input_4to1_1_ir1[3]), .EX1(input_4to1_1_ir1[2]),
    .DR1(input_4to1_1_ir1[1]), .IR1(input_4to1_1_ir1[0]), .AX0(input_4to1_1_ir0[6]),
    .BX0(input_4to1_1_ir0[5]), .CX0(input_4to1_1_ir0[4]), .DX0(input_4to1_1_ir0[3]),
    .EX0(input_4to1_1_ir0[2]), .DR0(input_4to1_1_ir0[1]), .IR0(input_4to1_1_ir0[0]));
  AND_1 and_1_2 (
    .AX_2(AX_2), .BX_2(BX_2), .CX_2(CX_2), .DX_2(DX_2), .EX_2(EX_2), .DR_2(DR_2), .IR_2(IR_2),
    .AX(input_4to1_1_ir2[6]), .BX(input_4to1_1_ir2[5]), .CX(input_4to1_1_ir2[4]), .DX(input_4to1_1_ir2[3]),
    .EX(input_4to1_1_ir2[2]), .DR(input_4to1_1_ir2[1]), .IR(input_4to1_1_ir2[0]), .OUTPUT(out_15[2]));
  AND_1 and_1_3 (
    .AX_2(AX_2), .BX_2(BX_2), .CX_2(CX_2), .DX_2(DX_2), .EX_2(EX_2), .DR_2(DR_2), .IR_2(IR_2),
    .AX(input_4to1_1_ir1[6]), .BX(input_4to1_1_ir1[5]), .CX(input_4to1_1_ir1[4]), .DX(input_4to1_1_ir1[3]),
    .EX(input_4to1_1_ir1[2]), .DR(input_4to1_1_ir1[1]), .IR(input_4to1_1_ir1[0]), .OUTPUT(out_15[1]));
  AND_1 and_1_4 (
    .AX_2(AX_2), .BX_2(BX_2), .CX_2(CX_2), .DX_2(DX_2), .EX_2(EX_2), .DR_2(DR_2), .IR_2(IR_2),
    .AX(input_4to1_1_ir0[6]), .BX(input_4to1_1_ir0[5]), .CX(input_4to1_1_ir0[4]), .DX(input_4to1_1_ir0[3]),
    .EX(input_4to1_1_ir0[2]), .DR(input_4to1_1_ir0[1]), .IR(input_4to1_1_ir0[0]), .OUTPUT(out_15[0]));
endmodule

// INPUT_ADJUSTER
module INPUT_4to1 (
  input  [3:0] AX,
  input  [3:0] BX,
  input  [3:0] CX,
  input  [3:0] DX,
  input  [3:0] EX,
  input  [3:0] DR,
  input  [3:0] IR,
  output AX3,
  output BX3,
  output CX3,
  output DX3,
  output EX3,
  output DR3,
  output IR3,
  output AX2,
  output BX2,
  output CX2,
  output DX2,
  output EX2,
  output DR2,
  output IR2,
  output AX1,
  output BX1,
  output CX1,
  output DX1,
  output EX1,
  output DR1,
  output IR1,
  output AX0,
  output BX0,
  output CX0,
  output DX0,
  output EX0,
  output DR0,
  output IR0
);


  assign AX0 = AX[0];
  assign AX1 = AX[1];
  assign AX2 = AX[2];
  assign AX3 = AX[3];
  assign BX0 = BX[0];
  assign BX1 = BX[1];
  assign BX2 = BX[2];
  assign BX3 = BX[3];
  assign CX0 = CX[0];
  assign CX1 = CX[1];
  assign CX2 = CX[2];
  assign CX3 = CX[3];
  assign DR0 = DR[0];
  assign DR1 = DR[1];
  assign DR2 = DR[2];
  assign DR3 = DR[3];
  assign DX0 = DX[0];
  assign DX1 = DX[1];
  assign DX2 = DX[2];
  assign DX3 = DX[3];
  assign EX0 = EX[0];
  assign EX1 = EX[1];
  assign EX2 = EX[2];
  assign EX3 = EX[3];
  assign IR0 = IR[0];
  assign IR1 = IR[1];
  assign IR2 = IR[2];
  assign IR3 = IR[3];
endmodule

module OR_4 (
  input  [3:0] AX,
  input  [3:0] BX,
  input  [3:0] CX,
  input  [3:0] DX,
  input  [3:0] EX,
  input  [3:0] DR,
  input  [3:0] IR,
  input  AX_2,
  input  BX_2,
  input  CX_2,
  input  DX_2,
  input  EX_2,
  input  DR_2,
  input  IR_2,
  output [3:0] out_15
);

  wire [6:0] input_4to1_1_ir0, input_4to1_1_ir1, input_4to1_1_ir2, input_4to1_1_ir3;

  OR_1 or_1_1 (
    .AX_2(AX_2), .BX_2(BX_2), .CX_2(CX_2), .DX_2(DX_2), .EX_2(EX_2), .DR_2(DR_2), .IR_2(IR_2),
    .AX(input_4to1_1_ir3[6]), .BX(input_4to1_1_ir3[5]), .CX(input_4to1_1_ir3[4]), .DX(input_4to1_1_ir3[3]),
    .EX(input_4to1_1_ir3[2]), .DR(input_4to1_1_ir3[1]), .IR(input_4to1_1_ir3[0]), .OUTPUT(out_15[3]));
  INPUT_4to1 input_4to1_1 (
    .AX(AX), .BX(BX), .CX(CX), .DX(DX), .EX(EX), .DR(DR), .IR(IR), .AX3(input_4to1_1_ir3[6]),
    .BX3(input_4to1_1_ir3[5]), .CX3(input_4to1_1_ir3[4]), .DX3(input_4to1_1_ir3[3]),
    .EX3(input_4to1_1_ir3[2]), .DR3(input_4to1_1_ir3[1]), .IR3(input_4to1_1_ir3[0]),
    .AX2(input_4to1_1_ir2[6]), .BX2(input_4to1_1_ir2[5]), .CX2(input_4to1_1_ir2[4]),
    .DX2(input_4to1_1_ir2[3]), .EX2(input_4to1_1_ir2[2]), .DR2(input_4to1_1_ir2[1]),
    .IR2(input_4to1_1_ir2[0]), .AX1(input_4to1_1_ir1[6]), .BX1(input_4to1_1_ir1[5]),
    .CX1(input_4to1_1_ir1[4]), .DX1(input_4to1_1_ir1[3]), .EX1(input_4to1_1_ir1[2]),
    .DR1(input_4to1_1_ir1[1]), .IR1(input_4to1_1_ir1[0]), .AX0(input_4to1_1_ir0[6]),
    .BX0(input_4to1_1_ir0[5]), .CX0(input_4to1_1_ir0[4]), .DX0(input_4to1_1_ir0[3]),
    .EX0(input_4to1_1_ir0[2]), .DR0(input_4to1_1_ir0[1]), .IR0(input_4to1_1_ir0[0]));
  OR_1 or_1_2 (
    .AX_2(AX_2), .BX_2(BX_2), .CX_2(CX_2), .DX_2(DX_2), .EX_2(EX_2), .DR_2(DR_2), .IR_2(IR_2),
    .AX(input_4to1_1_ir2[6]), .BX(input_4to1_1_ir2[5]), .CX(input_4to1_1_ir2[4]), .DX(input_4to1_1_ir2[3]),
    .EX(input_4to1_1_ir2[2]), .DR(input_4to1_1_ir2[1]), .IR(input_4to1_1_ir2[0]), .OUTPUT(out_15[2]));
  OR_1 or_1_3 (
    .AX_2(AX_2), .BX_2(BX_2), .CX_2(CX_2), .DX_2(DX_2), .EX_2(EX_2), .DR_2(DR_2), .IR_2(IR_2),
    .AX(input_4to1_1_ir1[6]), .BX(input_4to1_1_ir1[5]), .CX(input_4to1_1_ir1[4]), .DX(input_4to1_1_ir1[3]),
    .EX(input_4to1_1_ir1[2]), .DR(input_4to1_1_ir1[1]), .IR(input_4to1_1_ir1[0]), .OUTPUT(out_15[1]));
  OR_1 or_1_4 (
    .AX_2(AX_2), .BX_2(BX_2), .CX_2(CX_2), .DX_2(DX_2), .EX_2(EX_2), .DR_2(DR_2), .IR_2(IR_2),
    .AX(input_4to1_1_ir0[6]), .BX(input_4to1_1_ir0[5]), .CX(input_4to1_1_ir0[4]), .DX(input_4to1_1_ir0[3]),
    .EX(input_4to1_1_ir0[2]), .DR(input_4to1_1_ir0[1]), .IR(input_4to1_1_ir0[0]), .OUTPUT(out_15[0]));
endmodule

module XOR_4 (
  input  [3:0] AX,
  input  [3:0] BX,
  input  [3:0] CX,
  input  [3:0] DX,
  input  [3:0] EX,
  input  [3:0] DR,
  input  [3:0] IR,
  input  AX_2,
  input  BX_2,
  input  CX_2,
  input  DX_2,
  input  EX_2,
  input  DR_2,
  input  IR_2,
  output [3:0] out_15
);

  wire [6:0] input_4to1_1_ir0, input_4to1_1_ir1, input_4to1_1_ir2, input_4to1_1_ir3;

  XOR_1 xor_1_1 (
    .AX_2(AX_2), .BX_2(BX_2), .CX_2(CX_2), .DX_2(DX_2), .EX_2(EX_2), .DR_2(DR_2), .IR_2(IR_2),
    .AX(input_4to1_1_ir3[6]), .BX(input_4to1_1_ir3[5]), .CX(input_4to1_1_ir3[4]), .DX(input_4to1_1_ir3[3]),
    .EX(input_4to1_1_ir3[2]), .DR(input_4to1_1_ir3[1]), .IR(input_4to1_1_ir3[0]), .OUTPUT(out_15[3]));
  INPUT_4to1 input_4to1_1 (
    .AX(AX), .BX(BX), .CX(CX), .DX(DX), .EX(EX), .DR(DR), .IR(IR), .AX3(input_4to1_1_ir3[6]),
    .BX3(input_4to1_1_ir3[5]), .CX3(input_4to1_1_ir3[4]), .DX3(input_4to1_1_ir3[3]),
    .EX3(input_4to1_1_ir3[2]), .DR3(input_4to1_1_ir3[1]), .IR3(input_4to1_1_ir3[0]),
    .AX2(input_4to1_1_ir2[6]), .BX2(input_4to1_1_ir2[5]), .CX2(input_4to1_1_ir2[4]),
    .DX2(input_4to1_1_ir2[3]), .EX2(input_4to1_1_ir2[2]), .DR2(input_4to1_1_ir2[1]),
    .IR2(input_4to1_1_ir2[0]), .AX1(input_4to1_1_ir1[6]), .BX1(input_4to1_1_ir1[5]),
    .CX1(input_4to1_1_ir1[4]), .DX1(input_4to1_1_ir1[3]), .EX1(input_4to1_1_ir1[2]),
    .DR1(input_4to1_1_ir1[1]), .IR1(input_4to1_1_ir1[0]), .AX0(input_4to1_1_ir0[6]),
    .BX0(input_4to1_1_ir0[5]), .CX0(input_4to1_1_ir0[4]), .DX0(input_4to1_1_ir0[3]),
    .EX0(input_4to1_1_ir0[2]), .DR0(input_4to1_1_ir0[1]), .IR0(input_4to1_1_ir0[0]));
  XOR_1 xor_1_2 (
    .AX_2(AX_2), .BX_2(BX_2), .CX_2(CX_2), .DX_2(DX_2), .EX_2(EX_2), .DR_2(DR_2), .IR_2(IR_2),
    .AX(input_4to1_1_ir2[6]), .BX(input_4to1_1_ir2[5]), .CX(input_4to1_1_ir2[4]), .DX(input_4to1_1_ir2[3]),
    .EX(input_4to1_1_ir2[2]), .DR(input_4to1_1_ir2[1]), .IR(input_4to1_1_ir2[0]), .OUTPUT(out_15[2]));
  XOR_1 xor_1_3 (
    .AX_2(AX_2), .BX_2(BX_2), .CX_2(CX_2), .DX_2(DX_2), .EX_2(EX_2), .DR_2(DR_2), .IR_2(IR_2),
    .AX(input_4to1_1_ir1[6]), .BX(input_4to1_1_ir1[5]), .CX(input_4to1_1_ir1[4]), .DX(input_4to1_1_ir1[3]),
    .EX(input_4to1_1_ir1[2]), .DR(input_4to1_1_ir1[1]), .IR(input_4to1_1_ir1[0]), .OUTPUT(out_15[1]));
  XOR_1 xor_1_4 (
    .AX_2(AX_2), .BX_2(BX_2), .CX_2(CX_2), .DX_2(DX_2), .EX_2(EX_2), .DR_2(DR_2), .IR_2(IR_2),
    .AX(input_4to1_1_ir0[6]), .BX(input_4to1_1_ir0[5]), .CX(input_4to1_1_ir0[4]), .DX(input_4to1_1_ir0[3]),
    .EX(input_4to1_1_ir0[2]), .DR(input_4to1_1_ir0[1]), .IR(input_4to1_1_ir0[0]), .OUTPUT(out_15[0]));
endmodule

// INPUT_ADJUSTER
module INPUT_16to4 (
  input  [15:0] AX,
  input  [15:0] BX,
  input  [15:0] CX,
  input  [15:0] DX,
  input  [15:0] EX,
  input  [15:0] DR,
  input  [15:0] IR,
  output [3:0] AX_15_12,
  output [3:0] BX_15_12,
  output [3:0] CX_15_12,
  output [3:0] DX_15_12,
  output [3:0] EX_15_12,
  output [3:0] DR_15_12,
  output [3:0] IR_15_12,
  output [3:0] AX_8_11,
  output [3:0] BX_8_11,
  output [3:0] CX_8_11,
  output [3:0] DX_8_11,
  output [3:0] EX_8_11,
  output [3:0] DR_2,
  output [3:0] IR_8_11,
  output [3:0] AX_4_7,
  output [3:0] BX_4_7,
  output [3:0] CX_4_7,
  output [3:0] DX_4_7,
  output [3:0] EX_4_7,
  output [3:0] DR_4_7,
  output [3:0] IR_4_7,
  output [3:0] AX_0_3,
  output [3:0] BX_0_3,
  output [3:0] CX_0_3,
  output [3:0] DX_0_3,
  output [3:0] EX_0_3,
  output [3:0] DR_0_3,
  output [3:0] IR_0_3
);


  assign AX_0_3 = AX[3:0];
  assign AX_4_7 = AX[7:4];
  assign AX_8_11 = AX[11:8];
  assign AX_15_12 = AX[15:12];
  assign BX_0_3 = BX[3:0];
  assign BX_4_7 = BX[7:4];
  assign BX_8_11 = BX[11:8];
  assign BX_15_12 = BX[15:12];
  assign CX_0_3 = CX[3:0];
  assign CX_4_7 = CX[7:4];
  assign CX_8_11 = CX[11:8];
  assign CX_15_12 = CX[15:12];
  assign DR_0_3 = DR[3:0];
  assign DR_2 = DR[11:8];
  assign DR_4_7 = DR[7:4];
  assign DR_15_12 = DR[15:12];
  assign DX_0_3 = DX[3:0];
  assign DX_4_7 = DX[7:4];
  assign DX_8_11 = DX[11:8];
  assign DX_15_12 = DX[15:12];
  assign EX_0_3 = EX[3:0];
  assign EX_4_7 = EX[7:4];
  assign EX_8_11 = EX[11:8];
  assign EX_15_12 = EX[15:12];
  assign IR_0_3 = IR[3:0];
  assign IR_4_7 = IR[7:4];
  assign IR_8_11 = IR[11:8];
  assign IR_15_12 = IR[15:12];
endmodule
