// Logisim project CONTROL UNIT.circ as structural Verilog
module PC (
  input  T0,
  input  T1,
  input  T3,
  input  T4,
  input  M201,
  input  M202,
  input  M203,
  input  M204,
  input  M205,
  input  M206,
  input  M207,
  input  M208,
  input  M209,
  input  M210,
  input  M211,
  input  M212,
  input  M213,
  input  M214,
  input  M215,
  input  M216,
  input  M217,
  input  M218,
  output PC_BUS,
  output PC_INC,
  output PC_LOAD
);

  wire and_1_out, and_2_out, and_3_out, and_4_out, and_5_out, and_6_out, and_7_out, and_8_out, and_9_out,
       and_10_out, and_11_out, and_12_out, and_13_out, and_14_out, and_15_out, and_16_out, and_17_out,
       and_18_out;

  and and_1 (and_1_out, M201, T4);
  and and_2 (and_2_out, M202, T3);
  and and_3 (and_3_out, M203, T3);
  and and_4 (and_4_out, M204, T4);
  and and_5 (and_5_out, M205, T3);
  and and_6 (and_6_out, M206, T3);
  and and_7 (and_7_out, M207, T4);
  and and_8 (and_8_out, M208, T3);
  and and_9 (and_9_out, M209, T3);
  and and_10 (and_10_out, M210, T4);
  and and_11 (and_11_out, M211, T3);
  and and_12 (and_12_out, M212, T3);
  and and_13 (and_13_out, M213, T4);
  and and_14 (and_14_out, M214, T3);
  and and_15 (and_15_out, M215, T3);
  and and_16 (and_16_out, M216, T4);
  and and_17 (and_17_out, M217, T3);
  and and_18 (and_18_out, M218, T3);
  or or_1 (PC_LOAD, and_1_out, and_2_out, and_3_out, and_4_out, and_5_out, and_6_out, and_7_out, and_8_out, and_9_out, and_10_out, and_11_out, and_12_out, and_13_out, and_14_out, and_15_out, and_16_out, and_17_out, and_18_out);

  assign PC_BUS = T0;
  assign PC_INC = T1;
endmodule

module IR (
  input  T1,
  input  T2,
  output IR_BUS,
  output IR_LOAD
);


  assign IR_BUS = T2;
  assign IR_LOAD = T1;
endmodule

module AR (
  input  C,
  input  Z,
  input  T0,
  input  T2,
  input  T3,
  input  T4,
  input  M0,
  input  M1,
  input  M2,
  input  M3,
  input  M4,
  input  M17,
  input  M18,
  input  M19,
  input  M20,
  input  M21,
  input  M34,
  input  M35,
  input  M36,
  input  M37,
  input  M38,
  input  M51,
  input  M52,
  input  M53,
  input  M54,
  input  M55,
  input  M68,
  input  M69,
  input  M70,
  input  M71,
  input  M72,
  input  M85,
  input  M86,
  input  M87,
  input  M88,
  input  M89,
  input  M102,
  input  M103,
  input  M104,
  input  M105,
  input  M106,
  input  M119,
  input  M120,
  input  M121,
  input  M122,
  input  M123,
  input  M136,
  input  M137,
  input  M138,
  input  M139,
  input  M140,
  input  M153,
  input  M154,
  input  M155,
  input  M156,
  input  M157,
  input  M170,
  input  M171,
  input  M172,
  input  M173,
  input  M174,
  input  M180,
  input  M181,
  input  M182,
  input  M183,
  input  M184,
  input  M201,
  input  M202,
  input  M204,
  input  M205,
  input  M207,
  input  M208,
  input  M210,
  input  M211,
  input  M213,
  input  M214,
  input  M216,
  input  M217,
  output AR_BUS,
  output AR_LOAD
);

  wire and_1_out, and_2_out, and_3_out, and_4_out, and_5_out, and_6_out, and_7_out, and_8_out, and_9_out,
       and_10_out, and_11_out, and_12_out, not_1_out, not_2_out, not_3_out, not_4_out, not_5_out, not_6_out,
       or_1_out, or_2_out, or_3_out, or_4_out;

  not not_1 (not_1_out, Z);
  not not_2 (not_2_out, Z);
  not not_3 (not_3_out, Z);
  not not_4 (not_4_out, Z);
  not not_5 (not_5_out, C);
  not not_6 (not_6_out, C);
  and and_1 (and_1_out, M201, T4);
  and and_2 (and_2_out, M202, T3);
  and and_3 (and_3_out, M204, T4, Z);
  and and_4 (and_4_out, M205, T3, Z);
  and and_5 (and_5_out, M207, T4, not_1_out);
  and and_6 (and_6_out, M208, T3, not_2_out);
  and and_7 (and_7_out, M210, T4, not_3_out, C);
  and and_8 (and_8_out, M211, T3, not_4_out, C);
  and and_9 (and_9_out, M213, T4, Z, not_5_out);
  and and_10 (and_10_out, M214, T3, Z, not_6_out);
  and and_11 (and_11_out, M216, T4, Z, C);
  and and_12 (and_12_out, M217, T3, Z, C);
  or or_1 (or_1_out, M216, M213, M210, M207, M204, M201, M184, M183, M182, M181, M180, M174, M173, M172, M171, M170, M157, M156, M155, M154, M153, M140);
  or or_2 (or_2_out, M139, M138, M137, M136, M123, M122, M121, M120, M119, M106, M105, M104, M103, M102, M89, M88, M87, M86, M85, M72, M71, M70);
  or or_3 (or_3_out, M69, M68, M55, M54, M53, M52, M51, M38, M37, M36, M35, M34, M21, M20, M19, M18, M17, M4, M3, M2, M1, M0);
  or or_4 (or_4_out, or_1_out, or_2_out, or_3_out);
  or or_5 (AR_BUS, and_1_out, and_2_out, and_3_out, and_4_out, and_5_out, and_6_out, and_7_out, and_8_out, and_9_out, and_10_out, and_11_out, and_12_out);
  and and_13 (AR_LOAD, or_4_out, T3);
endmodule

module DR (
  input  T3,
  input  T4,
  input  T5,
  input  M0,
  input  M1,
  input  M2,
  input  M3,
  input  M4,
  input  M5,
  input  M6,
  input  M7,
  input  M8,
  input  M9,
  input  M15,
  input  M17,
  input  M18,
  input  M19,
  input  M20,
  input  M21,
  input  M22,
  input  M23,
  input  M24,
  input  M25,
  input  M26,
  input  M32,
  input  M34,
  input  M35,
  input  M36,
  input  M37,
  input  M38,
  input  M39,
  input  M40,
  input  M41,
  input  M42,
  input  M43,
  input  M49,
  input  M51,
  input  M52,
  input  M53,
  input  M54,
  input  M55,
  input  M56,
  input  M57,
  input  M58,
  input  M59,
  input  M60,
  input  M66,
  input  M68,
  input  M69,
  input  M70,
  input  M71,
  input  M72,
  input  M73,
  input  M74,
  input  M75,
  input  M76,
  input  M77,
  input  M83,
  input  M85,
  input  M86,
  input  M87,
  input  M88,
  input  M89,
  input  M90,
  input  M91,
  input  M92,
  input  M93,
  input  M94,
  input  M100,
  input  M102,
  input  M103,
  input  M104,
  input  M105,
  input  M106,
  input  M107,
  input  M108,
  input  M109,
  input  M110,
  input  M111,
  input  M117,
  input  M119,
  input  M120,
  input  M121,
  input  M122,
  input  M123,
  input  M124,
  input  M125,
  input  M126,
  input  M127,
  input  M128,
  input  M134,
  input  M136,
  input  M137,
  input  M138,
  input  M139,
  input  M140,
  input  M141,
  input  M142,
  input  M143,
  input  M144,
  input  M145,
  input  M151,
  input  M153,
  input  M154,
  input  M155,
  input  M156,
  input  M157,
  input  M158,
  input  M159,
  input  M160,
  input  M161,
  input  M162,
  input  M168,
  input  M170,
  input  M171,
  input  M172,
  input  M173,
  input  M174,
  input  M175,
  input  M176,
  input  M177,
  input  M178,
  input  M179,
  output DR_BUS,
  output DR_LOAD
);

  wire and_1_out, and_2_out, and_3_out, and_4_out, or_1_out, or_2_out, or_3_out, or_4_out, or_5_out,
       or_6_out, or_7_out, or_8_out, or_9_out, or_11_out, or_12_out;

  or or_1 (or_1_out, M179, M178, M177, M176, M175);
  or or_2 (or_2_out, M174, M173, M172, M171, M170);
  or or_3 (or_3_out, M174, M173, M172, M171, M170, M157, M156, M155, M154, M153, M140, M139, M138, M137, M136);
  or or_4 (or_4_out, M123, M122, M121, M120, M119, M106, M105, M104, M103, M102, M89, M88, M87, M86, M85, M72, M71, M70, M69, M68);
  or or_5 (or_5_out, M55, M54, M53, M52, M51, M38, M37, M36, M35, M34, M21, M20, M19, M18, M17, M4, M3, M2, M1, M0);
  or or_6 (or_6_out, M179, M178, M177, M176, M175, M168, M162, M161, M160, M159, M158, M151, M145, M144, M143, M142, M141, M134, M128, M127);
  or or_7 (or_7_out, M126, M125, M124, M117, M111, M110, M109, M108, M107, M100, M94, M93, M92, M91, M90, M83, M77, M76, M75, M74);
  or or_8 (or_8_out, M73, M66, M60, M59, M58, M57, M56, M49, M43, M42, M41, M40, M39, M32, M26, M25, M24, M23, M22, M15);
  or or_9 (or_9_out, M9, M8, M7, M6, M5);
  and and_1 (and_1_out, or_1_out, T4);
  or or_10 (DR_BUS, and_1_out, and_2_out);
  and and_2 (and_2_out, T5, or_2_out);
  or or_11 (or_11_out, or_3_out, or_4_out, or_5_out);
  or or_12 (or_12_out, or_6_out, or_7_out, or_8_out, or_9_out);
  and and_3 (and_3_out, or_11_out, T4);
  and and_4 (and_4_out, or_12_out, T3);
  or or_13 (DR_LOAD, and_3_out, and_4_out);
endmodule

module AX (
  input  C,
  input  Z,
  input  T3,
  input  T4,
  input  T5,
  input  E0,
  input  E1,
  input  E2,
  input  E3,
  input  E4,
  input  M0,
  input  M5,
  input  M10,
  input  M15,
  input  M16,
  input  M17,
  input  M22,
  input  M27,
  input  M32,
  input  M33,
  input  M34,
  input  M39,
  input  M44,
  input  M49,
  input  M50,
  input  M51,
  input  M56,
  input  M61,
  input  M66,
  input  M67,
  input  M68,
  input  M73,
  input  M78,
  input  M83,
  input  M84,
  input  M85,
  input  M90,
  input  M95,
  input  M100,
  input  M101,
  input  M102,
  input  M107,
  input  M112,
  input  M117,
  input  M118,
  input  M119,
  input  M124,
  input  M129,
  input  M134,
  input  M135,
  input  M136,
  input  M141,
  input  M146,
  input  M151,
  input  M152,
  input  M170,
  input  M175,
  input  M180,
  input  M185,
  input  M190,
  input  M203,
  input  M206,
  input  M209,
  input  M212,
  input  M215,
  input  M218,
  input  M219,
  input  M220,
  input  M221,
  input  M222,
  input  M223,
  input  M224,
  input  M225,
  input  M226,
  output INC,
  output DEC,
  output SHL,
  output SHR,
  output CIL,
  output CIR,
  output CML,
  output CLR,
  output BUS,
  output LOAD
);

  wire and_9_out, and_10_out, and_11_out, and_12_out, and_13_out, and_14_out, and_15_out, and_16_out,
       and_17_out, and_18_out, and_19_out, and_20_out, and_21_out, and_22_out, and_23_out, not_1_out,
       not_2_out, not_3_out, or_1_out, or_2_out, or_3_out, or_4_out, or_5_out, or_6_out;

  not not_1 (not_1_out, Z);
  not not_2 (not_2_out, Z);
  not not_3 (not_3_out, C);
  and and_1 (INC, M225, E0, T3);
  and and_2 (DEC, M226, E0, T3);
  and and_3 (SHL, M221, E0, T3);
  and and_4 (SHR, M222, E0, T3);
  and and_5 (CIL, M223, E0, T3);
  and and_6 (CIR, M224, E0, T3);
  and and_7 (CML, M220, E0, T3);
  and and_8 (CLR, M219, E0, T3);
  and and_9 (and_9_out, M180, T4);
  and and_10 (and_10_out, M185, T3);
  and and_11 (and_11_out, M203, E0, T3);
  and and_12 (and_12_out, M206, E0, T3, Z);
  and and_13 (and_13_out, M209, E0, T3, not_1_out);
  and and_14 (and_14_out, M212, E0, T3, not_2_out, C);
  and and_15 (and_15_out, M215, E0, T3, Z, not_3_out);
  and and_16 (and_16_out, M218, E0, T3, Z, C);
  or or_1 (or_1_out, E0, E1, E2, E3, E4);
  or or_2 (or_2_out, M152, M135, M118, M101, M84, M67, M50, M33, M16);
  or or_3 (or_3_out, M151, M134, M117, M100, M83, M66, M49, M32, M15);
  or or_4 (or_4_out, M175, M141, M124, M107, M90, M73, M56, M39, M22, M5);
  or or_5 (or_5_out, M190, M146, M129, M112, M95, M78, M61, M44, M27, M10);
  or or_6 (or_6_out, M170, M136, M119, M102, M85, M68, M51, M34, M17, M0);
  or or_7 (BUS, and_9_out, and_10_out, and_11_out, and_12_out, and_13_out, and_14_out, and_15_out, and_16_out);
  and and_17 (and_17_out, or_1_out, or_2_out);
  and and_18 (and_18_out, and_17_out, T3);
  and and_19 (and_19_out, or_1_out, or_3_out);
  and and_20 (and_20_out, and_19_out, T4);
  and and_21 (and_21_out, or_4_out, T4);
  and and_22 (and_22_out, or_5_out, T3);
  and and_23 (and_23_out, or_6_out, T5);
  or or_8 (LOAD, and_18_out, and_20_out, and_21_out, and_22_out, and_23_out);
endmodule

module BX (
  input  C,
  input  Z,
  input  T3,
  input  T4,
  input  T5,
  input  E1,
  input  E5,
  input  E6,
  input  E7,
  input  E8,
  input  E9,
  input  M1,
  input  M6,
  input  M11,
  input  M15,
  input  M16,
  input  M18,
  input  M23,
  input  M28,
  input  M32,
  input  M33,
  input  M35,
  input  M40,
  input  M45,
  input  M49,
  input  M50,
  input  M52,
  input  M57,
  input  M62,
  input  M66,
  input  M67,
  input  M69,
  input  M74,
  input  M79,
  input  M83,
  input  M84,
  input  M86,
  input  M91,
  input  M96,
  input  M100,
  input  M101,
  input  M103,
  input  M108,
  input  M113,
  input  M117,
  input  M118,
  input  M120,
  input  M125,
  input  M130,
  input  M134,
  input  M135,
  input  M137,
  input  M142,
  input  M147,
  input  M151,
  input  M152,
  input  M171,
  input  M176,
  input  M181,
  input  M186,
  input  M191,
  input  M203,
  input  M206,
  input  M209,
  input  M212,
  input  M215,
  input  M218,
  input  M219,
  input  M220,
  input  M221,
  input  M222,
  input  M223,
  input  M224,
  input  M225,
  input  M226,
  output INC,
  output DEC,
  output SHL,
  output SHR,
  output CIL,
  output CIR,
  output CML,
  output CLR,
  output BUS,
  output LOAD
);

  wire and_9_out, and_10_out, and_11_out, and_12_out, and_13_out, and_14_out, and_15_out, and_16_out,
       and_17_out, and_18_out, and_19_out, and_20_out, and_21_out, and_22_out, and_23_out, not_1_out,
       not_2_out, not_3_out, or_1_out, or_2_out, or_3_out, or_4_out, or_5_out, or_6_out;

  not not_1 (not_1_out, Z);
  not not_2 (not_2_out, Z);
  not not_3 (not_3_out, C);
  and and_1 (INC, M225, E1, T3);
  and and_2 (DEC, M226, E1, T3);
  and and_3 (SHL, M221, E1, T3);
  and and_4 (SHR, M222, E1, T3);
  and and_5 (CIL, M223, E1, T3);
  and and_6 (CIR, M224, E1, T3);
  and and_7 (CML, M220, E1, T3);
  and and_8 (CLR, M219, E1, T3);
  and and_9 (and_9_out, M181, T4);
  and and_10 (and_10_out, M186, T3);
  and and_11 (and_11_out, M203, E1, T3);
  and and_12 (and_12_out, M206, E1, T3, Z);
  and and_13 (and_13_out, M209, E1, T3, not_1_out);
  and and_14 (and_14_out, M212, E1, T3, not_2_out, C);
  and and_15 (and_15_out, M215, E1, T3, Z, not_3_out);
  and and_16 (and_16_out, M218, E1, T3, Z, C);
  or or_1 (or_1_out, E5, E6, E7, E8, E9);
  or or_2 (or_2_out, M152, M135, M118, M101, M84, M67, M50, M33, M16);
  or or_3 (or_3_out, M151, M134, M117, M100, M83, M66, M49, M32, M15);
  or or_4 (or_4_out, M176, M142, M125, M108, M91, M74, M57, M40, M23, M6);
  or or_5 (or_5_out, M191, M147, M130, M113, M96, M79, M62, M45, M28, M11);
  or or_6 (or_6_out, M171, M137, M120, M103, M86, M69, M52, M35, M18, M1);
  or or_7 (BUS, and_9_out, and_10_out, and_11_out, and_12_out, and_13_out, and_14_out, and_15_out, and_16_out);
  and and_17 (and_17_out, or_1_out, or_2_out);
  and and_18 (and_18_out, and_17_out, T3);
  and and_19 (and_19_out, or_1_out, or_3_out);
  and and_20 (and_20_out, and_19_out, T4);
  and and_21 (and_21_out, or_4_out, T4);
  and and_22 (and_22_out, or_5_out, T3);
  and and_23 (and_23_out, or_6_out, T5);
  or or_8 (LOAD, and_18_out, and_20_out, and_21_out, and_22_out, and_23_out);
endmodule

module CX (
  input  C,
  input  Z,
  input  T3,
  input  T4,
  input  T5,
  input  E2,
  input  E10,
  input  E11,
  input  E12,
  input  E13,
  input  E14,
  input  M2,
  input  M7,
  input  M12,
  input  M15,
  input  M16,
  input  M19,
  input  M24,
  input  M29,
  input  M32,
  input  M33,
  input  M36,
  input  M41,
  input  M46,
  input  M49,
  input  M50,
  input  M53,
  input  M58,
  input  M63,
  input  M66,
  input  M67,
  input  M70,
  input  M75,
  input  M80,
  input  M83,
  input  M84,
  input  M87,
  input  M92,
  input  M97,
  input  M100,
  input  M101,
  input  M104,
  input  M109,
  input  M114,
  input  M117,
  input  M118,
  input  M121,
  input  M126,
  input  M131,
  input  M134,
  input  M135,
  input  M138,
  input  M143,
  input  M148,
  input  M151,
  input  M152,
  input  M172,
  input  M177,
  input  M182,
  input  M187,
  input  M192,
  input  M203,
  input  M206,
  input  M209,
  input  M212,
  input  M215,
  input  M218,
  input  M219,
  input  M220,
  input  M221,
  input  M222,
  input  M223,
  input  M224,
  input  M225,
  input  M226,
  output INC,
  output DEC,
  output SHL,
  output SHR,
  output CIL,
  output CIR,
  output CML,
  output CLR,
  output BUS,
  output LOAD
);

  wire and_9_out, and_10_out, and_11_out, and_12_out, and_13_out, and_14_out, and_15_out, and_16_out,
       and_17_out, and_18_out, and_19_out, and_20_out, and_21_out, and_22_out, and_23_out, not_1_out,
       not_2_out, not_3_out, or_1_out, or_2_out, or_3_out, or_4_out, or_5_out, or_6_out;

  not not_1 (not_1_out, Z);
  not not_2 (not_2_out, Z);
  not not_3 (not_3_out, C);
  and and_1 (INC, M225, E2, T3);
  and and_2 (DEC, M226, E2, T3);
  and and_3 (SHL, M221, E2, T3);
  and and_4 (SHR, M222, E2, T3);
  and and_5 (CIL, M223, E2, T3);
  and and_6 (CIR, M224, E2, T3);
  and and_7 (CML, M220, E2, T3);
  and and_8 (CLR, M219, E2, T3);
  and and_9 (and_9_out, M182, T4);
  and and_10 (and_10_out, M187, T3);
  and and_11 (and_11_out, M203, E2, T3);
  and and_12 (and_12_out, M206, E2, T3, Z);
  and and_13 (and_13_out, M209, E2, T3, not_1_out);
  and and_14 (and_14_out, M212, E2, T3, not_2_out, C);
  and and_15 (and_15_out, M215, E2, T3, Z, not_3_out);
  and and_16 (and_16_out, M218, E2, T3, Z, C);
  or or_1 (or_1_out, E10, E11, E12, E13, E14);
  or or_2 (or_2_out, M152, M135, M118, M101, M84, M67, M50, M33, M16);
  or or_3 (or_3_out, M151, M134, M117, M100, M83, M66, M49, M32, M15);
  or or_4 (or_4_out, M177, M143, M126, M109, M92, M75, M58, M41, M24, M7);
  or or_5 (or_5_out, M192, M148, M131, M114, M97, M80, M63, M46, M29, M12);
  or or_6 (or_6_out, M172, M138, M121, M104, M87, M70, M53, M36, M19, M2);
  or or_7 (BUS, and_9_out, and_10_out, and_11_out, and_12_out, and_13_out, and_14_out, and_15_out, and_16_out);
  and and_17 (and_17_out, or_1_out, or_2_out);
  and and_18 (and_18_out, and_17_out, T3);
  and and_19 (and_19_out, or_1_out, or_3_out);
  and and_20 (and_20_out, and_19_out, T4);
  and and_21 (and_21_out, or_4_out, T4);
  and and_22 (and_22_out, or_5_out, T3);
  and and_23 (and_23_out, or_6_out, T5);
  or or_8 (LOAD, and_18_out, and_20_out, and_21_out, and_22_out, and_23_out);
endmodule

module DX (
  input  C,
  input  Z,
  input  T3,
  input  T4,
  input  T5,
  input  E3,
  input  E15,
  input  E16,
  input  E17,
  input  E18,
  input  E19,
  input  M3,
  input  M8,
  input  M13,
  input  M15,
  input  M16,
  input  M20,
  input  M25,
  input  M30,
  input  M32,
  input  M33,
  input  M37,
  input  M42,
  input  M47,
  input  M49,
  input  M50,
  input  M54,
  input  M59,
  input  M64,
  input  M66,
  input  M67,
  input  M71,
  input  M76,
  input  M81,
  input  M83,
  input  M84,
  input  M88,
  input  M93,
  input  M98,
  input  M100,
  input  M101,
  input  M105,
  input  M110,
  input  M115,
  input  M117,
  input  M118,
  input  M122,
  input  M127,
  input  M132,
  input  M134,
  input  M135,
  input  M139,
  input  M144,
  input  M149,
  input  M151,
  input  M152,
  input  M173,
  input  M178,
  input  M183,
  input  M188,
  input  M193,
  input  M203,
  input  M206,
  input  M209,
  input  M212,
  input  M215,
  input  M218,
  input  M219,
  input  M220,
  input  M221,
  input  M222,
  input  M223,
  input  M224,
  input  M225,
  input  M226,
  output INC,
  output DEC,
  output SHL,
  output SHR,
  output CIL,
  output CIR,
  output CML,
  output CLR,
  output BUS,
  output LOAD
);

  wire and_9_out, and_10_out, and_11_out, and_12_out, and_13_out, and_14_out, and_15_out, and_16_out,
       and_17_out, and_18_out, and_19_out, and_20_out, and_21_out, and_22_out, and_23_out, not_1_out,
       not_2_out, not_3_out, or_1_out, or_2_out, or_3_out, or_4_out, or_5_out, or_6_out;

  not not_1 (not_1_out, Z);
  not not_2 (not_2_out, Z);
  not not_3 (not_3_out, C);
  and and_1 (INC, M225, E3, T3);
  and and_2 (DEC, M226, E3, T3);
  and and_3 (SHL, M221, E3, T3);
  and and_4 (SHR, M222, E3, T3);
  and and_5 (CIL, M223, E3, T3);
  and and_6 (CIR, M224, E3, T3);
  and and_7 (CML, M220, E3, T3);
  and and_8 (CLR, M219, E3, T3);
  and and_9 (and_9_out, M183, T4);
  and and_10 (and_10_out, M188, T3);
  and and_11 (and_11_out, M203, E3, T3);
  and and_12 (and_12_out, M206, E3, T3, Z);
  and and_13 (and_13_out, M209, E3, T3, not_1_out);
  and and_14 (and_14_out, M212, E3, T3, not_2_out, C);
  and and_15 (and_15_out, M215, E3, T3, Z, not_3_out);
  and and_16 (and_16_out, M218, E3, T3, Z, C);
  or or_1 (or_1_out, E15, E16, E17, E18, E19);
  or or_2 (or_2_out, M152, M135, M118, M101, M84, M67, M50, M33, M16);
  or or_3 (or_3_out, M151, M134, M117, M100, M83, M66, M49, M32, M15);
  or or_4 (or_4_out, M178, M144, M127, M110, M93, M76, M59, M42, M25, M8);
  or or_5 (or_5_out, M193, M149, M132, M115, M98, M81, M64, M47, M30, M13);
  or or_6 (or_6_out, M173, M139, M122, M105, M88, M71, M54, M37, M20, M3);
  or or_7 (BUS, and_9_out, and_10_out, and_11_out, and_12_out, and_13_out, and_14_out, and_15_out, and_16_out);
  and and_17 (and_17_out, or_1_out, or_2_out);
  and and_18 (and_18_out, and_17_out, T3);
  and and_19 (and_19_out, or_1_out, or_3_out);
  and and_20 (and_20_out, and_19_out, T4);
  and and_21 (and_21_out, or_4_out, T4);
  and and_22 (and_22_out, or_5_out, T3);
  and and_23 (and_23_out, or_6_out, T5);
  or or_8 (LOAD, and_18_out, and_20_out, and_21_out, and_22_out, and_23_out);
endmodule

module EX (
  input  C,
  input  Z,
  input  T3,
  input  T4,
  input  T5,
  input  E4,
  input  E20,
  input  E21,
  input  E22,
  input  E23,
  input  E24,
  input  M4,
  input  M9,
  input  M14,
  input  M15,
  input  M16,
  input  M21,
  input  M26,
  input  M31,
  input  M32,
  input  M33,
  input  M38,
  input  M43,
  input  M48,
  input  M49,
  input  M50,
  input  M55,
  input  M60,
  input  M65,
  input  M66,
  input  M67,
  input  M72,
  input  M77,
  input  M82,
  input  M83,
  input  M84,
  input  M89,
  input  M94,
  input  M99,
  input  M100,
  input  M101,
  input  M106,
  input  M111,
  input  M116,
  input  M117,
  input  M118,
  input  M123,
  input  M128,
  input  M133,
  input  M134,
  input  M135,
  input  M140,
  input  M145,
  input  M150,
  input  M151,
  input  M152,
  input  M174,
  input  M179,
  input  M184,
  input  M189,
  input  M194,
  input  M203,
  input  M206,
  input  M209,
  input  M212,
  input  M215,
  input  M218,
  input  M219,
  input  M220,
  input  M221,
  input  M222,
  input  M223,
  input  M224,
  input  M225,
  input  M226,
  output INC,
  output DEC,
  output SHL,
  output SHR,
  output CIL,
  output CIR,
  output CML,
  output CLR,
  output BUS,
  output LOAD
);

  wire and_9_out, and_10_out, and_11_out, and_12_out, and_13_out, and_14_out, and_15_out, and_16_out,
       and_17_out, and_18_out, and_19_out, and_20_out, and_21_out, and_22_out, and_23_out, not_1_out,
       not_2_out, not_3_out, or_1_out, or_2_out, or_3_out, or_4_out, or_5_out, or_6_out;

  not not_1 (not_1_out, Z);
  not not_2 (not_2_out, Z);
  not not_3 (not_3_out, C);
  and and_1 (INC, M225, E4, T3);
  and and_2 (DEC, M226, E4, T3);
  and and_3 (SHL, M221, E4, T3);
  and and_4 (SHR, M222, E4, T3);
  and and_5 (CIL, M223, E4, T3);
  and and_6 (CIR, M224, E4, T3);
  and and_7 (CML, M220, E4, T3);
  and and_8 (CLR, M219, E4, T3);
  and and_9 (and_9_out, M184, T4);
  and and_10 (and_10_out, M189, T3);
  and and_11 (and_11_out, M203, E4, T3);
  and and_12 (and_12_out, M206, E4, T3, Z);
  and and_13 (and_13_out, M209, E4, T3, not_1_out);
  and and_14 (and_14_out, M212, E4, T3, not_2_out, C);
  and and_15 (and_15_out, M215, E4, T3, Z, not_3_out);
  and and_16 (and_16_out, M218, E4, T3, Z, C);
  or or_1 (or_1_out, E20, E21, E22, E23, E24);
  or or_2 (or_2_out, M152, M135, M118, M101, M84, M67, M50, M33, M16);
  or or_3 (or_3_out, M151, M134, M117, M100, M83, M66, M49, M32, M15);
  or or_4 (or_4_out, M179, M145, M128, M111, M94, M77, M60, M43, M26, M9);
  or or_5 (or_5_out, M194, M150, M133, M116, M99, M82, M65, M48, M31, M14);
  or or_6 (or_6_out, M174, M140, M123, M106, M89, M72, M55, M38, M21, M4);
  or or_7 (BUS, and_9_out, and_10_out, and_11_out, and_12_out, and_13_out, and_14_out, and_15_out, and_16_out);
  and and_17 (and_17_out, or_1_out, or_2_out);
  and and_18 (and_18_out, and_17_out, T3);
  and and_19 (and_19_out, or_1_out, or_3_out);
  and and_20 (and_20_out, and_19_out, T4);
  and and_21 (and_21_out, or_4_out, T4);
  and and_22 (and_22_out, or_5_out, T3);
  and and_23 (and_23_out, or_6_out, T5);
  or or_8 (LOAD, and_18_out, and_20_out, and_21_out, and_22_out, and_23_out);
endmodule

module MEMORY (
  input  T1,
  input  T3,
  input  T4,
  input  M0,
  input  M11,
  input  M2,
  input  M3,
  input  M4,
  input  M5,
  input  M6,
  input  M7,
  input  M8,
  input  M9,
  input  M15,
  input  M17,
  input  M18,
  input  M19,
  input  M20,
  input  M21,
  input  M22,
  input  M23,
  input  M24,
  input  M25,
  input  M26,
  input  M32,
  input  M34,
  input  M35,
  input  M36,
  input  M37,
  input  M38,
  input  M39,
  input  M40,
  input  M41,
  input  M42,
  input  M43,
  input  M49,
  input  M51,
  input  M52,
  input  M53,
  input  M54,
  input  M55,
  input  M56,
  input  M57,
  input  M58,
  input  M59,
  input  M60,
  input  M66,
  input  M68,
  input  M69,
  input  M70,
  input  M71,
  input  M72,
  input  M73,
  input  M74,
  input  M75,
  input  M76,
  input  M77,
  input  M83,
  input  M85,
  input  M86,
  input  M87,
  input  M88,
  input  M89,
  input  M90,
  input  M91,
  input  M92,
  input  M93,
  input  M94,
  input  M100,
  input  M102,
  input  M103,
  input  M104,
  input  M105,
  input  M106,
  input  M107,
  input  M108,
  input  M109,
  input  M110,
  input  M111,
  input  M117,
  input  M119,
  input  M120,
  input  M121,
  input  M122,
  input  M123,
  input  M124,
  input  M125,
  input  M126,
  input  M127,
  input  M128,
  input  M134,
  input  M136,
  input  M137,
  input  M138,
  input  M139,
  input  M140,
  input  M141,
  input  M142,
  input  M143,
  input  M144,
  input  M145,
  input  M151,
  input  M153,
  input  M154,
  input  M155,
  input  M156,
  input  M157,
  input  M158,
  input  M159,
  input  M160,
  input  M161,
  input  M162,
  input  M168,
  input  M170,
  input  M171,
  input  M172,
  input  M173,
  input  M174,
  input  M175,
  input  M176,
  input  M177,
  input  M178,
  input  M179,
  input  M180,
  input  M181,
  input  M182,
  input  M183,
  input  M184,
  input  M185,
  input  M186,
  input  M187,
  input  M188,
  input  M189,
  input  M195,
  input  M196,
  input  M197,
  input  M198,
  input  M199,
  input  M201,
  input  M204,
  input  M207,
  input  M210,
  input  M213,
  input  M216,
  input  E0,
  input  E1,
  input  E2,
  input  E3,
  input  E4,
  input  E5,
  input  E6,
  input  E7,
  input  E8,
  input  E9,
  input  E10,
  input  E11,
  input  E12,
  input  E13,
  input  E14,
  input  E15,
  input  E16,
  input  E17,
  input  E18,
  input  E19,
  input  E20,
  input  E21,
  input  E22,
  input  E23,
  input  E24,
  output STR,
  output BUS,
  output [2:0] MUX
);

  wire and_1_out, and_2_out, and_3_out, and_4_out, and_5_out, and_6_out, and_7_out, and_8_out, and_9_out,
       and_10_out, and_11_out, or_1_out, or_2_out, or_3_out, or_4_out, or_5_out, or_6_out, or_7_out,
       or_8_out, or_9_out, or_10_out, or_11_out, or_12_out, or_13_out, or_14_out, or_15_out, or_16_out,
       or_17_out, or_18_out, or_19_out, or_20_out, or_21_out, or_22_out, or_23_out, or_24_out, or_25_out,
       or_26_out, or_28_out, or_29_out, or_30_out;

  or or_1 (or_1_out, M184, M183, M182, M181, M180);
  or or_2 (or_2_out, M199, M198, M197, M196, M195, M189, M188, M187, M186, M185);
  or or_3 (or_3_out, M216, M213, M210, M207, M204, M201, M184, M183, M182, M181, M180, M179, M178, M177, M176, M175, M174, M173, M172, M171, M170, M168, M162, M161, M160, M159, M158, M157, M156, M155, M154, M153);
  or or_4 (or_4_out, M151, M145, M144, M143, M142, M141, M140, M139, M138, M137, M136, M134, M128, M127, M126, M125, M124, M123, M122, M121, M120, M119, M117, M111, M110, M109, M108, M107, M106, M105, M104, M103);
  or or_5 (or_5_out, M102, M100, M94, M93, M92, M91, M90, M89, M88, M87, M86, M85, M83, M77, M76, M75, M74, M73, M72, M71, M70, M69, M68, M66, M60, M59, M58, M57, M56, M55, M54, M53);
  or or_6 (or_6_out, M52, M51, M49, M43, M42, M41, M40, M39, M38, M37, M36, M35, M34, M32, M26, M25, M24, M23, M22, M21, M20, M19, M18, M17, M15, M9, M8, M7, M6, M5, M4, M3);
  or or_7 (or_7_out, M174, M173, M172, M171, M170, M157, M156, M155, M154, M153, M140, M139, M138, M137, M136, M123, M122, M121, M120, M119, M106, M105, M104, M103, M102, M89, M88, M87, M86, M85, M72, M71);
  or or_8 (or_8_out, M70, M69, M68, M55, M54, M53, M52, M51, M38, M37, M36, M35, M34, M21, M20, M19, M18, M17, M4, M3, M2, M11, M0);
  or or_9 (or_9_out, M216, M213, M210, M207, M204, M201, M184, M183, M182, M181, M180, M179, M178, M177, M176, M175, M174, M173, M172, M171, M170, M162, M161, M160, M159, M158, M157, M156, M155, M154, M153, M145);
  or or_10 (or_10_out, M144, M143, M142, M141, M140, M139, M138, M137, M136, M128, M127, M126, M125, M124, M123, M122, M121, M120, M119, M111, M110, M109, M108, M107, M106, M105, M104, M103, M102, M94, M93, M92);
  or or_11 (or_11_out, M91, M90, M89, M88, M87, M85, M85, M77, M76, M75, M74, M73, M72, M71, M70, M69, M68, M60, M59, M58, M57, M56, M55, M54, M53, M52, M51, M43, M42, M41, M40, M39);
  or or_12 (or_12_out, M38, M37, M36, M35, M34, M26, M25, M24, M23, M22, M21, M20, M19, M18, M17, M9, M8, M7, M6, M5, M4, M3, M2, M11, M0);
  or or_13 (or_13_out, M174, M173, M172, M171, M170, M157, M156, M155, M154, M153, M140, M139, M138, M137, M136, M123, M122, M121, M120, M119, M106, M105, M104, M103, M102, M89, M88, M87, M85, M85, M72, M71);
  or or_14 (or_14_out, M70, M69, M68, M55, M54, M53, M52, M51, M38, M37, M36, M35, M34, M21, M20, M19, M18, M17, M4, M3, M2, M11, M0);
  or or_15 (or_15_out, M168, M151, M134, M117, M100, M83, M66, M49, M32, M15);
  or or_16 (or_16_out, E0, E5, E10, E15, E20);
  or or_17 (or_17_out, M168, M151, M134, M117, M100, M83, M66, M49, M32, M15);
  or or_18 (or_18_out, E1, E6, E11, E16, E21);
  or or_19 (or_19_out, M168, M151, M134, M117, M100, M83, M66, M49, M32, M15);
  or or_20 (or_20_out, E2, E7, E12, E17, E22);
  or or_21 (or_21_out, M168, M151, M134, M117, M100, M83, M66, M49, M32, M15);
  or or_22 (or_22_out, E3, E8, E13, E18, E23);
  or or_23 (or_23_out, M168, M151, M134, M117, M100, M83, M66, M49, M32, M15);
  or or_24 (or_24_out, E4, E9, E14, E19, E24);
  and and_1 (and_1_out, or_1_out, T4);
  and and_2 (and_2_out, or_2_out, T3);
  or or_25 (or_25_out, or_7_out, or_8_out);
  or or_26 (or_26_out, or_13_out, or_14_out);
  and and_3 (and_3_out, or_15_out, T3, or_16_out);
  and and_4 (and_4_out, or_17_out, T3, or_18_out);
  and and_5 (and_5_out, or_19_out, T3, or_20_out);
  and and_6 (and_6_out, or_21_out, T3, or_22_out);
  and and_7 (and_7_out, or_23_out, T3, or_24_out);
  or or_27 (STR, and_1_out, and_2_out);
  or or_28 (or_28_out, M0, M11, M2, or_3_out, or_4_out, or_5_out, or_6_out);
  and and_8 (and_8_out, or_25_out, T4);
  or or_29 (or_29_out, or_9_out, or_10_out, or_11_out, or_12_out);
  and and_9 (and_9_out, or_29_out, T3);
  and and_10 (and_10_out, or_26_out, T4);
  and and_11 (and_11_out, or_28_out, T3);
  or or_30 (or_30_out, T1, and_9_out, and_10_out);
  or or_31 (BUS, T1, and_11_out, and_8_out);
  assign MUX = or_30_out ? 3'b000 : 3'bz;  // Controlled_Buffer controlled_buffer_1
  assign MUX = and_3_out ? 3'b001 : 3'bz;  // Controlled_Buffer controlled_buffer_2
  assign MUX = and_4_out ? 3'b010 : 3'bz;  // Controlled_Buffer controlled_buffer_3
  assign MUX = and_5_out ? 3'b011 : 3'bz;  // Controlled_Buffer controlled_buffer_4
  assign MUX = and_6_out ? 3'b100 : 3'bz;  // Controlled_Buffer controlled_buffer_5
  assign MUX = and_7_out ? 3'b101 : 3'bz;  // Controlled_Buffer controlled_buffer_6
endmodule

module SPECIAL_PURPOSE_REGISTERS (
  input  C,
  input  Z,
  input  T0,
  input  T1,
  input  T2,
  input  T3,
  input  T4,
  input  T5,
  input  M0,
  input  M1,
  input  M2,
  input  M3,
  input  M4,
  input  M5,
  input  M6,
  input  M7,
  input  M8,
  input  M9,
  input  M15,
  input  M17,
  input  M18,
  input  M19,
  input  M20,
  input  M21,
  input  M22,
  input  M23,
  input  M24,
  input  M25,
  input  M26,
  input  M32,
  input  M34,
  input  M35,
  input  M36,
  input  M37,
  input  M38,
  input  M39,
  input  M40,
  input  M41,
  input  M42,
  input  M43,
  input  M49,
  input  M51,
  input  M52,
  input  M53,
  input  M54,
  input  M55,
  input  M56,
  input  M57,
  input  M58,
  input  M59,
  input  M60,
  input  M66,
  input  M68,
  input  M69,
  input  M70,
  input  M71,
  input  M72,
  input  M73,
  input  M74,
  input  M75,
  input  M76,
  input  M77,
  input  M83,
  input  M85,
  input  M86,
  input  M87,
  input  M88,
  input  M89,
  input  M90,
  input  M91,
  input  M92,
  input  M93,
  input  M94,
  input  M100,
  input  M102,
  input  M103,
  input  M104,
  input  M105,
  input  M106,
  input  M107,
  input  M108,
  input  M109,
  input  M110,
  input  M111,
  input  M117,
  input  M119,
  input  M120,
  input  M121,
  input  M122,
  input  M123,
  input  M124,
  input  M125,
  input  M126,
  input  M127,
  input  M128,
  input  M134,
  input  M136,
  input  M137,
  input  M138,
  input  M139,
  input  M140,
  input  M141,
  input  M142,
  input  M143,
  input  M144,
  input  M145,
  input  M151,
  input  M153,
  input  M154,
  input  M155,
  input  M156,
  input  M157,
  input  M158,
  input  M159,
  input  M160,
  input  M161,
  input  M162,
  input  M168,
  input  M170,
  input  M171,
  input  M172,
  input  M173,
  input  M174,
  input  M175,
  input  M176,
  input  M177,
  input  M178,
  input  M179,
  input  M180,
  input  M181,
  input  M182,
  input  M183,
  input  M184,
  input  M201,
  input  M202,
  input  M203,
  input  M204,
  input  M205,
  input  M206,
  input  M207,
  input  M208,
  input  M209,
  input  M210,
  input  M211,
  input  M212,
  input  M213,
  input  M214,
  input  M215,
  input  M216,
  input  M217,
  input  M218,
  output DR_BUS,
  output DR_LOAD,
  output IR_BUS,
  output IR_LOAD,
  output PC_BUS,
  output PC_INC,
  output PC_LOAD,
  output AR_BUS,
  output AR_LOAD
);

  IR ir_1 (.T1(T1), .T2(T2), .IR_BUS(IR_BUS), .IR_LOAD(IR_LOAD));
  AR ar_1 (
    .C(C), .Z(Z), .T0(T0), .T2(T2), .T3(T3), .T4(T4), .M0(M0), .M1(M1), .M2(M2), .M3(M3), .M4(M4), .M17(M17),
    .M18(M18), .M19(M19), .M20(M20), .M21(M21), .M34(M34), .M35(M35), .M36(M36), .M37(M37), .M38(M38),
    .M51(M51), .M52(M52), .M53(M53), .M54(M54), .M55(M55), .M68(M68), .M69(M69), .M70(M70), .M71(M71),
    .M72(M72), .M85(M85), .M86(M86), .M87(M87), .M88(M88), .M89(M89), .M102(M102), .M103(M103), .M104(M104),
    .M105(M105), .M106(M106), .M119(M119), .M120(M120), .M121(M121), .M122(M122), .M123(M123), .M136(M136),
    .M137(M137), .M138(M138), .M139(M139), .M140(M140), .M153(M153), .M154(M154), .M155(M155), .M156(M156),
    .M157(M157), .M170(M170), .M171(M171), .M172(M172), .M173(M173), .M174(M174), .M180(M180), .M181(M181),
    .M182(M182), .M183(M183), .M184(M184), .M201(M201), .M202(M202), .M204(M204), .M205(M205), .M207(M207),
    .M208(M208), .M210(M210), .M211(M211), .M213(M213), .M214(M214), .M216(M216), .M217(M217),
    .AR_BUS(AR_BUS), .AR_LOAD(AR_LOAD));
  PC pc_1 (
    .T0(T0), .T1(T1), .T3(T3), .T4(T4), .M201(M201), .M202(M202), .M203(M203), .M204(M204), .M205(M205),
    .M206(M206), .M207(M207), .M208(M208), .M209(M209), .M210(M210), .M211(M211), .M212(M212), .M213(M213),
    .M214(M214), .M215(M215), .M216(M216), .M217(M217), .M218(M218), .PC_BUS(PC_BUS), .PC_INC(PC_INC),
    .PC_LOAD(PC_LOAD));
  DR dr_1 (
    .T3(T3), .T4(T4), .T5(T5), .M0(M0), .M1(M1), .M2(M2), .M3(M3), .M4(M4), .M5(M5), .M6(M6), .M7(M7),
    .M8(M8), .M9(M9), .M15(M15), .M17(M17), .M18(M18), .M19(M19), .M20(M20), .M21(M21), .M22(M22), .M23(M23),
    .M24(M24), .M25(M25), .M26(M26), .M32(M32), .M34(M34), .M35(M35), .M36(M36), .M37(M37), .M38(M38),
    .M39(M39), .M40(M40), .M41(M41), .M42(M42), .M43(M43), .M49(M49), .M51(M51), .M52(M52), .M53(M53),
    .M54(M54), .M55(M55), .M56(M56), .M57(M57), .M58(M58), .M59(M59), .M60(M60), .M66(M66), .M68(M68),
    .M69(M69), .M70(M70), .M71(M71), .M72(M72), .M73(M73), .M74(M74), .M75(M75), .M76(M76), .M77(M77),
    .M83(M83), .M85(M85), .M86(M86), .M87(M87), .M88(M88), .M89(M89), .M90(M90), .M91(M91), .M92(M92),
    .M93(M93), .M94(M94), .M100(M100), .M102(M102), .M103(M103), .M104(M104), .M105(M105), .M106(M106),
    .M107(M107), .M108(M108), .M109(M109), .M110(M110), .M111(M111), .M117(M117), .M119(M119), .M120(M120),
    .M121(M121), .M122(M122), .M123(M123), .M124(M124), .M125(M125), .M126(M126), .M127(M127), .M128(M128),
    .M134(M134), .M136(M136), .M137(M137), .M138(M138), .M139(M139), .M140(M140), .M141(M141), .M142(M142),
    .M143(M143), .M144(M144), .M145(M145), .M151(M151), .M153(M153), .M154(M154), .M155(M155), .M156(M156),
    .M157(M157), .M158(M158), .M159(M159), .M160(M160), .M161(M161), .M162(M162), .M168(M168), .M170(M170),
    .M171(M171), .M172(M172), .M173(M173), .M174(M174), .M175(M175), .M176(M176), .M177(M177), .M178(M178),
    .M179(M179), .DR_BUS(DR_BUS), .DR_LOAD(DR_LOAD));
endmodule

module GENERAL_PURPOSE_REGISTERS (
  input  C,
  input  Z,
  input  T3,
  input  T4,
  input  T5,
  input  M0,
  input  M1,
  input  M2,
  input  M3,
  input  M4,
  input  M5,
  input  M6,
  input  M7,
  input  M8,
  input  M9,
  input  M10,
  input  M11,
  input  M12,
  input  M13,
  input  M14,
  input  M15,
  input  M16,
  input  M17,
  input  M18,
  input  M19,
  input  M20,
  input  M21,
  input  M22,
  input  M23,
  input  M24,
  input  M25,
  input  M26,
  input  M27,
  input  M28,
  input  M29,
  input  M30,
  input  M31,
  input  M32,
  input  M33,
  input  M34,
  input  M35,
  input  M36,
  input  M37,
  input  M38,
  input  M39,
  input  M40,
  input  M41,
  input  M42,
  input  M43,
  input  M44,
  input  M45,
  input  M46,
  input  M47,
  input  M48,
  input  M49,
  input  M50,
  input  M51,
  input  M52,
  input  M53,
  input  M54,
  input  M55,
  input  M56,
  input  _57M,
  input  M58,
  input  M59,
  input  M60,
  input  M61,
  input  M62,
  input  M63,
  input  M64,
  input  M65,
  input  M66,
  input  M67,
  input  M68,
  input  M69,
  input  M70,
  input  M71,
  input  M72,
  input  M73,
  input  M74,
  input  M75,
  input  M76,
  input  M77,
  input  M78,
  input  M79,
  input  M80,
  input  M81,
  input  M82,
  input  M83,
  input  M84,
  input  M85,
  input  M86,
  input  M87,
  input  M88,
  input  M89,
  input  M90,
  input  M91,
  input  M92,
  input  M93,
  input  M94,
  input  M95,
  input  M96,
  input  M97,
  input  M98,
  input  M99,
  input  M100,
  input  M101,
  input  M102,
  input  M103,
  input  M104,
  input  M105,
  input  M106,
  input  M107,
  input  M108,
  input  M109,
  input  M110,
  input  M111,
  input  M112,
  input  M113,
  input  M114,
  input  M115,
  input  M116,
  input  M117,
  input  M118,
  input  M119,
  input  M120,
  input  M121,
  input  M122,
  input  M123,
  input  M124,
  input  M125,
  input  M126,
  input  M127,
  input  M128,
  input  M129,
  input  M130,
  input  M131,
  input  M132,
  input  M133,
  input  M134,
  input  M135,
  input  M136,
  input  M137,
  input  M138,
  input  M139,
  input  M140,
  input  M141,
  input  M142,
  input  M143,
  input  M144,
  input  M145,
  input  M146,
  input  M147,
  input  M148,
  input  M149,
  input  M150,
  input  M151,
  input  M152,
  input  M170,
  input  M171,
  input  M172,
  input  M173,
  input  M174,
  input  M175,
  input  M176,
  input  M177,
  input  M178,
  input  M179,
  input  M180,
  input  M181,
  input  M182,
  input  M183,
  input  M184,
  input  M185,
  input  M186,
  input  M187,
  input  M188,
  input  M189,
  input  M190,
  input  M191,
  input  M192,
  input  M193,
  input  M194,
  input  M203,
  input  M206,
  input  M209,
  input  M212,
  input  M215,
  input  M218,
  input  M219,
  input  M220,
  input  M221,
  input  M222,
  input  M223,
  input  M224,
  input  M225,
  input  M226,
  input  E0,
  input  E1,
  input  E2,
  input  E3,
  input  E4,
  input  E5,
  input  E6,
  input  E7,
  input  E8,
  input  E9,
  input  E10,
  input  E11,
  input  E12,
  input  E13,
  input  E14,
  input  E15,
  input  E16,
  input  E17,
  input  E18,
  input  E19,
  input  E20,
  input  E21,
  input  E22,
  input  E23,
  input  E24,
  output AX_INC,
  output AX_DEC,
  output AX_SHL,
  output AX_SHR,
  output AX_CIL,
  output AX_CIR,
  output AX_CML,
  output AX_CLR,
  output AX_BUS,
  output AX_LOAD,
  output BX_INC,
  output BX_DEC,
  output BX_SHL,
  output BX_SHR,
  output BX_CIL,
  output BX_CIR,
  output BX_CML,
  output BX_CLR,
  output BX_BUS,
  output BX_LOAD,
  output CX_INC,
  output CX_DEC,
  output CX_SHL,
  output CX_SHR,
  output CX_CIL,
  output CX_CIR,
  output CX_CML,
  output CX_CLR,
  output CX_BUS,
  output CX_LOAD,
  output DX_INC,
  output DX_DEC,
  output DX_SHL,
  output DX_SHR,
  output DX_CIL,
  output DX_CIR,
  output DX_CML,
  output DX_CLR,
  output DX_BUS,
  output DX_LOAD,
  output EX_INC,
  output EX_DEC,
  output EX_SHL,
  output EX_SHR,
  output EX_CIL,
  output EX_CIR,
  output EX_CML,
  output EX_CLR,
  output EX_BUS,
  output EX_LOAD
);

  AX ax_1 (
    .C(C), .Z(Z), .T3(T3), .T4(T4), .T5(T5), .E0(E0), .E1(E1), .E2(E2), .E3(E3), .E4(E4), .M0(M0), .M5(M5),
    .M10(M10), .M15(M15), .M16(M16), .M17(M17), .M22(M22), .M27(M27), .M32(M32), .M33(M33), .M34(M34),
    .M39(M39), .M44(M44), .M49(M49), .M50(M50), .M51(M51), .M56(M56), .M61(M61), .M66(M66), .M67(M67),
    .M68(M68), .M73(M73), .M78(M78), .M83(M83), .M84(M84), .M85(M85), .M90(M90), .M95(M95), .M100(M100),
    .M101(M101), .M102(M102), .M107(M107), .M112(M112), .M117(M117), .M118(M118), .M119(M119), .M124(M124),
    .M129(M129), .M134(M134), .M135(M135), .M136(M136), .M141(M141), .M146(M146), .M151(M151), .M152(M152),
    .M170(M170), .M175(M175), .M180(M180), .M185(M185), .M190(M190), .M203(M203), .M206(M206), .M209(M209),
    .M212(M212), .M215(M215), .M218(M218), .M219(M219), .M220(M220), .M221(M221), .M222(M222), .M223(M223),
    .M224(M224), .M225(M225), .M226(M226), .INC(AX_INC), .DEC(AX_DEC), .SHL(AX_SHL), .SHR(AX_SHR),
    .CIL(AX_CIL), .CIR(AX_CIR), .CML(AX_CML), .CLR(AX_CLR), .BUS(AX_BUS), .LOAD(AX_LOAD));
  BX bx_1 (
    .C(C), .Z(Z), .T3(T3), .T4(T4), .T5(T5), .E1(E1), .E5(E5), .E6(E6), .E7(E7), .E8(E8), .E9(E9), .M1(M1),
    .M6(M6), .M11(M11), .M15(M15), .M16(M16), .M18(M18), .M23(M23), .M28(M28), .M32(M32), .M33(M33),
    .M35(M35), .M40(M40), .M45(M45), .M49(M49), .M50(M50), .M52(M52), .M57(_57M), .M62(M62), .M66(M66),
    .M67(M67), .M69(M69), .M74(M74), .M79(M79), .M83(M83), .M84(M84), .M86(M86), .M91(M91), .M96(M96),
    .M100(M100), .M101(M101), .M103(M103), .M108(M108), .M113(M113), .M117(M117), .M118(M118), .M120(M120),
    .M125(M125), .M130(M130), .M134(M134), .M135(M135), .M137(M137), .M142(M142), .M147(M147), .M151(M151),
    .M152(M152), .M171(M171), .M176(M176), .M181(M181), .M186(M186), .M191(M191), .M203(M203), .M206(M206),
    .M209(M209), .M212(M212), .M215(M215), .M218(M218), .M219(M219), .M220(M220), .M221(M221), .M222(M222),
    .M223(M223), .M224(M224), .M225(M225), .M226(M226), .INC(BX_INC), .DEC(BX_DEC), .SHL(BX_SHL),
    .SHR(BX_SHR), .CIL(BX_CIL), .CIR(BX_CIR), .CML(BX_CML), .CLR(BX_CLR), .BUS(BX_BUS), .LOAD(BX_LOAD));
  CX cx_1 (
    .C(C), .Z(Z), .T3(T3), .T4(T4), .T5(T5), .E2(E0), .E10(E10), .E11(E11), .E12(E12), .E13(E13), .E14(E14),
    .M2(M2), .M7(M7), .M12(M12), .M15(M15), .M16(M16), .M19(M19), .M24(M24), .M29(M29), .M32(M32), .M33(M33),
    .M36(M36), .M41(M41), .M46(M46), .M49(M49), .M50(M50), .M53(M53), .M58(M58), .M63(M63), .M66(M66),
    .M67(M67), .M70(M70), .M75(M75), .M80(M80), .M83(M83), .M84(M84), .M87(M87), .M92(M92), .M97(M97),
    .M100(M100), .M101(M101), .M104(M104), .M109(M109), .M114(M114), .M117(M117), .M118(M118), .M121(M121),
    .M126(M126), .M131(M131), .M134(M134), .M135(M135), .M138(M138), .M143(M143), .M148(M148), .M151(M151),
    .M152(M152), .M172(M172), .M177(M177), .M182(M182), .M187(M187), .M192(M192), .M203(M203), .M206(M206),
    .M209(M209), .M212(M212), .M215(M215), .M218(M218), .M219(M219), .M220(M220), .M221(M221), .M222(M222),
    .M223(M223), .M224(M224), .M225(M225), .M226(M226), .INC(CX_INC), .DEC(CX_DEC), .SHL(CX_SHL),
    .SHR(CX_SHR), .CIL(CX_CIL), .CIR(CX_CIR), .CML(CX_CML), .CLR(CX_CLR), .BUS(CX_BUS), .LOAD(CX_LOAD));
  DX dx_1 (
    .C(C), .Z(Z), .T3(T3), .T4(T4), .T5(T5), .E3(E2), .E15(E15), .E16(E16), .E17(E17), .E18(E18), .E19(E19),
    .M3(M3), .M8(M8), .M13(M13), .M15(M15), .M16(M16), .M20(M20), .M25(M25), .M30(M30), .M32(M32), .M33(M33),
    .M37(M37), .M42(M42), .M47(M47), .M49(M49), .M50(M50), .M54(M54), .M59(M59), .M64(M64), .M66(M66),
    .M67(M67), .M71(M71), .M76(M76), .M81(M81), .M83(M83), .M84(M84), .M88(M88), .M93(M93), .M98(M98),
    .M100(M100), .M101(M101), .M105(M105), .M110(M110), .M115(M115), .M117(M117), .M118(M118), .M122(M122),
    .M127(M127), .M132(M132), .M134(M134), .M135(M135), .M139(M139), .M144(M144), .M149(M149), .M151(M151),
    .M152(M152), .M173(M173), .M178(M178), .M183(M183), .M188(M188), .M193(M193), .M203(M203), .M206(M206),
    .M209(M209), .M212(M212), .M215(M215), .M218(M218), .M219(M219), .M220(M220), .M221(M221), .M222(M222),
    .M223(M223), .M224(M224), .M225(M225), .M226(M226), .INC(DX_INC), .DEC(DX_DEC), .SHL(DX_SHL),
    .SHR(DX_SHR), .CIL(DX_CIL), .CIR(DX_CIR), .CML(DX_CML), .CLR(DX_CLR), .BUS(DX_BUS), .LOAD(DX_LOAD));
  EX ex_1 (
    .C(C), .Z(Z), .T3(T3), .T4(T4), .T5(T5), .E4(E4), .E20(E20), .E21(E21), .E22(E22), .E23(E23), .E24(E24),
    .M4(M4), .M9(M9), .M14(M14), .M15(M15), .M16(M16), .M21(M21), .M26(M26), .M31(M31), .M32(M32), .M33(M33),
    .M38(M38), .M43(M43), .M48(M48), .M49(M49), .M50(M50), .M55(M55), .M60(M60), .M65(M65), .M66(M66),
    .M67(M67), .M72(M72), .M77(M77), .M82(M82), .M83(M83), .M84(M84), .M89(M89), .M94(M94), .M99(M99),
    .M100(M100), .M101(M101), .M106(M106), .M111(M111), .M116(M116), .M117(M117), .M118(M118), .M123(M123),
    .M128(M128), .M133(M133), .M134(M134), .M135(M135), .M140(M140), .M145(M145), .M150(M150), .M151(M151),
    .M152(M152), .M174(M174), .M179(M179), .M184(M184), .M189(M189), .M194(M194), .M203(M203), .M206(M206),
    .M209(M209), .M212(M212), .M215(M215), .M218(M218), .M219(M219), .M220(M220), .M221(M221), .M222(M222),
    .M223(M223), .M224(M224), .M225(M225), .M226(M226), .INC(EX_INC), .DEC(EX_DEC), .SHL(EX_SHL),
    .SHR(EX_SHR), .CIL(EX_CIL), .CIR(EX_CIR), .CML(EX_CML), .CLR(EX_CLR), .BUS(EX_BUS), .LOAD(EX_LOAD));
endmodule
