// Logisim project ALU.circ as structural Verilog: 1 circuit, main circuit ALU
module ALU (
  input  T3,
  input  T4,
  input  T5,
  input  E0,
  input  E1,
  input  E2,
  input  E3,
  input  E4,
  input  E5,
  input  E6,
  input  E7,
  input  E8,
  input  E9,
  input  E10,
  input  E11,
  input  E12,
  input  E13,
  input  E14,
  input  E15,
  input  E16,
  input  E17,
  input  E18,
  input  E19,
  input  E20,
  input  E21,
  input  E22,
  input  E23,
  input  E24,
  input  M0,
  input  M1,
  input  M2,
  input  M3,
  input  M4,
  input  M5,
  input  M6,
  input  M7,
  input  M8,
  input  M9,
  input  M10,
  input  M11,
  input  M12,
  input  M13,
  input  M14,
  input  M15,
  input  M16,
  input  M17,
  input  M18,
  input  M19,
  input  M20,
  input  M21,
  input  M22,
  input  M23,
  input  M24,
  input  M25,
  input  M26,
  input  M27,
  input  M28,
  input  M29,
  input  M30,
  input  M31,
  input  M32,
  input  M33,
  input  M34,
  input  M35,
  input  M36,
  input  M37,
  input  M38,
  input  M39,
  input  M40,
  input  M41,
  input  M42,
  input  M43,
  input  M44,
  input  M45,
  input  M46,
  input  M47,
  input  M48,
  input  M49,
  input  M50,
  input  M51,
  input  M52,
  input  M53,
  input  M54,
  input  M55,
  input  M56,
  input  M57,
  input  M58,
  input  M59,
  input  M60,
  input  M61,
  input  M62,
  input  M63,
  input  M64,
  input  M65,
  input  M66,
  input  M67,
  input  M68,
  input  M69,
  input  M70,
  input  M71,
  input  M72,
  input  M73,
  input  M74,
  input  M75,
  input  M76,
  input  M77,
  input  M78,
  input  M79,
  input  M80,
  input  M81,
  input  M82,
  input  M83,
  input  M84,
  input  M85,
  input  M86,
  input  M87,
  input  M88,
  input  M89,
  input  M90,
  input  M91,
  input  M92,
  input  M93,
  input  M94,
  input  M95,
  input  M96,
  input  M97,
  input  M98,
  input  M99,
  input  M100,
  input  M101,
  input  M102,
  input  M103,
  input  M104,
  input  M105,
  input  M106,
  input  M107,
  input  M108,
  input  M109,
  input  M110,
  input  M111,
  input  M112,
  input  M113,
  input  M114,
  input  M115,
  input  M116,
  input  M117,
  input  M118,
  input  M119,
  input  M120,
  input  M121,
  input  M122,
  input  M123,
  input  M124,
  input  M125,
  input  M126,
  input  M127,
  input  M128,
  input  M129,
  input  M130,
  input  M131,
  input  M132,
  input  M133,
  input  M134,
  input  M135,
  input  M136,
  input  M137,
  input  M138,
  input  M139,
  input  M140,
  input  M141,
  input  M142,
  input  M143,
  input  M144,
  input  M145,
  input  M146,
  input  M147,
  input  M148,
  input  M149,
  input  M150,
  input  M151,
  input  M152,
  input  M153,
  input  M154,
  input  M155,
  input  M156,
  input  M157,
  input  M158,
  input  M159,
  input  M160,
  input  M161,
  input  M162,
  input  M163,
  input  M164,
  input  M165,
  input  M166,
  input  M167,
  input  M168,
  input  M169,
  input  M170,
  input  M171,
  input  M172,
  input  M173,
  input  M174,
  input  M175,
  input  M176,
  input  M177,
  input  M178,
  input  M179,
  input  M190,
  input  M191,
  input  M192,
  input  M193,
  input  M194,
  input  M195,
  output AX_1,
  output BX_1,
  output CX_1,
  output DX_1,
  output EX_1,
  output AND,
  output OR,
  output XOR,
  output ADD,
  output ADC,
  output SUB,
  output SBB,
  output MUL,
  output DIV,
  output CMP,
  output LOAD,
  output AX_2,
  output BX_2,
  output CX_2,
  output DX_2,
  output EX_2,
  output DR_2,
  output IR_2
);

  INSTRUCTION instruction_1 (
    .T3(T3), .T4(T4), .T5(T5), .M0(M0), .M1(M1), .M2(M2), .M3(M3), .M4(M4), .M5(M5), .M6(M6), .M7(M7),
    .M8(M8), .M9(M9), .M10(M10), .M11(M11), .M12(M12), .M13(M13), .M14(M14), .M15(M15), .M16(M16), .M17(M17),
    .M18(M18), .M19(M19), .M20(M20), .M21(M21), .M22(M22), .M23(M23), .M24(M24), .M25(M25), .M26(M26),
    .M27(M27), .M28(M28), .M29(M29), .M30(M30), .M31(M31), .M32(M32), .M33(M33), .M34(M34), .M35(M35),
    .M36(M36), .M37(M37), .M38(M38), .M39(M39), .M40(M40), .M41(M41), .M42(M42), .M43(M43), .M44(M44),
    .M45(M45), .M46(M46), .M47(M47), .M48(M48), .M49(M49), .M50(M50), .M51(M51), .M52(M52), .M53(M53),
    .M54(M54), .M55(M55), .M56(M56), .M57(M57), .M58(M58), .M59(M59), .M60(M60), .M61(M61), .M62(M62),
    .M63(M63), .M64(M64), .M65(M65), .M66(M66), .M67(M67), .M68(M68), .M69(M69), .M70(M70), .M71(M71),
    .M72(M72), .M73(M73), .M74(M74), .M75(M75), .M76(M76), .M77(M77), .M78(M78), .M79(M79), .M80(M80),
    .M81(M81), .M82(M82), .M83(M83), .M84(M84), .M85(M85), .M86(M86), .M87(M87), .M88(M88), .M89(M89),
    .M90(M90), .M91(M91), .M92(M92), .M93(M93), .M94(M94), .M95(M95), .M96(M96), .M97(M97), .M98(M98),
    .M99(M99), .M100(M100), .M101(M101), .M102(M102), .M103(M103), .M104(M104), .M105(M105), .M106(M106),
    .M107(M107), .M108(M108), .M109(M109), .M110(M110), .M111(M111), .M112(M112), .M113(M113), .M114(M114),
    .M115(M115), .M116(M116), .M117(M117), .M118(M118), .M119(M119), .M120(M120), .M121(M121), .M122(M122),
    .M123(M123), .M124(M124), .M125(M125), .M126(M126), .M127(M127), .M128(M128), .M129(M129), .M130(M130),
    .M131(M131), .M132(M132), .M133(M133), .M134(M134), .M135(M135), .M136(M136), .M137(M137), .M138(M138),
    .M139(M139), .M140(M140), .M141(M141), .M142(M142), .M143(M143), .M144(M144), .M145(M145), .M146(M146),
    .M147(M147), .M148(M148), .M149(M149), .M150(M150), .M151(M151), .M152(M152), .M153(M153), .M154(M154),
    .M155(M155), .M156(M156), .M157(M157), .M158(M158), .M159(M159), .M160(M160), .M161(M161), .M162(M162),
    .M163(M163), .M164(M164), .M165(M165), .M166(M166), .M167(M167), .M168(M168), .M169(M169), .M170(M170),
    .M171(M171), .M172(M172), .M173(M173), .M174(M174), .M175(M175), .M176(M176), .M177(M177), .M178(M178),
    .M179(M179), .M190(M190), .M191(M191), .M192(M192), .M193(M193), .M194(M194), .M195(M195), .AND(AND),
    .OR(OR), .XOR(XOR), .ADD(ADD), .ADC(ADC), .SUB(SUB), .SBB(SBB), .MUL(MUL), .DIV(DIV), .CMP(CMP),
    .LOAD(LOAD));
  FIRST_REGISTER first_register_1 (
    .T3(T3), .T4(T4), .T5(T5), .E0(E0), .E1(E1), .E2(E2), .E3(E3), .E4(E4), .E5(E5), .E6(E6), .E7(E7),
    .E8(E8), .E9(E9), .E10(E10), .E11(E11), .E12(E12), .E13(E13), .E14(E14), .E15(E15), .E16(E16), .E17(E17),
    .E18(E18), .E19(E19), .E20(E20), .E21(E21), .E22(E22), .E23(E23), .E24(E24), .M0(M0), .M1(M1), .M2(M2),
    .M3(M3), .M4(M4), .M5(M5), .M6(M6), .M7(M7), .M8(M8), .M9(M9), .M10(M10), .M11(M11), .M12(M12),
    .M13(M13), .M14(M14), .M15(M15), .M16(M16), .M17(M17), .M18(M18), .M19(M19), .M20(M20), .M21(M21),
    .M22(M22), .M23(M23), .M24(M24), .M25(M25), .M26(M26), .M27(M27), .M28(M28), .M29(M29), .M30(M30),
    .M31(M31), .M32(M32), .M33(M33), .M34(M34), .M35(M35), .M36(M36), .M37(M37), .M38(M38), .M39(M39),
    .M40(M40), .M41(M41), .M42(M42), .M43(M43), .M44(M44), .M45(M45), .M46(M46), .M47(M47), .M48(M48),
    .M49(M49), .M50(M50), .M51(M51), .M52(M52), .M53(M53), .M54(M54), .M55(M55), .M56(M56), .M57(M57),
    .M58(M58), .M59(M59), .M60(M60), .M61(M61), .M62(M62), .M63(M63), .M64(M64), .M65(M65), .M66(M66),
    .M67(M67), .M68(M68), .M69(M69), .M70(M70), .M71(M71), .M72(M72), .M73(M73), .M74(M74), .M75(M75),
    .M76(M76), .M77(M77), .M78(M78), .M79(M79), .M80(M80), .M81(M81), .M82(M82), .M83(M83), .M84(M84),
    .M85(M85), .M86(M86), .M87(M87), .M88(M88), .M89(M89), .M90(M90), .M91(M91), .M92(M92), .M93(M93),
    .M94(M94), .M95(M95), .M96(M96), .M97(M97), .M98(M98), .M99(M99), .M100(M100), .M101(M101), .M102(M102),
    .M103(M103), .M104(M104), .M105(M105), .M106(M106), .M107(M107), .M108(M108), .M109(M109), .M110(M110),
    .M111(M111), .M112(M112), .M113(M113), .M114(M114), .M115(M115), .M116(M116), .M117(M117), .M118(M118),
    .M119(M119), .M120(M120), .M121(M121), .M122(M122), .M123(M123), .M124(M124), .M125(M125), .M126(M126),
    .M127(M127), .M128(M128), .M129(M129), .M130(M130), .M131(M131), .M132(M132), .M133(M133), .M134(M134),
    .M135(M135), .M136(M136), .M137(M137), .M138(M138), .M139(M139), .M140(M140), .M141(M141), .M142(M142),
    .M143(M143), .M144(M144), .M145(M145), .M146(M146), .M147(M147), .M148(M148), .M149(M149), .M150(M150),
    .M151(M151), .M152(M152), .M153(M153), .M154(M154), .M155(M155), .M156(M156), .M157(M157), .M158(M158),
    .M159(M159), .M160(M160), .M161(M161), .M162(M162), .M163(M163), .M164(M164), .M165(M165), .M166(M166),
    .M167(M167), .M168(M168), .M169(M169), .M170(M170), .M171(M171), .M172(M172), .M173(M173), .M174(M174),
    .M175(M175), .M176(M176), .M177(M177), .M178(M178), .M179(M179), .M190(M190), .M191(M191), .M192(M192),
    .M193(M193), .M194(M194), .M195(M195), .AX(AX_1), .BX(BX_1), .CX(CX_1), .DX(DX_1), .EX(EX_1));
  SECOND_REGISTER second_register_1 (
    .T3(T3), .T4(T4), .T5(T5), .E0(E0), .E1(E1), .E2(E2), .E3(E3), .E4(E4), .E5(E5), .E6(E6), .E7(E7),
    .E8(E8), .E9(E9), .E10(E10), .E11(E11), .E12(E12), .E13(E13), .E14(E14), .E15(E15), .E16(E16), .E17(E17),
    .E18(E18), .E19(E19), .E20(E20), .E21(E21), .E22(E22), .E23(E23), .E24(E24), .M0(M0), .M1(M1), .M2(M2),
    .M3(M3), .M4(M4), .M5(M5), .M6(M6), .M7(M7), .M8(M8), .M9(M9), .M10(M10), .M11(M11), .M12(M12),
    .M13(M13), .M14(M14), .M15(M15), .M16(M16), .M17(M17), .M18(M18), .M19(M19), .M20(M20), .M21(M21),
    .M22(M22), .M23(M23), .M24(M24), .M25(M25), .M26(M26), .M27(M27), .M28(M28), .M29(M29), .M30(M30),
    .M31(M31), .M32(M32), .M33(M33), .M34(M34), .M35(M35), .M36(M36), .M37(M37), .M38(M38), .M39(M39),
    .M40(M40), .M41(M41), .M42(M42), .M43(M43), .M44(M44), .M45(M45), .M46(M46), .M47(M47), .M48(M48),
    .M49(M49), .M50(M50), .M51(M51), .M52(M52), .M53(M53), .M54(M54), .M55(M55), .M56(M56), .M57(M57),
    .M58(M58), .M59(M59), .M60(M60), .M61(M61), .M62(M62), .M63(M63), .M64(M64), .M65(M65), .M66(M66),
    .M67(M67), .M68(M68), .M69(M69), .M70(M70), .M71(M71), .M72(M72), .M73(M73), .M74(M74), .M75(M75),
    .M76(M76), .M77(M77), .M78(M78), .M79(M79), .M80(M80), .M81(M81), .M82(M82), .M83(M83), .M84(M84),
    .M85(M85), .M86(M86), .M87(M87), .M88(M88), .M89(M89), .M90(M90), .M91(M91), .M92(M92), .M93(M93),
    .M94(M94), .M95(M95), .M96(M96), .M97(M97), .M98(M98), .M99(M99), .M100(M100), .M101(M101), .M102(M102),
    .M103(M103), .M104(M104), .M105(M105), .M106(M106), .M107(M107), .M108(M108), .M109(M109), .M110(M110),
    .M111(M111), .M112(M112), .M113(M113), .M114(M114), .M115(M115), .M116(M116), .M117(M117), .M118(M118),
    .M119(M119), .M120(M120), .M121(M121), .M122(M122), .M123(M123), .M124(M124), .M125(M125), .M126(M126),
    .M127(M127), .M128(M128), .M129(M129), .M130(M130), .M131(M131), .M132(M132), .M133(M133), .M134(M134),
    .M135(M135), .M136(M136), .M137(M137), .M138(M138), .M139(M139), .M140(M140), .M141(M141), .M142(M142),
    .M143(M143), .M144(M144), .M145(M145), .M146(M146), .M147(M147), .M148(M148), .M149(M149), .M150(M150),
    .M151(M151), .M152(M152), .M153(M153), .M154(M154), .M155(M155), .M156(M156), .M157(M157), .M158(M158),
    .M159(M159), .M160(M160), .M161(M161), .M162(M162), .M163(M163), .M164(M164), .M165(M165), .M166(M166),
    .M167(M167), .M168(M168), .M169(M169), .M170(M170), .M171(M171), .M172(M172), .M173(M173), .M174(M174),
    .M175(M175), .M176(M176), .M177(M177), .M178(M178), .M179(M179), .M190(M190), .M191(M191), .M192(M192),
    .M193(M193), .M194(M194), .M195(M195), .AX(AX_2), .BX(BX_2), .CX(CX_2), .DX(DX_2), .EX(EX_2), .DR(DR_2),
    .IR(IR_2));
endmodule
