// Logisim project FLAGS.circ as structural Verilog: 1 circuit, main circuit FLAGS
module FLAGS (
  input  T3,
  input  T4,
  input  T5,
  input  M0,
  input  M1,
  input  M2,
  input  M3,
  input  M4,
  input  M5,
  input  M6,
  input  M7,
  input  M8,
  input  M9,
  input  M10,
  input  M11,
  input  M12,
  input  M13,
  input  M14,
  input  M15,
  input  M16,
  input  M17,
  input  M18,
  input  M19,
  input  M20,
  input  M21,
  input  M22,
  input  M23,
  input  M24,
  input  M25,
  input  M26,
  input  M27,
  input  M28,
  input  M29,
  input  M30,
  input  M31,
  input  M32,
  input  M33,
  input  M34,
  input  M35,
  input  M36,
  input  M37,
  input  M38,
  input  M39,
  input  M40,
  input  M41,
  input  M42,
  input  M43,
  input  M44,
  input  M45,
  input  M46,
  input  M47,
  input  M48,
  input  M49,
  input  M50,
  input  M51,
  input  M52,
  input  M53,
  input  M54,
  input  M55,
  input  M56,
  input  M57,
  input  M58,
  input  M59,
  input  M60,
  input  M61,
  input  M62,
  input  M63,
  input  M64,
  input  M65,
  input  M66,
  input  M67,
  input  M68,
  input  M69,
  input  M70,
  input  M71,
  input  M72,
  input  M73,
  input  M74,
  input  M75,
  input  M76,
  input  M77,
  input  M78,
  input  M79,
  input  M80,
  input  M81,
  input  M82,
  input  M83,
  input  M84,
  input  M85,
  input  M86,
  input  M87,
  input  M88,
  input  M89,
  input  M90,
  input  M91,
  input  M92,
  input  M93,
  input  M94,
  input  M95,
  input  M96,
  input  M97,
  input  M98,
  input  M99,
  input  M100,
  input  M101,
  input  M102,
  input  M103,
  input  M104,
  input  M105,
  input  M106,
  input  M107,
  input  M108,
  input  M109,
  input  M110,
  input  M111,
  input  M112,
  input  M113,
  input  M114,
  input  M115,
  input  M116,
  input  M117,
  input  M118,
  input  M119,
  input  M120,
  input  M121,
  input  M122,
  input  M123,
  input  M124,
  input  M125,
  input  M126,
  input  M127,
  input  M128,
  input  M129,
  input  M130,
  input  M131,
  input  M132,
  input  M133,
  input  M134,
  input  M135,
  input  M136,
  input  M137,
  input  M138,
  input  M139,
  input  M140,
  input  M141,
  input  M142,
  input  M143,
  input  M144,
  input  M145,
  input  M146,
  input  M147,
  input  M148,
  input  M149,
  input  M150,
  input  M151,
  input  M152,
  input  M153,
  input  M154,
  input  M155,
  input  M156,
  input  M157,
  input  M158,
  input  M159,
  input  M160,
  input  M161,
  input  M162,
  input  M163,
  input  M164,
  input  M165,
  input  M166,
  input  M167,
  input  M168,
  input  M169,
  input  M222,
  input  M223,
  input  M224,
  input  M225,
  output Z_LOAD,
  output Z_CLR,
  output Z_CML,
  output C_LOAD,
  output C_CLR,
  output C_CML
);

  wire and_1_out, and_2_out, and_3_out, and_4_out, and_5_out, and_6_out, or_1_out, or_2_out, or_3_out,
       or_4_out, or_5_out, or_6_out, or_7_out, or_8_out, or_9_out;

  or or_1 (or_1_out, M169, M167, M166, M165, M164, M163, M152, M150, M149, M148, M147, M146, M135, M133, M132, M131, M130, M129, M118, M116, M115, M114, M113, M112, M101, M99, M98, M97, M96, M95, M84, M82);
  or or_2 (or_2_out, or_1_out, M81, M80, M79, M78, M67, M65, M64, M63, M62, M61, M50, M48, M47, M46, M45, M44, M33, M31, M30, M29, M28, M27, M16, M14, M13, M12, M11, M10);
  or or_3 (or_3_out, M168, M162, M161, M160, M159, M158, M151, M145, M144, M143, M142, M141, M134, M128, M127, M126, M125, M124, M117, M111, M110, M109, M108, M107, M100, M94, M93, M92, M91, M90, M83, M77);
  or or_4 (or_4_out, or_3_out, M76, M75, M74, M73, M66, M60, M59, M58, M57, M56, M49, M43, M42, M41, M40, M39, M32, M26, M25, M24, M23, M22, M15, M9, M8, M7, M6, M5);
  or or_5 (or_5_out, M157, M156, M155, M154, M153, M140, M139, M138, M137, M136, M123, M122, M121, M120, M119, M106, M105, M104, M103, M102, M89, M88, M87, M86, M85, M72);
  or or_6 (or_6_out, or_5_out, M71, M70, M69, M68, M55, M54, M53, M52, M51, M38, M37, M36, M35, M34, M21, M20, M19, M18, M17, M4, M3, M2, M1, M0);
  or or_7 (or_7_out, M169, M167, M166, M165, M164, M163, M118, M116, M115, M114, M113, M112, M101, M99, M98, M97, M96, M95, M84, M82, M81, M80, M79, M78, M67, M65, M64, M63, M62, M61);
  or or_8 (or_8_out, M168, M162, M161, M160, M159, M158, M117, M111, M110, M109, M108, M107, M100, M94, M93, M92, M91, M90, M83, M77, M76, M75, M74, M73, M66, M60, M59, M58, M57, M56);
  or or_9 (or_9_out, M157, M156, M155, M154, M153, M106, M105, M104, M103, M102, M89, M88, M87, M86, M85, M72, M71, M70, M69, M68, M55, M54, M53, M52, M51);
  and and_1 (and_1_out, or_2_out, T3);
  and and_2 (and_2_out, or_4_out, T4);
  and and_3 (and_3_out, or_6_out, T5);
  and and_4 (and_4_out, or_7_out, T3);
  and and_5 (and_5_out, or_8_out, T4);
  and and_6 (and_6_out, or_9_out, T5);
  or or_10 (Z_LOAD, and_1_out, and_2_out, and_3_out);
  or or_11 (C_LOAD, and_4_out, and_5_out, and_6_out);

  assign C_CLR = M222;
  assign C_CML = M223;
  assign Z_CLR = M224;
  assign Z_CML = M225;
endmodule
