// Logisim project GENERAL_PURPOSE.circ as structural Verilog: 1 circuit, main circuit GENERAL_PURPOSE
// GENERAL_PURPOSE_REGISTERS
module GENERAL_PURPOSE (
  input  E0,
  input  E1,
  input  E2,
  input  M0,
  input  M1,
  input  M2,
  input  M3,
  input  M4,
  input  M5,
  input  M6,
  input  M7,
  input  M8,
  input  M9,
  input  M10,
  input  M11,
  input  M12,
  input  M13,
  input  M14,
  input  M15,
  input  M16,
  input  M17,
  input  M18,
  input  M19,
  input  M20,
  input  M21,
  input  M22,
  input  M23,
  input  M24,
  input  M25,
  input  M26,
  input  M27,
  input  M28,
  input  M29,
  input  M30,
  input  M31,
  input  M32,
  input  M33,
  input  M34,
  input  M35,
  input  M36,
  input  M37,
  input  M38,
  input  M39,
  input  M40,
  input  M41,
  input  M42,
  input  M43,
  input  M44,
  input  M45,
  input  M46,
  input  M47,
  input  M48,
  input  M49,
  input  M50,
  input  M51,
  input  M52,
  input  M53,
  input  M54,
  input  M55,
  input  M56,
  input  M57,
  input  M58,
  input  M59,
  input  M60,
  input  M61,
  input  M62,
  input  M63,
  input  M64,
  input  M65,
  input  M66,
  input  M67,
  input  M68,
  input  M69,
  input  M70,
  input  M71,
  input  M72,
  input  M73,
  input  M74,
  input  M75,
  input  M76,
  input  M77,
  input  M78,
  input  M79,
  input  M80,
  input  M81,
  input  M82,
  input  M83,
  input  M84,
  input  M85,
  input  M86,
  input  M87,
  input  M88,
  input  M89,
  input  M90,
  input  M91,
  input  M92,
  input  M93,
  input  M94,
  input  M95,
  input  M96,
  input  M97,
  input  M98,
  input  M99,
  input  M100,
  input  M101,
  input  M102,
  input  M103,
  input  M104,
  input  M105,
  input  M106,
  input  M107,
  input  M108,
  input  M109,
  input  M110,
  input  M111,
  input  M112,
  input  M113,
  input  M114,
  input  M115,
  input  M116,
  input  M117,
  input  M118,
  input  M119,
  input  M120,
  input  M121,
  input  M122,
  input  M123,
  input  M124,
  input  M125,
  input  M126,
  input  M127,
  input  M128,
  input  M129,
  input  M130,
  input  M131,
  input  M132,
  input  M133,
  input  M134,
  input  M135,
  input  M136,
  input  M137,
  input  M138,
  input  M139,
  input  M140,
  input  M141,
  input  M142,
  input  M143,
  input  M144,
  input  M145,
  input  M146,
  input  M147,
  input  M148,
  input  M149,
  input  M150,
  input  M151,
  input  M152,
  input  M170,
  input  M171,
  input  M172,
  input  M173,
  input  M174,
  input  M175,
  input  M176,
  input  M177,
  input  M178,
  input  M179,
  input  M180,
  input  M181,
  input  M182,
  input  M183,
  input  M184,
  input  M185,
  input  M186,
  input  M187,
  input  M188,
  input  M189,
  input  M190,
  input  M191,
  input  M192,
  input  M193,
  input  M194,
  input  M195,
  input  M198,
  input  M201,
  input  M204,
  input  M207,
  input  M210,
  input  M213,
  input  M214,
  input  M215,
  input  M216,
  input  M217,
  input  M218,
  input  M219,
  input  M220,
  input  M221,
  input  E3,
  input  E4,
  input  E5,
  input  E6,
  input  E7,
  input  E8,
  input  E9,
  input  E10,
  input  E11,
  input  E12,
  input  E13,
  input  E14,
  input  E15,
  input  E16,
  input  E17,
  input  E18,
  input  E19,
  input  E20,
  input  E21,
  input  E22,
  input  E23,
  input  E24,
  input  T3,
  input  T4,
  input  T5,
  input  C,
  input  Z,
  output AX_INC,
  output AX_DEX,
  output AX_SHL,
  output AX_SHR,
  output AX_CIL,
  output AX_CIR,
  output AX_CML,
  output AX_CLR,
  output AX_LOAD,
  output AX_BUS,
  output BX_INC,
  output BX_DEX,
  output BX_SHL,
  output BX_SHR,
  output BX_CIL,
  output BX_CIR,
  output BX_CML,
  output BX_CLR,
  output BX_LOAD,
  output BX_BUS,
  output CX_INC,
  output CX_DEX,
  output CX_SHL,
  output CX_SHR,
  output CX_CIL,
  output CX_CIR,
  output CX_CML,
  output CX_CLR,
  output CX_LOAD,
  output CX_BUS,
  output DX_INC,
  output DX_DEX,
  output DX_SHL,
  output DX_SHR,
  output DX_CIL,
  output DX_CIR,
  output DX_CML,
  output DX_CLR,
  output DX_LOAD,
  output DX_BUS,
  output EX_INC,
  output EX_DEX,
  output EX_SHL,
  output EX_SHR,
  output EX_CIL,
  output EX_CIR,
  output EX_CML,
  output EX_CLR,
  output EX_LOAD,
  output EX_BUS
);

  AX ax_1 (
    .C(C), .Z(Z), .T3(T3), .T4(T4), .T5(T5), .E0(E0), .E1(E1), .E2(E2), .E3(E3), .E4(E4), .E20(E20),
    .E21(E21), .E22(E22), .E23(E23), .E24(E24), .M0(M0), .M5(M5), .M10(M10), .M15(M15), .M16(M16), .M17(M17),
    .M22(M22), .M27(M27), .M32(M32), .M33(M33), .M34(M34), .M39(M39), .M44(M44), .M49(M49), .M50(M50),
    .M51(M51), .M56(M56), .M61(M61), .M66(M66), .M67(M67), .M68(M68), .M73(M73), .M78(M78), .M83(M83),
    .M84(M84), .M85(M85), .M90(M90), .M95(M95), .M100(M100), .M101(M101), .M102(M102), .M107(M107),
    .M112(M112), .M117(M117), .M118(M118), .M119(M119), .M123(M123), .M124(M124), .M128(M128), .M129(M129),
    .M133(M133), .M134(M134), .M135(M135), .M136(M136), .M140(M140), .M141(M141), .M145(M145), .M146(M146),
    .M150(M150), .M151(M151), .M152(M152), .M170(M170), .M175(M175), .M180(M180), .M185(M185), .M190(M190),
    .M195(M195), .M198(M198), .M201(M201), .M204(M204), .M207(M207), .M210(M210), .M213(M213), .M214(M214),
    .M215(M215), .M216(M216), .M217(M217), .M218(M218), .M219(M219), .M220(M220), .M221(M221),
    .AX_INC(AX_INC), .AX_DEC(AX_DEX), .AX_SHL(AX_SHL), .AX_SHR(AX_SHR), .AX_CIL(AX_CIL), .AX_CIR(AX_CIR),
    .AX_CML(AX_CML), .AX_CLR(AX_CLR), .AX_LOAD(AX_LOAD), .AX_BUS(AX_BUS));
  BX bx_1 (
    .C(C), .Z(Z), .T3(T3), .T4(T4), .T5(T5), .E0(E0), .E1(E1), .E2(E2), .E3(E3), .E4(E4), .E5(E5), .E6(E6),
    .E7(E7), .E8(E8), .E9(E9), .M1(M1), .M6(M6), .M11(M11), .M15(M15), .M16(M16), .M18(M18), .M23(M23),
    .M28(M28), .M32(M32), .M33(M33), .M35(M35), .M40(M40), .M45(M45), .M49(M49), .M50(M50), .M52(M52),
    .M57(M57), .M62(M62), .M66(M66), .M67(M67), .M69(M69), .M74(M74), .M79(M79), .M83(M83), .M84(M84),
    .M86(M86), .M91(M91), .M96(M96), .M100(M100), .M101(M101), .M103(M103), .M108(M108), .M113(M113),
    .M117(M117), .M118(M118), .M119(M119), .M120(M120), .M124(M124), .M125(M125), .M129(M129), .M130(M130),
    .M134(M134), .M135(M135), .M136(M136), .M137(M137), .M141(M141), .M142(M142), .M146(M146), .M147(M147),
    .M151(M151), .M152(M152), .M171(M171), .M176(M176), .M181(M181), .M186(M186), .M191(M191), .M195(M195),
    .M198(M198), .M201(M201), .M204(M204), .M207(M207), .M210(M210), .M213(M213), .M214(M214), .M215(M215),
    .M216(M216), .M217(M217), .M218(M218), .M219(M219), .M220(M220), .M221(M221), .BX_INC(BX_INC),
    .BX_DEC(BX_DEX), .BX_SHL(BX_SHL), .BX_SHR(BX_SHR), .BX_CIL(BX_CIL), .BX_CIR(BX_CIR), .BX_CML(BX_CML),
    .BX_CLR(BX_CLR), .BX_LOAD(BX_LOAD), .BX_BUS(BX_BUS));
  CX cx_1 (
    .C(C), .Z(Z), .T3(T3), .T4(T4), .T5(T5), .E2(E2), .E5(E5), .E6(E6), .E7(E7), .E8(E8), .E9(E9), .E10(E10),
    .E11(E11), .E12(E12), .E13(E13), .E14(E14), .M2(M2), .M7(M7), .M12(M12), .M15(M15), .M16(M16), .M19(M19),
    .M24(M24), .M29(M29), .M32(M32), .M33(M33), .M36(M36), .M41(M41), .M46(M46), .M49(M49), .M50(M50),
    .M53(M53), .M58(M58), .M63(M63), .M66(M66), .M67(M67), .M70(M70), .M75(M75), .M80(M80), .M83(M83),
    .M84(M84), .M87(M87), .M92(M92), .M97(M97), .M100(M100), .M101(M101), .M104(M104), .M109(M109),
    .M114(M114), .M117(M117), .M118(M118), .M120(M120), .M121(M121), .M125(M125), .M126(M126), .M130(M130),
    .M131(M131), .M134(M134), .M135(M135), .M137(M137), .M138(M138), .M142(M142), .M143(M143), .M147(M147),
    .M148(M148), .M151(M151), .M152(M152), .M172(M172), .M177(M177), .M182(M182), .M187(M187), .M192(M192),
    .M195(M195), .M198(M198), .M201(M201), .M204(M204), .M207(M207), .M210(M210), .M213(M213), .M214(M214),
    .M215(M215), .M216(M216), .M217(M217), .M218(M218), .M219(M219), .M220(M220), .M221(M221),
    .CX_INC(CX_INC), .CX_DEC(CX_DEX), .CX_SHL(CX_SHL), .CX_SHR(CX_SHR), .CX_CIL(CX_CIL), .CX_CIR(CX_CIR),
    .CX_CML(CX_CML), .CX_CLR(CX_CLR), .CX_LOAD(CX_LOAD), .CX_BUS(CX_BUS));
  DX dx_1 (
    .C(C), .Z(Z), .T3(T3), .T4(T4), .T5(T5), .E3(E3), .E10(E10), .E11(E11), .E12(E12), .E13(E13), .E14(E14),
    .E15(E15), .E16(E16), .E17(E17), .E18(E18), .E19(E19), .M3(M3), .M8(M8), .M13(M13), .M15(M15), .M16(M16),
    .M20(M20), .M25(M25), .M30(M30), .M32(M32), .M33(M33), .M37(M37), .M42(M42), .M47(M47), .M49(M49),
    .M50(M50), .M54(M54), .M59(M59), .M64(M64), .M66(M66), .M67(M67), .M71(M71), .M76(M76), .M81(M81),
    .M83(M83), .M84(M84), .M88(M88), .M93(M93), .M98(M98), .M100(M100), .M101(M101), .M105(M105),
    .M110(M110), .M115(M115), .M117(M117), .M118(M118), .M121(M121), .M122(M122), .M126(M126), .M127(M127),
    .M131(M131), .M132(M132), .M134(M134), .M135(M135), .M138(M138), .M139(M139), .M143(M143), .M144(M144),
    .M148(M148), .M149(M149), .M151(M151), .M152(M152), .M173(M173), .M178(M178), .M183(M183), .M188(M188),
    .M193(M193), .M195(M195), .M198(M198), .M201(M201), .M204(M204), .M207(M207), .M210(M210), .M213(M213),
    .M214(M214), .M215(M215), .M216(M216), .M217(M217), .M218(M218), .M219(M219), .M220(M220), .M221(M221),
    .DX_INC(DX_INC), .DX_DEC(DX_DEX), .CX_SHL(DX_SHL), .DX_SHR(DX_SHR), .DX_CIL(DX_CIL), .DX_CIR(DX_CIR),
    .DX_CML(DX_CML), .DX_CLR(DX_CLR), .DX_LOAD(DX_LOAD), .DX_BUS(DX_BUS));
  EX ex_1 (
    .C(C), .Z(Z), .T3(T3), .T4(T4), .T5(T5), .E4(E4), .E15(E15), .E16(E16), .E17(E17), .E18(E18), .E19(E19),
    .E20(E20), .E21(E21), .E22(E22), .E23(E23), .E24(E24), .M4(M4), .M9(M9), .M14(M14), .M15(M15), .M16(M16),
    .M21(M21), .M26(M26), .M31(M31), .M32(M32), .M33(M33), .M38(M38), .M43(M43), .M48(M48), .M49(M49),
    .M50(M50), .M55(M55), .M60(M60), .M65(M65), .M66(M66), .M67(M67), .M72(M72), .M77(M77), .M82(M82),
    .M83(M83), .M84(M84), .M89(M89), .M94(M94), .M99(M99), .M100(M100), .M101(M101), .M106(M106),
    .M111(M111), .M116(M116), .M117(M117), .M118(M118), .M122(M122), .M123(M123), .M127(M127), .M128(M128),
    .M132(M132), .M133(M133), .M134(M134), .M135(M135), .M139(M139), .M140(M140), .M144(M144), .M145(M145),
    .M149(M149), .M150(M150), .M151(M151), .M152(M152), .M174(M174), .M179(M179), .M184(M184), .M189(M189),
    .M194(M194), .M195(M195), .M198(M198), .M201(M201), .M204(M204), .M207(M207), .M210(M210), .M213(M213),
    .M214(M214), .M215(M215), .M216(M216), .M217(M217), .M218(M218), .M219(M219), .M220(M220), .M221(M221),
    .EX_INC(EX_INC), .EX_DEC(EX_DEX), .EX_SHL(EX_SHL), .EX_SHR(EX_SHR), .EX_CIL(EX_CIL), .EX_CIR(EX_CIR),
    .EX_CML(EX_CML), .EX_CLR(EX_CLR), .EX_LOAD(EX_LOAD), .EX_BUS(EX_BUS));
endmodule
