// Logisim project MEMORY.circ as structural Verilog: 1 circuit, main circuit MEMORY
module MEMORY (
  input  T1,
  input  T3,
  input  T4,
  input  E0,
  input  E1,
  input  E2,
  input  E3,
  input  E4,
  input  E5,
  input  E6,
  input  E7,
  input  E8,
  input  E9,
  input  E10,
  input  E11,
  input  E12,
  input  E13,
  input  E14,
  input  E15,
  input  E16,
  input  E17,
  input  E18,
  input  E19,
  input  E20,
  input  E21,
  input  E22,
  input  E23,
  input  E24,
  input  M0,
  input  M1,
  input  M2,
  input  M3,
  input  M4,
  input  M5,
  input  M6,
  input  M7,
  input  M8,
  input  M9,
  input  M15,
  input  M17,
  input  M18,
  input  M19,
  input  M20,
  input  M21,
  input  M22,
  input  M23,
  input  M24,
  input  M25,
  input  M26,
  input  M32,
  input  M34,
  input  M35,
  input  M36,
  input  M37,
  input  M38,
  input  M39,
  input  M40,
  input  M41,
  input  M42,
  input  M43,
  input  M49,
  input  M51,
  input  M52,
  input  M53,
  input  M54,
  input  M55,
  input  M56,
  input  M57,
  input  M58,
  input  M59,
  input  M60,
  input  M66,
  input  M68,
  input  M69,
  input  M70,
  input  M71,
  input  M72,
  input  M73,
  input  M74,
  input  M75,
  input  M76,
  input  M77,
  input  M83,
  input  M85,
  input  M86,
  input  M87,
  input  M88,
  input  M89,
  input  M90,
  input  M91,
  input  M92,
  input  M93,
  input  M94,
  input  M100,
  input  M102,
  input  M103,
  input  M104,
  input  M105,
  input  M106,
  input  M107,
  input  M108,
  input  M109,
  input  M110,
  input  M111,
  input  M117,
  input  M119,
  input  M120,
  input  M121,
  input  M122,
  input  M123,
  input  M124,
  input  M125,
  input  M126,
  input  M127,
  input  M128,
  input  M134,
  input  M136,
  input  M137,
  input  M138,
  input  M139,
  input  M140,
  input  M141,
  input  M142,
  input  M143,
  input  M144,
  input  M145,
  input  M151,
  input  M153,
  input  M154,
  input  M155,
  input  M156,
  input  M157,
  input  M158,
  input  M159,
  input  M160,
  input  M161,
  input  M162,
  input  M168,
  input  M170,
  input  M171,
  input  M172,
  input  M173,
  input  M174,
  input  M175,
  input  M176,
  input  M177,
  input  M178,
  input  M179,
  input  M180,
  input  M181,
  input  M182,
  input  M183,
  input  M184,
  input  M185,
  input  M186,
  input  M187,
  input  M188,
  input  M189,
  input  M196,
  input  M199,
  input  M202,
  input  M205,
  input  M208,
  input  M211,
  output STR,
  output BUS,
  output [2:0] MUX
);

  wire and_1_out, and_2_out, and_3_out, and_4_out, and_5_out, and_6_out, and_7_out, and_8_out, and_9_out,
       and_10_out, and_11_out, and_12_out, and_13_out, or_1_out, or_2_out, or_3_out, or_4_out, or_5_out,
       or_6_out, or_7_out, or_8_out, or_9_out, or_10_out, or_11_out, or_12_out, or_13_out, or_14_out,
       or_15_out, or_16_out, or_17_out, or_18_out, or_19_out, or_20_out, or_21_out, or_22_out, or_23_out,
       or_24_out, or_25_out, or_27_out, or_28_out, or_30_out;

  or or_1 (or_1_out, M189, M188, M187, M186, M185);
  or or_2 (or_2_out, M184, M183, M182, M181, M180);
  or or_3 (or_3_out, E24, E23, E22, E21, E20, E19, E18, E17, E16, E15, E14, E13, E12, E11, E10, E9, E8, E7, E6, E5, E4, E3, E2, E1, E0);
  or or_4 (or_4_out, M168, M151, M134, M117, M100, M83, M66, M49, M32, M15);
  or or_5 (or_5_out, M211, M208, M205, M202, M199, M196, M184, M183, M182, M181, M180, M179, M178, M177, M176, M175, M174, M173, M172, M171, M170, M162, M161, M160, M159, M158, M157, M156, M155, M154, M153, M145);
  or or_6 (or_6_out, or_5_out, M144, M143, M142, M141, M140, M139, M138, M137, M136, M128, M127, M126, M125, M124, M123, M122, M121, M120, M119, M111, M110, M109, M108, M107, M106, M105, M104, M103, M102, M94, M93);
  or or_7 (or_7_out, or_6_out, M92, M91, M90, M89, M88, M87, M86, M85, M77, M76, M75, M74, M73, M72, M71, M70, M69, M68, M60, M59, M58, M57, M56, M55, M54, M53, M52, M51, M43, M42, M41);
  or or_8 (or_8_out, or_7_out, M40, M39, M38, M37, M36, M35, M34, M26, M25, M24, M23, M22, M21, M20, M19, M18, M17, M9, M8, M7, M6, M5, M4, M3, M2, M1, M0);
  or or_9 (or_9_out, M174, M173, M172, M171, M170, M157, M156, M155, M154, M153, M140, M139, M138, M137, M136, M123, M122, M121, M120, M119, M106, M105);
  or or_10 (or_10_out, or_9_out, M104, M103, M102, M89, M88, M87, M86, M85, M72, M71, M70, M69, M68, M55, M54, M53, M52, M51, M38, M37, M36);
  or or_11 (or_11_out, or_10_out, M35, M34, M21, M20, M19, M18, M17, M4, M3, M2, M1, M0);
  or or_12 (or_12_out, M211, M208, M205, M202, M199, M196, M189, M188, M187, M186, M185, M184, M183, M182, M181, M180, M179, M178, M177, M176, M175, M174);
  or or_13 (or_13_out, or_12_out, M173, M172, M171, M170, M162, M161, M160, M159, M158, M157, M156, M155, M154, M153, M145, M144, M143, M142, M141, M140, M139);
  or or_14 (or_14_out, or_13_out, M138, M137, M136, M128, M127, M126, M125, M124, M123, M122, M121, M120, M119, M111, M110, M109, M108, M107, M106, M105, M104);
  or or_15 (or_15_out, or_14_out, M103, M102, M94, M93, M92, M91, M90, M89, M88, M87, M86, M85, M77, M76, M75, M74, M73, M72, M71, M70, M69);
  or or_16 (or_16_out, or_15_out, M68, M60, M59, M58, M57, M56, M55, M54, M53, M52, M51, M43, M42, M41, M40, M39, M38, M37, M36, M35, M34);
  or or_17 (or_17_out, or_16_out, M26, M25, M24, M23, M22, M21, M20, M19, M18, M17, M9, M8, M7, M6, M5, M4, M3, M2, M1, M0);
  or or_18 (or_18_out, M184, M183, M182, M181, M180, M174, M173, M172, M171, M170, M157, M156, M155, M154, M153, M140, M139, M138, M137, M136, M123, M122, M121, M120, M119, M106, M105, M104, M103, M102, M89, M88);
  or or_19 (or_19_out, or_18_out, M87, M86, M85, M72, M71, M70, M69, M68, M55, M54, M53, M52, M51, M38, M37, M36, M35, M34, M21, M20, M19, M18, M17, M4, M3, M2, M1, M0);
  or or_20 (or_20_out, E20, E15, E10, E5, E0);
  or or_21 (or_21_out, E21, E16, E11, E6, E1);
  or or_22 (or_22_out, E22, E17, E12, E7, E2);
  or or_23 (or_23_out, E23, E18, E13, E8, E3);
  or or_24 (or_24_out, E24, E19, E14, E9, E4);
  and and_1 (and_1_out, or_1_out, T3);
  and and_2 (and_2_out, T4, or_2_out);
  and and_3 (and_3_out, or_11_out, T4);
  or or_25 (or_25_out, M168, M151, M134, M117, M100, M83, M66, M49, M32, M15);
  or or_26 (STR, and_1_out, and_2_out);
  and and_4 (and_4_out, or_3_out, or_4_out);
  and and_5 (and_5_out, or_17_out, T3);
  and and_6 (and_6_out, or_19_out, T4);
  or or_27 (or_27_out, and_4_out, or_8_out);
  and and_7 (and_7_out, or_27_out, T3);
  or or_28 (or_28_out, and_5_out, and_6_out);
  and and_8 (and_8_out, or_25_out, or_20_out, T3);
  and and_9 (and_9_out, or_25_out, or_21_out, T3);
  and and_10 (and_10_out, or_25_out, or_22_out, T3);
  and and_11 (and_11_out, or_25_out, or_23_out, T3);
  and and_12 (and_12_out, or_25_out, or_24_out, T3);
  or or_29 (BUS, and_7_out, and_3_out, T1);
  and and_13 (and_13_out, ~and_8_out, ~and_9_out, ~and_10_out, ~and_11_out, ~and_12_out);  // AND_Gate
  assign MUX = or_30_out ? 3'b000 : 3'bz;  // Controlled_Buffer controlled_buffer_1
  or or_30 (or_30_out, or_28_out, and_13_out);
  assign MUX = and_8_out ? 3'b001 : 3'bz;  // Controlled_Buffer controlled_buffer_2
  assign MUX = and_9_out ? 3'b010 : 3'bz;  // Controlled_Buffer controlled_buffer_3
  assign MUX = and_10_out ? 3'b011 : 3'bz;  // Controlled_Buffer controlled_buffer_4
  assign MUX = and_11_out ? 3'b100 : 3'bz;  // Controlled_Buffer controlled_buffer_5
  assign MUX = and_12_out ? 3'b101 : 3'bz;  // Controlled_Buffer controlled_buffer_6
endmodule
