// Logisim project SPECIAL_PURPOSE.circ as structural Verilog: 1 circuit, main circuit SPECIAL_PURPOSE
module SPECIAL_PURPOSE (
  input  C,
  input  Z,
  input  T0,
  input  T1,
  input  T2,
  input  T3,
  input  T4,
  input  T5,
  input  M0,
  input  M1,
  input  M2,
  input  M3,
  input  M4,
  input  M5,
  input  M6,
  input  M7,
  input  M8,
  input  M9,
  input  M15,
  input  M17,
  input  M18,
  input  M19,
  input  M20,
  input  M21,
  input  M22,
  input  M23,
  input  M24,
  input  M25,
  input  M26,
  input  M32,
  input  M34,
  input  M35,
  input  M36,
  input  M37,
  input  M38,
  input  M39,
  input  M40,
  input  M41,
  input  M42,
  input  M43,
  input  M49,
  input  M51,
  input  M52,
  input  M53,
  input  M54,
  input  M55,
  input  M56,
  input  M57,
  input  M58,
  input  M59,
  input  M60,
  input  M66,
  input  M68,
  input  M69,
  input  M70,
  input  M71,
  input  M72,
  input  M73,
  input  M74,
  input  M75,
  input  M76,
  input  M77,
  input  M83,
  input  M85,
  input  M86,
  input  M87,
  input  M88,
  input  M89,
  input  M90,
  input  M91,
  input  M92,
  input  M93,
  input  M94,
  input  M100,
  input  M102,
  input  M103,
  input  M104,
  input  M105,
  input  M106,
  input  M107,
  input  M108,
  input  M109,
  input  M110,
  input  M111,
  input  M117,
  input  M119,
  input  M120,
  input  M121,
  input  M122,
  input  M123,
  input  M124,
  input  M125,
  input  M126,
  input  M127,
  input  M128,
  input  M134,
  input  M136,
  input  M137,
  input  M138,
  input  M139,
  input  M140,
  input  M141,
  input  M142,
  input  M143,
  input  M144,
  input  M145,
  input  M151,
  input  M153,
  input  M154,
  input  M155,
  input  M156,
  input  M157,
  input  M158,
  input  M159,
  input  M160,
  input  M161,
  input  M162,
  input  M168,
  input  M170,
  input  M171,
  input  M172,
  input  M173,
  input  M174,
  input  M175,
  input  M176,
  input  M177,
  input  M178,
  input  M179,
  input  M180,
  input  M181,
  input  M182,
  input  M183,
  input  M184,
  input  M190,
  input  M191,
  input  M192,
  input  M193,
  input  M194,
  input  M196,
  input  M197,
  input  M198,
  input  M199,
  input  M200,
  input  M201,
  input  M202,
  input  M203,
  input  M204,
  input  M205,
  input  M206,
  input  M207,
  input  M208,
  input  M209,
  input  M210,
  input  M211,
  input  M212,
  input  M213,
  output PC_BUS,
  output PC_INC,
  output PC_LOAD,
  output IR_BUS,
  output IR_LOAD,
  output AR_LOAD,
  output AR_BUS,
  output DR_LOAD
);

  IR ir_1 (
    .T1(T1), .T2(T2), .T3(T3), .M190(M190), .M191(M191), .M192(M192), .M193(M193), .M194(M194),
    .IR_BUS(IR_BUS), .IR_LOAD(IR_LOAD));
  PC pc_1 (
    .C(C), .Z(Z), .T0(T0), .T1(T1), .T3(T3), .T4(T4), .M196(M196), .M197(M197), .M198(M198), .M199(M199),
    .M200(M200), .M201(M201), .M202(M202), .M203(M203), .M204(M204), .M205(M205), .M206(M206), .M207(M207),
    .M208(M208), .M209(M209), .M210(M210), .M211(M211), .M212(M212), .M213(M213), .PC_BUS(PC_BUS),
    .PC_INC(PC_INC), .PC_LOAD(PC_LOAD));
  AR ar_1 (
    .C(C), .Z(Z), .T0(T0), .T2(T2), .T3(T3), .T4(T4), .M0(M0), .M1(M1), .M2(M2), .M3(M3), .M4(M4), .M17(M17),
    .M18(M18), .M19(M19), .M20(M20), .M21(M21), .M34(M34), .M35(M35), .M36(M36), .M37(M37), .M38(M38),
    .M51(M51), .M52(M52), .M53(M53), .M54(M54), .M55(M55), .M68(M68), .M69(M69), .M70(M70), .M71(M71),
    .M72(M72), .M85(M85), .M86(M86), .M87(M87), .M88(M88), .M89(M89), .M102(M102), .M103(M103), .M104(M104),
    .M105(M105), .M106(M106), .M119(M119), .M120(M120), .M121(M121), .M122(M122), .M123(M123), .M136(M136),
    .M137(M137), .M138(M138), .M139(M139), .M140(M140), .M153(M153), .M154(M154), .M155(M155), .M156(M156),
    .M157(M157), .M170(M170), .M171(M171), .M172(M172), .M173(M173), .M174(M174), .M180(M180), .M181(M181),
    .M182(M182), .M183(M183), .M184(M184), .M196(M196), .M197(M197), .M199(M199), .M200(M200), .M202(M202),
    .M203(M203), .M205(M205), .M206(M206), .M208(M208), .M209(M209), .M211(M211), .M212(M212),
    .AR_LOAD(AR_LOAD), .AR_BUS(AR_BUS));
  DR dr_1 (
    .T3(T3), .T4(T4), .T5(T5), .M0(M0), .M1(M1), .M2(M2), .M3(M3), .M4(M4), .M5(M5), .M6(M6), .M7(M7),
    .M8(M8), .M9(M9), .M15(M15), .M17(M17), .M18(M18), .M19(M19), .M20(M20), .M21(M21), .M22(M22), .M23(M23),
    .M24(M24), .M25(M25), .M26(M26), .M32(M32), .M34(M34), .M35(M35), .M36(M36), .M37(M37), .M38(M38),
    .M39(M39), .M40(M40), .M41(M41), .M42(M42), .M43(M43), .M49(M49), .M51(M51), .M52(M52), .M53(M53),
    .M54(M54), .M55(M55), .M56(M56), .M57(M57), .M58(M58), .M59(M59), .M60(M60), .M66(M66), .M68(M68),
    .M69(M69), .M70(M70), .M71(M71), .M72(M72), .M73(M73), .M74(M74), .M75(M75), .M76(M76), .M77(M77),
    .M83(M83), .M85(M85), .M86(M86), .M87(M87), .M88(M88), .M89(M89), .M90(M90), .M91(M91), .M92(M92),
    .M93(M93), .M94(M94), .M100(M100), .M102(M102), .M103(M103), .M104(M104), .M105(M105), .M106(M106),
    .M107(M107), .M108(M108), .M109(M109), .M110(M110), .M111(M111), .M117(M117), .M119(M119), .M120(M120),
    .M121(M121), .M122(M122), .M123(M123), .M124(M124), .M125(M125), .M126(M126), .M127(M127), .M128(M128),
    .M134(M134), .M136(M136), .M137(M137), .M138(M138), .M139(M139), .M140(M140), .M141(M141), .M142(M142),
    .M143(M143), .M144(M144), .M145(M145), .M151(M151), .M153(M153), .M154(M154), .M155(M155), .M156(M156),
    .M157(M157), .M158(M158), .M159(M159), .M160(M160), .M161(M161), .M162(M162), .M168(M168), .M170(M170),
    .M171(M171), .M172(M172), .M173(M173), .M174(M174), .M175(M175), .M176(M176), .M177(M177), .M178(M178),
    .M179(M179), .DR_LOAD(DR_LOAD));  // open: DR_BUS
endmodule
