// Logisim project FLAG.circ as structural Verilog: 1 circuit, main circuit FLAG
module FLAG (
  input  INPUT,
  input  CLK,
  input  LOAD,
  input  CLR,
  input  CML,
  output OUTPUT
);

  wire and_1_out, and_2_out, and_3_out, multiplexer_1_out, or_1_out, or_2_out, or_3_out;

  and and_1 (and_1_out, INPUT, LOAD);
  and and_2 (and_2_out, 1'b0, CLR);
  or or_1 (or_1_out, and_1_out, and_2_out);
  and and_3 (and_3_out, ~OUTPUT, CML);  // AND_Gate
  or or_2 (or_2_out, LOAD, CLR, CML);
  or or_3 (or_3_out, or_1_out, and_3_out);
  Multiplexer #(.enable("false")) multiplexer_1 (.in0(OUTPUT), .in1(or_3_out), .out(multiplexer_1_out), .sel(or_2_out));
  D_Flip_Flop d_ff_1 (.clk(CLK), .D(multiplexer_1_out), .Q(OUTPUT));  // open: Qn, preset, en, reset
endmodule
