// Logisim project Microprocessor.circ as structural Verilog: 36 circuits, main circuit main
module main (
  input  in_1,
  input  in_2,
  input  clk
);

  wire control_deney_1_ax_ld, control_deney_1_dr_ld, control_deney_1_mem_bus, control_deney_1_or;
  wire [2:0] control_deney_1_count, control_deney_1_mux;
  wire [15:0] controlled_buffer_1_out, general_purpose_1_output, general_purpose_2_output, multiplexer_1_out,
       or_1_output, ram_1_data, special_purpose_1_output, special_purpose_2_output;

  // Probe on control_deney_1_count
  control_deney control_deney_1 (
    .clk(clk), .count(control_deney_1_count), .mux(control_deney_1_mux), .dr_ld(control_deney_1_dr_ld),
    .mem_bus(control_deney_1_mem_bus), .\or (control_deney_1_or), .ax_ld(control_deney_1_ax_ld));
  SPECIAL_PURPOSE special_purpose_1 (.INC(in_2), .CLK(clk), .OUTPUT(special_purpose_1_output));  // open: INPUT, LD
  SPECIAL_PURPOSE special_purpose_2 (
    .INPUT(controlled_buffer_1_out), .INC(in_2), .LD(control_deney_1_dr_ld), .CLK(clk),
    .OUTPUT(special_purpose_2_output));
  GENERAL_PURPOSE general_purpose_1 (
    .INPUT(or_1_output), .INC(in_2), .LD(control_deney_1_ax_ld), .DEC(in_2), .SHL(in_2), .SHR(in_2),
    .CIL(in_2), .CIR(in_2), .CML(in_2), .CLR(in_2), .CLK(clk), .OUTPUT(general_purpose_1_output));
  GENERAL_PURPOSE general_purpose_2 (
    .INPUT(or_1_output), .INC(in_2), .LD(in_2), .DEC(in_2), .SHL(in_2), .SHR(in_2), .CIL(in_2), .CIR(in_2),
    .CML(in_2), .CLR(in_2), .CLK(clk), .OUTPUT(general_purpose_2_output));
  Multiplexer #(.select(3), .width(16)) multiplexer_1 (
    .in0(special_purpose_1_output), .in1(general_purpose_1_output), .in2(general_purpose_2_output),
    .out(multiplexer_1_out), .sel(control_deney_1_mux));  // open: in3, in4, in5, in6, in7, en
  // Probe on special_purpose_2_output
  // Probe on general_purpose_1_output
  // Probe on general_purpose_2_output
  // Probe on or_1_output
  OR or_1 (
    .AX(general_purpose_1_output), .BX(general_purpose_2_output), .DR(special_purpose_2_output),
    .AX__DR(control_deney_1_or), .BX__DR(1'b0), .CX__DR(1'b0), .DX__DR(1'b0), .EX__DR(1'b0), .AX__IR(1'b0),
    .BX__IR(1'b0), .CX__IR(1'b0), .DX__IR(1'b0), .EX__IR(1'b0), .AX__BX(1'b0), .AX__CX(1'b0), .AX__DX(1'b0),
    .AX__EX(1'b0), .BX__CX(1'b0), .BX__DX(1'b0), .BX__EX(1'b0), .CX__DX(1'b0), .CX__EX(1'b0), .DX__EX(1'b0),
    .OUTPUT(or_1_output));  // open: CX, DX, EX, IR
  RAM #(.addrWidth(16), .dataWidth(16), .bus("separate")) ram_1 (
    .addr(multiplexer_1_out), .din(controlled_buffer_1_out), .data(ram_1_data), .str(in_1));  // open: sel, clk, ld, clr
  assign controlled_buffer_1_out = control_deney_1_mem_bus ? ram_1_data : 16'bz;  // Controlled_Buffer controlled_buffer_1
  // Probe on controlled_buffer_1_out
endmodule

module AND_1 (
  input  AX,
  input  BX,
  input  CX,
  input  DX,
  input  EX,
  input  DR,
  input  IR,
  input  AX__DR,
  input  BX__DR,
  input  CX__DR,
  input  DX__DR,
  input  EX__DR,
  input  AX__IR,
  input  BX__IR,
  input  CX__IR,
  input  DX__IR,
  input  EX__IR,
  input  AX__BX,
  input  AX__CX,
  input  AX__DX,
  input  AX__EX,
  input  BX__CX,
  input  BX__DX,
  input  BX__EX,
  input  CX__DX,
  input  CX__EX,
  input  DX__EX,
  output OUTPUT
);

  wire and_1_out, and_2_out, and_3_out, and_4_out, and_5_out, and_6_out, and_7_out, and_8_out, and_9_out,
       and_10_out, and_11_out, and_12_out, and_13_out, and_14_out, and_15_out, and_16_out, and_17_out,
       and_18_out, and_19_out, and_20_out;

  and and_1 (and_1_out, AX__DR, DR, AX);
  and and_2 (and_2_out, BX__DR, DR, BX);
  and and_3 (and_3_out, CX__DR, DR, CX);
  and and_4 (and_4_out, DX__DR, DR, DX);
  and and_5 (and_5_out, EX__DR, DR, EX);
  and and_6 (and_6_out, AX__IR, IR, AX);
  and and_7 (and_7_out, BX__IR, IR, BX);
  and and_8 (and_8_out, CX__IR, IR, CX);
  and and_9 (and_9_out, DX__IR, IR, DX);
  and and_10 (and_10_out, EX__IR, IR, EX);
  and and_11 (and_11_out, AX__BX, BX, AX);
  and and_12 (and_12_out, AX__CX, CX, AX);
  and and_13 (and_13_out, AX__DX, DX, AX);
  and and_14 (and_14_out, AX__EX, EX, AX);
  and and_15 (and_15_out, BX__CX, CX, BX);
  and and_16 (and_16_out, BX__DX, DX, BX);
  and and_17 (and_17_out, BX__EX, EX, BX);
  and and_18 (and_18_out, CX__DX, DX, CX);
  and and_19 (and_19_out, CX__EX, EX, CX);
  and and_20 (and_20_out, DX__EX, EX, CX);
  or or_1 (OUTPUT, and_1_out, and_2_out, and_3_out, and_4_out, and_5_out, and_6_out, and_7_out, and_8_out, and_9_out, and_10_out, and_11_out, and_12_out, and_13_out, and_14_out, and_15_out, and_16_out, and_17_out, and_18_out, and_19_out, and_20_out);
endmodule

module OR_1 (
  input  AX,
  input  BX,
  input  CX,
  input  DX,
  input  EX,
  input  DR,
  input  IR,
  input  AX__DR,
  input  BX__DR,
  input  CX__DR,
  input  DX__DR,
  input  EX__DR,
  input  AX__IR,
  input  BX__IR,
  input  CX__IR,
  input  DX__IR,
  input  EX__IR,
  input  AX__BX,
  input  AX__CX,
  input  AX__DX,
  input  AX__EX,
  input  BX__CX,
  input  BX__DX,
  input  BX__EX,
  input  CX__DX,
  input  CX__EX,
  input  DX__EX,
  output OUTPUT
);

  wire and_1_out, and_2_out, and_3_out, and_4_out, and_5_out, and_6_out, and_7_out, and_8_out, and_9_out,
       and_10_out, and_11_out, and_12_out, and_13_out, and_14_out, and_15_out, and_16_out, and_17_out,
       and_18_out, and_19_out, and_20_out, or_1_out, or_2_out, or_3_out, or_4_out, or_5_out, or_6_out,
       or_7_out, or_8_out, or_9_out, or_10_out, or_11_out, or_12_out, or_13_out, or_14_out, or_15_out,
       or_16_out, or_17_out, or_18_out, or_19_out, or_20_out;

  or or_1 (or_1_out, DR, AX);
  or or_2 (or_2_out, DR, BX);
  or or_3 (or_3_out, DR, CX);
  or or_4 (or_4_out, DR, DX);
  or or_5 (or_5_out, DR, EX);
  or or_6 (or_6_out, IR, AX);
  or or_7 (or_7_out, IR, BX);
  or or_8 (or_8_out, IR, CX);
  or or_9 (or_9_out, IR, DX);
  or or_10 (or_10_out, IR, EX);
  or or_11 (or_11_out, BX, AX);
  or or_12 (or_12_out, CX, AX);
  or or_13 (or_13_out, DX, AX);
  or or_14 (or_14_out, EX, AX);
  or or_15 (or_15_out, CX, BX);
  or or_16 (or_16_out, DX, BX);
  or or_17 (or_17_out, EX, BX);
  or or_18 (or_18_out, DX, CX);
  or or_19 (or_19_out, EX, CX);
  or or_20 (or_20_out, EX, CX);
  and and_1 (and_1_out, AX__DR, or_1_out);
  and and_2 (and_2_out, BX__DR, or_2_out);
  and and_3 (and_3_out, CX__DR, or_3_out);
  and and_4 (and_4_out, DX__DR, or_4_out);
  and and_5 (and_5_out, EX__DR, or_5_out);
  and and_6 (and_6_out, AX__IR, or_6_out);
  and and_7 (and_7_out, BX__IR, or_7_out);
  and and_8 (and_8_out, CX__IR, or_8_out);
  and and_9 (and_9_out, DX__IR, or_9_out);
  and and_10 (and_10_out, EX__IR, or_10_out);
  and and_11 (and_11_out, AX__BX, or_11_out);
  and and_12 (and_12_out, AX__CX, or_12_out);
  and and_13 (and_13_out, AX__DX, or_13_out);
  and and_14 (and_14_out, AX__EX, or_14_out);
  and and_15 (and_15_out, BX__CX, or_15_out);
  and and_16 (and_16_out, BX__DX, or_16_out);
  and and_17 (and_17_out, BX__EX, or_17_out);
  and and_18 (and_18_out, CX__DX, or_18_out);
  and and_19 (and_19_out, CX__EX, or_19_out);
  and and_20 (and_20_out, DX__EX, or_20_out);
  or or_21 (OUTPUT, and_1_out, and_2_out, and_3_out, and_4_out, and_5_out, and_6_out, and_7_out, and_8_out, and_9_out, and_10_out, and_11_out, and_12_out, and_13_out, and_14_out, and_15_out, and_16_out, and_17_out, and_18_out, and_19_out, and_20_out);
endmodule

module XOR_1 (
  input  AX,
  input  BX,
  input  CX,
  input  DX,
  input  EX,
  input  DR,
  input  IR,
  input  AX__DR,
  input  BX__DR,
  input  CX__DR,
  input  DX__DR,
  input  EX__DR,
  input  AX__IR,
  input  BX__IR,
  input  CX__IR,
  input  DX__IR,
  input  EX__IR,
  input  AX__BX,
  input  AX__CX,
  input  AX__DX,
  input  AX__EX,
  input  BX__CX,
  input  BX__DX,
  input  BX__EX,
  input  CX__DX,
  input  CX__EX,
  input  DX__EX,
  output OUTPUT
);

  wire and_1_out, and_2_out, and_3_out, and_4_out, and_5_out, and_6_out, and_7_out, and_8_out, and_9_out,
       and_10_out, and_11_out, and_12_out, and_13_out, and_14_out, and_15_out, and_16_out, and_17_out,
       and_18_out, and_19_out, and_20_out, xor_1_out, xor_2_out, xor_3_out, xor_4_out, xor_5_out, xor_6_out,
       xor_7_out, xor_8_out, xor_9_out, xor_10_out, xor_11_out, xor_12_out, xor_13_out, xor_14_out,
       xor_15_out, xor_16_out, xor_17_out, xor_18_out, xor_19_out, xor_20_out;

  xor xor_1 (xor_1_out, DR, AX);
  xor xor_2 (xor_2_out, DR, BX);
  xor xor_3 (xor_3_out, DR, CX);
  xor xor_4 (xor_4_out, DR, DX);
  xor xor_5 (xor_5_out, DR, EX);
  xor xor_6 (xor_6_out, IR, AX);
  xor xor_7 (xor_7_out, IR, BX);
  xor xor_8 (xor_8_out, IR, CX);
  xor xor_9 (xor_9_out, IR, DX);
  xor xor_10 (xor_10_out, IR, EX);
  xor xor_11 (xor_11_out, BX, AX);
  xor xor_12 (xor_12_out, CX, AX);
  xor xor_13 (xor_13_out, DX, AX);
  xor xor_14 (xor_14_out, EX, AX);
  xor xor_15 (xor_15_out, CX, BX);
  xor xor_16 (xor_16_out, DX, BX);
  xor xor_17 (xor_17_out, EX, BX);
  xor xor_18 (xor_18_out, DX, CX);
  xor xor_19 (xor_19_out, EX, CX);
  xor xor_20 (xor_20_out, EX, CX);
  and and_1 (and_1_out, AX__DR, xor_1_out);
  and and_2 (and_2_out, BX__DR, xor_2_out);
  and and_3 (and_3_out, CX__DR, xor_3_out);
  and and_4 (and_4_out, DX__DR, xor_4_out);
  and and_5 (and_5_out, EX__DR, xor_5_out);
  and and_6 (and_6_out, AX__IR, xor_6_out);
  and and_7 (and_7_out, BX__IR, xor_7_out);
  and and_8 (and_8_out, CX__IR, xor_8_out);
  and and_9 (and_9_out, DX__IR, xor_9_out);
  and and_10 (and_10_out, EX__IR, xor_10_out);
  and and_11 (and_11_out, AX__BX, xor_11_out);
  and and_12 (and_12_out, AX__CX, xor_12_out);
  and and_13 (and_13_out, AX__DX, xor_13_out);
  and and_14 (and_14_out, AX__EX, xor_14_out);
  and and_15 (and_15_out, BX__CX, xor_15_out);
  and and_16 (and_16_out, BX__DX, xor_16_out);
  and and_17 (and_17_out, BX__EX, xor_17_out);
  and and_18 (and_18_out, CX__DX, xor_18_out);
  and and_19 (and_19_out, CX__EX, xor_19_out);
  and and_20 (and_20_out, DX__EX, xor_20_out);
  or or_1 (OUTPUT, and_1_out, and_2_out, and_3_out, and_4_out, and_5_out, and_6_out, and_7_out, and_8_out, and_9_out, and_10_out, and_11_out, and_12_out, and_13_out, and_14_out, and_15_out, and_16_out, and_17_out, and_18_out, and_19_out, and_20_out);
endmodule

// INPUT ADJUSTER
module INPUT_4to1 (
  input  [3:0] AX,
  input  [3:0] BX,
  input  [3:0] CX,
  input  [3:0] DX,
  input  [3:0] EX,
  input  [3:0] DR,
  input  [3:0] IR,
  output AX3,
  output BX3,
  output CX3,
  output DX3,
  output EX3,
  output DR3,
  output IR3,
  output AX2,
  output BX2,
  output CX2,
  output DX2,
  output EX2,
  output DR2,
  output IR2,
  output AX1,
  output BX1,
  output CX1,
  output DX1,
  output EX1,
  output DR1,
  output IR1,
  output AX0,
  output BX0,
  output CX0,
  output DX0,
  output EX0,
  output DR0,
  output IR0
);


  assign AX0 = AX[0];
  assign AX1 = AX[1];
  assign AX2 = AX[2];
  assign AX3 = AX[3];
  assign BX0 = BX[0];
  assign BX1 = BX[1];
  assign BX2 = BX[2];
  assign BX3 = BX[3];
  assign CX0 = CX[0];
  assign CX1 = CX[1];
  assign CX2 = CX[2];
  assign CX3 = CX[3];
  assign DR0 = DR[0];
  assign DR1 = DR[1];
  assign DR2 = DR[2];
  assign DR3 = DR[3];
  assign DX0 = DX[0];
  assign DX1 = DX[1];
  assign DX2 = DX[2];
  assign DX3 = DX[3];
  assign EX0 = EX[0];
  assign EX1 = EX[1];
  assign EX2 = EX[2];
  assign EX3 = EX[3];
  assign IR0 = IR[0];
  assign IR1 = IR[1];
  assign IR2 = IR[2];
  assign IR3 = IR[3];
endmodule

module AND_4 (
  input  AX__DR,
  input  BX__DR,
  input  CX__DR,
  input  DX__DR,
  input  EX__DR,
  input  AX__IR,
  input  BX__IR,
  input  CX__IR,
  input  DX__IR,
  input  EX__IR,
  input  AX__BX,
  input  AX__CX,
  input  AX__DX,
  input  AX__EX,
  input  BX__CX,
  input  BX__DX,
  input  BX__EX,
  input  CX__DX,
  input  CX__EX,
  input  DX__EX,
  input  [3:0] AX,
  input  [3:0] BX,
  input  [3:0] CX,
  input  [3:0] DX,
  input  [3:0] EX,
  input  [3:0] DR,
  input  [3:0] IR,
  output [3:0] OUTPUT
);

  wire [6:0] input_4to1_1_ir0, input_4to1_1_ir1, input_4to1_1_ir2, input_4to1_1_ir3;

  INPUT_4to1 input_4to1_1 (
    .AX(AX), .BX(BX), .CX(CX), .DX(DX), .EX(EX), .DR(DR), .IR(IR), .AX3(input_4to1_1_ir3[6]),
    .BX3(input_4to1_1_ir3[5]), .CX3(input_4to1_1_ir3[4]), .DX3(input_4to1_1_ir3[3]),
    .EX3(input_4to1_1_ir3[2]), .DR3(input_4to1_1_ir3[1]), .IR3(input_4to1_1_ir3[0]),
    .AX2(input_4to1_1_ir2[6]), .BX2(input_4to1_1_ir2[5]), .CX2(input_4to1_1_ir2[4]),
    .DX2(input_4to1_1_ir2[3]), .EX2(input_4to1_1_ir2[2]), .DR2(input_4to1_1_ir2[1]),
    .IR2(input_4to1_1_ir2[0]), .AX1(input_4to1_1_ir1[6]), .BX1(input_4to1_1_ir1[5]),
    .CX1(input_4to1_1_ir1[4]), .DX1(input_4to1_1_ir1[3]), .EX1(input_4to1_1_ir1[2]),
    .DR1(input_4to1_1_ir1[1]), .IR1(input_4to1_1_ir1[0]), .AX0(input_4to1_1_ir0[6]),
    .BX0(input_4to1_1_ir0[5]), .CX0(input_4to1_1_ir0[4]), .DX0(input_4to1_1_ir0[3]),
    .EX0(input_4to1_1_ir0[2]), .DR0(input_4to1_1_ir0[1]), .IR0(input_4to1_1_ir0[0]));
  AND_1 and_1_1 (
    .AX__DR(AX__DR), .BX__DR(BX__DR), .CX__DR(CX__DR), .DX__DR(DX__DR), .EX__DR(EX__DR), .AX__IR(AX__IR),
    .BX__IR(BX__IR), .CX__IR(CX__IR), .DX__IR(DX__IR), .EX__IR(EX__IR), .AX__BX(AX__BX), .AX__CX(AX__CX),
    .AX__DX(AX__DX), .AX__EX(AX__EX), .BX__CX(BX__CX), .BX__DX(BX__DX), .BX__EX(BX__EX), .CX__DX(CX__DX),
    .CX__EX(CX__EX), .DX__EX(DX__EX), .AX(input_4to1_1_ir3[6]), .BX(input_4to1_1_ir3[5]),
    .CX(input_4to1_1_ir3[4]), .DX(input_4to1_1_ir3[3]), .EX(input_4to1_1_ir3[2]), .DR(input_4to1_1_ir3[1]),
    .IR(input_4to1_1_ir3[0]), .OUTPUT(OUTPUT[3]));
  AND_1 and_1_2 (
    .AX__DR(AX__DR), .BX__DR(BX__DR), .CX__DR(CX__DR), .DX__DR(DX__DR), .EX__DR(EX__DR), .AX__IR(AX__IR),
    .BX__IR(BX__IR), .CX__IR(CX__IR), .DX__IR(DX__IR), .EX__IR(EX__IR), .AX__BX(AX__BX), .AX__CX(AX__CX),
    .AX__DX(AX__DX), .AX__EX(AX__EX), .BX__CX(BX__CX), .BX__DX(BX__DX), .BX__EX(BX__EX), .CX__DX(CX__DX),
    .CX__EX(CX__EX), .DX__EX(DX__EX), .AX(input_4to1_1_ir2[6]), .BX(input_4to1_1_ir2[5]),
    .CX(input_4to1_1_ir2[4]), .DX(input_4to1_1_ir2[3]), .EX(input_4to1_1_ir2[2]), .DR(input_4to1_1_ir2[1]),
    .IR(input_4to1_1_ir2[0]), .OUTPUT(OUTPUT[2]));
  AND_1 and_1_3 (
    .AX__DR(AX__DR), .BX__DR(BX__DR), .CX__DR(CX__DR), .DX__DR(DX__DR), .EX__DR(EX__DR), .AX__IR(AX__IR),
    .BX__IR(BX__IR), .CX__IR(CX__IR), .DX__IR(DX__IR), .EX__IR(EX__IR), .AX__BX(AX__BX), .AX__CX(AX__CX),
    .AX__DX(AX__DX), .AX__EX(AX__EX), .BX__CX(BX__CX), .BX__DX(BX__DX), .BX__EX(BX__EX), .CX__DX(CX__DX),
    .CX__EX(CX__EX), .DX__EX(DX__EX), .AX(input_4to1_1_ir1[6]), .BX(input_4to1_1_ir1[5]),
    .CX(input_4to1_1_ir1[4]), .DX(input_4to1_1_ir1[3]), .EX(input_4to1_1_ir1[2]), .DR(input_4to1_1_ir1[1]),
    .IR(input_4to1_1_ir1[0]), .OUTPUT(OUTPUT[1]));
  AND_1 and_1_4 (
    .AX__DR(AX__DR), .BX__DR(BX__DR), .CX__DR(CX__DR), .DX__DR(DX__DR), .EX__DR(EX__DR), .AX__IR(AX__IR),
    .BX__IR(BX__IR), .CX__IR(CX__IR), .DX__IR(DX__IR), .EX__IR(EX__IR), .AX__BX(AX__BX), .AX__CX(AX__CX),
    .AX__DX(AX__DX), .AX__EX(AX__EX), .BX__CX(BX__CX), .BX__DX(BX__DX), .BX__EX(BX__EX), .CX__DX(CX__DX),
    .CX__EX(CX__EX), .DX__EX(DX__EX), .AX(input_4to1_1_ir0[6]), .BX(input_4to1_1_ir0[5]),
    .CX(input_4to1_1_ir0[4]), .DX(input_4to1_1_ir0[3]), .EX(input_4to1_1_ir0[2]), .DR(input_4to1_1_ir0[1]),
    .IR(input_4to1_1_ir0[0]), .OUTPUT(OUTPUT[0]));
endmodule

module OR_4 (
  input  AX__DR,
  input  BX__DR,
  input  CX__DR,
  input  DX__DR,
  input  EX__DR,
  input  AX__IR,
  input  BX__IR,
  input  CX__IR,
  input  DX__IR,
  input  EX__IR,
  input  AX__BX,
  input  AX__CX,
  input  AX__DX,
  input  AX__EX,
  input  BX__CX,
  input  BX__DX,
  input  BX__EX,
  input  CX__DX,
  input  CX__EX,
  input  DX__EX,
  input  [3:0] AX,
  input  [3:0] BX,
  input  [3:0] CX,
  input  [3:0] DX,
  input  [3:0] EX,
  input  [3:0] DR,
  input  [3:0] IR,
  output [3:0] OUTPUT
);

  wire [6:0] input_4to1_1_ir0, input_4to1_1_ir1, input_4to1_1_ir2, input_4to1_1_ir3;

  INPUT_4to1 input_4to1_1 (
    .AX(AX), .BX(BX), .CX(CX), .DX(DX), .EX(EX), .DR(DR), .IR(IR), .AX3(input_4to1_1_ir3[6]),
    .BX3(input_4to1_1_ir3[5]), .CX3(input_4to1_1_ir3[4]), .DX3(input_4to1_1_ir3[3]),
    .EX3(input_4to1_1_ir3[2]), .DR3(input_4to1_1_ir3[1]), .IR3(input_4to1_1_ir3[0]),
    .AX2(input_4to1_1_ir2[6]), .BX2(input_4to1_1_ir2[5]), .CX2(input_4to1_1_ir2[4]),
    .DX2(input_4to1_1_ir2[3]), .EX2(input_4to1_1_ir2[2]), .DR2(input_4to1_1_ir2[1]),
    .IR2(input_4to1_1_ir2[0]), .AX1(input_4to1_1_ir1[6]), .BX1(input_4to1_1_ir1[5]),
    .CX1(input_4to1_1_ir1[4]), .DX1(input_4to1_1_ir1[3]), .EX1(input_4to1_1_ir1[2]),
    .DR1(input_4to1_1_ir1[1]), .IR1(input_4to1_1_ir1[0]), .AX0(input_4to1_1_ir0[6]),
    .BX0(input_4to1_1_ir0[5]), .CX0(input_4to1_1_ir0[4]), .DX0(input_4to1_1_ir0[3]),
    .EX0(input_4to1_1_ir0[2]), .DR0(input_4to1_1_ir0[1]), .IR0(input_4to1_1_ir0[0]));
  OR_1 or_1_1 (
    .AX__DR(AX__DR), .BX__DR(BX__DR), .CX__DR(CX__DR), .DX__DR(DX__DR), .EX__DR(EX__DR), .AX__IR(AX__IR),
    .BX__IR(BX__IR), .CX__IR(CX__IR), .DX__IR(DX__IR), .EX__IR(EX__IR), .AX__BX(AX__BX), .AX__CX(AX__CX),
    .AX__DX(AX__DX), .AX__EX(AX__EX), .BX__CX(BX__CX), .BX__DX(BX__DX), .BX__EX(BX__EX), .CX__DX(CX__DX),
    .CX__EX(CX__EX), .DX__EX(DX__EX), .AX(input_4to1_1_ir3[6]), .BX(input_4to1_1_ir3[5]),
    .CX(input_4to1_1_ir3[4]), .DX(input_4to1_1_ir3[3]), .EX(input_4to1_1_ir3[2]), .DR(input_4to1_1_ir3[1]),
    .IR(input_4to1_1_ir3[0]), .OUTPUT(OUTPUT[3]));
  OR_1 or_1_2 (
    .AX__DR(AX__DR), .BX__DR(BX__DR), .CX__DR(CX__DR), .DX__DR(DX__DR), .EX__DR(EX__DR), .AX__IR(AX__IR),
    .BX__IR(BX__IR), .CX__IR(CX__IR), .DX__IR(DX__IR), .EX__IR(EX__IR), .AX__BX(AX__BX), .AX__CX(AX__CX),
    .AX__DX(AX__DX), .AX__EX(AX__EX), .BX__CX(BX__CX), .BX__DX(BX__DX), .BX__EX(BX__EX), .CX__DX(CX__DX),
    .CX__EX(CX__EX), .DX__EX(DX__EX), .AX(input_4to1_1_ir2[6]), .BX(input_4to1_1_ir2[5]),
    .CX(input_4to1_1_ir2[4]), .DX(input_4to1_1_ir2[3]), .EX(input_4to1_1_ir2[2]), .DR(input_4to1_1_ir2[1]),
    .IR(input_4to1_1_ir2[0]), .OUTPUT(OUTPUT[2]));
  OR_1 or_1_3 (
    .AX__DR(AX__DR), .BX__DR(BX__DR), .CX__DR(CX__DR), .DX__DR(DX__DR), .EX__DR(EX__DR), .AX__IR(AX__IR),
    .BX__IR(BX__IR), .CX__IR(CX__IR), .DX__IR(DX__IR), .EX__IR(EX__IR), .AX__BX(AX__BX), .AX__CX(AX__CX),
    .AX__DX(AX__DX), .AX__EX(AX__EX), .BX__CX(BX__CX), .BX__DX(BX__DX), .BX__EX(BX__EX), .CX__DX(CX__DX),
    .CX__EX(CX__EX), .DX__EX(DX__EX), .AX(input_4to1_1_ir1[6]), .BX(input_4to1_1_ir1[5]),
    .CX(input_4to1_1_ir1[4]), .DX(input_4to1_1_ir1[3]), .EX(input_4to1_1_ir1[2]), .DR(input_4to1_1_ir1[1]),
    .IR(input_4to1_1_ir1[0]), .OUTPUT(OUTPUT[1]));
  OR_1 or_1_4 (
    .AX__DR(AX__DR), .BX__DR(BX__DR), .CX__DR(CX__DR), .DX__DR(DX__DR), .EX__DR(EX__DR), .AX__IR(AX__IR),
    .BX__IR(BX__IR), .CX__IR(CX__IR), .DX__IR(DX__IR), .EX__IR(EX__IR), .AX__BX(AX__BX), .AX__CX(AX__CX),
    .AX__DX(AX__DX), .AX__EX(AX__EX), .BX__CX(BX__CX), .BX__DX(BX__DX), .BX__EX(BX__EX), .CX__DX(CX__DX),
    .CX__EX(CX__EX), .DX__EX(DX__EX), .AX(input_4to1_1_ir0[6]), .BX(input_4to1_1_ir0[5]),
    .CX(input_4to1_1_ir0[4]), .DX(input_4to1_1_ir0[3]), .EX(input_4to1_1_ir0[2]), .DR(input_4to1_1_ir0[1]),
    .IR(input_4to1_1_ir0[0]), .OUTPUT(OUTPUT[0]));
endmodule

module XOR_4 (
  input  AX__DR,
  input  BX__DR,
  input  CX__DR,
  input  DX__DR,
  input  EX__DR,
  input  AX__IR,
  input  BX__IR,
  input  CX__IR,
  input  DX__IR,
  input  EX__IR,
  input  AX__BX,
  input  AX__CX,
  input  AX__DX,
  input  AX__EX,
  input  BX__CX,
  input  BX__DX,
  input  BX__EX,
  input  CX__DX,
  input  CX__EX,
  input  DX__EX,
  input  [3:0] AX,
  input  [3:0] BX,
  input  [3:0] CX,
  input  [3:0] DX,
  input  [3:0] EX,
  input  [3:0] DR,
  input  [3:0] IR,
  output [3:0] OUTPUT
);

  wire [6:0] input_4to1_1_ir0, input_4to1_1_ir1, input_4to1_1_ir2, input_4to1_1_ir3;

  INPUT_4to1 input_4to1_1 (
    .AX(AX), .BX(BX), .CX(CX), .DX(DX), .EX(EX), .DR(DR), .IR(IR), .AX3(input_4to1_1_ir3[6]),
    .BX3(input_4to1_1_ir3[5]), .CX3(input_4to1_1_ir3[4]), .DX3(input_4to1_1_ir3[3]),
    .EX3(input_4to1_1_ir3[2]), .DR3(input_4to1_1_ir3[1]), .IR3(input_4to1_1_ir3[0]),
    .AX2(input_4to1_1_ir2[6]), .BX2(input_4to1_1_ir2[5]), .CX2(input_4to1_1_ir2[4]),
    .DX2(input_4to1_1_ir2[3]), .EX2(input_4to1_1_ir2[2]), .DR2(input_4to1_1_ir2[1]),
    .IR2(input_4to1_1_ir2[0]), .AX1(input_4to1_1_ir1[6]), .BX1(input_4to1_1_ir1[5]),
    .CX1(input_4to1_1_ir1[4]), .DX1(input_4to1_1_ir1[3]), .EX1(input_4to1_1_ir1[2]),
    .DR1(input_4to1_1_ir1[1]), .IR1(input_4to1_1_ir1[0]), .AX0(input_4to1_1_ir0[6]),
    .BX0(input_4to1_1_ir0[5]), .CX0(input_4to1_1_ir0[4]), .DX0(input_4to1_1_ir0[3]),
    .EX0(input_4to1_1_ir0[2]), .DR0(input_4to1_1_ir0[1]), .IR0(input_4to1_1_ir0[0]));
  XOR_1 xor_1_1 (
    .AX__DR(AX__DR), .BX__DR(BX__DR), .CX__DR(CX__DR), .DX__DR(DX__DR), .EX__DR(EX__DR), .AX__IR(AX__IR),
    .BX__IR(BX__IR), .CX__IR(CX__IR), .DX__IR(DX__IR), .EX__IR(EX__IR), .AX__BX(AX__BX), .AX__CX(AX__CX),
    .AX__DX(AX__DX), .AX__EX(AX__EX), .BX__CX(BX__CX), .BX__DX(BX__DX), .BX__EX(BX__EX), .CX__DX(CX__DX),
    .CX__EX(CX__EX), .DX__EX(DX__EX), .AX(input_4to1_1_ir3[6]), .BX(input_4to1_1_ir3[5]),
    .CX(input_4to1_1_ir3[4]), .DX(input_4to1_1_ir3[3]), .EX(input_4to1_1_ir3[2]), .DR(input_4to1_1_ir3[1]),
    .IR(input_4to1_1_ir3[0]), .OUTPUT(OUTPUT[3]));
  XOR_1 xor_1_2 (
    .AX__DR(AX__DR), .BX__DR(BX__DR), .CX__DR(CX__DR), .DX__DR(DX__DR), .EX__DR(EX__DR), .AX__IR(AX__IR),
    .BX__IR(BX__IR), .CX__IR(CX__IR), .DX__IR(DX__IR), .EX__IR(EX__IR), .AX__BX(AX__BX), .AX__CX(AX__CX),
    .AX__DX(AX__DX), .AX__EX(AX__EX), .BX__CX(BX__CX), .BX__DX(BX__DX), .BX__EX(BX__EX), .CX__DX(CX__DX),
    .CX__EX(CX__EX), .DX__EX(DX__EX), .AX(input_4to1_1_ir2[6]), .BX(input_4to1_1_ir2[5]),
    .CX(input_4to1_1_ir2[4]), .DX(input_4to1_1_ir2[3]), .EX(input_4to1_1_ir2[2]), .DR(input_4to1_1_ir2[1]),
    .IR(input_4to1_1_ir2[0]), .OUTPUT(OUTPUT[2]));
  XOR_1 xor_1_3 (
    .AX__DR(AX__DR), .BX__DR(BX__DR), .CX__DR(CX__DR), .DX__DR(DX__DR), .EX__DR(EX__DR), .AX__IR(AX__IR),
    .BX__IR(BX__IR), .CX__IR(CX__IR), .DX__IR(DX__IR), .EX__IR(EX__IR), .AX__BX(AX__BX), .AX__CX(AX__CX),
    .AX__DX(AX__DX), .AX__EX(AX__EX), .BX__CX(BX__CX), .BX__DX(BX__DX), .BX__EX(BX__EX), .CX__DX(CX__DX),
    .CX__EX(CX__EX), .DX__EX(DX__EX), .AX(input_4to1_1_ir1[6]), .BX(input_4to1_1_ir1[5]),
    .CX(input_4to1_1_ir1[4]), .DX(input_4to1_1_ir1[3]), .EX(input_4to1_1_ir1[2]), .DR(input_4to1_1_ir1[1]),
    .IR(input_4to1_1_ir1[0]), .OUTPUT(OUTPUT[1]));
  XOR_1 xor_1_4 (
    .AX__DR(AX__DR), .BX__DR(BX__DR), .CX__DR(CX__DR), .DX__DR(DX__DR), .EX__DR(EX__DR), .AX__IR(AX__IR),
    .BX__IR(BX__IR), .CX__IR(CX__IR), .DX__IR(DX__IR), .EX__IR(EX__IR), .AX__BX(AX__BX), .AX__CX(AX__CX),
    .AX__DX(AX__DX), .AX__EX(AX__EX), .BX__CX(BX__CX), .BX__DX(BX__DX), .BX__EX(BX__EX), .CX__DX(CX__DX),
    .CX__EX(CX__EX), .DX__EX(DX__EX), .AX(input_4to1_1_ir0[6]), .BX(input_4to1_1_ir0[5]),
    .CX(input_4to1_1_ir0[4]), .DX(input_4to1_1_ir0[3]), .EX(input_4to1_1_ir0[2]), .DR(input_4to1_1_ir0[1]),
    .IR(input_4to1_1_ir0[0]), .OUTPUT(OUTPUT[0]));
endmodule

// INPUT ADJUSTER
module INPUT_16to4 (
  input  [15:0] AX,
  input  [15:0] BX,
  input  [15:0] CX,
  input  [15:0] DX,
  input  [15:0] EX,
  input  [15:0] DR,
  input  [15:0] IR,
  output [3:0] AX_0_3,
  output [3:0] BX_0_3,
  output [3:0] CX_0_3,
  output [3:0] DX_0_3,
  output [3:0] EX_0_3,
  output [3:0] DR_0_3,
  output [3:0] IR_0_3,
  output [3:0] AX_4_7,
  output [3:0] BX_4_7,
  output [3:0] CX_4_7,
  output [3:0] DX_4_7,
  output [3:0] EX_4_7,
  output [3:0] DR_4_7,
  output [3:0] IR_4_7,
  output [3:0] AX_8_11,
  output [3:0] BX_8_11,
  output [3:0] CX_8_11,
  output [3:0] DX_8_11,
  output [3:0] EX_8_11,
  output [3:0] DR_8_11,
  output [3:0] IR_0_3_2,
  output [3:0] AX_12_15,
  output [3:0] BX_12_15,
  output [3:0] CX_12_15,
  output [3:0] DX_12_15,
  output [3:0] EX_12_15,
  output [3:0] DR_12_15,
  output [3:0] IR_12_15
);


  assign AX_0_3 = AX[3:0];
  assign AX_4_7 = AX[7:4];
  assign AX_8_11 = AX[11:8];
  assign AX_12_15 = AX[15:12];
  assign BX_0_3 = BX[3:0];
  assign BX_4_7 = BX[7:4];
  assign BX_8_11 = BX[11:8];
  assign BX_12_15 = BX[15:12];
  assign CX_0_3 = CX[3:0];
  assign CX_4_7 = CX[7:4];
  assign CX_8_11 = CX[11:8];
  assign CX_12_15 = CX[15:12];
  assign DR_0_3 = DR[3:0];
  assign DR_4_7 = DR[7:4];
  assign DR_8_11 = DR[11:8];
  assign DR_12_15 = DR[15:12];
  assign DX_0_3 = DX[3:0];
  assign DX_4_7 = DX[7:4];
  assign DX_8_11 = DX[11:8];
  assign DX_12_15 = DX[15:12];
  assign EX_0_3 = EX[3:0];
  assign EX_4_7 = EX[7:4];
  assign EX_8_11 = EX[11:8];
  assign EX_12_15 = EX[15:12];
  assign IR_0_3 = IR[3:0];
  assign IR_0_3_2 = IR[11:8];
  assign IR_4_7 = IR[7:4];
  assign IR_12_15 = IR[15:12];
endmodule

module AND (
  input  AX__DR,
  input  BX__DR,
  input  CX__DR,
  input  DX__DR,
  input  EX__DR,
  input  AX__IR,
  input  BX__IR,
  input  CX__IR,
  input  DX__IR,
  input  EX__IR,
  input  AX__BX,
  input  AX__CX,
  input  AX__DX,
  input  AX__EX,
  input  BX__CX,
  input  BX__DX,
  input  BX__EX,
  input  CX__DX,
  input  CX__EX,
  input  DX__EX,
  input  [15:0] AX,
  input  [15:0] BX,
  input  [15:0] CX,
  input  [15:0] DX,
  input  [15:0] EX,
  input  [15:0] DR,
  input  [15:0] IR,
  output [15:0] OUTPUT
);

  wire [3:0] input_16to4_1_ax_0_3, input_16to4_1_ax_4_7, input_16to4_1_ax_8_11, input_16to4_1_ax_12_15,
       input_16to4_1_bx_0_3, input_16to4_1_bx_4_7, input_16to4_1_bx_8_11, input_16to4_1_bx_12_15,
       input_16to4_1_cx_0_3, input_16to4_1_cx_4_7, input_16to4_1_cx_8_11, input_16to4_1_cx_12_15,
       input_16to4_1_dr_0_3, input_16to4_1_dr_4_7, input_16to4_1_dr_8_11, input_16to4_1_dr_12_15,
       input_16to4_1_dx_0_3, input_16to4_1_dx_4_7, input_16to4_1_dx_8_11, input_16to4_1_dx_12_15,
       input_16to4_1_ex_0_3, input_16to4_1_ex_4_7, input_16to4_1_ex_8_11, input_16to4_1_ex_12_15,
       input_16to4_1_ir_0_3, input_16to4_1_ir_0_3_2, input_16to4_1_ir_4_7, input_16to4_1_ir_12_15;

  INPUT_16to4 input_16to4_1 (
    .AX(AX), .BX(BX), .CX(CX), .DX(DX), .EX(EX), .DR(DR), .IR(IR), .AX_0_3(input_16to4_1_ax_0_3),
    .BX_0_3(input_16to4_1_bx_0_3), .CX_0_3(input_16to4_1_cx_0_3), .DX_0_3(input_16to4_1_dx_0_3),
    .EX_0_3(input_16to4_1_ex_0_3), .DR_0_3(input_16to4_1_dr_0_3), .IR_0_3(input_16to4_1_ir_0_3),
    .AX_4_7(input_16to4_1_ax_4_7), .BX_4_7(input_16to4_1_bx_4_7), .CX_4_7(input_16to4_1_cx_4_7),
    .DX_4_7(input_16to4_1_dx_4_7), .EX_4_7(input_16to4_1_ex_4_7), .DR_4_7(input_16to4_1_dr_4_7),
    .IR_4_7(input_16to4_1_ir_4_7), .AX_8_11(input_16to4_1_ax_8_11), .BX_8_11(input_16to4_1_bx_8_11),
    .CX_8_11(input_16to4_1_cx_8_11), .DX_8_11(input_16to4_1_dx_8_11), .EX_8_11(input_16to4_1_ex_8_11),
    .DR_8_11(input_16to4_1_dr_8_11), .IR_0_3_2(input_16to4_1_ir_0_3_2), .AX_12_15(input_16to4_1_ax_12_15),
    .BX_12_15(input_16to4_1_bx_12_15), .CX_12_15(input_16to4_1_cx_12_15), .DX_12_15(input_16to4_1_dx_12_15),
    .EX_12_15(input_16to4_1_ex_12_15), .DR_12_15(input_16to4_1_dr_12_15), .IR_12_15(input_16to4_1_ir_12_15));
  AND_4 and_4_1 (
    .AX(input_16to4_1_ax_0_3), .BX(input_16to4_1_bx_0_3), .CX(input_16to4_1_cx_0_3),
    .DX(input_16to4_1_dx_0_3), .EX(input_16to4_1_ex_0_3), .DR(input_16to4_1_dr_0_3),
    .IR(input_16to4_1_ir_0_3), .AX__DR(AX__DR), .BX__DR(BX__DR), .CX__DR(CX__DR), .DX__DR(DX__DR),
    .EX__DR(EX__DR), .AX__IR(AX__IR), .BX__IR(BX__IR), .CX__IR(CX__IR), .DX__IR(DX__IR), .EX__IR(EX__IR),
    .AX__BX(AX__BX), .AX__CX(AX__CX), .AX__DX(AX__DX), .AX__EX(AX__EX), .BX__CX(BX__CX), .BX__DX(BX__DX),
    .BX__EX(BX__EX), .CX__DX(CX__DX), .CX__EX(CX__EX), .DX__EX(DX__EX), .OUTPUT(OUTPUT[3:0]));
  AND_4 and_4_2 (
    .AX(input_16to4_1_ax_4_7), .BX(input_16to4_1_bx_4_7), .CX(input_16to4_1_cx_4_7),
    .DX(input_16to4_1_dx_4_7), .EX(input_16to4_1_ex_4_7), .DR(input_16to4_1_dr_4_7),
    .IR(input_16to4_1_ir_4_7), .AX__DR(AX__DR), .BX__DR(BX__DR), .CX__DR(CX__DR), .DX__DR(DX__DR),
    .EX__DR(EX__DR), .AX__IR(AX__IR), .BX__IR(BX__IR), .CX__IR(CX__IR), .DX__IR(DX__IR), .EX__IR(EX__IR),
    .AX__BX(AX__BX), .AX__CX(AX__CX), .AX__DX(AX__DX), .AX__EX(AX__EX), .BX__CX(BX__CX), .BX__DX(BX__DX),
    .BX__EX(BX__EX), .CX__DX(CX__DX), .CX__EX(CX__EX), .DX__EX(DX__EX), .OUTPUT(OUTPUT[7:4]));
  AND_4 and_4_3 (
    .AX(input_16to4_1_ax_8_11), .BX(input_16to4_1_bx_8_11), .CX(input_16to4_1_cx_8_11),
    .DX(input_16to4_1_dx_8_11), .EX(input_16to4_1_ex_8_11), .DR(input_16to4_1_dr_8_11),
    .IR(input_16to4_1_ir_0_3_2), .AX__DR(AX__DR), .BX__DR(BX__DR), .CX__DR(CX__DR), .DX__DR(DX__DR),
    .EX__DR(EX__DR), .AX__IR(AX__IR), .BX__IR(BX__IR), .CX__IR(CX__IR), .DX__IR(DX__IR), .EX__IR(EX__IR),
    .AX__BX(AX__BX), .AX__CX(AX__CX), .AX__DX(AX__DX), .AX__EX(AX__EX), .BX__CX(BX__CX), .BX__DX(BX__DX),
    .BX__EX(BX__EX), .CX__DX(CX__DX), .CX__EX(CX__EX), .DX__EX(DX__EX), .OUTPUT(OUTPUT[11:8]));
  AND_4 and_4_4 (
    .AX(input_16to4_1_ax_12_15), .BX(input_16to4_1_bx_12_15), .CX(input_16to4_1_cx_12_15),
    .DX(input_16to4_1_dx_12_15), .EX(input_16to4_1_ex_12_15), .DR(input_16to4_1_dr_12_15),
    .IR(input_16to4_1_ir_12_15), .AX__DR(AX__DR), .BX__DR(BX__DR), .CX__DR(CX__DR), .DX__DR(DX__DR),
    .EX__DR(EX__DR), .AX__IR(AX__IR), .BX__IR(BX__IR), .CX__IR(CX__IR), .DX__IR(DX__IR), .EX__IR(EX__IR),
    .AX__BX(AX__BX), .AX__CX(AX__CX), .AX__DX(AX__DX), .AX__EX(AX__EX), .BX__CX(BX__CX), .BX__DX(BX__DX),
    .BX__EX(BX__EX), .CX__DX(CX__DX), .CX__EX(CX__EX), .DX__EX(DX__EX), .OUTPUT(OUTPUT[15:12]));
endmodule

module OR (
  input  AX__DR,
  input  BX__DR,
  input  CX__DR,
  input  DX__DR,
  input  EX__DR,
  input  AX__IR,
  input  BX__IR,
  input  CX__IR,
  input  DX__IR,
  input  EX__IR,
  input  AX__BX,
  input  AX__CX,
  input  AX__DX,
  input  AX__EX,
  input  BX__CX,
  input  BX__DX,
  input  BX__EX,
  input  CX__DX,
  input  CX__EX,
  input  DX__EX,
  input  [15:0] AX,
  input  [15:0] BX,
  input  [15:0] CX,
  input  [15:0] DX,
  input  [15:0] EX,
  input  [15:0] DR,
  input  [15:0] IR,
  output [15:0] OUTPUT
);

  wire [3:0] input_16to4_1_ax_0_3, input_16to4_1_ax_4_7, input_16to4_1_ax_8_11, input_16to4_1_ax_12_15,
       input_16to4_1_bx_0_3, input_16to4_1_bx_4_7, input_16to4_1_bx_8_11, input_16to4_1_bx_12_15,
       input_16to4_1_cx_0_3, input_16to4_1_cx_4_7, input_16to4_1_cx_8_11, input_16to4_1_cx_12_15,
       input_16to4_1_dr_0_3, input_16to4_1_dr_4_7, input_16to4_1_dr_8_11, input_16to4_1_dr_12_15,
       input_16to4_1_dx_0_3, input_16to4_1_dx_4_7, input_16to4_1_dx_8_11, input_16to4_1_dx_12_15,
       input_16to4_1_ex_0_3, input_16to4_1_ex_4_7, input_16to4_1_ex_8_11, input_16to4_1_ex_12_15,
       input_16to4_1_ir_0_3, input_16to4_1_ir_0_3_2, input_16to4_1_ir_4_7, input_16to4_1_ir_12_15;

  INPUT_16to4 input_16to4_1 (
    .AX(AX), .BX(BX), .CX(CX), .DX(DX), .EX(EX), .DR(DR), .IR(IR), .AX_0_3(input_16to4_1_ax_0_3),
    .BX_0_3(input_16to4_1_bx_0_3), .CX_0_3(input_16to4_1_cx_0_3), .DX_0_3(input_16to4_1_dx_0_3),
    .EX_0_3(input_16to4_1_ex_0_3), .DR_0_3(input_16to4_1_dr_0_3), .IR_0_3(input_16to4_1_ir_0_3),
    .AX_4_7(input_16to4_1_ax_4_7), .BX_4_7(input_16to4_1_bx_4_7), .CX_4_7(input_16to4_1_cx_4_7),
    .DX_4_7(input_16to4_1_dx_4_7), .EX_4_7(input_16to4_1_ex_4_7), .DR_4_7(input_16to4_1_dr_4_7),
    .IR_4_7(input_16to4_1_ir_4_7), .AX_8_11(input_16to4_1_ax_8_11), .BX_8_11(input_16to4_1_bx_8_11),
    .CX_8_11(input_16to4_1_cx_8_11), .DX_8_11(input_16to4_1_dx_8_11), .EX_8_11(input_16to4_1_ex_8_11),
    .DR_8_11(input_16to4_1_dr_8_11), .IR_0_3_2(input_16to4_1_ir_0_3_2), .AX_12_15(input_16to4_1_ax_12_15),
    .BX_12_15(input_16to4_1_bx_12_15), .CX_12_15(input_16to4_1_cx_12_15), .DX_12_15(input_16to4_1_dx_12_15),
    .EX_12_15(input_16to4_1_ex_12_15), .DR_12_15(input_16to4_1_dr_12_15), .IR_12_15(input_16to4_1_ir_12_15));
  OR_4 or_4_1 (
    .AX(input_16to4_1_ax_0_3), .BX(input_16to4_1_bx_0_3), .CX(input_16to4_1_cx_0_3),
    .DX(input_16to4_1_dx_0_3), .EX(input_16to4_1_ex_0_3), .DR(input_16to4_1_dr_0_3),
    .IR(input_16to4_1_ir_0_3), .AX__DR(AX__DR), .BX__DR(BX__DR), .CX__DR(CX__DR), .DX__DR(DX__DR),
    .EX__DR(EX__DR), .AX__IR(AX__IR), .BX__IR(BX__IR), .CX__IR(CX__IR), .DX__IR(DX__IR), .EX__IR(EX__IR),
    .AX__BX(AX__BX), .AX__CX(AX__CX), .AX__DX(AX__DX), .AX__EX(AX__EX), .BX__CX(BX__CX), .BX__DX(BX__DX),
    .BX__EX(BX__EX), .CX__DX(CX__DX), .CX__EX(CX__EX), .DX__EX(DX__EX), .OUTPUT(OUTPUT[3:0]));
  OR_4 or_4_2 (
    .AX(input_16to4_1_ax_4_7), .BX(input_16to4_1_bx_4_7), .CX(input_16to4_1_cx_4_7),
    .DX(input_16to4_1_dx_4_7), .EX(input_16to4_1_ex_4_7), .DR(input_16to4_1_dr_4_7),
    .IR(input_16to4_1_ir_4_7), .AX__DR(AX__DR), .BX__DR(BX__DR), .CX__DR(CX__DR), .DX__DR(DX__DR),
    .EX__DR(EX__DR), .AX__IR(AX__IR), .BX__IR(BX__IR), .CX__IR(CX__IR), .DX__IR(DX__IR), .EX__IR(EX__IR),
    .AX__BX(AX__BX), .AX__CX(AX__CX), .AX__DX(AX__DX), .AX__EX(AX__EX), .BX__CX(BX__CX), .BX__DX(BX__DX),
    .BX__EX(BX__EX), .CX__DX(CX__DX), .CX__EX(CX__EX), .DX__EX(DX__EX), .OUTPUT(OUTPUT[7:4]));
  OR_4 or_4_3 (
    .AX(input_16to4_1_ax_8_11), .BX(input_16to4_1_bx_8_11), .CX(input_16to4_1_cx_8_11),
    .DX(input_16to4_1_dx_8_11), .EX(input_16to4_1_ex_8_11), .DR(input_16to4_1_dr_8_11),
    .IR(input_16to4_1_ir_0_3_2), .AX__DR(AX__DR), .BX__DR(BX__DR), .CX__DR(CX__DR), .DX__DR(DX__DR),
    .EX__DR(EX__DR), .AX__IR(AX__IR), .BX__IR(BX__IR), .CX__IR(CX__IR), .DX__IR(DX__IR), .EX__IR(EX__IR),
    .AX__BX(AX__BX), .AX__CX(AX__CX), .AX__DX(AX__DX), .AX__EX(AX__EX), .BX__CX(BX__CX), .BX__DX(BX__DX),
    .BX__EX(BX__EX), .CX__DX(CX__DX), .CX__EX(CX__EX), .DX__EX(DX__EX), .OUTPUT(OUTPUT[11:8]));
  OR_4 or_4_4 (
    .AX(input_16to4_1_ax_12_15), .BX(input_16to4_1_bx_12_15), .CX(input_16to4_1_cx_12_15),
    .DX(input_16to4_1_dx_12_15), .EX(input_16to4_1_ex_12_15), .DR(input_16to4_1_dr_12_15),
    .IR(input_16to4_1_ir_12_15), .AX__DR(AX__DR), .BX__DR(BX__DR), .CX__DR(CX__DR), .DX__DR(DX__DR),
    .EX__DR(EX__DR), .AX__IR(AX__IR), .BX__IR(BX__IR), .CX__IR(CX__IR), .DX__IR(DX__IR), .EX__IR(EX__IR),
    .AX__BX(AX__BX), .AX__CX(AX__CX), .AX__DX(AX__DX), .AX__EX(AX__EX), .BX__CX(BX__CX), .BX__DX(BX__DX),
    .BX__EX(BX__EX), .CX__DX(CX__DX), .CX__EX(CX__EX), .DX__EX(DX__EX), .OUTPUT(OUTPUT[15:12]));
endmodule

module XOR (
  input  AX__DR,
  input  BX__DR,
  input  CX__DR,
  input  DX__DR,
  input  EX__DR,
  input  AX__IR,
  input  BX__IR,
  input  CX__IR,
  input  DX__IR,
  input  EX__IR,
  input  AX__BX,
  input  AX__CX,
  input  AX__DX,
  input  AX__EX,
  input  BX__CX,
  input  BX__DX,
  input  BX__EX,
  input  CX__DX,
  input  CX__EX,
  input  DX__EX,
  input  [15:0] AX,
  input  [15:0] BX,
  input  [15:0] CX,
  input  [15:0] DX,
  input  [15:0] EX,
  input  [15:0] DR,
  input  [15:0] IR,
  output [15:0] OUTPUT
);

  wire [3:0] input_16to4_1_ax_0_3, input_16to4_1_ax_4_7, input_16to4_1_ax_8_11, input_16to4_1_ax_12_15,
       input_16to4_1_bx_0_3, input_16to4_1_bx_4_7, input_16to4_1_bx_8_11, input_16to4_1_bx_12_15,
       input_16to4_1_cx_0_3, input_16to4_1_cx_4_7, input_16to4_1_cx_8_11, input_16to4_1_cx_12_15,
       input_16to4_1_dr_0_3, input_16to4_1_dr_4_7, input_16to4_1_dr_8_11, input_16to4_1_dr_12_15,
       input_16to4_1_dx_0_3, input_16to4_1_dx_4_7, input_16to4_1_dx_8_11, input_16to4_1_dx_12_15,
       input_16to4_1_ex_0_3, input_16to4_1_ex_4_7, input_16to4_1_ex_8_11, input_16to4_1_ex_12_15,
       input_16to4_1_ir_0_3, input_16to4_1_ir_0_3_2, input_16to4_1_ir_4_7, input_16to4_1_ir_12_15;

  INPUT_16to4 input_16to4_1 (
    .AX(AX), .BX(BX), .CX(CX), .DX(DX), .EX(EX), .DR(DR), .IR(IR), .AX_0_3(input_16to4_1_ax_0_3),
    .BX_0_3(input_16to4_1_bx_0_3), .CX_0_3(input_16to4_1_cx_0_3), .DX_0_3(input_16to4_1_dx_0_3),
    .EX_0_3(input_16to4_1_ex_0_3), .DR_0_3(input_16to4_1_dr_0_3), .IR_0_3(input_16to4_1_ir_0_3),
    .AX_4_7(input_16to4_1_ax_4_7), .BX_4_7(input_16to4_1_bx_4_7), .CX_4_7(input_16to4_1_cx_4_7),
    .DX_4_7(input_16to4_1_dx_4_7), .EX_4_7(input_16to4_1_ex_4_7), .DR_4_7(input_16to4_1_dr_4_7),
    .IR_4_7(input_16to4_1_ir_4_7), .AX_8_11(input_16to4_1_ax_8_11), .BX_8_11(input_16to4_1_bx_8_11),
    .CX_8_11(input_16to4_1_cx_8_11), .DX_8_11(input_16to4_1_dx_8_11), .EX_8_11(input_16to4_1_ex_8_11),
    .DR_8_11(input_16to4_1_dr_8_11), .IR_0_3_2(input_16to4_1_ir_0_3_2), .AX_12_15(input_16to4_1_ax_12_15),
    .BX_12_15(input_16to4_1_bx_12_15), .CX_12_15(input_16to4_1_cx_12_15), .DX_12_15(input_16to4_1_dx_12_15),
    .EX_12_15(input_16to4_1_ex_12_15), .DR_12_15(input_16to4_1_dr_12_15), .IR_12_15(input_16to4_1_ir_12_15));
  XOR_4 xor_4_1 (
    .AX(input_16to4_1_ax_0_3), .BX(input_16to4_1_bx_0_3), .CX(input_16to4_1_cx_0_3),
    .DX(input_16to4_1_dx_0_3), .EX(input_16to4_1_ex_0_3), .DR(input_16to4_1_dr_0_3),
    .IR(input_16to4_1_ir_0_3), .AX__DR(AX__DR), .BX__DR(BX__DR), .CX__DR(CX__DR), .DX__DR(DX__DR),
    .EX__DR(EX__DR), .AX__IR(AX__IR), .BX__IR(BX__IR), .CX__IR(CX__IR), .DX__IR(DX__IR), .EX__IR(EX__IR),
    .AX__BX(AX__BX), .AX__CX(AX__CX), .AX__DX(AX__DX), .AX__EX(AX__EX), .BX__CX(BX__CX), .BX__DX(BX__DX),
    .BX__EX(BX__EX), .CX__DX(CX__DX), .CX__EX(CX__EX), .DX__EX(DX__EX), .OUTPUT(OUTPUT[3:0]));
  XOR_4 xor_4_2 (
    .AX(input_16to4_1_ax_4_7), .BX(input_16to4_1_bx_4_7), .CX(input_16to4_1_cx_4_7),
    .DX(input_16to4_1_dx_4_7), .EX(input_16to4_1_ex_4_7), .DR(input_16to4_1_dr_4_7),
    .IR(input_16to4_1_ir_4_7), .AX__DR(AX__DR), .BX__DR(BX__DR), .CX__DR(CX__DR), .DX__DR(DX__DR),
    .EX__DR(EX__DR), .AX__IR(AX__IR), .BX__IR(BX__IR), .CX__IR(CX__IR), .DX__IR(DX__IR), .EX__IR(EX__IR),
    .AX__BX(AX__BX), .AX__CX(AX__CX), .AX__DX(AX__DX), .AX__EX(AX__EX), .BX__CX(BX__CX), .BX__DX(BX__DX),
    .BX__EX(BX__EX), .CX__DX(CX__DX), .CX__EX(CX__EX), .DX__EX(DX__EX), .OUTPUT(OUTPUT[7:4]));
  XOR_4 xor_4_3 (
    .AX(input_16to4_1_ax_8_11), .BX(input_16to4_1_bx_8_11), .CX(input_16to4_1_cx_8_11),
    .DX(input_16to4_1_dx_8_11), .EX(input_16to4_1_ex_8_11), .DR(input_16to4_1_dr_8_11),
    .IR(input_16to4_1_ir_0_3_2), .AX__DR(AX__DR), .BX__DR(BX__DR), .CX__DR(CX__DR), .DX__DR(DX__DR),
    .EX__DR(EX__DR), .AX__IR(AX__IR), .BX__IR(BX__IR), .CX__IR(CX__IR), .DX__IR(DX__IR), .EX__IR(EX__IR),
    .AX__BX(AX__BX), .AX__CX(AX__CX), .AX__DX(AX__DX), .AX__EX(AX__EX), .BX__CX(BX__CX), .BX__DX(BX__DX),
    .BX__EX(BX__EX), .CX__DX(CX__DX), .CX__EX(CX__EX), .DX__EX(DX__EX), .OUTPUT(OUTPUT[11:8]));
  XOR_4 xor_4_4 (
    .AX(input_16to4_1_ax_12_15), .BX(input_16to4_1_bx_12_15), .CX(input_16to4_1_cx_12_15),
    .DX(input_16to4_1_dx_12_15), .EX(input_16to4_1_ex_12_15), .DR(input_16to4_1_dr_12_15),
    .IR(input_16to4_1_ir_12_15), .AX__DR(AX__DR), .BX__DR(BX__DR), .CX__DR(CX__DR), .DX__DR(DX__DR),
    .EX__DR(EX__DR), .AX__IR(AX__IR), .BX__IR(BX__IR), .CX__IR(CX__IR), .DX__IR(DX__IR), .EX__IR(EX__IR),
    .AX__BX(AX__BX), .AX__CX(AX__CX), .AX__DX(AX__DX), .AX__EX(AX__EX), .BX__CX(BX__CX), .BX__DX(BX__DX),
    .BX__EX(BX__EX), .CX__DX(CX__DX), .CX__EX(CX__EX), .DX__EX(DX__EX), .OUTPUT(OUTPUT[15:12]));
endmodule

// LINE SPLIT
module MUL_LINE_SPLIT (
  input  MULTIPLIER_1,
  input  [15:0] MULTIPLIED,
  output _0,
  output _1,
  output _2,
  output _3,
  output _4,
  output _5,
  output _6,
  output _7,
  output _8,
  output _9,
  output _10,
  output _11,
  output _12,
  output _13,
  output _14,
  output _15
);

  and and_1 (_0, MULTIPLIER_1, MULTIPLIED[0]);
  and and_2 (_1, MULTIPLIER_1, MULTIPLIED[1]);
  and and_3 (_2, MULTIPLIER_1, MULTIPLIED[2]);
  and and_4 (_3, MULTIPLIER_1, MULTIPLIED[3]);
  and and_5 (_4, MULTIPLIER_1, MULTIPLIED[4]);
  and and_6 (_5, MULTIPLIER_1, MULTIPLIED[5]);
  and and_7 (_6, MULTIPLIER_1, MULTIPLIED[6]);
  and and_8 (_7, MULTIPLIER_1, MULTIPLIED[7]);
  and and_9 (_8, MULTIPLIER_1, MULTIPLIED[8]);
  and and_10 (_9, MULTIPLIER_1, MULTIPLIED[9]);
  and and_11 (_10, MULTIPLIER_1, MULTIPLIED[10]);
  and and_12 (_11, MULTIPLIER_1, MULTIPLIED[11]);
  and and_13 (_12, MULTIPLIER_1, MULTIPLIED[12]);
  and and_14 (_13, MULTIPLIER_1, MULTIPLIED[13]);
  and and_15 (_14, MULTIPLIER_1, MULTIPLIED[14]);
  and and_16 (_15, MULTIPLIER_1, MULTIPLIED[15]);
endmodule

module DIV_1 (
  input  A,
  input  Cin,
  input  B,
  input  C_Mux,
  output Q,
  output C_Mux_2,
  output OUT
);

  wire and_1_out, and_2_out, and_3_out, and_4_out, not_1_out, not_2_out, xor_1_out, xor_2_out, xor_3_out;

  not not_1 (not_1_out, B);
  xor xor_1 (xor_1_out, A, not_1_out);
  xor xor_2 (xor_2_out, Cin, xor_1_out);
  and and_1 (and_1_out, Cin, not_1_out);
  xor xor_3 (xor_3_out, Cin, not_1_out);
  and and_2 (and_2_out, xor_3_out, A);
  or or_1 (Q, and_1_out, and_2_out);
  not not_2 (not_2_out, C_Mux);
  and and_3 (and_3_out, xor_2_out, C_Mux);
  or or_2 (OUT, and_3_out, and_4_out);
  and and_4 (and_4_out, A, not_2_out);

  assign C_Mux_2 = C_Mux;
endmodule

module MUL_4_LINE_ADDER (
  input  [3:0] MULTIPLIER,
  input  [15:0] MULTIPLIED,
  output [19:0] OUTPUT
);

  wire [14:0] mul_line_split_1__1;
  wire [15:0] mul_line_split_2__0, mul_line_split_3__0, mul_line_split_4__0;
  wire [15:1] adder_1_out, adder_2_out;
  wire [15:15] adder_1_cout, adder_2_cout;

  MUL_LINE_SPLIT mul_line_split_1 (
    .MULTIPLIED(MULTIPLIED), .MULTIPLIER_1(MULTIPLIER[0]), ._0(OUTPUT[0]), ._1(mul_line_split_1__1[0]),
    ._2(mul_line_split_1__1[1]), ._3(mul_line_split_1__1[2]), ._4(mul_line_split_1__1[3]),
    ._5(mul_line_split_1__1[4]), ._6(mul_line_split_1__1[5]), ._7(mul_line_split_1__1[6]),
    ._8(mul_line_split_1__1[7]), ._9(mul_line_split_1__1[8]), ._10(mul_line_split_1__1[9]),
    ._11(mul_line_split_1__1[10]), ._12(mul_line_split_1__1[11]), ._13(mul_line_split_1__1[12]),
    ._14(mul_line_split_1__1[13]), ._15(mul_line_split_1__1[14]));
  MUL_LINE_SPLIT mul_line_split_2 (
    .MULTIPLIED(MULTIPLIED), .MULTIPLIER_1(MULTIPLIER[1]), ._0(mul_line_split_2__0[0]),
    ._1(mul_line_split_2__0[1]), ._2(mul_line_split_2__0[2]), ._3(mul_line_split_2__0[3]),
    ._4(mul_line_split_2__0[4]), ._5(mul_line_split_2__0[5]), ._6(mul_line_split_2__0[6]),
    ._7(mul_line_split_2__0[7]), ._8(mul_line_split_2__0[8]), ._9(mul_line_split_2__0[9]),
    ._10(mul_line_split_2__0[10]), ._11(mul_line_split_2__0[11]), ._12(mul_line_split_2__0[12]),
    ._13(mul_line_split_2__0[13]), ._14(mul_line_split_2__0[14]), ._15(mul_line_split_2__0[15]));
  MUL_LINE_SPLIT mul_line_split_3 (
    .MULTIPLIED(MULTIPLIED), .MULTIPLIER_1(MULTIPLIER[2]), ._0(mul_line_split_3__0[0]),
    ._1(mul_line_split_3__0[1]), ._2(mul_line_split_3__0[2]), ._3(mul_line_split_3__0[3]),
    ._4(mul_line_split_3__0[4]), ._5(mul_line_split_3__0[5]), ._6(mul_line_split_3__0[6]),
    ._7(mul_line_split_3__0[7]), ._8(mul_line_split_3__0[8]), ._9(mul_line_split_3__0[9]),
    ._10(mul_line_split_3__0[10]), ._11(mul_line_split_3__0[11]), ._12(mul_line_split_3__0[12]),
    ._13(mul_line_split_3__0[13]), ._14(mul_line_split_3__0[14]), ._15(mul_line_split_3__0[15]));
  Adder #(.width(16)) adder_1 (
    .a(mul_line_split_2__0), .b({1'b0, mul_line_split_1__1}), .out({adder_1_out, OUTPUT[1]}),
    .cout(adder_1_cout[15]));  // open: cin
  Adder #(.width(16)) adder_2 (
    .a(mul_line_split_3__0), .b({adder_1_cout[15], adder_1_out}), .out({adder_2_out, OUTPUT[2]}),
    .cout(adder_2_cout[15]));  // open: cin
  MUL_LINE_SPLIT mul_line_split_4 (
    .MULTIPLIED(MULTIPLIED), .MULTIPLIER_1(MULTIPLIER[3]), ._0(mul_line_split_4__0[0]),
    ._1(mul_line_split_4__0[1]), ._2(mul_line_split_4__0[2]), ._3(mul_line_split_4__0[3]),
    ._4(mul_line_split_4__0[4]), ._5(mul_line_split_4__0[5]), ._6(mul_line_split_4__0[6]),
    ._7(mul_line_split_4__0[7]), ._8(mul_line_split_4__0[8]), ._9(mul_line_split_4__0[9]),
    ._10(mul_line_split_4__0[10]), ._11(mul_line_split_4__0[11]), ._12(mul_line_split_4__0[12]),
    ._13(mul_line_split_4__0[13]), ._14(mul_line_split_4__0[14]), ._15(mul_line_split_4__0[15]));
  Adder #(.width(16)) adder_3 (
    .a(mul_line_split_4__0), .b({adder_2_cout[15], adder_2_out}), .out(OUTPUT[18:3]), .cout(OUTPUT[19]));  // open: cin
endmodule

module DIV_LINE_PROCESS_UNIT (
  input  A15,
  input  A14,
  input  A13,
  input  A12,
  input  A11,
  input  A10,
  input  A9,
  input  A8,
  input  A7,
  input  A6,
  input  A5,
  input  A4,
  input  A3,
  input  A2,
  input  A1,
  input  A0,
  input  B15,
  input  B14,
  input  B13,
  input  B12,
  input  B11,
  input  B10,
  input  B9,
  input  B8,
  input  B7,
  input  B6,
  input  B5,
  input  B4,
  input  B3,
  input  B2,
  input  B1,
  input  B0,
  output out_33,
  output _0,
  output _1,
  output _2,
  output _3,
  output _4,
  output _5,
  output _6,
  output _7,
  output _8,
  output _9,
  output _10,
  output _11,
  output _12,
  output _13,
  output _14,
  output _15
);

  wire div_1_1_c_mux_2, div_1_2_c_mux_2, div_1_2_q, div_1_3_c_mux_2, div_1_3_q, div_1_4_c_mux_2, div_1_4_q,
       div_1_5_c_mux_2, div_1_5_q, div_1_6_c_mux_2, div_1_6_q, div_1_7_c_mux_2, div_1_7_q, div_1_8_c_mux_2,
       div_1_8_q, div_1_9_c_mux_2, div_1_9_q, div_1_10_c_mux_2, div_1_10_q, div_1_11_c_mux_2, div_1_11_q,
       div_1_12_c_mux_2, div_1_12_q, div_1_13_c_mux_2, div_1_13_q, div_1_14_c_mux_2, div_1_14_q,
       div_1_15_c_mux_2, div_1_15_q, div_1_16_q;

  DIV_1 div_1_1 (.Q(out_33), .C_Mux(out_33), .A(A15), .B(B15), .Cin(div_1_2_q), .C_Mux_2(div_1_1_c_mux_2), .OUT(_15));
  DIV_1 div_1_2 (
    .Q(div_1_2_q), .C_Mux(div_1_1_c_mux_2), .A(A14), .B(B14), .Cin(div_1_3_q), .C_Mux_2(div_1_2_c_mux_2),
    .OUT(_14));
  DIV_1 div_1_3 (
    .Q(div_1_3_q), .C_Mux(div_1_2_c_mux_2), .A(A13), .B(B13), .Cin(div_1_4_q), .C_Mux_2(div_1_3_c_mux_2),
    .OUT(_13));
  DIV_1 div_1_4 (
    .Q(div_1_4_q), .C_Mux(div_1_3_c_mux_2), .A(A12), .B(B12), .Cin(div_1_5_q), .C_Mux_2(div_1_4_c_mux_2),
    .OUT(_12));
  DIV_1 div_1_5 (
    .Q(div_1_5_q), .C_Mux(div_1_4_c_mux_2), .A(A11), .B(B11), .Cin(div_1_6_q), .C_Mux_2(div_1_5_c_mux_2),
    .OUT(_11));
  DIV_1 div_1_6 (
    .Q(div_1_6_q), .C_Mux(div_1_5_c_mux_2), .A(A10), .B(B10), .Cin(div_1_7_q), .C_Mux_2(div_1_6_c_mux_2),
    .OUT(_10));
  DIV_1 div_1_7 (
    .Q(div_1_7_q), .C_Mux(div_1_6_c_mux_2), .A(A9), .B(B9), .Cin(div_1_8_q), .C_Mux_2(div_1_7_c_mux_2),
    .OUT(_9));
  DIV_1 div_1_8 (
    .Q(div_1_8_q), .C_Mux(div_1_7_c_mux_2), .A(A8), .B(B8), .Cin(div_1_9_q), .C_Mux_2(div_1_8_c_mux_2),
    .OUT(_8));
  DIV_1 div_1_9 (
    .Q(div_1_9_q), .C_Mux(div_1_8_c_mux_2), .A(A7), .B(B7), .Cin(div_1_10_q), .C_Mux_2(div_1_9_c_mux_2),
    .OUT(_7));
  DIV_1 div_1_10 (
    .Q(div_1_10_q), .C_Mux(div_1_9_c_mux_2), .A(A6), .B(B6), .Cin(div_1_11_q), .C_Mux_2(div_1_10_c_mux_2),
    .OUT(_6));
  DIV_1 div_1_11 (
    .Q(div_1_11_q), .C_Mux(div_1_10_c_mux_2), .A(A5), .B(B5), .Cin(div_1_12_q), .C_Mux_2(div_1_11_c_mux_2),
    .OUT(_5));
  DIV_1 div_1_12 (
    .Q(div_1_12_q), .C_Mux(div_1_11_c_mux_2), .A(A4), .B(B4), .Cin(div_1_13_q), .C_Mux_2(div_1_12_c_mux_2),
    .OUT(_4));
  DIV_1 div_1_13 (
    .Q(div_1_13_q), .C_Mux(div_1_12_c_mux_2), .A(A3), .B(B3), .Cin(div_1_15_q), .C_Mux_2(div_1_13_c_mux_2),
    .OUT(_3));
  DIV_1 div_1_14 (
    .Q(div_1_14_q), .C_Mux(div_1_15_c_mux_2), .A(A1), .B(B1), .Cin(div_1_16_q), .C_Mux_2(div_1_14_c_mux_2),
    .OUT(_1));
  DIV_1 div_1_15 (
    .Q(div_1_15_q), .C_Mux(div_1_13_c_mux_2), .A(A2), .B(B2), .Cin(div_1_14_q), .C_Mux_2(div_1_15_c_mux_2),
    .OUT(_2));
  DIV_1 div_1_16 (.Q(div_1_16_q), .C_Mux(div_1_14_c_mux_2), .A(A0), .B(B0), .Cin(1'b1), .OUT(_0));  // open: C_Mux_2
endmodule

module MUL (
  input  AX__DR,
  input  BX__DR,
  input  CX__DR,
  input  DX__DR,
  input  EX__DR,
  input  AX__IR,
  input  BX__IR,
  input  CX__IR,
  input  DX__IR,
  input  EX__IR,
  input  AX__BX,
  input  AX__CX,
  input  AX__DX,
  input  AX__EX,
  input  BX__CX,
  input  BX__DX,
  input  BX__EX,
  input  CX__DX,
  input  CX__EX,
  input  DX__EX,
  input  [15:0] AX,
  input  [15:0] BX,
  input  [15:0] CX,
  input  [15:0] DX,
  input  [15:0] EX,
  input  [15:0] DR,
  input  [15:0] IR,
  output [15:0] LOW_16,
  output [15:0] HIGH_16
);

  wire [15:0] mul_input_adjuster_1_multiplied, mul_input_adjuster_1_multiplier;
  wire [19:0] mul_4_line_adder_1_output, mul_4_line_adder_3_output, mul_4_line_adder_4_output;
  wire [19:4] adder_1_out, adder_2_out, mul_4_line_adder_2_output;

  MUL_INPUT_ADJUSTER mul_input_adjuster_1 (
    .AX(AX), .BX(BX), .CX(CX), .DX(DX), .EX(EX), .DR(DR), .IR(IR), .AX__DR(AX__DR), .BX__DR(BX__DR),
    .CX__DR(CX__DR), .DX__DR(DX__DR), .EX__DR(EX__DR), .AX__IR(AX__IR), .BX__IR(BX__IR), .CX__IR(CX__IR),
    .DX__IR(DX__IR), .EX__IR(EX__IR), .AX__BX(AX__BX), .AX__CX(AX__CX), .AX__DX(AX__DX), .AX__EX(AX__EX),
    .BX__CX(BX__CX), .BX__DX(BX__DX), .BX__EX(BX__EX), .CX__DX(CX__DX), .CX__EX(CX__EX), .DX__EX(DX__EX),
    .MULTIPLIER(mul_input_adjuster_1_multiplier), .MULTIPLIED(mul_input_adjuster_1_multiplied));
  MUL_4_LINE_ADDER mul_4_line_adder_1 (
    .MULTIPLIED(mul_input_adjuster_1_multiplied), .MULTIPLIER(mul_input_adjuster_1_multiplier[7:4]),
    .OUTPUT(mul_4_line_adder_1_output));
  MUL_4_LINE_ADDER mul_4_line_adder_2 (
    .MULTIPLIED(mul_input_adjuster_1_multiplied), .MULTIPLIER(mul_input_adjuster_1_multiplier[3:0]),
    .OUTPUT({mul_4_line_adder_2_output, LOW_16[3:0]}));
  MUL_4_LINE_ADDER mul_4_line_adder_3 (
    .MULTIPLIED(mul_input_adjuster_1_multiplied), .MULTIPLIER(mul_input_adjuster_1_multiplier[11:8]),
    .OUTPUT(mul_4_line_adder_3_output));
  Adder #(.width(20)) adder_1 (
    .a(mul_4_line_adder_1_output), .b({4'b0000, mul_4_line_adder_2_output}), .out({adder_1_out, LOW_16[7:4]}));  // open: cin, cout
  MUL_4_LINE_ADDER mul_4_line_adder_4 (
    .MULTIPLIED(mul_input_adjuster_1_multiplied), .MULTIPLIER(mul_input_adjuster_1_multiplier[15:12]),
    .OUTPUT(mul_4_line_adder_4_output));
  Adder #(.width(20)) adder_2 (
    .a(mul_4_line_adder_3_output), .b({4'b0000, adder_1_out}), .out({adder_2_out, LOW_16[11:8]}));  // open: cin, cout
  Adder #(.width(20)) adder_3 (
    .a(mul_4_line_adder_4_output), .b({4'b0000, adder_2_out}), .out({HIGH_16, LOW_16[15:12]}));  // open: cin, cout
endmodule

module DIV_4_LINE (
  input  [3:0] DIVIDEND_4,
  input  [15:0] R_FROM_UP_LINE,
  input  [15:0] DIVISOR,
  output [3:0] Q,
  output [15:0] R
);

  wire [15:0] div_line_process_unit_1__0, div_line_process_unit_2__0, div_line_process_unit_3__0;

  DIV_LINE_PROCESS_UNIT div_line_process_unit_1 (
    .A15(R_FROM_UP_LINE[14]), .A14(R_FROM_UP_LINE[13]), .A13(R_FROM_UP_LINE[12]), .A12(R_FROM_UP_LINE[11]),
    .A11(R_FROM_UP_LINE[10]), .A10(R_FROM_UP_LINE[9]), .A9(R_FROM_UP_LINE[8]), .A8(R_FROM_UP_LINE[7]),
    .A7(R_FROM_UP_LINE[6]), .A6(R_FROM_UP_LINE[5]), .A5(R_FROM_UP_LINE[4]), .A4(R_FROM_UP_LINE[3]),
    .A3(R_FROM_UP_LINE[2]), .A2(R_FROM_UP_LINE[1]), .A1(R_FROM_UP_LINE[0]), .A0(DIVIDEND_4[3]),
    .B15(DIVISOR[15]), .B14(DIVISOR[14]), .B13(DIVISOR[13]), .B12(DIVISOR[12]), .B11(DIVISOR[11]),
    .B10(DIVISOR[10]), .B9(DIVISOR[9]), .B8(DIVISOR[8]), .B7(DIVISOR[7]), .B6(DIVISOR[6]), .B5(DIVISOR[5]),
    .B4(DIVISOR[4]), .B3(DIVISOR[3]), .B2(DIVISOR[2]), .B1(DIVISOR[1]), .B0(DIVISOR[0]), .out_33(Q[3]),
    ._0(div_line_process_unit_1__0[0]), ._1(div_line_process_unit_1__0[1]),
    ._2(div_line_process_unit_1__0[2]), ._3(div_line_process_unit_1__0[3]),
    ._4(div_line_process_unit_1__0[4]), ._5(div_line_process_unit_1__0[5]),
    ._6(div_line_process_unit_1__0[6]), ._7(div_line_process_unit_1__0[7]),
    ._8(div_line_process_unit_1__0[8]), ._9(div_line_process_unit_1__0[9]),
    ._10(div_line_process_unit_1__0[10]), ._11(div_line_process_unit_1__0[11]),
    ._12(div_line_process_unit_1__0[12]), ._13(div_line_process_unit_1__0[13]),
    ._14(div_line_process_unit_1__0[14]), ._15(div_line_process_unit_1__0[15]));
  DIV_LINE_PROCESS_UNIT div_line_process_unit_2 (
    .A15(div_line_process_unit_1__0[14]), .A14(div_line_process_unit_1__0[13]),
    .A13(div_line_process_unit_1__0[12]), .A12(div_line_process_unit_1__0[11]),
    .A11(div_line_process_unit_1__0[10]), .A10(div_line_process_unit_1__0[9]),
    .A9(div_line_process_unit_1__0[8]), .A8(div_line_process_unit_1__0[7]),
    .A7(div_line_process_unit_1__0[6]), .A6(div_line_process_unit_1__0[5]),
    .A5(div_line_process_unit_1__0[4]), .A4(div_line_process_unit_1__0[3]),
    .A3(div_line_process_unit_1__0[2]), .A2(div_line_process_unit_1__0[1]),
    .A1(div_line_process_unit_1__0[0]), .A0(DIVIDEND_4[2]), .B15(DIVISOR[15]), .B14(DIVISOR[14]),
    .B13(DIVISOR[13]), .B12(DIVISOR[12]), .B11(DIVISOR[11]), .B10(DIVISOR[10]), .B9(DIVISOR[9]),
    .B8(DIVISOR[8]), .B7(DIVISOR[7]), .B6(DIVISOR[6]), .B5(DIVISOR[5]), .B4(DIVISOR[4]), .B3(DIVISOR[3]),
    .B2(DIVISOR[2]), .B1(DIVISOR[1]), .B0(DIVISOR[0]), .out_33(Q[2]), ._0(div_line_process_unit_2__0[0]),
    ._1(div_line_process_unit_2__0[1]), ._2(div_line_process_unit_2__0[2]),
    ._3(div_line_process_unit_2__0[3]), ._4(div_line_process_unit_2__0[4]),
    ._5(div_line_process_unit_2__0[5]), ._6(div_line_process_unit_2__0[6]),
    ._7(div_line_process_unit_2__0[7]), ._8(div_line_process_unit_2__0[8]),
    ._9(div_line_process_unit_2__0[9]), ._10(div_line_process_unit_2__0[10]),
    ._11(div_line_process_unit_2__0[11]), ._12(div_line_process_unit_2__0[12]),
    ._13(div_line_process_unit_2__0[13]), ._14(div_line_process_unit_2__0[14]),
    ._15(div_line_process_unit_2__0[15]));
  DIV_LINE_PROCESS_UNIT div_line_process_unit_3 (
    .A15(div_line_process_unit_2__0[14]), .A14(div_line_process_unit_2__0[13]),
    .A13(div_line_process_unit_2__0[12]), .A12(div_line_process_unit_2__0[11]),
    .A11(div_line_process_unit_2__0[10]), .A10(div_line_process_unit_2__0[9]),
    .A9(div_line_process_unit_2__0[8]), .A8(div_line_process_unit_2__0[7]),
    .A7(div_line_process_unit_2__0[6]), .A6(div_line_process_unit_2__0[5]),
    .A5(div_line_process_unit_2__0[4]), .A4(div_line_process_unit_2__0[3]),
    .A3(div_line_process_unit_2__0[2]), .A2(div_line_process_unit_2__0[1]),
    .A1(div_line_process_unit_2__0[0]), .A0(DIVIDEND_4[1]), .B15(DIVISOR[15]), .B14(DIVISOR[14]),
    .B13(DIVISOR[13]), .B12(DIVISOR[12]), .B11(DIVISOR[11]), .B10(DIVISOR[10]), .B9(DIVISOR[9]),
    .B8(DIVISOR[8]), .B7(DIVISOR[7]), .B6(DIVISOR[6]), .B5(DIVISOR[5]), .B4(DIVISOR[4]), .B3(DIVISOR[3]),
    .B2(DIVISOR[2]), .B1(DIVISOR[1]), .B0(DIVISOR[0]), .out_33(Q[1]), ._0(div_line_process_unit_3__0[0]),
    ._1(div_line_process_unit_3__0[1]), ._2(div_line_process_unit_3__0[2]),
    ._3(div_line_process_unit_3__0[3]), ._4(div_line_process_unit_3__0[4]),
    ._5(div_line_process_unit_3__0[5]), ._6(div_line_process_unit_3__0[6]),
    ._7(div_line_process_unit_3__0[7]), ._8(div_line_process_unit_3__0[8]),
    ._9(div_line_process_unit_3__0[9]), ._10(div_line_process_unit_3__0[10]),
    ._11(div_line_process_unit_3__0[11]), ._12(div_line_process_unit_3__0[12]),
    ._13(div_line_process_unit_3__0[13]), ._14(div_line_process_unit_3__0[14]),
    ._15(div_line_process_unit_3__0[15]));
  DIV_LINE_PROCESS_UNIT div_line_process_unit_4 (
    .A15(div_line_process_unit_3__0[14]), .A14(div_line_process_unit_3__0[13]),
    .A13(div_line_process_unit_3__0[12]), .A12(div_line_process_unit_3__0[11]),
    .A11(div_line_process_unit_3__0[10]), .A10(div_line_process_unit_3__0[9]),
    .A9(div_line_process_unit_3__0[8]), .A8(div_line_process_unit_3__0[7]),
    .A7(div_line_process_unit_3__0[6]), .A6(div_line_process_unit_3__0[5]),
    .A5(div_line_process_unit_3__0[4]), .A4(div_line_process_unit_3__0[3]),
    .A3(div_line_process_unit_3__0[2]), .A2(div_line_process_unit_3__0[1]),
    .A1(div_line_process_unit_3__0[0]), .A0(DIVIDEND_4[0]), .B15(DIVISOR[15]), .B14(DIVISOR[14]),
    .B13(DIVISOR[13]), .B12(DIVISOR[12]), .B11(DIVISOR[11]), .B10(DIVISOR[10]), .B9(DIVISOR[9]),
    .B8(DIVISOR[8]), .B7(DIVISOR[7]), .B6(DIVISOR[6]), .B5(DIVISOR[5]), .B4(DIVISOR[4]), .B3(DIVISOR[3]),
    .B2(DIVISOR[2]), .B1(DIVISOR[1]), .B0(DIVISOR[0]), .out_33(Q[0]), ._0(R[0]), ._1(R[1]), ._2(R[2]),
    ._3(R[3]), ._4(R[4]), ._5(R[5]), ._6(R[6]), ._7(R[7]), ._8(R[8]), ._9(R[9]), ._10(R[10]), ._11(R[11]),
    ._12(R[12]), ._13(R[13]), ._14(R[14]), ._15(R[15]));
endmodule

module DIV (
  input  AX__DR,
  input  BX__DR,
  input  CX__DR,
  input  DX__DR,
  input  EX__DR,
  input  AX__IR,
  input  BX__IR,
  input  CX__IR,
  input  DX__IR,
  input  EX__IR,
  input  AX__BX,
  input  AX__CX,
  input  AX__DX,
  input  AX__EX,
  input  BX__AX,
  input  BX__CX,
  input  BX__DX,
  input  BX__EX,
  input  CX__AX,
  input  CX__BX,
  input  CX__DX,
  input  CX__EX,
  input  DX__AX,
  input  DX__BX,
  input  DX__CX,
  input  DX__EX,
  input  EX__AX,
  input  EX__BX,
  input  EX__CX,
  input  EX__DX,
  input  [15:0] AX,
  input  [15:0] BX,
  input  [15:0] CX,
  input  [15:0] DX,
  input  [15:0] EX,
  input  [15:0] DR,
  input  [15:0] IR,
  output [15:0] QUOTIENT,
  output [15:0] REMAINDER
);

  wire [15:0] div_4_line_1_r, div_4_line_2_r, div_4_line_3_r, div_input_adjuster_1_dividend,
       div_input_adjuster_1_divisor;

  DIV_INPUT_ADJUSTER div_input_adjuster_1 (
    .AX(AX), .BX(BX), .CX(CX), .DX(DX), .EX(EX), .DR(DR), .IR(IR), .AX__DR(AX__DR), .BX__DR(BX__DR),
    .CX__DR(CX__DR), .DX__DR(DX__DR), .EX__DR(EX__DR), .AX__IR(AX__IR), .BX__IR(BX__IR), .CX__IR(CX__IR),
    .DX__IR(DX__IR), .EX__IR(EX__IR), .AX__BX(AX__BX), .AX__CX(AX__CX), .AX__DX(AX__DX), .AX__EX(AX__EX),
    .BX__AX(BX__AX), .BX__CX(BX__CX), .BX__DX(BX__DX), .BX__EX(BX__EX), .CX__AX(CX__AX), .CX__BX(CX__BX),
    .CX__DX(CX__DX), .CX__EX(CX__EX), .DX__AX(DX__AX), .DX__BX(DX__BX), .DX__CX(DX__CX), .DX__EX(DX__EX),
    .EX__AX(EX__AX), .EX__BX(EX__BX), .EX__CX(EX__CX), .EX__DX(EX__DX),
    .DIVIDEND(div_input_adjuster_1_dividend), .DIVISOR(div_input_adjuster_1_divisor));
  DIV_4_LINE div_4_line_1 (
    .DIVIDEND_4(div_input_adjuster_1_dividend[15:12]), .R_FROM_UP_LINE({16{1'b0}}),
    .DIVISOR(div_input_adjuster_1_divisor), .Q(QUOTIENT[15:12]), .R(div_4_line_1_r));
  DIV_4_LINE div_4_line_2 (
    .DIVIDEND_4(div_input_adjuster_1_dividend[11:8]), .R_FROM_UP_LINE(div_4_line_1_r),
    .DIVISOR(div_input_adjuster_1_divisor), .Q(QUOTIENT[11:8]), .R(div_4_line_2_r));
  DIV_4_LINE div_4_line_3 (
    .DIVIDEND_4(div_input_adjuster_1_dividend[7:4]), .R_FROM_UP_LINE(div_4_line_2_r),
    .DIVISOR(div_input_adjuster_1_divisor), .Q(QUOTIENT[7:4]), .R(div_4_line_3_r));
  DIV_4_LINE div_4_line_4 (
    .DIVIDEND_4(div_input_adjuster_1_dividend[3:0]), .R_FROM_UP_LINE(div_4_line_3_r),
    .DIVISOR(div_input_adjuster_1_divisor), .Q(QUOTIENT[3:0]), .R(REMAINDER));
endmodule

module CMP_1 (
  input  A,
  input  B,
  output A___B,
  output A___B_2,
  output A___B_3
);

  wire not_1_out, not_2_out;

  not not_1 (not_1_out, A);
  not not_2 (not_2_out, B);
  and and_1 (A___B, not_1_out, B);
  xnor xnor_1 (A___B_2, A, B);
  and and_2 (A___B_3, A, not_2_out);
endmodule

module CMP_4 (
  input  [3:0] A,
  input  [3:0] B,
  output A___B,
  output A___B_2,
  output A___B_3
);

  wire and_1_out, and_2_out, and_3_out, and_4_out, and_5_out, and_6_out, cmp_1_1_a___b, cmp_1_1_a___b_2,
       cmp_1_1_a___b_3, cmp_1_2_a___b, cmp_1_2_a___b_2, cmp_1_2_a___b_3, cmp_1_3_a___b, cmp_1_3_a___b_2,
       cmp_1_3_a___b_3, cmp_1_4_a___b, cmp_1_4_a___b_2, cmp_1_4_a___b_3;

  CMP_1 cmp_1_1 (.A(A[0]), .B(B[0]), .A___B(cmp_1_1_a___b), .A___B_2(cmp_1_1_a___b_2), .A___B_3(cmp_1_1_a___b_3));
  CMP_1 cmp_1_2 (.A(A[1]), .B(B[1]), .A___B(cmp_1_2_a___b), .A___B_2(cmp_1_2_a___b_2), .A___B_3(cmp_1_2_a___b_3));
  CMP_1 cmp_1_3 (.A(A[2]), .B(B[2]), .A___B(cmp_1_3_a___b), .A___B_2(cmp_1_3_a___b_2), .A___B_3(cmp_1_3_a___b_3));
  CMP_1 cmp_1_4 (.A(A[3]), .B(B[3]), .A___B(cmp_1_4_a___b), .A___B_2(cmp_1_4_a___b_2), .A___B_3(cmp_1_4_a___b_3));
  and and_1 (and_1_out, cmp_1_4_a___b_2, cmp_1_3_a___b);
  and and_2 (and_2_out, cmp_1_4_a___b_2, cmp_1_3_a___b_2, cmp_1_2_a___b);
  and and_3 (and_3_out, cmp_1_4_a___b_2, cmp_1_3_a___b_2, cmp_1_2_a___b_2, cmp_1_1_a___b);
  and and_4 (and_4_out, cmp_1_1_a___b_3, cmp_1_2_a___b_2, cmp_1_3_a___b_2, cmp_1_4_a___b_2);
  and and_5 (and_5_out, cmp_1_2_a___b_3, cmp_1_3_a___b_2, cmp_1_4_a___b_2);
  and and_6 (and_6_out, cmp_1_3_a___b_3, cmp_1_4_a___b_2);
  or or_1 (A___B, cmp_1_4_a___b, and_1_out, and_2_out, and_3_out);
  and and_7 (A___B_2, cmp_1_1_a___b_2, cmp_1_2_a___b_2, cmp_1_3_a___b_2, cmp_1_4_a___b_2);
  or or_2 (A___B_3, and_4_out, and_5_out, and_6_out, cmp_1_4_a___b_3);
endmodule

module CMP (
  input  AX__DR,
  input  BX__DR,
  input  CX__DR,
  input  DX__DR,
  input  EX__DR,
  input  AX__IR,
  input  BX__IR,
  input  CX__IR,
  input  DX__IR,
  input  EX__IR,
  input  AX__BX,
  input  AX__CX,
  input  AX__DX,
  input  AX__EX,
  input  BX__AX,
  input  BX__CX,
  input  BX__DX,
  input  BX__EX,
  input  CX__AX,
  input  CX__BX,
  input  CX__DX,
  input  CX__EX,
  input  DX__AX,
  input  DX__BX,
  input  DX__CX,
  input  DX__EX,
  input  EX__AX,
  input  EX__BX,
  input  EX__CX,
  input  EX__DX,
  input  [15:0] AX,
  input  [15:0] BX,
  input  [15:0] CX,
  input  [15:0] DX,
  input  [15:0] EX,
  input  [15:0] DR,
  input  [15:0] IR,
  output A___B,
  output A___B_2,
  output A___B_3
);

  wire and_1_out, and_2_out, and_3_out, and_4_out, and_5_out, and_6_out, cmp_4_1_a___b, cmp_4_1_a___b_2,
       cmp_4_1_a___b_3, cmp_4_2_a___b, cmp_4_2_a___b_2, cmp_4_2_a___b_3, cmp_4_3_a___b, cmp_4_3_a___b_2,
       cmp_4_3_a___b_3, cmp_4_4_a___b, cmp_4_4_a___b_2, cmp_4_4_a___b_3;
  wire [15:0] cmp_input_adjuster_1_a, cmp_input_adjuster_1_b;

  CMP_INPUT_ADJUSTER cmp_input_adjuster_1 (
    .AX(AX), .BX(BX), .CX(CX), .DX(DX), .EX(EX), .DR(DR), .IR(IR), .AX__DR(AX__DR), .BX__DR(BX__DR),
    .CX__DR(CX__DR), .DX__DR(DX__DR), .EX__DR(EX__DR), .AX__IR(AX__IR), .BX__IR(BX__IR), .CX__IR(CX__IR),
    .DX__IR(DX__IR), .EX__IR(EX__IR), .AX__BX(AX__BX), .AX__CX(AX__CX), .AX__DX(AX__DX), .AX__EX(AX__EX),
    .BX__AX(BX__AX), .BX__CX(BX__CX), .BX__DX(BX__DX), .BX__EX(BX__EX), .CX__AX(CX__AX), .CX__BX(CX__BX),
    .CX__DX(CX__DX), .CX__EX(CX__EX), .DX__AX(DX__AX), .DX__BX(DX__BX), .DX__CX(DX__CX), .DX__EX(DX__EX),
    .EX__AX(EX__AX), .EX__BX(EX__BX), .EX__CX(EX__CX), .EX__DX(EX__DX), .A(cmp_input_adjuster_1_a),
    .B(cmp_input_adjuster_1_b));
  CMP_4 cmp_4_1 (
    .A(cmp_input_adjuster_1_a[3:0]), .B(cmp_input_adjuster_1_b[3:0]), .A___B(cmp_4_1_a___b),
    .A___B_2(cmp_4_1_a___b_2), .A___B_3(cmp_4_1_a___b_3));
  CMP_4 cmp_4_2 (
    .A(cmp_input_adjuster_1_a[7:4]), .B(cmp_input_adjuster_1_b[7:4]), .A___B(cmp_4_2_a___b),
    .A___B_2(cmp_4_2_a___b_2), .A___B_3(cmp_4_2_a___b_3));
  CMP_4 cmp_4_3 (
    .A(cmp_input_adjuster_1_a[11:8]), .B(cmp_input_adjuster_1_b[11:8]), .A___B(cmp_4_3_a___b),
    .A___B_2(cmp_4_3_a___b_2), .A___B_3(cmp_4_3_a___b_3));
  CMP_4 cmp_4_4 (
    .A(cmp_input_adjuster_1_a[15:12]), .B(cmp_input_adjuster_1_b[15:12]), .A___B(cmp_4_4_a___b),
    .A___B_2(cmp_4_4_a___b_2), .A___B_3(cmp_4_4_a___b_3));
  and and_1 (and_1_out, cmp_4_4_a___b_2, cmp_4_3_a___b);
  and and_2 (and_2_out, cmp_4_4_a___b_2, cmp_4_3_a___b_2, cmp_4_2_a___b);
  and and_3 (and_3_out, cmp_4_4_a___b_2, cmp_4_3_a___b_2, cmp_4_2_a___b_2, cmp_4_1_a___b);
  and and_4 (and_4_out, cmp_4_1_a___b_3, cmp_4_2_a___b_2, cmp_4_3_a___b_2, cmp_4_4_a___b_2);
  and and_5 (and_5_out, cmp_4_2_a___b_3, cmp_4_3_a___b_2, cmp_4_4_a___b_2);
  and and_6 (and_6_out, cmp_4_3_a___b_3, cmp_4_4_a___b_2);
  or or_1 (A___B, cmp_4_4_a___b, and_1_out, and_2_out, and_3_out);
  and and_7 (A___B_2, cmp_4_1_a___b_2, cmp_4_2_a___b_2, cmp_4_3_a___b_2, cmp_4_4_a___b_2);
  or or_2 (A___B_3, and_4_out, and_5_out, and_6_out, cmp_4_4_a___b_3);
endmodule

module ADD_ADC_4 (
  input  AX__DR,
  input  BX__DR,
  input  CX__DR,
  input  DX__DR,
  input  EX__DR,
  input  AX__IR,
  input  BX__IR,
  input  CX__IR,
  input  DX__IR,
  input  EX__IR,
  input  AX__BX,
  input  AX__CX,
  input  AX__DX,
  input  AX__EX,
  input  BX__CX,
  input  BX__DX,
  input  BX__EX,
  input  CX__DX,
  input  CX__EX,
  input  DX__EX,
  input  [3:0] AX,
  input  [3:0] BX,
  input  [3:0] CX,
  input  [3:0] DX,
  input  [3:0] EX,
  input  [3:0] DR,
  input  [3:0] IR,
  input  Cin,
  output [3:0] OUTPUT,
  output Cout
);

  wire add_adc_1_2_cout, add_adc_1_3_cout, add_adc_1_4_cout;
  wire [6:0] input_4to1_1_ir0, input_4to1_1_ir1, input_4to1_1_ir2, input_4to1_1_ir3;

  INPUT_4to1 input_4to1_1 (
    .AX(AX), .BX(BX), .CX(CX), .DX(DX), .EX(EX), .DR(DR), .IR(IR), .AX3(input_4to1_1_ir3[6]),
    .BX3(input_4to1_1_ir3[5]), .CX3(input_4to1_1_ir3[4]), .DX3(input_4to1_1_ir3[3]),
    .EX3(input_4to1_1_ir3[2]), .DR3(input_4to1_1_ir3[1]), .IR3(input_4to1_1_ir3[0]),
    .AX2(input_4to1_1_ir2[6]), .BX2(input_4to1_1_ir2[5]), .CX2(input_4to1_1_ir2[4]),
    .DX2(input_4to1_1_ir2[3]), .EX2(input_4to1_1_ir2[2]), .DR2(input_4to1_1_ir2[1]),
    .IR2(input_4to1_1_ir2[0]), .AX1(input_4to1_1_ir1[6]), .BX1(input_4to1_1_ir1[5]),
    .CX1(input_4to1_1_ir1[4]), .DX1(input_4to1_1_ir1[3]), .EX1(input_4to1_1_ir1[2]),
    .DR1(input_4to1_1_ir1[1]), .IR1(input_4to1_1_ir1[0]), .AX0(input_4to1_1_ir0[6]),
    .BX0(input_4to1_1_ir0[5]), .CX0(input_4to1_1_ir0[4]), .DX0(input_4to1_1_ir0[3]),
    .EX0(input_4to1_1_ir0[2]), .DR0(input_4to1_1_ir0[1]), .IR0(input_4to1_1_ir0[0]));
  ADD_ADC_1 add_adc_1_1 (
    .AX__DR(AX__DR), .BX__DR(BX__DR), .CX__DR(CX__DR), .DX__DR(DX__DR), .EX__DR(EX__DR), .AX__IR(AX__IR),
    .BX__IR(BX__IR), .CX__IR(CX__IR), .DX__IR(DX__IR), .EX__IR(EX__IR), .AX__BX(AX__BX), .AX__CX(AX__CX),
    .AX__DX(AX__DX), .AX__EX(AX__EX), .BX__CX(BX__CX), .BX__DX(BX__DX), .BX__EX(BX__EX), .CX__DX(CX__DX),
    .CX__EX(CX__EX), .DX__EX(DX__EX), .AX(input_4to1_1_ir3[6]), .BX(input_4to1_1_ir3[5]),
    .CX(input_4to1_1_ir3[4]), .DX(input_4to1_1_ir3[3]), .EX(input_4to1_1_ir3[2]), .DR(input_4to1_1_ir3[1]),
    .IR(input_4to1_1_ir3[0]), .Cin(add_adc_1_2_cout), .Cout(Cout), .OUTPUT(OUTPUT[3]));
  ADD_ADC_1 add_adc_1_2 (
    .AX__DR(AX__DR), .BX__DR(BX__DR), .CX__DR(CX__DR), .DX__DR(DX__DR), .EX__DR(EX__DR), .AX__IR(AX__IR),
    .BX__IR(BX__IR), .CX__IR(CX__IR), .DX__IR(DX__IR), .EX__IR(EX__IR), .AX__BX(AX__BX), .AX__CX(AX__CX),
    .AX__DX(AX__DX), .AX__EX(AX__EX), .BX__CX(BX__CX), .BX__DX(BX__DX), .BX__EX(BX__EX), .CX__DX(CX__DX),
    .CX__EX(CX__EX), .DX__EX(DX__EX), .AX(input_4to1_1_ir2[6]), .BX(input_4to1_1_ir2[5]),
    .CX(input_4to1_1_ir2[4]), .DX(input_4to1_1_ir2[3]), .EX(input_4to1_1_ir2[2]), .DR(input_4to1_1_ir2[1]),
    .IR(input_4to1_1_ir2[0]), .Cin(add_adc_1_3_cout), .Cout(add_adc_1_2_cout), .OUTPUT(OUTPUT[2]));
  ADD_ADC_1 add_adc_1_3 (
    .AX__DR(AX__DR), .BX__DR(BX__DR), .CX__DR(CX__DR), .DX__DR(DX__DR), .EX__DR(EX__DR), .AX__IR(AX__IR),
    .BX__IR(BX__IR), .CX__IR(CX__IR), .DX__IR(DX__IR), .EX__IR(EX__IR), .AX__BX(AX__BX), .AX__CX(AX__CX),
    .AX__DX(AX__DX), .AX__EX(AX__EX), .BX__CX(BX__CX), .BX__DX(BX__DX), .BX__EX(BX__EX), .CX__DX(CX__DX),
    .CX__EX(CX__EX), .DX__EX(DX__EX), .AX(input_4to1_1_ir1[6]), .BX(input_4to1_1_ir1[5]),
    .CX(input_4to1_1_ir1[4]), .DX(input_4to1_1_ir1[3]), .EX(input_4to1_1_ir1[2]), .DR(input_4to1_1_ir1[1]),
    .IR(input_4to1_1_ir1[0]), .Cin(add_adc_1_4_cout), .Cout(add_adc_1_3_cout), .OUTPUT(OUTPUT[1]));
  ADD_ADC_1 add_adc_1_4 (
    .AX__DR(AX__DR), .BX__DR(BX__DR), .CX__DR(CX__DR), .DX__DR(DX__DR), .EX__DR(EX__DR), .AX__IR(AX__IR),
    .BX__IR(BX__IR), .CX__IR(CX__IR), .DX__IR(DX__IR), .EX__IR(EX__IR), .AX__BX(AX__BX), .AX__CX(AX__CX),
    .AX__DX(AX__DX), .AX__EX(AX__EX), .BX__CX(BX__CX), .BX__DX(BX__DX), .BX__EX(BX__EX), .CX__DX(CX__DX),
    .CX__EX(CX__EX), .DX__EX(DX__EX), .AX(input_4to1_1_ir0[6]), .BX(input_4to1_1_ir0[5]),
    .CX(input_4to1_1_ir0[4]), .DX(input_4to1_1_ir0[3]), .EX(input_4to1_1_ir0[2]), .DR(input_4to1_1_ir0[1]),
    .IR(input_4to1_1_ir0[0]), .Cin(Cin), .Cout(add_adc_1_4_cout), .OUTPUT(OUTPUT[0]));
endmodule

module ADD_ADC (
  input  AX__DR,
  input  BX__DR,
  input  CX__DR,
  input  DX__DR,
  input  EX__DR,
  input  AX__IR,
  input  BX__IR,
  input  CX__IR,
  input  DX__IR,
  input  EX__IR,
  input  AX__BX,
  input  AX__CX,
  input  AX__DX,
  input  AX__EX,
  input  BX__CX,
  input  BX__DX,
  input  BX__EX,
  input  CX__DX,
  input  CX__EX,
  input  DX__EX,
  input  [15:0] AX,
  input  [15:0] BX,
  input  [15:0] CX,
  input  [15:0] DX,
  input  [15:0] EX,
  input  [15:0] DR,
  input  [15:0] IR,
  input  Cin,
  output [15:0] OUTPUT,
  output Cout
);

  wire add_adc_4_1_cout, add_adc_4_2_cout, add_adc_4_3_cout;
  wire [3:0] input_16to4_1_ax_0_3, input_16to4_1_ax_4_7, input_16to4_1_ax_8_11, input_16to4_1_ax_12_15,
       input_16to4_1_bx_0_3, input_16to4_1_bx_4_7, input_16to4_1_bx_8_11, input_16to4_1_bx_12_15,
       input_16to4_1_cx_0_3, input_16to4_1_cx_4_7, input_16to4_1_cx_8_11, input_16to4_1_cx_12_15,
       input_16to4_1_dr_0_3, input_16to4_1_dr_4_7, input_16to4_1_dr_8_11, input_16to4_1_dr_12_15,
       input_16to4_1_dx_0_3, input_16to4_1_dx_4_7, input_16to4_1_dx_8_11, input_16to4_1_dx_12_15,
       input_16to4_1_ex_0_3, input_16to4_1_ex_4_7, input_16to4_1_ex_8_11, input_16to4_1_ex_12_15,
       input_16to4_1_ir_0_3, input_16to4_1_ir_0_3_2, input_16to4_1_ir_4_7, input_16to4_1_ir_12_15;

  INPUT_16to4 input_16to4_1 (
    .AX(AX), .BX(BX), .CX(CX), .DX(DX), .EX(EX), .DR(DR), .IR(IR), .AX_0_3(input_16to4_1_ax_0_3),
    .BX_0_3(input_16to4_1_bx_0_3), .CX_0_3(input_16to4_1_cx_0_3), .DX_0_3(input_16to4_1_dx_0_3),
    .EX_0_3(input_16to4_1_ex_0_3), .DR_0_3(input_16to4_1_dr_0_3), .IR_0_3(input_16to4_1_ir_0_3),
    .AX_4_7(input_16to4_1_ax_4_7), .BX_4_7(input_16to4_1_bx_4_7), .CX_4_7(input_16to4_1_cx_4_7),
    .DX_4_7(input_16to4_1_dx_4_7), .EX_4_7(input_16to4_1_ex_4_7), .DR_4_7(input_16to4_1_dr_4_7),
    .IR_4_7(input_16to4_1_ir_4_7), .AX_8_11(input_16to4_1_ax_8_11), .BX_8_11(input_16to4_1_bx_8_11),
    .CX_8_11(input_16to4_1_cx_8_11), .DX_8_11(input_16to4_1_dx_8_11), .EX_8_11(input_16to4_1_ex_8_11),
    .DR_8_11(input_16to4_1_dr_8_11), .IR_0_3_2(input_16to4_1_ir_0_3_2), .AX_12_15(input_16to4_1_ax_12_15),
    .BX_12_15(input_16to4_1_bx_12_15), .CX_12_15(input_16to4_1_cx_12_15), .DX_12_15(input_16to4_1_dx_12_15),
    .EX_12_15(input_16to4_1_ex_12_15), .DR_12_15(input_16to4_1_dr_12_15), .IR_12_15(input_16to4_1_ir_12_15));
  ADD_ADC_4 add_adc_4_1 (
    .AX(input_16to4_1_ax_0_3), .BX(input_16to4_1_bx_0_3), .CX(input_16to4_1_cx_0_3),
    .DX(input_16to4_1_dx_0_3), .EX(input_16to4_1_ex_0_3), .DR(input_16to4_1_dr_0_3),
    .IR(input_16to4_1_ir_0_3), .Cin(Cin), .AX__DR(AX__DR), .BX__DR(BX__DR), .CX__DR(CX__DR), .DX__DR(DX__DR),
    .EX__DR(EX__DR), .AX__IR(AX__IR), .BX__IR(BX__IR), .CX__IR(CX__IR), .DX__IR(DX__IR), .EX__IR(EX__IR),
    .AX__BX(AX__BX), .AX__CX(AX__CX), .AX__DX(AX__DX), .AX__EX(AX__EX), .BX__CX(BX__CX), .BX__DX(BX__DX),
    .BX__EX(BX__EX), .CX__DX(CX__DX), .CX__EX(CX__EX), .DX__EX(DX__EX), .OUTPUT(OUTPUT[3:0]),
    .Cout(add_adc_4_1_cout));
  ADD_ADC_4 add_adc_4_2 (
    .AX(input_16to4_1_ax_4_7), .BX(input_16to4_1_bx_4_7), .CX(input_16to4_1_cx_4_7),
    .DX(input_16to4_1_dx_4_7), .EX(input_16to4_1_ex_4_7), .DR(input_16to4_1_dr_4_7),
    .IR(input_16to4_1_ir_4_7), .Cin(add_adc_4_1_cout), .AX__DR(AX__DR), .BX__DR(BX__DR), .CX__DR(CX__DR),
    .DX__DR(DX__DR), .EX__DR(EX__DR), .AX__IR(AX__IR), .BX__IR(BX__IR), .CX__IR(CX__IR), .DX__IR(DX__IR),
    .EX__IR(EX__IR), .AX__BX(AX__BX), .AX__CX(AX__CX), .AX__DX(AX__DX), .AX__EX(AX__EX), .BX__CX(BX__CX),
    .BX__DX(BX__DX), .BX__EX(BX__EX), .CX__DX(CX__DX), .CX__EX(CX__EX), .DX__EX(DX__EX),
    .OUTPUT(OUTPUT[7:4]), .Cout(add_adc_4_2_cout));
  ADD_ADC_4 add_adc_4_3 (
    .AX(input_16to4_1_ax_8_11), .BX(input_16to4_1_bx_8_11), .CX(input_16to4_1_cx_8_11),
    .DX(input_16to4_1_dx_8_11), .EX(input_16to4_1_ex_8_11), .DR(input_16to4_1_dr_8_11),
    .IR(input_16to4_1_ir_0_3_2), .Cin(add_adc_4_2_cout), .AX__DR(AX__DR), .BX__DR(BX__DR), .CX__DR(CX__DR),
    .DX__DR(DX__DR), .EX__DR(EX__DR), .AX__IR(AX__IR), .BX__IR(BX__IR), .CX__IR(CX__IR), .DX__IR(DX__IR),
    .EX__IR(EX__IR), .AX__BX(AX__BX), .AX__CX(AX__CX), .AX__DX(AX__DX), .AX__EX(AX__EX), .BX__CX(BX__CX),
    .BX__DX(BX__DX), .BX__EX(BX__EX), .CX__DX(CX__DX), .CX__EX(CX__EX), .DX__EX(DX__EX),
    .OUTPUT(OUTPUT[11:8]), .Cout(add_adc_4_3_cout));
  ADD_ADC_4 add_adc_4_4 (
    .AX(input_16to4_1_ax_12_15), .BX(input_16to4_1_bx_12_15), .CX(input_16to4_1_cx_12_15),
    .DX(input_16to4_1_dx_12_15), .EX(input_16to4_1_ex_12_15), .DR(input_16to4_1_dr_12_15),
    .IR(input_16to4_1_ir_12_15), .Cin(add_adc_4_3_cout), .AX__DR(AX__DR), .BX__DR(BX__DR), .CX__DR(CX__DR),
    .DX__DR(DX__DR), .EX__DR(EX__DR), .AX__IR(AX__IR), .BX__IR(BX__IR), .CX__IR(CX__IR), .DX__IR(DX__IR),
    .EX__IR(EX__IR), .AX__BX(AX__BX), .AX__CX(AX__CX), .AX__DX(AX__DX), .AX__EX(AX__EX), .BX__CX(BX__CX),
    .BX__DX(BX__DX), .BX__EX(BX__EX), .CX__DX(CX__DX), .CX__EX(CX__EX), .DX__EX(DX__EX),
    .OUTPUT(OUTPUT[15:12]), .Cout(Cout));
endmodule

module SUB_SBB_4 (
  input  AX__DR,
  input  BX__DR,
  input  CX__DR,
  input  DX__DR,
  input  EX__DR,
  input  AX__IR,
  input  BX__IR,
  input  CX__IR,
  input  DX__IR,
  input  EX__IR,
  input  AX__BX,
  input  AX__CX,
  input  AX__DX,
  input  AX__EX,
  input  BX__AX,
  input  BX__CX,
  input  BX__DX,
  input  BX__EX,
  input  CX__AX,
  input  CX__BX,
  input  CX__DX,
  input  CX__EX,
  input  DX__AX,
  input  DX__BX,
  input  DX__CX,
  input  DX__EX,
  input  EX__AX,
  input  EX__BX,
  input  EX__CX,
  input  EX__DX,
  input  [3:0] AX,
  input  [3:0] BX,
  input  [3:0] CX,
  input  [3:0] DX,
  input  [3:0] EX,
  input  [3:0] DR,
  input  [3:0] IR,
  input  Bin,
  output [3:0] OUTPUT,
  output Bout
);

  wire sub_sbb_1_2_bout, sub_sbb_1_3_bout, sub_sbb_1_4_bout;
  wire [6:0] input_4to1_1_ir0, input_4to1_1_ir1, input_4to1_1_ir2, input_4to1_1_ir3;

  SUB_SBB_1 sub_sbb_1_1 (
    .AX__DR(AX__DR), .BX__DR(BX__DR), .CX__DR(CX__DR), .DX__DR(DX__DR), .EX__DR(EX__DR), .AX__IR(AX__IR),
    .BX__IR(BX__IR), .CX__IR(CX__IR), .DX__IR(DX__IR), .EX__IR(EX__IR), .AX__BX(AX__BX), .AX__CX(AX__CX),
    .AX__DX(AX__DX), .AX__EX(AX__EX), .BX_AX(BX__AX), .BX__CX(BX__CX), .BX__DX(BX__DX), .BX__EX(BX__EX),
    .CX__AX(CX__AX), .CX__BX(CX__BX), .CX__DX(CX__DX), .CX__EX(CX__EX), .DX__AX(DX__AX), .DX__BX(DX__BX),
    .DX__CX(DX__CX), .DX__EX(DX__EX), .EX__AX(EX__AX), .EX__BX(EX__BX), .EX__CX(EX__CX), .EX__DX(EX__DX),
    .AX(input_4to1_1_ir3[6]), .BX(input_4to1_1_ir3[5]), .CX(input_4to1_1_ir3[4]), .DX(input_4to1_1_ir3[3]),
    .EX(input_4to1_1_ir3[2]), .DR(input_4to1_1_ir3[1]), .IR(input_4to1_1_ir3[0]), .Bin(sub_sbb_1_2_bout),
    .Bout(Bout), .OUTPUT(OUTPUT[3]));
  INPUT_4to1 input_4to1_1 (
    .AX(AX), .BX(BX), .CX(CX), .DX(DX), .EX(EX), .DR(DR), .IR(IR), .AX3(input_4to1_1_ir3[6]),
    .BX3(input_4to1_1_ir3[5]), .CX3(input_4to1_1_ir3[4]), .DX3(input_4to1_1_ir3[3]),
    .EX3(input_4to1_1_ir3[2]), .DR3(input_4to1_1_ir3[1]), .IR3(input_4to1_1_ir3[0]),
    .AX2(input_4to1_1_ir2[6]), .BX2(input_4to1_1_ir2[5]), .CX2(input_4to1_1_ir2[4]),
    .DX2(input_4to1_1_ir2[3]), .EX2(input_4to1_1_ir2[2]), .DR2(input_4to1_1_ir2[1]),
    .IR2(input_4to1_1_ir2[0]), .AX1(input_4to1_1_ir1[6]), .BX1(input_4to1_1_ir1[5]),
    .CX1(input_4to1_1_ir1[4]), .DX1(input_4to1_1_ir1[3]), .EX1(input_4to1_1_ir1[2]),
    .DR1(input_4to1_1_ir1[1]), .IR1(input_4to1_1_ir1[0]), .AX0(input_4to1_1_ir0[6]),
    .BX0(input_4to1_1_ir0[5]), .CX0(input_4to1_1_ir0[4]), .DX0(input_4to1_1_ir0[3]),
    .EX0(input_4to1_1_ir0[2]), .DR0(input_4to1_1_ir0[1]), .IR0(input_4to1_1_ir0[0]));
  SUB_SBB_1 sub_sbb_1_2 (
    .AX__DR(AX__DR), .BX__DR(BX__DR), .CX__DR(CX__DR), .DX__DR(DX__DR), .EX__DR(EX__DR), .AX__IR(AX__IR),
    .BX__IR(BX__IR), .CX__IR(CX__IR), .DX__IR(DX__IR), .EX__IR(EX__IR), .AX__BX(AX__BX), .AX__CX(AX__CX),
    .AX__DX(AX__DX), .AX__EX(AX__EX), .BX_AX(BX__AX), .BX__CX(BX__CX), .BX__DX(BX__DX), .BX__EX(BX__EX),
    .CX__AX(CX__AX), .CX__BX(CX__BX), .CX__DX(CX__DX), .CX__EX(CX__EX), .DX__AX(DX__AX), .DX__BX(DX__BX),
    .DX__CX(DX__CX), .DX__EX(DX__EX), .EX__AX(EX__AX), .EX__BX(EX__BX), .EX__CX(EX__CX), .EX__DX(EX__DX),
    .AX(input_4to1_1_ir2[6]), .BX(input_4to1_1_ir2[5]), .CX(input_4to1_1_ir2[4]), .DX(input_4to1_1_ir2[3]),
    .EX(input_4to1_1_ir2[2]), .DR(input_4to1_1_ir2[1]), .IR(input_4to1_1_ir2[0]), .Bin(sub_sbb_1_3_bout),
    .Bout(sub_sbb_1_2_bout), .OUTPUT(OUTPUT[2]));
  SUB_SBB_1 sub_sbb_1_3 (
    .AX__DR(AX__DR), .BX__DR(BX__DR), .CX__DR(CX__DR), .DX__DR(DX__DR), .EX__DR(EX__DR), .AX__IR(AX__IR),
    .BX__IR(BX__IR), .CX__IR(CX__IR), .DX__IR(DX__IR), .EX__IR(EX__IR), .AX__BX(AX__BX), .AX__CX(AX__CX),
    .AX__DX(AX__DX), .AX__EX(AX__EX), .BX_AX(BX__AX), .BX__CX(BX__CX), .BX__DX(BX__DX), .BX__EX(BX__EX),
    .CX__AX(CX__AX), .CX__BX(CX__BX), .CX__DX(CX__DX), .CX__EX(CX__EX), .DX__AX(DX__AX), .DX__BX(DX__BX),
    .DX__CX(DX__CX), .DX__EX(DX__EX), .EX__AX(EX__AX), .EX__BX(EX__BX), .EX__CX(EX__CX), .EX__DX(EX__DX),
    .AX(input_4to1_1_ir1[6]), .BX(input_4to1_1_ir1[5]), .CX(input_4to1_1_ir1[4]), .DX(input_4to1_1_ir1[3]),
    .EX(input_4to1_1_ir1[2]), .DR(input_4to1_1_ir1[1]), .IR(input_4to1_1_ir1[0]), .Bin(sub_sbb_1_4_bout),
    .Bout(sub_sbb_1_3_bout), .OUTPUT(OUTPUT[1]));
  SUB_SBB_1 sub_sbb_1_4 (
    .AX__DR(AX__DR), .BX__DR(BX__DR), .CX__DR(CX__DR), .DX__DR(DX__DR), .EX__DR(EX__DR), .AX__IR(AX__IR),
    .BX__IR(BX__IR), .CX__IR(CX__IR), .DX__IR(DX__IR), .EX__IR(EX__IR), .AX__BX(AX__BX), .AX__CX(AX__CX),
    .AX__DX(AX__DX), .AX__EX(AX__EX), .BX_AX(BX__AX), .BX__CX(BX__CX), .BX__DX(BX__DX), .BX__EX(BX__EX),
    .CX__AX(CX__AX), .CX__BX(CX__BX), .CX__DX(CX__DX), .CX__EX(CX__EX), .DX__AX(DX__AX), .DX__BX(DX__BX),
    .DX__CX(DX__CX), .DX__EX(DX__EX), .EX__AX(EX__AX), .EX__BX(EX__BX), .EX__CX(EX__CX), .EX__DX(EX__DX),
    .AX(input_4to1_1_ir0[6]), .BX(input_4to1_1_ir0[5]), .CX(input_4to1_1_ir0[4]), .DX(input_4to1_1_ir0[3]),
    .EX(input_4to1_1_ir0[2]), .DR(input_4to1_1_ir0[1]), .IR(input_4to1_1_ir0[0]), .Bin(Bin),
    .Bout(sub_sbb_1_4_bout), .OUTPUT(OUTPUT[0]));
endmodule

module SUB_SBB_1 (
  input  AX,
  input  BX,
  input  CX,
  input  DX,
  input  EX,
  input  DR,
  input  IR,
  input  Bin,
  input  AX__DR,
  input  BX__DR,
  input  CX__DR,
  input  DX__DR,
  input  EX__DR,
  input  AX__IR,
  input  BX__IR,
  input  CX__IR,
  input  DX__IR,
  input  EX__IR,
  input  AX__BX,
  input  AX__CX,
  input  AX__DX,
  input  AX__EX,
  input  BX_AX,
  input  BX__CX,
  input  BX__DX,
  input  BX__EX,
  input  CX__AX,
  input  CX__BX,
  input  CX__DX,
  input  CX__EX,
  input  DX__AX,
  input  DX__BX,
  input  DX__CX,
  input  DX__EX,
  input  EX__AX,
  input  EX__BX,
  input  EX__CX,
  input  EX__DX,
  output OUTPUT,
  output Bout
);

  wire and_1_out, and_2_out, and_3_out, and_4_out, and_5_out, and_6_out, and_7_out, and_8_out, and_9_out,
       and_10_out, and_11_out, and_12_out, and_13_out, and_14_out, and_15_out, and_16_out, and_17_out,
       and_18_out, and_19_out, and_20_out, and_21_out, and_22_out, and_23_out, and_24_out, and_25_out,
       and_26_out, and_27_out, and_28_out, and_29_out, and_30_out, and_31_out, and_32_out, and_33_out,
       and_34_out, and_35_out, and_36_out, and_37_out, and_38_out, and_39_out, and_40_out, and_41_out,
       and_42_out, and_43_out, and_44_out, and_45_out, and_46_out, and_47_out, and_48_out, and_49_out,
       and_50_out, and_51_out, and_52_out, and_53_out, and_54_out, and_55_out, and_56_out, and_57_out,
       and_58_out, and_59_out, and_60_out, or_1_out, or_2_out, or_3_out, or_4_out, or_5_out, or_6_out,
       or_7_out, or_8_out, or_9_out, or_10_out, or_11_out, or_12_out, or_13_out, or_14_out, or_15_out,
       or_16_out, or_17_out, or_18_out, or_19_out, or_20_out, or_21_out, or_22_out, or_23_out, or_24_out,
       or_25_out, or_26_out, or_27_out, or_28_out, subtractor_1_bout, subtractor_1_out, subtractor_2_bout,
       subtractor_2_out, subtractor_3_bout, subtractor_3_out, subtractor_4_bout, subtractor_4_out,
       subtractor_5_bout, subtractor_5_out, subtractor_6_bout, subtractor_6_out, subtractor_7_bout,
       subtractor_7_out, subtractor_8_bout, subtractor_8_out, subtractor_9_bout, subtractor_9_out,
       subtractor_10_bout, subtractor_10_out, subtractor_11_bout, subtractor_11_out, subtractor_12_bout,
       subtractor_12_out, subtractor_13_bout, subtractor_13_out, subtractor_14_bout, subtractor_14_out,
       subtractor_15_bout, subtractor_15_out, subtractor_16_bout, subtractor_16_out, subtractor_17_bout,
       subtractor_17_out, subtractor_18_bout, subtractor_18_out, subtractor_19_bout, subtractor_19_out,
       subtractor_20_bout, subtractor_20_out, subtractor_21_bout, subtractor_21_out, subtractor_22_bout,
       subtractor_22_out, subtractor_23_bout, subtractor_23_out, subtractor_24_bout, subtractor_24_out,
       subtractor_25_bout, subtractor_25_out, subtractor_26_bout, subtractor_26_out, subtractor_27_bout,
       subtractor_27_out, subtractor_28_bout, subtractor_28_out, subtractor_29_bout, subtractor_29_out,
       subtractor_30_bout, subtractor_30_out;

  Subtractor #(.width(1)) subtractor_1 (.a(AX), .b(DR), .out(subtractor_1_out), .bin(Bin), .bout(subtractor_1_bout));
  and and_1 (and_1_out, subtractor_1_bout, AX__DR);
  Subtractor #(.width(1)) subtractor_2 (.a(BX), .b(DR), .out(subtractor_2_out), .bin(Bin), .bout(subtractor_2_bout));
  and and_2 (and_2_out, subtractor_2_bout, BX__DR);
  Subtractor #(.width(1)) subtractor_3 (.a(CX), .b(DR), .out(subtractor_3_out), .bin(Bin), .bout(subtractor_3_bout));
  and and_3 (and_3_out, subtractor_3_bout, CX__DR);
  Subtractor #(.width(1)) subtractor_4 (.a(DX), .b(DR), .out(subtractor_4_out), .bin(Bin), .bout(subtractor_4_bout));
  and and_4 (and_4_out, subtractor_4_bout, DX__DR);
  Subtractor #(.width(1)) subtractor_5 (.a(EX), .b(DR), .out(subtractor_5_out), .bin(Bin), .bout(subtractor_5_bout));
  and and_5 (and_5_out, subtractor_5_bout, EX__DR);
  Subtractor #(.width(1)) subtractor_6 (.a(AX), .b(IR), .out(subtractor_6_out), .bin(Bin), .bout(subtractor_6_bout));
  and and_6 (and_6_out, subtractor_6_bout, AX__IR);
  Subtractor #(.width(1)) subtractor_7 (.a(BX), .b(IR), .out(subtractor_7_out), .bin(Bin), .bout(subtractor_7_bout));
  and and_7 (and_7_out, subtractor_7_bout, BX__IR);
  Subtractor #(.width(1)) subtractor_8 (.a(CX), .b(IR), .out(subtractor_8_out), .bin(Bin), .bout(subtractor_8_bout));
  and and_8 (and_8_out, subtractor_8_bout, CX__IR);
  Subtractor #(.width(1)) subtractor_9 (.a(DX), .b(IR), .out(subtractor_9_out), .bin(Bin), .bout(subtractor_9_bout));
  and and_9 (and_9_out, subtractor_9_bout, DX__IR);
  Subtractor #(.width(1)) subtractor_10 (.a(EX), .b(IR), .out(subtractor_10_out), .bin(Bin), .bout(subtractor_10_bout));
  and and_10 (and_10_out, subtractor_10_bout, EX__IR);
  Subtractor #(.width(1)) subtractor_11 (.a(AX), .b(BX), .out(subtractor_11_out), .bin(Bin), .bout(subtractor_11_bout));
  and and_11 (and_11_out, subtractor_11_bout, AX__BX);
  Subtractor #(.width(1)) subtractor_12 (.a(AX), .b(CX), .out(subtractor_12_out), .bin(Bin), .bout(subtractor_12_bout));
  and and_12 (and_12_out, subtractor_12_bout, AX__CX);
  Subtractor #(.width(1)) subtractor_13 (.a(AX), .b(DX), .out(subtractor_13_out), .bin(Bin), .bout(subtractor_13_bout));
  and and_13 (and_13_out, subtractor_13_bout, AX__DX);
  Subtractor #(.width(1)) subtractor_14 (.a(AX), .b(EX), .out(subtractor_14_out), .bin(Bin), .bout(subtractor_14_bout));
  and and_14 (and_14_out, subtractor_14_bout, AX__EX);
  Subtractor #(.width(1)) subtractor_15 (.a(BX), .b(AX), .out(subtractor_15_out), .bin(Bin), .bout(subtractor_15_bout));
  and and_15 (and_15_out, subtractor_15_bout, BX_AX);
  Subtractor #(.width(1)) subtractor_16 (.a(BX), .b(CX), .out(subtractor_16_out), .bin(Bin), .bout(subtractor_16_bout));
  and and_16 (and_16_out, subtractor_16_bout, BX__CX);
  Subtractor #(.width(1)) subtractor_17 (.a(BX), .b(DX), .out(subtractor_17_out), .bin(Bin), .bout(subtractor_17_bout));
  and and_17 (and_17_out, subtractor_17_bout, BX__DX);
  Subtractor #(.width(1)) subtractor_18 (.a(BX), .b(EX), .out(subtractor_18_out), .bin(Bin), .bout(subtractor_18_bout));
  and and_18 (and_18_out, subtractor_18_bout, BX__EX);
  Subtractor #(.width(1)) subtractor_19 (.a(CX), .b(AX), .out(subtractor_19_out), .bin(Bin), .bout(subtractor_19_bout));
  and and_19 (and_19_out, subtractor_19_bout, CX__AX);
  Subtractor #(.width(1)) subtractor_20 (.a(CX), .b(BX), .out(subtractor_20_out), .bin(Bin), .bout(subtractor_20_bout));
  and and_20 (and_20_out, subtractor_20_bout, CX__BX);
  Subtractor #(.width(1)) subtractor_21 (.a(CX), .b(DX), .out(subtractor_21_out), .bin(Bin), .bout(subtractor_21_bout));
  and and_21 (and_21_out, subtractor_21_bout, CX__DX);
  Subtractor #(.width(1)) subtractor_22 (.a(CX), .b(EX), .out(subtractor_22_out), .bin(Bin), .bout(subtractor_22_bout));
  and and_22 (and_22_out, subtractor_22_bout, CX__EX);
  Subtractor #(.width(1)) subtractor_23 (.a(DX), .b(AX), .out(subtractor_23_out), .bin(Bin), .bout(subtractor_23_bout));
  and and_23 (and_23_out, subtractor_23_bout, DX__AX);
  Subtractor #(.width(1)) subtractor_24 (.a(DX), .b(BX), .out(subtractor_24_out), .bin(Bin), .bout(subtractor_24_bout));
  and and_24 (and_24_out, subtractor_24_bout, DX__BX);
  Subtractor #(.width(1)) subtractor_25 (.a(DX), .b(CX), .out(subtractor_25_out), .bin(Bin), .bout(subtractor_25_bout));
  and and_25 (and_25_out, subtractor_25_bout, DX__CX);
  Subtractor #(.width(1)) subtractor_26 (.a(DX), .b(EX), .out(subtractor_26_out), .bin(Bin), .bout(subtractor_26_bout));
  and and_26 (and_26_out, subtractor_26_bout, DX__EX);
  Subtractor #(.width(1)) subtractor_27 (.a(EX), .b(AX), .out(subtractor_27_out), .bin(Bin), .bout(subtractor_27_bout));
  and and_27 (and_27_out, subtractor_27_bout, EX__AX);
  Subtractor #(.width(1)) subtractor_28 (.a(EX), .b(BX), .out(subtractor_28_out), .bin(Bin), .bout(subtractor_28_bout));
  and and_28 (and_28_out, subtractor_28_bout, EX__BX);
  Subtractor #(.width(1)) subtractor_29 (.a(EX), .b(CX), .out(subtractor_29_out), .bin(Bin), .bout(subtractor_29_bout));
  and and_29 (and_29_out, subtractor_29_bout, EX__CX);
  Subtractor #(.width(1)) subtractor_30 (.a(EX), .b(DX), .out(subtractor_30_out), .bin(Bin), .bout(subtractor_30_bout));
  and and_30 (and_30_out, subtractor_30_bout, EX__DX);
  or or_1 (or_1_out, and_2_out, and_1_out);
  or or_2 (or_2_out, and_3_out, or_1_out);
  or or_3 (or_3_out, and_4_out, or_2_out);
  or or_4 (or_4_out, and_5_out, or_3_out);
  or or_5 (or_5_out, and_6_out, or_4_out);
  or or_6 (or_6_out, and_7_out, or_5_out);
  or or_7 (or_7_out, and_8_out, or_6_out);
  or or_8 (or_8_out, and_9_out, or_7_out);
  or or_9 (or_9_out, and_10_out, or_8_out);
  or or_10 (or_10_out, and_11_out, or_9_out);
  or or_11 (or_11_out, and_12_out, or_10_out);
  or or_12 (or_12_out, and_13_out, or_11_out);
  or or_13 (or_13_out, and_14_out, or_12_out);
  or or_14 (or_14_out, and_15_out, or_13_out);
  or or_15 (or_15_out, and_16_out, or_14_out);
  or or_16 (or_16_out, and_17_out, or_15_out);
  or or_17 (or_17_out, and_18_out, or_16_out);
  or or_18 (or_18_out, and_19_out, or_17_out);
  or or_19 (or_19_out, and_20_out, or_18_out);
  or or_20 (or_20_out, and_21_out, or_19_out);
  or or_21 (or_21_out, and_22_out, or_20_out);
  or or_22 (or_22_out, and_23_out, or_21_out);
  or or_23 (or_23_out, and_24_out, or_22_out);
  or or_24 (or_24_out, and_25_out, or_23_out);
  or or_25 (or_25_out, and_26_out, or_24_out);
  or or_26 (or_26_out, and_27_out, or_25_out);
  or or_27 (or_27_out, and_28_out, or_26_out);
  or or_28 (or_28_out, and_29_out, or_27_out);
  or or_29 (Bout, and_30_out, or_28_out);
  and and_31 (and_31_out, AX__DR, subtractor_1_out);
  and and_32 (and_32_out, BX__DR, subtractor_2_out);
  and and_33 (and_33_out, CX__DR, subtractor_3_out);
  and and_34 (and_34_out, DX__DR, subtractor_4_out);
  and and_35 (and_35_out, EX__DR, subtractor_5_out);
  and and_36 (and_36_out, AX__IR, subtractor_6_out);
  and and_37 (and_37_out, BX__IR, subtractor_7_out);
  and and_38 (and_38_out, CX__IR, subtractor_8_out);
  and and_39 (and_39_out, DX__IR, subtractor_9_out);
  and and_40 (and_40_out, EX__IR, subtractor_10_out);
  and and_41 (and_41_out, AX__BX, subtractor_11_out);
  and and_42 (and_42_out, AX__CX, subtractor_12_out);
  and and_43 (and_43_out, AX__DX, subtractor_13_out);
  and and_44 (and_44_out, AX__EX, subtractor_14_out);
  and and_45 (and_45_out, BX_AX, subtractor_15_out);
  and and_46 (and_46_out, BX__CX, subtractor_16_out);
  and and_47 (and_47_out, BX__DX, subtractor_17_out);
  and and_48 (and_48_out, BX__EX, subtractor_18_out);
  and and_49 (and_49_out, CX__AX, subtractor_19_out);
  and and_50 (and_50_out, CX__BX, subtractor_20_out);
  and and_51 (and_51_out, CX__DX, subtractor_21_out);
  and and_52 (and_52_out, CX__EX, subtractor_22_out);
  and and_53 (and_53_out, DX__AX, subtractor_23_out);
  and and_54 (and_54_out, DX__BX, subtractor_24_out);
  and and_55 (and_55_out, DX__CX, subtractor_25_out);
  and and_56 (and_56_out, DX__EX, subtractor_26_out);
  and and_57 (and_57_out, EX__AX, subtractor_27_out);
  and and_58 (and_58_out, EX__BX, subtractor_28_out);
  and and_59 (and_59_out, EX__CX, subtractor_29_out);
  and and_60 (and_60_out, EX__DX, subtractor_30_out);
  or or_30 (OUTPUT, and_31_out, and_32_out, and_33_out, and_34_out, and_35_out, and_36_out, and_37_out, and_38_out, and_39_out, and_40_out, and_41_out, and_42_out, and_43_out, and_44_out, and_45_out, and_46_out, and_47_out, and_48_out, and_49_out, and_50_out, and_51_out, and_52_out, and_53_out, and_54_out, and_55_out, and_56_out, and_57_out, and_58_out, and_59_out, and_60_out);
endmodule

module ADD_ADC_1 (
  input  AX,
  input  BX,
  input  CX,
  input  DX,
  input  EX,
  input  DR,
  input  IR,
  input  Cin,
  input  AX__DR,
  input  BX__DR,
  input  CX__DR,
  input  DX__DR,
  input  EX__DR,
  input  AX__IR,
  input  BX__IR,
  input  CX__IR,
  input  DX__IR,
  input  EX__IR,
  input  AX__BX,
  input  AX__CX,
  input  AX__DX,
  input  AX__EX,
  input  BX__CX,
  input  BX__DX,
  input  BX__EX,
  input  CX__DX,
  input  CX__EX,
  input  DX__EX,
  output OUTPUT,
  output Cout
);

  wire adder_1_cout, adder_1_out, adder_2_cout, adder_2_out, adder_3_cout, adder_3_out, adder_4_cout,
       adder_4_out, adder_5_cout, adder_5_out, adder_6_cout, adder_6_out, adder_7_cout, adder_7_out,
       adder_8_cout, adder_8_out, adder_9_cout, adder_9_out, adder_10_cout, adder_10_out, adder_11_cout,
       adder_11_out, adder_12_cout, adder_12_out, adder_13_cout, adder_13_out, adder_14_cout, adder_14_out,
       adder_15_cout, adder_15_out, adder_16_cout, adder_16_out, adder_17_cout, adder_17_out, adder_18_cout,
       adder_18_out, adder_19_cout, adder_19_out, adder_20_cout, adder_20_out, and_1_out, and_2_out,
       and_3_out, and_4_out, and_5_out, and_6_out, and_7_out, and_8_out, and_9_out, and_10_out, and_11_out,
       and_12_out, and_13_out, and_14_out, and_15_out, and_16_out, and_17_out, and_18_out, and_19_out,
       and_20_out, and_21_out, and_22_out, and_23_out, and_24_out, and_25_out, and_26_out, and_27_out,
       and_28_out, and_29_out, and_30_out, and_31_out, and_32_out, and_33_out, and_34_out, and_35_out,
       and_36_out, and_37_out, and_38_out, and_39_out, and_40_out, or_1_out, or_2_out, or_3_out, or_4_out,
       or_5_out, or_6_out, or_7_out, or_8_out, or_9_out, or_10_out, or_11_out, or_12_out, or_13_out,
       or_14_out, or_15_out, or_16_out, or_17_out, or_18_out;

  Adder #(.width(1)) adder_1 (.a(AX), .b(DR), .out(adder_1_out), .cin(Cin), .cout(adder_1_cout));
  and and_1 (and_1_out, adder_1_cout, AX__DR);
  Adder #(.width(1)) adder_2 (.a(BX), .b(DR), .out(adder_2_out), .cin(Cin), .cout(adder_2_cout));
  and and_2 (and_2_out, adder_2_cout, BX__DR);
  Adder #(.width(1)) adder_3 (.a(CX), .b(DR), .out(adder_3_out), .cin(Cin), .cout(adder_3_cout));
  and and_3 (and_3_out, adder_3_cout, CX__DR);
  Adder #(.width(1)) adder_4 (.a(DX), .b(DR), .out(adder_4_out), .cin(Cin), .cout(adder_4_cout));
  and and_4 (and_4_out, adder_4_cout, DX__DR);
  Adder #(.width(1)) adder_5 (.a(EX), .b(DR), .out(adder_5_out), .cin(Cin), .cout(adder_5_cout));
  and and_5 (and_5_out, adder_5_cout, EX__DR);
  Adder #(.width(1)) adder_6 (.a(AX), .b(IR), .out(adder_6_out), .cin(Cin), .cout(adder_6_cout));
  and and_6 (and_6_out, adder_6_cout, AX__IR);
  Adder #(.width(1)) adder_7 (.a(BX), .b(IR), .out(adder_7_out), .cin(Cin), .cout(adder_7_cout));
  and and_7 (and_7_out, adder_7_cout, BX__IR);
  Adder #(.width(1)) adder_8 (.a(CX), .b(IR), .out(adder_8_out), .cin(Cin), .cout(adder_8_cout));
  and and_8 (and_8_out, adder_8_cout, CX__IR);
  Adder #(.width(1)) adder_9 (.a(DX), .b(IR), .out(adder_9_out), .cin(Cin), .cout(adder_9_cout));
  and and_9 (and_9_out, adder_9_cout, DX__IR);
  Adder #(.width(1)) adder_10 (.a(EX), .b(IR), .out(adder_10_out), .cin(Cin), .cout(adder_10_cout));
  and and_10 (and_10_out, adder_10_cout, EX__IR);
  Adder #(.width(1)) adder_11 (.a(AX), .b(BX), .out(adder_11_out), .cin(Cin), .cout(adder_11_cout));
  and and_11 (and_11_out, adder_11_cout, AX__BX);
  Adder #(.width(1)) adder_12 (.a(AX), .b(CX), .out(adder_12_out), .cin(Cin), .cout(adder_12_cout));
  and and_12 (and_12_out, adder_12_cout, AX__CX);
  Adder #(.width(1)) adder_13 (.a(AX), .b(DX), .out(adder_13_out), .cin(Cin), .cout(adder_13_cout));
  and and_13 (and_13_out, adder_13_cout, AX__DX);
  Adder #(.width(1)) adder_14 (.a(AX), .b(EX), .out(adder_14_out), .cin(Cin), .cout(adder_14_cout));
  and and_14 (and_14_out, adder_14_cout, AX__EX);
  Adder #(.width(1)) adder_15 (.a(BX), .b(CX), .out(adder_15_out), .cin(Cin), .cout(adder_15_cout));
  and and_15 (and_15_out, adder_15_cout, BX__CX);
  Adder #(.width(1)) adder_16 (.a(BX), .b(DX), .out(adder_16_out), .cin(Cin), .cout(adder_16_cout));
  and and_16 (and_16_out, adder_16_cout, BX__DX);
  Adder #(.width(1)) adder_17 (.a(BX), .b(EX), .out(adder_17_out), .cin(Cin), .cout(adder_17_cout));
  and and_17 (and_17_out, adder_17_cout, BX__EX);
  Adder #(.width(1)) adder_18 (.a(CX), .b(DX), .out(adder_18_out), .cin(Cin), .cout(adder_18_cout));
  and and_18 (and_18_out, adder_18_cout, CX__DX);
  Adder #(.width(1)) adder_19 (.a(CX), .b(EX), .out(adder_19_out), .cin(Cin), .cout(adder_19_cout));
  and and_19 (and_19_out, adder_19_cout, CX__EX);
  Adder #(.width(1)) adder_20 (.a(DX), .b(EX), .out(adder_20_out), .cin(Cin), .cout(adder_20_cout));
  and and_20 (and_20_out, adder_20_cout, DX__EX);
  or or_1 (or_1_out, and_2_out, and_1_out);
  or or_2 (or_2_out, and_3_out, or_1_out);
  or or_3 (or_3_out, and_4_out, or_2_out);
  or or_4 (or_4_out, and_5_out, or_3_out);
  or or_5 (or_5_out, and_6_out, or_4_out);
  or or_6 (or_6_out, and_7_out, or_5_out);
  or or_7 (or_7_out, and_8_out, or_6_out);
  or or_8 (or_8_out, and_9_out, or_7_out);
  or or_9 (or_9_out, and_10_out, or_8_out);
  or or_10 (or_10_out, and_11_out, or_9_out);
  or or_11 (or_11_out, and_12_out, or_10_out);
  or or_12 (or_12_out, and_13_out, or_11_out);
  or or_13 (or_13_out, and_14_out, or_12_out);
  or or_14 (or_14_out, and_15_out, or_13_out);
  or or_15 (or_15_out, and_16_out, or_14_out);
  or or_16 (or_16_out, and_17_out, or_15_out);
  or or_17 (or_17_out, and_18_out, or_16_out);
  or or_18 (or_18_out, and_19_out, or_17_out);
  or or_19 (Cout, and_20_out, or_18_out);
  and and_21 (and_21_out, AX__DR, adder_1_out);
  and and_22 (and_22_out, BX__DR, adder_2_out);
  and and_23 (and_23_out, CX__DR, adder_3_out);
  and and_24 (and_24_out, DX__DR, adder_4_out);
  and and_25 (and_25_out, EX__DR, adder_5_out);
  and and_26 (and_26_out, AX__IR, adder_6_out);
  and and_27 (and_27_out, BX__IR, adder_7_out);
  and and_28 (and_28_out, CX__IR, adder_8_out);
  and and_29 (and_29_out, DX__IR, adder_9_out);
  and and_30 (and_30_out, EX__IR, adder_10_out);
  and and_31 (and_31_out, AX__BX, adder_11_out);
  and and_32 (and_32_out, AX__CX, adder_12_out);
  and and_33 (and_33_out, AX__DX, adder_13_out);
  and and_34 (and_34_out, AX__EX, adder_14_out);
  and and_35 (and_35_out, BX__CX, adder_15_out);
  and and_36 (and_36_out, BX__DX, adder_16_out);
  and and_37 (and_37_out, BX__EX, adder_17_out);
  and and_38 (and_38_out, CX__DX, adder_18_out);
  and and_39 (and_39_out, CX__EX, adder_19_out);
  and and_40 (and_40_out, DX__EX, adder_20_out);
  or or_20 (OUTPUT, and_21_out, and_22_out, and_23_out, and_24_out, and_25_out, and_26_out, and_27_out, and_28_out, and_29_out, and_30_out, and_31_out, and_32_out, and_33_out, and_34_out, and_35_out, and_36_out, and_37_out, and_38_out, and_39_out, and_40_out);
endmodule
module SUB_SBB (
  input  AX__DR,
  input  BX__DR,
  input  CX__DR,
  input  DX__DR,
  input  EX__DR,
  input  AX__IR,
  input  BX__IR,
  input  CX__IR,
  input  DX__IR,
  input  EX__IR,
  input  AX__BX,
  input  AX__CX,
  input  AX__DX,
  input  AX__EX,
  input  BX__AX,
  input  BX__CX,
  input  BX__DX,
  input  BX__EX,
  input  CX__AX,
  input  CX__BX,
  input  CX__DX,
  input  CX__EX,
  input  DX__AX,
  input  DX__BX,
  input  DX__CX,
  input  DX__EX,
  input  EX__AX,
  input  EX__BX,
  input  EX__CX,
  input  EX__DX,
  input  [15:0] AX,
  input  [15:0] BX,
  input  [15:0] CX,
  input  [15:0] DX,
  input  [15:0] EX,
  input  [15:0] DR,
  input  [15:0] IR,
  input  Bin,
  output [15:0] OUTPUT,
  output Bout
);

  wire sub_sbb_4_1_bout, sub_sbb_4_2_bout, sub_sbb_4_3_bout;
  wire [3:0] input_16to4_1_ax_0_3, input_16to4_1_ax_4_7, input_16to4_1_ax_8_11, input_16to4_1_ax_12_15,
       input_16to4_1_bx_0_3, input_16to4_1_bx_4_7, input_16to4_1_bx_8_11, input_16to4_1_bx_12_15,
       input_16to4_1_cx_0_3, input_16to4_1_cx_4_7, input_16to4_1_cx_8_11, input_16to4_1_cx_12_15,
       input_16to4_1_dr_0_3, input_16to4_1_dr_4_7, input_16to4_1_dr_8_11, input_16to4_1_dr_12_15,
       input_16to4_1_dx_0_3, input_16to4_1_dx_4_7, input_16to4_1_dx_8_11, input_16to4_1_dx_12_15,
       input_16to4_1_ex_0_3, input_16to4_1_ex_4_7, input_16to4_1_ex_8_11, input_16to4_1_ex_12_15,
       input_16to4_1_ir_0_3, input_16to4_1_ir_0_3_2, input_16to4_1_ir_4_7, input_16to4_1_ir_12_15;

  INPUT_16to4 input_16to4_1 (
    .AX(AX), .BX(BX), .CX(CX), .DX(DX), .EX(EX), .DR(DR), .IR(IR), .AX_0_3(input_16to4_1_ax_0_3),
    .BX_0_3(input_16to4_1_bx_0_3), .CX_0_3(input_16to4_1_cx_0_3), .DX_0_3(input_16to4_1_dx_0_3),
    .EX_0_3(input_16to4_1_ex_0_3), .DR_0_3(input_16to4_1_dr_0_3), .IR_0_3(input_16to4_1_ir_0_3),
    .AX_4_7(input_16to4_1_ax_4_7), .BX_4_7(input_16to4_1_bx_4_7), .CX_4_7(input_16to4_1_cx_4_7),
    .DX_4_7(input_16to4_1_dx_4_7), .EX_4_7(input_16to4_1_ex_4_7), .DR_4_7(input_16to4_1_dr_4_7),
    .IR_4_7(input_16to4_1_ir_4_7), .AX_8_11(input_16to4_1_ax_8_11), .BX_8_11(input_16to4_1_bx_8_11),
    .CX_8_11(input_16to4_1_cx_8_11), .DX_8_11(input_16to4_1_dx_8_11), .EX_8_11(input_16to4_1_ex_8_11),
    .DR_8_11(input_16to4_1_dr_8_11), .IR_0_3_2(input_16to4_1_ir_0_3_2), .AX_12_15(input_16to4_1_ax_12_15),
    .BX_12_15(input_16to4_1_bx_12_15), .CX_12_15(input_16to4_1_cx_12_15), .DX_12_15(input_16to4_1_dx_12_15),
    .EX_12_15(input_16to4_1_ex_12_15), .DR_12_15(input_16to4_1_dr_12_15), .IR_12_15(input_16to4_1_ir_12_15));
  SUB_SBB_4 sub_sbb_4_1 (
    .AX(input_16to4_1_ax_0_3), .BX(input_16to4_1_bx_0_3), .CX(input_16to4_1_cx_0_3),
    .DX(input_16to4_1_dx_0_3), .EX(input_16to4_1_ex_0_3), .DR(input_16to4_1_dr_0_3),
    .IR(input_16to4_1_ir_0_3), .Bin(Bin), .AX__DR(AX__DR), .BX__DR(BX__DR), .CX__DR(CX__DR), .DX__DR(DX__DR),
    .EX__DR(EX__DR), .AX__IR(AX__IR), .BX__IR(BX__IR), .CX__IR(CX__IR), .DX__IR(DX__IR), .EX__IR(EX__IR),
    .AX__BX(AX__BX), .AX__CX(AX__CX), .AX__DX(AX__DX), .AX__EX(AX__EX), .BX__AX(BX__AX), .BX__CX(BX__CX),
    .BX__DX(BX__DX), .BX__EX(BX__EX), .CX__AX(CX__AX), .CX__BX(CX__BX), .CX__DX(CX__DX), .CX__EX(CX__EX),
    .DX__AX(DX__AX), .DX__BX(DX__BX), .DX__CX(DX__CX), .DX__EX(DX__EX), .EX__AX(EX__AX), .EX__BX(EX__BX),
    .EX__CX(EX__CX), .EX__DX(EX__DX), .OUTPUT(OUTPUT[3:0]), .Bout(sub_sbb_4_1_bout));
  SUB_SBB_4 sub_sbb_4_2 (
    .AX(input_16to4_1_ax_4_7), .BX(input_16to4_1_bx_4_7), .CX(input_16to4_1_cx_4_7),
    .DX(input_16to4_1_dx_4_7), .EX(input_16to4_1_ex_4_7), .DR(input_16to4_1_dr_4_7),
    .IR(input_16to4_1_ir_4_7), .Bin(sub_sbb_4_1_bout), .AX__DR(AX__DR), .BX__DR(BX__DR), .CX__DR(CX__DR),
    .DX__DR(DX__DR), .EX__DR(EX__DR), .AX__IR(AX__IR), .BX__IR(BX__IR), .CX__IR(CX__IR), .DX__IR(DX__IR),
    .EX__IR(EX__IR), .AX__BX(AX__BX), .AX__CX(AX__CX), .AX__DX(AX__DX), .AX__EX(AX__EX), .BX__AX(BX__AX),
    .BX__CX(BX__CX), .BX__DX(BX__DX), .BX__EX(BX__EX), .CX__AX(CX__AX), .CX__BX(CX__BX), .CX__DX(CX__DX),
    .CX__EX(CX__EX), .DX__AX(DX__AX), .DX__BX(DX__BX), .DX__CX(DX__CX), .DX__EX(DX__EX), .EX__AX(EX__AX),
    .EX__BX(EX__BX), .EX__CX(EX__CX), .EX__DX(EX__DX), .OUTPUT(OUTPUT[7:4]), .Bout(sub_sbb_4_2_bout));
  SUB_SBB_4 sub_sbb_4_3 (
    .AX(input_16to4_1_ax_8_11), .BX(input_16to4_1_bx_8_11), .CX(input_16to4_1_cx_8_11),
    .DX(input_16to4_1_dx_8_11), .EX(input_16to4_1_ex_8_11), .DR(input_16to4_1_dr_8_11),
    .IR(input_16to4_1_ir_0_3_2), .Bin(sub_sbb_4_2_bout), .AX__DR(AX__DR), .BX__DR(BX__DR), .CX__DR(CX__DR),
    .DX__DR(DX__DR), .EX__DR(EX__DR), .AX__IR(AX__IR), .BX__IR(BX__IR), .CX__IR(CX__IR), .DX__IR(DX__IR),
    .EX__IR(EX__IR), .AX__BX(AX__BX), .AX__CX(AX__CX), .AX__DX(AX__DX), .AX__EX(AX__EX), .BX__AX(BX__AX),
    .BX__CX(BX__CX), .BX__DX(BX__DX), .BX__EX(BX__EX), .CX__AX(CX__AX), .CX__BX(CX__BX), .CX__DX(CX__DX),
    .CX__EX(CX__EX), .DX__AX(DX__AX), .DX__BX(DX__BX), .DX__CX(DX__CX), .DX__EX(DX__EX), .EX__AX(EX__AX),
    .EX__BX(EX__BX), .EX__CX(EX__CX), .EX__DX(EX__DX), .OUTPUT(OUTPUT[11:8]), .Bout(sub_sbb_4_3_bout));
  SUB_SBB_4 sub_sbb_4_4 (
    .AX(input_16to4_1_ax_12_15), .BX(input_16to4_1_bx_12_15), .CX(input_16to4_1_cx_12_15),
    .DX(input_16to4_1_dx_12_15), .EX(input_16to4_1_ex_12_15), .DR(input_16to4_1_dr_12_15),
    .IR(input_16to4_1_ir_12_15), .Bin(sub_sbb_4_3_bout), .AX__DR(AX__DR), .BX__DR(BX__DR), .CX__DR(CX__DR),
    .DX__DR(DX__DR), .EX__DR(EX__DR), .AX__IR(AX__IR), .BX__IR(BX__IR), .CX__IR(CX__IR), .DX__IR(DX__IR),
    .EX__IR(EX__IR), .AX__BX(AX__BX), .AX__CX(AX__CX), .AX__DX(AX__DX), .AX__EX(AX__EX), .BX__AX(BX__AX),
    .BX__CX(BX__CX), .BX__DX(BX__DX), .BX__EX(BX__EX), .CX__AX(CX__AX), .CX__BX(CX__BX), .CX__DX(CX__DX),
    .CX__EX(CX__EX), .DX__AX(DX__AX), .DX__BX(DX__BX), .DX__CX(DX__CX), .DX__EX(DX__EX), .EX__AX(EX__AX),
    .EX__BX(EX__BX), .EX__CX(EX__CX), .EX__DX(EX__DX), .OUTPUT(OUTPUT[15:12]), .Bout(Bout));
endmodule

module ALU (
  input  [15:0] AX,
  input  [15:0] BX,
  input  [15:0] CX,
  input  [15:0] DX,
  input  [15:0] EX,
  input  [15:0] DR,
  input  [15:0] IR,
  input  AX__DR,
  input  BX__DR,
  input  CX__DR,
  input  DX__DR,
  input  EX__DR,
  input  AX__IR,
  input  BX__IR,
  input  CX__IR,
  input  DX__IR,
  input  EX__IR,
  input  AX__BX,
  input  AX__CX,
  input  AX__DX,
  input  AX__EX,
  input  BX_AX,
  input  BX__CX,
  input  BX__DX,
  input  BX__EX,
  input  CX__AX,
  input  CX__BX,
  input  CX__DX,
  input  CX__EX,
  input  DX__AX,
  input  DX__BX,
  input  DX__CX,
  input  DX__EX,
  input  EX__AX,
  input  EX__BX,
  input  EX__CX,
  input  EX__DX,
  input  Cin,
  input  AND,
  input  OR,
  input  XOR,
  input  ADD,
  input  ADC,
  input  SUB,
  input  SBB,
  input  MUL,
  input  DIV,
  input  CMP,
  output Zero,
  output [15:0] MAIN_OUT,
  output [15:0] SECOND_OUT,
  output Cout
);

  wire add_adc_1_cout, and_1_out, and_3_out, cmp_1_a___b, cmp_1_a___b_2, cmp_1_a___b_3, or_2_out, or_3_out,
       sub_sbb_1_bout;
  wire [15:0] add_adc_1_output, and_2_output, div_1_quotient, div_1_remainder, mul_1_high_16, mul_1_low_16,
       or_1_output, sub_sbb_1_output, xor_1_output;
  wire [19:0] alu_register_adjuster_1__20;
  wire [29:0] alu_register_adjuster_1__30;

  and and_1 (and_1_out, Cin, ADC);
  ALU_REGISTER_ADJUSTER alu_register_adjuster_1 (
    .AX__DR(AX__DR), .BX__DR(BX__DR), .CX__DR(CX__DR), .DX__DR(DX__DR), .EX__DR(EX__DR), .AX__IR(AX__IR),
    .BX__IR(BX__IR), .CX__IR(CX__IR), .DX__IR(DX__IR), .EX__IR(EX__IR), .AX__BX(AX__BX), .AX__CX(AX__CX),
    .AX__DX(AX__DX), .AX__EX(AX__EX), .BX__AX(BX_AX), .BX__CX(BX__CX), .BX__DX(BX__DX), .BX__EX(BX__EX),
    .CX__AX(CX__AX), .CX__BX(CX__BX), .CX__DX(CX__DX), .CX__EX(CX__EX), .DX__AX(DX__AX), .DX__BX(DX__BX),
    .DX__CX(DX__CX), .DX__EX(DX__EX), .EX__AX(EX__AX), .EX__BX(EX__BX), .EX__CX(EX__CX), .EX__DX(EX__DX),
    ._30(alu_register_adjuster_1__30), ._20(alu_register_adjuster_1__20));
  AND and_2 (
    .AX(AX), .BX(BX), .CX(CX), .DX(DX), .EX(EX), .DR(DR), .IR(IR), .AX__DR(alu_register_adjuster_1__20[19]),
    .BX__DR(alu_register_adjuster_1__20[18]), .CX__DR(alu_register_adjuster_1__20[17]),
    .DX__DR(alu_register_adjuster_1__20[16]), .EX__DR(alu_register_adjuster_1__20[15]),
    .AX__IR(alu_register_adjuster_1__20[14]), .BX__IR(alu_register_adjuster_1__20[13]),
    .CX__IR(alu_register_adjuster_1__20[12]), .DX__IR(alu_register_adjuster_1__20[11]),
    .EX__IR(alu_register_adjuster_1__20[10]), .AX__BX(alu_register_adjuster_1__20[9]),
    .AX__CX(alu_register_adjuster_1__20[8]), .AX__DX(alu_register_adjuster_1__20[7]),
    .AX__EX(alu_register_adjuster_1__20[6]), .BX__CX(alu_register_adjuster_1__20[5]),
    .BX__DX(alu_register_adjuster_1__20[4]), .BX__EX(alu_register_adjuster_1__20[3]),
    .CX__DX(alu_register_adjuster_1__20[2]), .CX__EX(alu_register_adjuster_1__20[1]),
    .DX__EX(alu_register_adjuster_1__20[0]), .OUTPUT(and_2_output));
  OR or_1 (
    .AX(AX), .BX(BX), .CX(CX), .DX(DX), .EX(EX), .DR(DR), .IR(IR), .AX__DR(alu_register_adjuster_1__20[19]),
    .BX__DR(alu_register_adjuster_1__20[18]), .CX__DR(alu_register_adjuster_1__20[17]),
    .DX__DR(alu_register_adjuster_1__20[16]), .EX__DR(alu_register_adjuster_1__20[15]),
    .AX__IR(alu_register_adjuster_1__20[14]), .BX__IR(alu_register_adjuster_1__20[13]),
    .CX__IR(alu_register_adjuster_1__20[12]), .DX__IR(alu_register_adjuster_1__20[11]),
    .EX__IR(alu_register_adjuster_1__20[10]), .AX__BX(alu_register_adjuster_1__20[9]),
    .AX__CX(alu_register_adjuster_1__20[8]), .AX__DX(alu_register_adjuster_1__20[7]),
    .AX__EX(alu_register_adjuster_1__20[6]), .BX__CX(alu_register_adjuster_1__20[5]),
    .BX__DX(alu_register_adjuster_1__20[4]), .BX__EX(alu_register_adjuster_1__20[3]),
    .CX__DX(alu_register_adjuster_1__20[2]), .CX__EX(alu_register_adjuster_1__20[1]),
    .DX__EX(alu_register_adjuster_1__20[0]), .OUTPUT(or_1_output));
  XOR xor_1 (
    .AX(AX), .BX(BX), .CX(CX), .DX(DX), .EX(EX), .DR(DR), .IR(IR), .AX__DR(alu_register_adjuster_1__20[19]),
    .BX__DR(alu_register_adjuster_1__20[18]), .CX__DR(alu_register_adjuster_1__20[17]),
    .DX__DR(alu_register_adjuster_1__20[16]), .EX__DR(alu_register_adjuster_1__20[15]),
    .AX__IR(alu_register_adjuster_1__20[14]), .BX__IR(alu_register_adjuster_1__20[13]),
    .CX__IR(alu_register_adjuster_1__20[12]), .DX__IR(alu_register_adjuster_1__20[11]),
    .EX__IR(alu_register_adjuster_1__20[10]), .AX__BX(alu_register_adjuster_1__20[9]),
    .AX__CX(alu_register_adjuster_1__20[8]), .AX__DX(alu_register_adjuster_1__20[7]),
    .AX__EX(alu_register_adjuster_1__20[6]), .BX__CX(alu_register_adjuster_1__20[5]),
    .BX__DX(alu_register_adjuster_1__20[4]), .BX__EX(alu_register_adjuster_1__20[3]),
    .CX__DX(alu_register_adjuster_1__20[2]), .CX__EX(alu_register_adjuster_1__20[1]),
    .DX__EX(alu_register_adjuster_1__20[0]), .OUTPUT(xor_1_output));
  ADD_ADC add_adc_1 (
    .AX(AX), .BX(BX), .CX(CX), .DX(DX), .EX(EX), .DR(DR), .IR(IR), .Cin(and_1_out),
    .AX__DR(alu_register_adjuster_1__20[19]), .BX__DR(alu_register_adjuster_1__20[18]),
    .CX__DR(alu_register_adjuster_1__20[17]), .DX__DR(alu_register_adjuster_1__20[16]),
    .EX__DR(alu_register_adjuster_1__20[15]), .AX__IR(alu_register_adjuster_1__20[14]),
    .BX__IR(alu_register_adjuster_1__20[13]), .CX__IR(alu_register_adjuster_1__20[12]),
    .DX__IR(alu_register_adjuster_1__20[11]), .EX__IR(alu_register_adjuster_1__20[10]),
    .AX__BX(alu_register_adjuster_1__20[9]), .AX__CX(alu_register_adjuster_1__20[8]),
    .AX__DX(alu_register_adjuster_1__20[7]), .AX__EX(alu_register_adjuster_1__20[6]),
    .BX__CX(alu_register_adjuster_1__20[5]), .BX__DX(alu_register_adjuster_1__20[4]),
    .BX__EX(alu_register_adjuster_1__20[3]), .CX__DX(alu_register_adjuster_1__20[2]),
    .CX__EX(alu_register_adjuster_1__20[1]), .DX__EX(alu_register_adjuster_1__20[0]),
    .OUTPUT(add_adc_1_output), .Cout(add_adc_1_cout));
  MUL mul_1 (
    .AX(AX), .BX(BX), .CX(CX), .DX(DX), .EX(EX), .DR(DR), .IR(IR), .AX__DR(alu_register_adjuster_1__20[19]),
    .BX__DR(alu_register_adjuster_1__20[18]), .CX__DR(alu_register_adjuster_1__20[17]),
    .DX__DR(alu_register_adjuster_1__20[16]), .EX__DR(alu_register_adjuster_1__20[15]),
    .AX__IR(alu_register_adjuster_1__20[14]), .BX__IR(alu_register_adjuster_1__20[13]),
    .CX__IR(alu_register_adjuster_1__20[12]), .DX__IR(alu_register_adjuster_1__20[11]),
    .EX__IR(alu_register_adjuster_1__20[10]), .AX__BX(alu_register_adjuster_1__20[9]),
    .AX__CX(alu_register_adjuster_1__20[8]), .AX__DX(alu_register_adjuster_1__20[7]),
    .AX__EX(alu_register_adjuster_1__20[6]), .BX__CX(alu_register_adjuster_1__20[5]),
    .BX__DX(alu_register_adjuster_1__20[4]), .BX__EX(alu_register_adjuster_1__20[3]),
    .CX__DX(alu_register_adjuster_1__20[2]), .CX__EX(alu_register_adjuster_1__20[1]),
    .DX__EX(alu_register_adjuster_1__20[0]), .LOW_16(mul_1_low_16), .HIGH_16(mul_1_high_16));
  and and_3 (and_3_out, SBB, Cin);
  assign MAIN_OUT = or_2_out ? add_adc_1_output : 16'bz;  // Controlled_Buffer controlled_buffer_1
  assign SECOND_OUT = MUL ? mul_1_low_16 : 16'bz;  // Controlled_Buffer controlled_buffer_2
  assign MAIN_OUT = MUL ? mul_1_high_16 : 16'bz;  // Controlled_Buffer controlled_buffer_3
  or or_2 (or_2_out, ADD, ADC);
  assign SECOND_OUT = DIV ? div_1_remainder : 16'bz;  // Controlled_Buffer controlled_buffer_4
  assign MAIN_OUT = AND ? and_2_output : 16'bz;  // Controlled_Buffer controlled_buffer_5
  assign MAIN_OUT = OR ? or_1_output : 16'bz;  // Controlled_Buffer controlled_buffer_6
  assign MAIN_OUT = XOR ? xor_1_output : 16'bz;  // Controlled_Buffer controlled_buffer_7
  assign MAIN_OUT = or_3_out ? sub_sbb_1_output : 16'bz;  // Controlled_Buffer controlled_buffer_8
  assign MAIN_OUT = DIV ? div_1_quotient : 16'bz;  // Controlled_Buffer controlled_buffer_9
  or or_3 (or_3_out, SUB, SBB);
  SUB_SBB sub_sbb_1 (
    .AX(AX), .BX(BX), .CX(CX), .DX(DX), .EX(EX), .DR(DR), .IR(IR), .Bin(and_3_out),
    .AX__DR(alu_register_adjuster_1__30[29]), .BX__DR(alu_register_adjuster_1__30[28]),
    .CX__DR(alu_register_adjuster_1__30[27]), .DX__DR(alu_register_adjuster_1__30[26]),
    .EX__DR(alu_register_adjuster_1__30[25]), .AX__IR(alu_register_adjuster_1__30[24]),
    .BX__IR(alu_register_adjuster_1__30[23]), .CX__IR(alu_register_adjuster_1__30[22]),
    .DX__IR(alu_register_adjuster_1__30[21]), .EX__IR(alu_register_adjuster_1__30[20]),
    .AX__BX(alu_register_adjuster_1__30[19]), .AX__CX(alu_register_adjuster_1__30[18]),
    .AX__DX(alu_register_adjuster_1__30[17]), .AX__EX(alu_register_adjuster_1__30[16]),
    .BX__AX(alu_register_adjuster_1__30[15]), .BX__CX(alu_register_adjuster_1__30[14]),
    .BX__DX(alu_register_adjuster_1__30[13]), .BX__EX(alu_register_adjuster_1__30[12]),
    .CX__AX(alu_register_adjuster_1__30[11]), .CX__BX(alu_register_adjuster_1__30[10]),
    .CX__DX(alu_register_adjuster_1__30[9]), .CX__EX(alu_register_adjuster_1__30[8]),
    .DX__AX(alu_register_adjuster_1__30[7]), .DX__BX(alu_register_adjuster_1__30[6]),
    .DX__CX(alu_register_adjuster_1__30[5]), .DX__EX(alu_register_adjuster_1__30[4]),
    .EX__AX(alu_register_adjuster_1__30[3]), .EX__BX(alu_register_adjuster_1__30[2]),
    .EX__CX(alu_register_adjuster_1__30[1]), .EX__DX(alu_register_adjuster_1__30[0]),
    .OUTPUT(sub_sbb_1_output), .Bout(sub_sbb_1_bout));
  DIV div_1 (
    .AX(AX), .BX(BX), .CX(CX), .DX(DX), .EX(EX), .DR(DR), .IR(IR), .AX__DR(alu_register_adjuster_1__30[29]),
    .BX__DR(alu_register_adjuster_1__30[28]), .CX__DR(alu_register_adjuster_1__30[27]),
    .DX__DR(alu_register_adjuster_1__30[26]), .EX__DR(alu_register_adjuster_1__30[25]),
    .AX__IR(alu_register_adjuster_1__30[24]), .BX__IR(alu_register_adjuster_1__30[23]),
    .CX__IR(alu_register_adjuster_1__30[22]), .DX__IR(alu_register_adjuster_1__30[21]),
    .EX__IR(alu_register_adjuster_1__30[20]), .AX__BX(alu_register_adjuster_1__30[19]),
    .AX__CX(alu_register_adjuster_1__30[18]), .AX__DX(alu_register_adjuster_1__30[17]),
    .AX__EX(alu_register_adjuster_1__30[16]), .BX__AX(alu_register_adjuster_1__30[15]),
    .BX__CX(alu_register_adjuster_1__30[14]), .BX__DX(alu_register_adjuster_1__30[13]),
    .BX__EX(alu_register_adjuster_1__30[12]), .CX__AX(alu_register_adjuster_1__30[11]),
    .CX__BX(alu_register_adjuster_1__30[10]), .CX__DX(alu_register_adjuster_1__30[9]),
    .CX__EX(alu_register_adjuster_1__30[8]), .DX__AX(alu_register_adjuster_1__30[7]),
    .DX__BX(alu_register_adjuster_1__30[6]), .DX__CX(alu_register_adjuster_1__30[5]),
    .DX__EX(alu_register_adjuster_1__30[4]), .EX__AX(alu_register_adjuster_1__30[3]),
    .EX__BX(alu_register_adjuster_1__30[2]), .EX__CX(alu_register_adjuster_1__30[1]),
    .EX__DX(alu_register_adjuster_1__30[0]), .QUOTIENT(div_1_quotient), .REMAINDER(div_1_remainder));
  CMP cmp_1 (
    .AX(AX), .BX(BX), .CX(CX), .DX(DX), .EX(EX), .DR(DR), .IR(IR), .AX__DR(alu_register_adjuster_1__30[29]),
    .BX__DR(alu_register_adjuster_1__30[28]), .CX__DR(alu_register_adjuster_1__30[27]),
    .DX__DR(alu_register_adjuster_1__30[26]), .EX__DR(alu_register_adjuster_1__30[25]),
    .AX__IR(alu_register_adjuster_1__30[24]), .BX__IR(alu_register_adjuster_1__30[23]),
    .CX__IR(alu_register_adjuster_1__30[22]), .DX__IR(alu_register_adjuster_1__30[21]),
    .EX__IR(alu_register_adjuster_1__30[20]), .AX__BX(alu_register_adjuster_1__30[19]),
    .AX__CX(alu_register_adjuster_1__30[18]), .AX__DX(alu_register_adjuster_1__30[17]),
    .AX__EX(alu_register_adjuster_1__30[16]), .BX__AX(alu_register_adjuster_1__30[15]),
    .BX__CX(alu_register_adjuster_1__30[14]), .BX__DX(alu_register_adjuster_1__30[13]),
    .BX__EX(alu_register_adjuster_1__30[12]), .CX__AX(alu_register_adjuster_1__30[11]),
    .CX__BX(alu_register_adjuster_1__30[10]), .CX__DX(alu_register_adjuster_1__30[9]),
    .CX__EX(alu_register_adjuster_1__30[8]), .DX__AX(alu_register_adjuster_1__30[7]),
    .DX__BX(alu_register_adjuster_1__30[6]), .DX__CX(alu_register_adjuster_1__30[5]),
    .DX__EX(alu_register_adjuster_1__30[4]), .EX__AX(alu_register_adjuster_1__30[3]),
    .EX__BX(alu_register_adjuster_1__30[2]), .EX__CX(alu_register_adjuster_1__30[1]),
    .EX__DX(alu_register_adjuster_1__30[0]), .A___B(cmp_1_a___b), .A___B_2(cmp_1_a___b_2),
    .A___B_3(cmp_1_a___b_3));
  ALU_Zero alu_zero_1 (
    .MAIN_OUT(MAIN_OUT), .CMP(CMP), .A___B(cmp_1_a___b_3), .A___B_2(cmp_1_a___b_2), .A___B_3(cmp_1_a___b),
    .Zero(Zero));
  ALU_Cout alu_cout_1 (
    .ADD(ADD), .ADC(ADC), .Cout_from_add(add_adc_1_cout), .SUB(SUB), .SBB(SBB),
    .Bout_from_sub(sub_sbb_1_bout), .A___B(cmp_1_a___b_3), .A___B_2(cmp_1_a___b_2), .A___B_3(cmp_1_a___b),
    .CMP(CMP), .OUT(Cout));
endmodule

module MUL_INPUT_ADJUSTER (
  input  AX__DR,
  input  BX__DR,
  input  CX__DR,
  input  DX__DR,
  input  EX__DR,
  input  AX__IR,
  input  BX__IR,
  input  CX__IR,
  input  DX__IR,
  input  EX__IR,
  input  AX__BX,
  input  AX__CX,
  input  AX__DX,
  input  AX__EX,
  input  BX__CX,
  input  BX__DX,
  input  BX__EX,
  input  CX__DX,
  input  CX__EX,
  input  DX__EX,
  input  [15:0] AX,
  input  [15:0] BX,
  input  [15:0] CX,
  input  [15:0] DX,
  input  [15:0] EX,
  input  [15:0] DR,
  input  [15:0] IR,
  output [15:0] MULTIPLIER,
  output [15:0] MULTIPLIED
);

  wire or_1_out, or_2_out, or_3_out, or_4_out, or_5_out, or_6_out, or_7_out, or_8_out, or_9_out, or_10_out;

  or or_1 (or_1_out, AX__DR, AX__IR, AX__BX, AX__CX, AX__DX, AX__EX);
  assign MULTIPLIER = or_1_out ? AX : 16'bz;  // Controlled_Buffer controlled_buffer_1
  assign MULTIPLIER = or_2_out ? BX : 16'bz;  // Controlled_Buffer controlled_buffer_2
  assign MULTIPLIED = AX__BX ? BX : 16'bz;  // Controlled_Buffer controlled_buffer_3
  assign MULTIPLIER = or_3_out ? CX : 16'bz;  // Controlled_Buffer controlled_buffer_4
  assign MULTIPLIED = or_9_out ? CX : 16'bz;  // Controlled_Buffer controlled_buffer_5
  assign MULTIPLIER = or_4_out ? DX : 16'bz;  // Controlled_Buffer controlled_buffer_6
  assign MULTIPLIED = or_8_out ? DX : 16'bz;  // Controlled_Buffer controlled_buffer_7
  assign MULTIPLIER = or_5_out ? EX : 16'bz;  // Controlled_Buffer controlled_buffer_8
  assign MULTIPLIED = or_10_out ? EX : 16'bz;  // Controlled_Buffer controlled_buffer_9
  assign MULTIPLIED = or_6_out ? DR : 16'bz;  // Controlled_Buffer controlled_buffer_10
  assign MULTIPLIED = or_7_out ? IR : 16'bz;  // Controlled_Buffer controlled_buffer_11
  or or_2 (or_2_out, BX__DR, BX__IR, BX__CX, BX__DX, BX__EX);
  or or_3 (or_3_out, CX__DR, CX__IR, CX__DX, CX__EX);
  or or_4 (or_4_out, DX__DR, DX__IR, DX__EX);
  or or_5 (or_5_out, EX__DR, EX__IR);
  or or_6 (or_6_out, AX__DR, BX__DR, CX__DR, DX__DR, EX__DR);
  or or_7 (or_7_out, AX__IR, BX__IR, CX__IR, DX__IR, EX__IR);
  or or_8 (or_8_out, AX__DX, BX__DX, CX__DX);
  or or_9 (or_9_out, AX__CX, BX__CX);
  or or_10 (or_10_out, AX__EX, BX__EX, CX__EX, DX__EX);
endmodule

module DIV_INPUT_ADJUSTER (
  input  AX__DR,
  input  BX__DR,
  input  CX__DR,
  input  DX__DR,
  input  EX__DR,
  input  AX__IR,
  input  BX__IR,
  input  CX__IR,
  input  DX__IR,
  input  EX__IR,
  input  AX__BX,
  input  AX__CX,
  input  AX__DX,
  input  AX__EX,
  input  BX__AX,
  input  BX__CX,
  input  BX__DX,
  input  BX__EX,
  input  CX__AX,
  input  CX__BX,
  input  CX__DX,
  input  CX__EX,
  input  DX__AX,
  input  DX__BX,
  input  DX__CX,
  input  DX__EX,
  input  EX__AX,
  input  EX__BX,
  input  EX__CX,
  input  EX__DX,
  input  [15:0] AX,
  input  [15:0] BX,
  input  [15:0] CX,
  input  [15:0] DX,
  input  [15:0] EX,
  input  [15:0] DR,
  input  [15:0] IR,
  output [15:0] DIVIDEND,
  output [15:0] DIVISOR
);

  wire or_1_out, or_2_out, or_3_out, or_4_out, or_5_out, or_6_out, or_7_out, or_8_out, or_9_out, or_10_out,
       or_11_out, or_12_out;

  or or_1 (or_1_out, AX__DR, AX__IR, AX__BX, AX__CX, AX__DX, AX__EX);
  assign DIVIDEND = or_1_out ? AX : 16'bz;  // Controlled_Buffer controlled_buffer_1
  assign DIVISOR = or_7_out ? AX : 16'bz;  // Controlled_Buffer controlled_buffer_2
  assign DIVIDEND = or_2_out ? BX : 16'bz;  // Controlled_Buffer controlled_buffer_3
  assign DIVISOR = or_9_out ? BX : 16'bz;  // Controlled_Buffer controlled_buffer_4
  assign DIVIDEND = or_3_out ? CX : 16'bz;  // Controlled_Buffer controlled_buffer_5
  assign DIVISOR = or_10_out ? CX : 16'bz;  // Controlled_Buffer controlled_buffer_6
  assign DIVIDEND = or_4_out ? DX : 16'bz;  // Controlled_Buffer controlled_buffer_7
  assign DIVISOR = or_11_out ? DX : 16'bz;  // Controlled_Buffer controlled_buffer_8
  assign DIVIDEND = or_5_out ? EX : 16'bz;  // Controlled_Buffer controlled_buffer_9
  assign DIVISOR = or_12_out ? EX : 16'bz;  // Controlled_Buffer controlled_buffer_10
  assign DIVISOR = or_6_out ? DR : 16'bz;  // Controlled_Buffer controlled_buffer_11
  assign DIVISOR = or_8_out ? IR : 16'bz;  // Controlled_Buffer controlled_buffer_12
  or or_2 (or_2_out, BX__DR, BX__IR, BX__AX, BX__CX, BX__DX, BX__EX);
  or or_3 (or_3_out, CX__DR, CX__IR, CX__AX, CX__BX, CX__DX, CX__EX);
  or or_4 (or_4_out, DX__DR, DX__IR, DX__AX, DX__BX, DX__CX, DX__EX);
  or or_5 (or_5_out, EX__DR, EX__IR, EX__AX, EX__BX, EX__CX, EX__DX);
  or or_6 (or_6_out, AX__DR, BX__DR, CX__DR, DX__DR, EX__DR);
  or or_7 (or_7_out, BX__AX, CX__AX, DX__AX, EX__AX);
  or or_8 (or_8_out, AX__IR, BX__IR, CX__IR, DX__IR, EX__IR);
  or or_9 (or_9_out, AX__BX, CX__BX, DX__BX, EX__BX);
  or or_10 (or_10_out, AX__CX, BX__CX, DX__CX, EX__CX);
  or or_11 (or_11_out, AX__DX, BX__DX, CX__DX, EX__DX);
  or or_12 (or_12_out, AX__EX, CX__EX, BX__EX, DX__EX);
endmodule

module CMP_INPUT_ADJUSTER (
  input  AX__DR,
  input  BX__DR,
  input  CX__DR,
  input  DX__DR,
  input  EX__DR,
  input  AX__IR,
  input  BX__IR,
  input  CX__IR,
  input  DX__IR,
  input  EX__IR,
  input  AX__BX,
  input  AX__CX,
  input  AX__DX,
  input  AX__EX,
  input  BX__AX,
  input  BX__CX,
  input  BX__DX,
  input  BX__EX,
  input  CX__AX,
  input  CX__BX,
  input  CX__DX,
  input  CX__EX,
  input  DX__AX,
  input  DX__BX,
  input  DX__CX,
  input  DX__EX,
  input  EX__AX,
  input  EX__BX,
  input  EX__CX,
  input  EX__DX,
  input  [15:0] AX,
  input  [15:0] BX,
  input  [15:0] CX,
  input  [15:0] DX,
  input  [15:0] EX,
  input  [15:0] DR,
  input  [15:0] IR,
  output [15:0] A,
  output [15:0] B
);

  wire or_1_out, or_2_out, or_3_out, or_4_out, or_5_out, or_6_out, or_7_out, or_8_out, or_9_out, or_10_out,
       or_11_out, or_12_out;

  or or_1 (or_1_out, AX__DR, AX__IR, AX__BX, AX__CX, AX__DX, AX__EX);
  assign A = or_1_out ? AX : 16'bz;  // Controlled_Buffer controlled_buffer_1
  assign B = or_8_out ? AX : 16'bz;  // Controlled_Buffer controlled_buffer_2
  assign A = or_2_out ? BX : 16'bz;  // Controlled_Buffer controlled_buffer_3
  assign B = or_9_out ? BX : 16'bz;  // Controlled_Buffer controlled_buffer_4
  assign A = or_3_out ? CX : 16'bz;  // Controlled_Buffer controlled_buffer_5
  assign B = or_10_out ? CX : 16'bz;  // Controlled_Buffer controlled_buffer_6
  assign A = or_4_out ? DX : 16'bz;  // Controlled_Buffer controlled_buffer_7
  assign B = or_11_out ? DX : 16'bz;  // Controlled_Buffer controlled_buffer_8
  assign A = or_5_out ? EX : 16'bz;  // Controlled_Buffer controlled_buffer_9
  assign B = or_12_out ? EX : 16'bz;  // Controlled_Buffer controlled_buffer_10
  assign B = or_6_out ? DR : 16'bz;  // Controlled_Buffer controlled_buffer_11
  assign B = or_7_out ? IR : 16'bz;  // Controlled_Buffer controlled_buffer_12
  or or_2 (or_2_out, BX__DR, BX__IR, BX__AX, BX__CX, BX__DX, BX__EX);
  or or_3 (or_3_out, CX__DR, CX__IR, CX__AX, CX__BX, CX__DX, CX__EX);
  or or_4 (or_4_out, DX__DR, DX__IR, DX__AX, DX__BX, DX__CX, DX__EX);
  or or_5 (or_5_out, EX__DR, EX__IR, EX__AX, EX__BX, EX__CX, EX__DX);
  or or_6 (or_6_out, AX__DR, BX__DR, CX__DR, DX__DR, EX__DR);
  or or_7 (or_7_out, AX__IR, BX__IR, CX__IR, DX__IR, EX__IR);
  or or_8 (or_8_out, BX__AX, CX__AX, DX__AX, EX__AX);
  or or_9 (or_9_out, AX__BX, CX__BX, DX__BX, EX__BX);
  or or_10 (or_10_out, AX__CX, BX__CX, DX__CX, EX__CX);
  or or_11 (or_11_out, AX__DX, BX__DX, CX__DX, EX__DX);
  or or_12 (or_12_out, AX__EX, CX__EX, BX__EX, DX__EX);
endmodule

module ALU_REGISTER_ADJUSTER (
  input  AX__DR,
  input  BX__DR,
  input  CX__DR,
  input  DX__DR,
  input  EX__DR,
  input  AX__IR,
  input  BX__IR,
  input  CX__IR,
  input  DX__IR,
  input  EX__IR,
  input  AX__BX,
  input  AX__CX,
  input  AX__DX,
  input  AX__EX,
  input  BX__AX,
  input  BX__CX,
  input  BX__DX,
  input  BX__EX,
  input  CX__AX,
  input  CX__BX,
  input  CX__DX,
  input  CX__EX,
  input  DX__AX,
  input  DX__BX,
  input  DX__CX,
  input  DX__EX,
  input  EX__AX,
  input  EX__BX,
  input  EX__CX,
  input  EX__DX,
  output [29:0] _30,
  output [19:0] _20
);

  or or_1 (_20[9], AX__BX, BX__AX);
  or or_2 (_20[8], AX__CX, CX__AX);
  or or_3 (_20[7], BX__CX, CX__BX);
  or or_4 (_20[6], AX__DX, DX__AX);
  or or_5 (_20[5], BX__DX, DX__BX);
  or or_6 (_20[4], CX__DX, DX__CX);
  or or_7 (_20[3], AX__EX, EX__AX);
  or or_8 (_20[2], BX__EX, EX__BX);
  or or_9 (_20[1], CX__EX, EX__CX);
  or or_10 (_20[0], DX__EX, EX__DX);

  assign _20[19:10] = {AX__DR, BX__DR, CX__DR, DX__DR, EX__DR, AX__IR, BX__IR, CX__IR, DX__IR, EX__IR};
  assign _30 = {AX__DR, BX__DR, CX__DR, DX__DR, EX__DR, AX__IR, BX__IR, CX__IR, DX__IR, EX__IR, AX__BX, AX__CX, AX__DX, AX__EX, BX__AX, BX__CX, BX__DX, BX__EX, CX__AX, CX__BX, CX__DX, CX__EX, DX__AX, DX__BX, DX__CX, DX__EX, EX__AX, EX__BX, EX__CX, EX__DX};
endmodule

module ALU_Cout (
  input  ADD,
  input  ADC,
  input  Cout_from_add,
  input  SUB,
  input  SBB,
  input  Bout_from_sub,
  input  A___B,
  input  A___B_2,
  input  A___B_3,
  input  CMP,
  output OUT
);

  wire and_1_out, and_2_out, and_3_out, and_4_out, and_5_out, nand_1_out, not_1_out, or_1_out, or_2_out,
       or_3_out, or_4_out, or_5_out;

  or or_1 (or_1_out, ADD, ADC);
  or or_2 (or_2_out, SUB, SBB);
  or or_3 (or_3_out, A___B, A___B_2);
  and and_1 (and_1_out, or_1_out, Cout_from_add);
  and and_2 (and_2_out, or_2_out, Bout_from_sub);
  and and_3 (and_3_out, or_3_out, CMP);
  nand nand_1 (nand_1_out, A___B_3, CMP);
  or or_4 (or_4_out, and_1_out, and_2_out);
  or or_5 (or_5_out, and_3_out, nand_1_out);
  and and_4 (and_4_out, or_4_out, not_1_out);
  not not_1 (not_1_out, CMP);
  and and_5 (and_5_out, or_5_out, CMP);
  or or_6 (OUT, and_4_out, and_5_out);
endmodule

module ALU_Zero (
  input  [15:0] MAIN_OUT,
  input  CMP,
  input  A___B,
  input  A___B_2,
  input  A___B_3,
  output Zero
);

  wire and_1_out, and_2_out, not_1_out, not_2_out, not_3_out, or_1_out, or_2_out;

  not not_1 (not_1_out, A___B);
  or or_1 (or_1_out, A___B_2, A___B_3);
  and and_1 (and_1_out, CMP, not_1_out, or_1_out);
  not not_2 (not_2_out, CMP);
  or or_2 (or_2_out, MAIN_OUT[0], MAIN_OUT[1], MAIN_OUT[2], MAIN_OUT[3], MAIN_OUT[4], MAIN_OUT[5], MAIN_OUT[6], MAIN_OUT[7], MAIN_OUT[8], MAIN_OUT[9], MAIN_OUT[10], MAIN_OUT[11], MAIN_OUT[12], MAIN_OUT[13], MAIN_OUT[14], MAIN_OUT[15], 1'b0);
  not not_3 (not_3_out, or_2_out);
  and and_2 (and_2_out, not_3_out, not_2_out);
  or or_3 (Zero, and_2_out, and_1_out);
endmodule

module control_deney (
  input  clk,
  output [2:0] mux,
  output dr_ld,
  output mem_bus,
  output \or ,
  output ax_ld,
  output [2:0] count
);

  Decoder #(.select(3)) decoder_1 (
    .out2(dr_ld), .out3(ax_ld), .sel(count));  // open: out0, out1, out4, out5, out6, out7, en
  Counter #(.width(3), .max('h7)) counter_1 (.Q(count), .clk(clk));  // open: load, D, count, carry, clr
  assign mux = dr_ld ? 3'b010 : 3'bz;  // Controlled_Buffer controlled_buffer_1

  assign mem_bus = dr_ld;
  assign \or  = ax_ld;
endmodule
