// Logisim project 4BitShift.circ as structural Verilog: 2 circuits, main circuit main
module main (
  input  i3,
  input  i2,
  input  i1,
  input  i0,
  input  [2:0] s1_s0,
  input  Clr,
  output Q3,
  output Q2,
  output Q1,
  output Q0
);

  wire clock_1_out, multiplexer_1_out, multiplexer_2_out, multiplexer_3_out, multiplexer_4_out;

  Multiplexer #(.select(3)) multiplexer_1 (
    .in0(Q3), .in1(1'b0), .in2(Q2), .in3(i3), .in4(Q0), .in5(Q2), .out(multiplexer_1_out), .sel(s1_s0));  // open: in6, in7, en
  Multiplexer #(.select(3)) multiplexer_2 (
    .in0(Q2), .in1(Q3), .in2(Q1), .in3(i2), .in4(Q3), .in5(Q1), .out(multiplexer_2_out), .sel(s1_s0));  // open: in6, in7, en
  Multiplexer #(.select(3)) multiplexer_3 (
    .in0(Q1), .in1(Q2), .in2(Q0), .in3(i1), .in4(Q2), .in5(Q0), .out(multiplexer_3_out), .sel(s1_s0));  // open: in6, in7, en
  Multiplexer #(.select(3)) multiplexer_4 (
    .in0(Q0), .in1(Q1), .in2(1'b0), .in3(i0), .in4(Q1), .in5(Q3), .out(multiplexer_4_out), .sel(s1_s0));  // open: in6, in7, en
  Clock clock_1 (.out(clock_1_out));
  D_Flip_Flop d_ff_1 (.clk(clock_1_out), .D(multiplexer_1_out), .Q(Q3), .reset(Clr));  // open: Qn, preset, en
  D_Flip_Flop d_ff_2 (.clk(clock_1_out), .D(multiplexer_2_out), .Q(Q2), .reset(Clr));  // open: Qn, preset, en
  D_Flip_Flop d_ff_3 (.clk(clock_1_out), .D(multiplexer_3_out), .Q(Q1), .reset(Clr));  // open: Qn, preset, en
  D_Flip_Flop d_ff_4 (.clk(clock_1_out), .D(multiplexer_4_out), .Q(Q0), .reset(Clr));  // open: Qn, preset, en
endmodule

module SF (
  input  in_1,
  input  decrement,
  input  in_3,
  input  in_4,
  input  in_5,
  input  increment,
  input  in_7,
  input  in_8,
  input  [15:0] INPUT,
  input  inc,
  input  dec,
  input  shl,
  input  shr,
  input  cil,
  input  cir,
  input  cml,
  input  load,
  output [15:0] out_18
);

  wire and_1_out, and_2_out, not_1_out, not_2_out, or_1_out, or_2_out, xnor_1_out, xnor_2_out, xnor_3_out,
       xor_1_out, xor_2_out, xor_3_out;

  J_K_Flip_Flop j_k_ff_1 (.Q(out_18[0]));  // open: J, clk, K, Qn, preset, en, reset
  J_K_Flip_Flop j_k_ff_2 (.Q(out_18[1]));  // open: J, clk, K, Qn, preset, en, reset
  J_K_Flip_Flop j_k_ff_3 (.Q(out_18[2]));  // open: J, clk, K, Qn, preset, en, reset
  J_K_Flip_Flop j_k_ff_4 (.Q(out_18[3]));  // open: J, clk, K, Qn, preset, en, reset
  J_K_Flip_Flop j_k_ff_5 (.Q(out_18[4]));  // open: J, clk, K, Qn, preset, en, reset
  J_K_Flip_Flop j_k_ff_6 (.Q(out_18[5]));  // open: J, clk, K, Qn, preset, en, reset
  J_K_Flip_Flop j_k_ff_7 (.Q(out_18[6]));  // open: J, clk, K, Qn, preset, en, reset
  J_K_Flip_Flop j_k_ff_8 (.Q(out_18[7]));  // open: J, clk, K, Qn, preset, en, reset
  J_K_Flip_Flop j_k_ff_9 (.Q(out_18[8]));  // open: J, clk, K, Qn, preset, en, reset
  J_K_Flip_Flop j_k_ff_10 (.Q(out_18[9]));  // open: J, clk, K, Qn, preset, en, reset
  J_K_Flip_Flop j_k_ff_11 (.Q(out_18[10]));  // open: J, clk, K, Qn, preset, en, reset
  J_K_Flip_Flop j_k_ff_12 (.Q(out_18[11]));  // open: J, clk, K, Qn, preset, en, reset
  J_K_Flip_Flop j_k_ff_13 (.Q(out_18[12]));  // open: J, clk, K, Qn, preset, en, reset
  J_K_Flip_Flop j_k_ff_14 (.Q(out_18[13]));  // open: J, clk, K, Qn, preset, en, reset
  J_K_Flip_Flop j_k_ff_15 (.Q(out_18[14]));  // open: J, clk, K, Qn, preset, en, reset
  J_K_Flip_Flop j_k_ff_16 (.Q(out_18[15]));  // open: J, clk, K, Qn, preset, en, reset
  or or_1 (or_1_out, decrement, in_3, in_4);
  xnor xnor_1 (xnor_1_out, in_1, or_1_out);
  and and_1 (and_1_out, increment, in_7, in_8);
  xor xor_1 (xor_1_out, in_5, and_1_out);
  or or_2 (or_2_out, in_3, in_4);
  xnor xnor_2 (xnor_2_out, in_3, in_4);
  xnor xnor_3 (xnor_3_out, decrement, or_2_out);
  and and_2 (and_2_out, in_7, in_8);
  xor xor_2 (xor_2_out, in_7, in_8);
  xor xor_3 (xor_3_out, increment, and_2_out);
  not not_1 (not_1_out, in_4);
  not not_2 (not_2_out, in_8);
endmodule
