// Logisim project REGISTERS.circ as structural Verilog: 3 circuits, main circuit GENERAL_PURPOSE
module GENERAL_PURPOSE (
  input  [15:0] INPUT,
  input  CLK,
  input  INC,
  input  LD,
  input  DEC,
  input  SHL,
  input  SHR,
  input  CIL,
  input  CIR,
  input  CML,
  input  CLR,
  output [15:0] OUTPUT
);

  wire and_1_out, and_2_out, and_3_out, and_4_out, and_5_out, and_6_out, and_7_out, and_8_out, and_9_out,
       and_10_out, and_11_out, and_12_out, and_13_out, and_14_out, and_15_out, and_16_out, and_17_out,
       and_18_out, and_19_out, and_20_out, and_21_out, and_22_out, and_23_out, and_24_out, and_25_out,
       and_26_out, and_27_out, and_28_out, and_29_out, and_30_out, and_31_out, and_32_out, and_33_out,
       and_34_out, and_35_out, and_36_out, and_37_out, and_38_out, and_39_out, and_40_out, and_41_out,
       and_42_out, and_43_out, and_44_out, and_45_out, and_46_out, and_47_out, and_48_out, and_49_out,
       and_50_out, and_51_out, and_52_out, and_53_out, and_54_out, and_55_out, and_56_out, and_57_out,
       and_58_out, and_59_out, and_60_out, and_61_out, and_62_out, and_63_out, and_64_out, and_65_out,
       and_66_out, and_67_out, and_68_out, and_69_out, and_70_out, and_71_out, and_72_out, and_73_out,
       and_74_out, and_75_out, and_76_out, and_77_out, and_78_out, and_79_out, and_80_out, and_81_out,
       and_82_out, and_83_out, and_84_out, and_85_out, and_86_out, and_87_out, and_88_out, and_89_out,
       and_90_out, and_91_out, and_92_out, and_93_out, and_94_out, and_95_out, and_96_out, and_97_out,
       and_98_out, and_99_out, and_100_out, and_101_out, and_102_out, and_103_out, and_104_out, and_105_out,
       and_106_out, and_107_out, and_108_out, and_109_out, and_110_out, and_111_out, and_112_out,
       and_113_out, and_114_out, and_115_out, and_116_out, and_117_out, and_118_out, and_119_out,
       and_120_out, and_121_out, and_122_out, and_123_out, and_124_out, and_125_out, and_126_out,
       and_127_out, and_128_out, and_129_out, and_130_out, and_131_out, and_132_out, and_133_out,
       and_134_out, and_135_out, and_136_out, and_137_out, and_138_out, and_139_out, and_140_out,
       and_141_out, and_142_out, and_143_out, and_144_out, and_145_out, and_146_out, and_147_out,
       and_148_out, and_149_out, and_150_out, and_151_out, and_152_out, and_153_out, and_154_out,
       and_155_out, and_156_out, and_157_out, and_158_out, multiplexer_1_out, multiplexer_2_out,
       multiplexer_3_out, multiplexer_4_out, multiplexer_5_out, multiplexer_6_out, multiplexer_7_out,
       multiplexer_8_out, multiplexer_9_out, multiplexer_10_out, multiplexer_11_out, multiplexer_12_out,
       multiplexer_13_out, multiplexer_14_out, multiplexer_15_out, multiplexer_16_out, not_1_out, not_2_out,
       not_3_out, not_4_out, not_5_out, not_6_out, not_7_out, not_8_out, not_9_out, not_10_out, not_11_out,
       not_12_out, not_13_out, not_14_out, not_15_out, not_16_out, not_17_out, not_18_out, or_1_out,
       or_2_out, or_3_out, or_4_out, or_5_out, or_6_out, or_7_out, or_8_out, or_9_out, or_10_out, or_11_out,
       or_12_out, or_13_out, or_14_out, or_15_out, or_16_out, or_17_out, or_18_out, or_19_out, or_20_out,
       or_21_out, or_22_out, or_23_out, or_24_out, or_25_out, or_26_out, or_27_out, or_28_out, or_29_out,
       or_30_out, or_31_out, or_32_out, or_33_out, or_34_out, or_35_out, or_36_out, or_37_out, or_38_out,
       or_39_out, or_40_out, or_41_out, or_42_out, or_43_out, or_44_out, or_45_out, or_46_out, or_47_out,
       or_48_out, or_49_out, or_50_out, or_51_out, or_52_out, or_53_out, or_54_out, or_55_out, or_56_out,
       or_57_out, or_58_out, or_59_out, or_60_out, or_61_out, or_62_out, or_63_out, or_64_out, or_65_out,
       or_66_out, or_67_out, or_68_out, or_69_out, or_70_out, or_71_out, or_72_out, or_73_out, or_74_out,
       or_75_out, or_76_out, or_77_out, or_78_out, or_79_out, or_80_out, or_81_out, or_82_out, or_83_out,
       or_84_out, or_85_out, or_86_out, or_87_out, or_88_out, or_89_out, or_90_out, or_91_out, or_92_out,
       or_93_out, or_94_out, or_95_out, or_96_out, or_97_out, or_98_out, or_99_out, or_100_out, or_101_out,
       or_102_out, or_103_out, or_104_out, or_105_out, or_106_out, or_107_out, or_108_out, or_109_out,
       or_110_out, or_111_out, or_112_out, or_113_out, or_114_out, or_115_out, or_116_out, or_117_out,
       or_118_out, or_119_out, or_120_out, or_121_out, or_122_out, or_123_out, or_124_out, or_125_out,
       or_126_out, or_127_out, or_128_out, or_129_out, or_130_out, or_131_out, or_132_out, or_133_out,
       or_134_out, or_135_out, or_136_out, or_137_out, or_138_out, or_139_out, or_140_out, or_141_out,
       or_142_out, or_143_out, or_144_out, or_145_out, or_146_out, or_147_out, or_148_out, or_149_out,
       or_150_out, xnor_1_out, xnor_2_out, xnor_3_out, xnor_4_out, xnor_5_out, xnor_6_out, xnor_7_out,
       xnor_8_out, xnor_9_out, xnor_10_out, xnor_11_out, xnor_12_out, xnor_13_out, xnor_14_out, xnor_15_out,
       xor_1_out, xor_2_out, xor_3_out, xor_4_out, xor_5_out, xor_6_out, xor_7_out, xor_8_out, xor_9_out,
       xor_10_out, xor_11_out, xor_12_out, xor_13_out, xor_14_out, xor_15_out;

  and and_1 (and_1_out, and_2_out, OUTPUT[14]);
  and and_2 (and_2_out, OUTPUT[13], and_3_out);
  and and_3 (and_3_out, and_4_out, OUTPUT[12]);
  and and_4 (and_4_out, OUTPUT[11], and_5_out);
  and and_5 (and_5_out, and_6_out, OUTPUT[10]);
  and and_6 (and_6_out, OUTPUT[9], and_7_out);
  and and_7 (and_7_out, and_8_out, OUTPUT[8]);
  and and_8 (and_8_out, OUTPUT[7], and_9_out);
  and and_9 (and_9_out, and_10_out, OUTPUT[6]);
  and and_10 (and_10_out, OUTPUT[5], and_11_out);
  and and_11 (and_11_out, and_12_out, OUTPUT[4]);
  and and_12 (and_12_out, OUTPUT[3], and_13_out);
  and and_13 (and_13_out, and_14_out, OUTPUT[2]);
  and and_14 (and_14_out, OUTPUT[0], OUTPUT[1]);
  xor xor_1 (xor_1_out, OUTPUT[15], and_1_out);
  and and_15 (and_15_out, xor_1_out, INC);
  xor xor_2 (xor_2_out, OUTPUT[14], and_2_out);
  and and_16 (and_16_out, xor_2_out, INC);
  xor xor_3 (xor_3_out, OUTPUT[13], and_3_out);
  and and_17 (and_17_out, xor_3_out, INC);
  xor xor_4 (xor_4_out, OUTPUT[12], and_4_out);
  and and_18 (and_18_out, xor_4_out, INC);
  xor xor_5 (xor_5_out, OUTPUT[11], and_5_out);
  and and_19 (and_19_out, xor_5_out, INC);
  xor xor_6 (xor_6_out, OUTPUT[10], and_6_out);
  and and_20 (and_20_out, xor_6_out, INC);
  xor xor_7 (xor_7_out, OUTPUT[9], and_7_out);
  and and_21 (and_21_out, xor_7_out, INC);
  xor xor_8 (xor_8_out, OUTPUT[8], and_8_out);
  and and_22 (and_22_out, xor_8_out, INC);
  xor xor_9 (xor_9_out, OUTPUT[7], and_9_out);
  and and_23 (and_23_out, xor_9_out, INC);
  xor xor_10 (xor_10_out, OUTPUT[6], and_10_out);
  and and_24 (and_24_out, xor_10_out, INC);
  xor xor_11 (xor_11_out, OUTPUT[5], and_11_out);
  and and_25 (and_25_out, xor_11_out, INC);
  xor xor_12 (xor_12_out, OUTPUT[4], and_12_out);
  and and_26 (and_26_out, xor_12_out, INC);
  xor xor_13 (xor_13_out, OUTPUT[3], and_13_out);
  and and_27 (and_27_out, xor_13_out, INC);
  xor xor_14 (xor_14_out, OUTPUT[2], and_14_out);
  and and_28 (and_28_out, xor_14_out, INC);
  xor xor_15 (xor_15_out, OUTPUT[1], OUTPUT[0]);
  and and_29 (and_29_out, xor_15_out, INC);
  not not_1 (not_1_out, OUTPUT[0]);
  and and_30 (and_30_out, not_1_out, INC);
  and and_31 (and_31_out, INPUT[15], LD);
  and and_32 (and_32_out, INPUT[14], LD);
  and and_33 (and_33_out, INPUT[13], LD);
  and and_34 (and_34_out, INPUT[12], LD);
  and and_35 (and_35_out, INPUT[11], LD);
  and and_36 (and_36_out, INPUT[10], LD);
  and and_37 (and_37_out, INPUT[9], LD);
  and and_38 (and_38_out, INPUT[8], LD);
  and and_39 (and_39_out, INPUT[7], LD);
  and and_40 (and_40_out, INPUT[6], LD);
  and and_41 (and_41_out, INPUT[5], LD);
  and and_42 (and_42_out, INPUT[4], LD);
  and and_43 (and_43_out, INPUT[3], LD);
  and and_44 (and_44_out, INPUT[2], LD);
  and and_45 (and_45_out, INPUT[1], LD);
  and and_46 (and_46_out, INPUT[0], LD);
  or or_1 (or_1_out, INC, LD);
  or or_2 (or_2_out, and_15_out, and_31_out);
  or or_3 (or_3_out, or_5_out, OUTPUT[14]);
  or or_4 (or_4_out, and_16_out, and_32_out);
  or or_5 (or_5_out, OUTPUT[13], or_7_out);
  or or_6 (or_6_out, and_17_out, and_33_out);
  or or_7 (or_7_out, or_9_out, OUTPUT[12]);
  or or_8 (or_8_out, and_18_out, and_34_out);
  or or_9 (or_9_out, OUTPUT[11], or_11_out);
  or or_10 (or_10_out, and_19_out, and_35_out);
  or or_11 (or_11_out, or_13_out, OUTPUT[10]);
  or or_12 (or_12_out, and_20_out, and_36_out);
  or or_13 (or_13_out, OUTPUT[9], or_15_out);
  or or_14 (or_14_out, and_21_out, and_37_out);
  or or_15 (or_15_out, or_17_out, OUTPUT[8]);
  or or_16 (or_16_out, and_22_out, and_38_out);
  or or_17 (or_17_out, OUTPUT[7], or_19_out);
  or or_18 (or_18_out, and_23_out, and_39_out);
  or or_19 (or_19_out, or_21_out, OUTPUT[6]);
  or or_20 (or_20_out, and_24_out, and_40_out);
  or or_21 (or_21_out, OUTPUT[5], or_23_out);
  or or_22 (or_22_out, and_25_out, and_41_out);
  or or_23 (or_23_out, or_25_out, OUTPUT[4]);
  or or_24 (or_24_out, and_26_out, and_42_out);
  or or_25 (or_25_out, OUTPUT[3], or_27_out);
  or or_26 (or_26_out, and_27_out, and_43_out);
  or or_27 (or_27_out, or_29_out, OUTPUT[2]);
  or or_28 (or_28_out, and_28_out, and_44_out);
  or or_29 (or_29_out, OUTPUT[0], OUTPUT[1]);
  or or_30 (or_30_out, and_29_out, and_45_out);
  not not_2 (not_2_out, OUTPUT[0]);
  or or_31 (or_31_out, and_30_out, and_46_out);
  xnor xnor_1 (xnor_1_out, OUTPUT[15], or_3_out);
  and and_47 (and_47_out, xnor_1_out, DEC);
  xnor xnor_2 (xnor_2_out, OUTPUT[14], or_5_out);
  and and_48 (and_48_out, xnor_2_out, DEC);
  xnor xnor_3 (xnor_3_out, OUTPUT[13], or_7_out);
  and and_49 (and_49_out, xnor_3_out, DEC);
  xnor xnor_4 (xnor_4_out, OUTPUT[12], or_9_out);
  and and_50 (and_50_out, xnor_4_out, DEC);
  xnor xnor_5 (xnor_5_out, OUTPUT[11], or_11_out);
  and and_51 (and_51_out, xnor_5_out, DEC);
  xnor xnor_6 (xnor_6_out, OUTPUT[10], or_13_out);
  and and_52 (and_52_out, xnor_6_out, DEC);
  xnor xnor_7 (xnor_7_out, OUTPUT[9], or_15_out);
  and and_53 (and_53_out, xnor_7_out, DEC);
  xnor xnor_8 (xnor_8_out, OUTPUT[8], or_17_out);
  and and_54 (and_54_out, xnor_8_out, DEC);
  xnor xnor_9 (xnor_9_out, OUTPUT[7], or_19_out);
  and and_55 (and_55_out, xnor_9_out, DEC);
  xnor xnor_10 (xnor_10_out, OUTPUT[6], or_21_out);
  and and_56 (and_56_out, xnor_10_out, DEC);
  xnor xnor_11 (xnor_11_out, OUTPUT[5], or_23_out);
  and and_57 (and_57_out, xnor_11_out, DEC);
  xnor xnor_12 (xnor_12_out, OUTPUT[4], or_25_out);
  and and_58 (and_58_out, xnor_12_out, DEC);
  xnor xnor_13 (xnor_13_out, OUTPUT[3], or_27_out);
  and and_59 (and_59_out, xnor_13_out, DEC);
  xnor xnor_14 (xnor_14_out, OUTPUT[2], or_29_out);
  and and_60 (and_60_out, xnor_14_out, DEC);
  xnor xnor_15 (xnor_15_out, OUTPUT[1], OUTPUT[0]);
  and and_61 (and_61_out, xnor_15_out, DEC);
  and and_62 (and_62_out, not_2_out, DEC);
  or or_32 (or_32_out, and_47_out, or_2_out);
  or or_33 (or_33_out, and_48_out, or_4_out);
  or or_34 (or_34_out, and_49_out, or_6_out);
  or or_35 (or_35_out, and_50_out, or_8_out);
  or or_36 (or_36_out, and_51_out, or_10_out);
  or or_37 (or_37_out, and_52_out, or_12_out);
  or or_38 (or_38_out, and_53_out, or_14_out);
  or or_39 (or_39_out, and_54_out, or_16_out);
  or or_40 (or_40_out, and_55_out, or_18_out);
  or or_41 (or_41_out, and_56_out, or_20_out);
  or or_42 (or_42_out, and_57_out, or_22_out);
  or or_43 (or_43_out, and_58_out, or_24_out);
  or or_44 (or_44_out, and_59_out, or_26_out);
  or or_45 (or_45_out, and_60_out, or_28_out);
  or or_46 (or_46_out, and_61_out, or_30_out);
  or or_47 (or_47_out, and_62_out, or_31_out);
  or or_48 (or_48_out, DEC, or_1_out);
  and and_63 (and_63_out, SHL, OUTPUT[14]);
  or or_49 (or_49_out, and_63_out, or_32_out);
  and and_64 (and_64_out, SHL, OUTPUT[13]);
  or or_50 (or_50_out, and_64_out, or_33_out);
  and and_65 (and_65_out, SHL, OUTPUT[12]);
  or or_51 (or_51_out, and_65_out, or_34_out);
  and and_66 (and_66_out, SHL, OUTPUT[11]);
  or or_52 (or_52_out, and_66_out, or_35_out);
  and and_67 (and_67_out, SHL, OUTPUT[10]);
  or or_53 (or_53_out, and_67_out, or_36_out);
  and and_68 (and_68_out, SHL, OUTPUT[9]);
  or or_54 (or_54_out, and_68_out, or_37_out);
  and and_69 (and_69_out, SHL, OUTPUT[8]);
  or or_55 (or_55_out, and_69_out, or_38_out);
  and and_70 (and_70_out, SHL, OUTPUT[7]);
  or or_56 (or_56_out, and_70_out, or_39_out);
  and and_71 (and_71_out, SHL, OUTPUT[6]);
  or or_57 (or_57_out, and_71_out, or_40_out);
  and and_72 (and_72_out, SHL, OUTPUT[5]);
  or or_58 (or_58_out, and_72_out, or_41_out);
  and and_73 (and_73_out, SHL, OUTPUT[4]);
  or or_59 (or_59_out, and_73_out, or_42_out);
  and and_74 (and_74_out, SHL, OUTPUT[3]);
  or or_60 (or_60_out, and_74_out, or_43_out);
  and and_75 (and_75_out, SHL, OUTPUT[2]);
  or or_61 (or_61_out, and_75_out, or_44_out);
  and and_76 (and_76_out, SHL, OUTPUT[1]);
  or or_62 (or_62_out, and_76_out, or_45_out);
  and and_77 (and_77_out, SHL, OUTPUT[0]);
  or or_63 (or_63_out, and_77_out, or_46_out);
  and and_78 (and_78_out, 1'b0, SHL);
  or or_64 (or_64_out, and_78_out, or_47_out);
  or or_65 (or_65_out, or_48_out, SHL);
  and and_79 (and_79_out, 1'b0, SHR);
  and and_80 (and_80_out, OUTPUT[15], SHR);
  and and_81 (and_81_out, OUTPUT[14], SHR);
  and and_82 (and_82_out, OUTPUT[13], SHR);
  and and_83 (and_83_out, OUTPUT[12], SHR);
  and and_84 (and_84_out, OUTPUT[11], SHR);
  and and_85 (and_85_out, OUTPUT[10], SHR);
  and and_86 (and_86_out, OUTPUT[9], SHR);
  and and_87 (and_87_out, OUTPUT[8], SHR);
  and and_88 (and_88_out, OUTPUT[7], SHR);
  and and_89 (and_89_out, OUTPUT[6], SHR);
  and and_90 (and_90_out, OUTPUT[5], SHR);
  and and_91 (and_91_out, OUTPUT[4], SHR);
  and and_92 (and_92_out, OUTPUT[3], SHR);
  and and_93 (and_93_out, OUTPUT[2], SHR);
  and and_94 (and_94_out, OUTPUT[1], SHR);
  or or_66 (or_66_out, SHR, or_65_out);
  and and_95 (and_95_out, CIL, OUTPUT[14]);
  or or_67 (or_67_out, or_49_out, and_79_out);
  and and_96 (and_96_out, CIL, OUTPUT[13]);
  or or_68 (or_68_out, or_50_out, and_80_out);
  and and_97 (and_97_out, CIL, OUTPUT[12]);
  or or_69 (or_69_out, or_51_out, and_81_out);
  and and_98 (and_98_out, CIL, OUTPUT[11]);
  or or_70 (or_70_out, or_52_out, and_82_out);
  and and_99 (and_99_out, CIL, OUTPUT[10]);
  or or_71 (or_71_out, or_53_out, and_83_out);
  and and_100 (and_100_out, CIL, OUTPUT[9]);
  or or_72 (or_72_out, or_54_out, and_84_out);
  and and_101 (and_101_out, CIL, OUTPUT[8]);
  or or_73 (or_73_out, or_55_out, and_85_out);
  and and_102 (and_102_out, CIL, OUTPUT[7]);
  or or_74 (or_74_out, or_56_out, and_86_out);
  and and_103 (and_103_out, CIL, OUTPUT[6]);
  or or_75 (or_75_out, or_57_out, and_87_out);
  and and_104 (and_104_out, CIL, OUTPUT[5]);
  or or_76 (or_76_out, or_58_out, and_88_out);
  and and_105 (and_105_out, CIL, OUTPUT[4]);
  or or_77 (or_77_out, or_59_out, and_89_out);
  and and_106 (and_106_out, CIL, OUTPUT[3]);
  or or_78 (or_78_out, or_60_out, and_90_out);
  and and_107 (and_107_out, CIL, OUTPUT[2]);
  or or_79 (or_79_out, or_61_out, and_91_out);
  and and_108 (and_108_out, CIL, OUTPUT[1]);
  or or_80 (or_80_out, or_62_out, and_92_out);
  and and_109 (and_109_out, CIL, OUTPUT[0]);
  or or_81 (or_81_out, or_63_out, and_93_out);
  and and_110 (and_110_out, OUTPUT[15], CIL);
  or or_82 (or_82_out, or_64_out, and_94_out);
  or or_83 (or_83_out, and_95_out, or_67_out);
  or or_84 (or_84_out, and_96_out, or_68_out);
  or or_85 (or_85_out, and_97_out, or_69_out);
  or or_86 (or_86_out, and_98_out, or_70_out);
  or or_87 (or_87_out, and_99_out, or_71_out);
  or or_88 (or_88_out, and_100_out, or_72_out);
  or or_89 (or_89_out, and_101_out, or_73_out);
  or or_90 (or_90_out, and_102_out, or_74_out);
  or or_91 (or_91_out, and_103_out, or_75_out);
  or or_92 (or_92_out, and_104_out, or_76_out);
  or or_93 (or_93_out, and_105_out, or_77_out);
  or or_94 (or_94_out, and_106_out, or_78_out);
  or or_95 (or_95_out, and_107_out, or_79_out);
  or or_96 (or_96_out, and_108_out, or_80_out);
  or or_97 (or_97_out, and_109_out, or_81_out);
  or or_98 (or_98_out, and_110_out, or_82_out);
  or or_99 (or_99_out, or_66_out, CIL);
  or or_100 (or_100_out, or_83_out, and_111_out);
  and and_111 (and_111_out, OUTPUT[0], CIR);
  or or_101 (or_101_out, or_84_out, and_112_out);
  and and_112 (and_112_out, OUTPUT[15], CIR);
  or or_102 (or_102_out, or_85_out, and_113_out);
  and and_113 (and_113_out, OUTPUT[14], CIR);
  or or_103 (or_103_out, or_86_out, and_114_out);
  and and_114 (and_114_out, OUTPUT[13], CIR);
  or or_104 (or_104_out, or_87_out, and_115_out);
  and and_115 (and_115_out, OUTPUT[12], CIR);
  or or_105 (or_105_out, or_88_out, and_116_out);
  and and_116 (and_116_out, OUTPUT[11], CIR);
  or or_106 (or_106_out, or_89_out, and_117_out);
  and and_117 (and_117_out, OUTPUT[10], CIR);
  or or_107 (or_107_out, or_90_out, and_118_out);
  and and_118 (and_118_out, OUTPUT[9], CIR);
  or or_108 (or_108_out, or_91_out, and_119_out);
  and and_119 (and_119_out, OUTPUT[8], CIR);
  or or_109 (or_109_out, or_92_out, and_120_out);
  and and_120 (and_120_out, OUTPUT[7], CIR);
  or or_110 (or_110_out, or_93_out, and_121_out);
  and and_121 (and_121_out, OUTPUT[6], CIR);
  or or_111 (or_111_out, or_94_out, and_122_out);
  and and_122 (and_122_out, OUTPUT[5], CIR);
  or or_112 (or_112_out, or_95_out, and_123_out);
  and and_123 (and_123_out, OUTPUT[4], CIR);
  or or_113 (or_113_out, or_96_out, and_124_out);
  and and_124 (and_124_out, OUTPUT[3], CIR);
  or or_114 (or_114_out, or_97_out, and_125_out);
  and and_125 (and_125_out, OUTPUT[2], CIR);
  or or_115 (or_115_out, or_98_out, and_126_out);
  and and_126 (and_126_out, OUTPUT[1], CIR);
  or or_116 (or_116_out, CIR, or_99_out);
  not not_3 (not_3_out, OUTPUT[15]);
  not not_4 (not_4_out, OUTPUT[14]);
  not not_5 (not_5_out, OUTPUT[13]);
  not not_6 (not_6_out, OUTPUT[12]);
  not not_7 (not_7_out, OUTPUT[11]);
  not not_8 (not_8_out, OUTPUT[10]);
  not not_9 (not_9_out, OUTPUT[9]);
  not not_10 (not_10_out, OUTPUT[8]);
  not not_11 (not_11_out, OUTPUT[7]);
  not not_12 (not_12_out, OUTPUT[6]);
  not not_13 (not_13_out, OUTPUT[5]);
  not not_14 (not_14_out, OUTPUT[4]);
  not not_15 (not_15_out, OUTPUT[3]);
  not not_16 (not_16_out, OUTPUT[2]);
  not not_17 (not_17_out, OUTPUT[1]);
  not not_18 (not_18_out, OUTPUT[0]);
  or or_117 (or_117_out, or_116_out, CML);
  and and_127 (and_127_out, not_3_out, CML);
  or or_118 (or_118_out, and_127_out, or_100_out);
  and and_128 (and_128_out, not_4_out, CML);
  or or_119 (or_119_out, and_128_out, or_101_out);
  and and_129 (and_129_out, not_5_out, CML);
  or or_120 (or_120_out, and_129_out, or_102_out);
  and and_130 (and_130_out, not_6_out, CML);
  or or_121 (or_121_out, and_130_out, or_103_out);
  and and_131 (and_131_out, not_7_out, CML);
  or or_122 (or_122_out, and_131_out, or_104_out);
  and and_132 (and_132_out, not_8_out, CML);
  or or_123 (or_123_out, and_132_out, or_105_out);
  and and_133 (and_133_out, not_9_out, CML);
  or or_124 (or_124_out, and_133_out, or_106_out);
  and and_134 (and_134_out, not_10_out, CML);
  or or_125 (or_125_out, and_134_out, or_107_out);
  and and_135 (and_135_out, not_11_out, CML);
  or or_126 (or_126_out, and_135_out, or_108_out);
  and and_136 (and_136_out, not_12_out, CML);
  or or_127 (or_127_out, and_136_out, or_109_out);
  and and_137 (and_137_out, not_13_out, CML);
  or or_128 (or_128_out, and_137_out, or_110_out);
  and and_138 (and_138_out, not_14_out, CML);
  or or_129 (or_129_out, and_138_out, or_111_out);
  and and_139 (and_139_out, not_15_out, CML);
  or or_130 (or_130_out, and_139_out, or_112_out);
  and and_140 (and_140_out, not_16_out, CML);
  or or_131 (or_131_out, and_140_out, or_113_out);
  and and_141 (and_141_out, not_17_out, CML);
  or or_132 (or_132_out, and_141_out, or_114_out);
  and and_142 (and_142_out, not_18_out, CML);
  or or_133 (or_133_out, and_142_out, or_115_out);
  or or_134 (or_134_out, or_118_out, and_143_out);
  and and_143 (and_143_out, 1'b0, CLR);
  or or_135 (or_135_out, or_119_out, and_144_out);
  and and_144 (and_144_out, 1'b0, CLR);
  or or_136 (or_136_out, or_120_out, and_145_out);
  and and_145 (and_145_out, 1'b0, CLR);
  or or_137 (or_137_out, or_121_out, and_146_out);
  and and_146 (and_146_out, 1'b0, CLR);
  or or_138 (or_138_out, or_122_out, and_147_out);
  and and_147 (and_147_out, 1'b0, CLR);
  or or_139 (or_139_out, or_123_out, and_148_out);
  and and_148 (and_148_out, 1'b0, CLR);
  or or_140 (or_140_out, or_124_out, and_149_out);
  and and_149 (and_149_out, 1'b0, CLR);
  or or_141 (or_141_out, or_125_out, and_150_out);
  and and_150 (and_150_out, 1'b0, CLR);
  or or_142 (or_142_out, or_126_out, and_151_out);
  and and_151 (and_151_out, 1'b0, CLR);
  or or_143 (or_143_out, or_127_out, and_152_out);
  and and_152 (and_152_out, 1'b0, CLR);
  or or_144 (or_144_out, or_128_out, and_153_out);
  and and_153 (and_153_out, 1'b0, CLR);
  or or_145 (or_145_out, or_129_out, and_154_out);
  and and_154 (and_154_out, 1'b0, CLR);
  or or_146 (or_146_out, or_130_out, and_155_out);
  and and_155 (and_155_out, 1'b0, CLR);
  or or_147 (or_147_out, or_131_out, and_156_out);
  and and_156 (and_156_out, 1'b0, CLR);
  or or_148 (or_148_out, or_132_out, and_157_out);
  and and_157 (and_157_out, 1'b0, CLR);
  or or_149 (or_149_out, or_133_out, and_158_out);
  and and_158 (and_158_out, 1'b0, CLR);
  or or_150 (or_150_out, CLR, or_117_out);
  Multiplexer #(.enable("false")) multiplexer_1 (
    .in0(OUTPUT[15]), .in1(or_134_out), .out(multiplexer_1_out), .sel(or_150_out));
  Multiplexer #(.enable("false")) multiplexer_2 (
    .in0(OUTPUT[14]), .in1(or_135_out), .out(multiplexer_2_out), .sel(or_150_out));
  Multiplexer #(.enable("false")) multiplexer_3 (
    .in0(OUTPUT[13]), .in1(or_136_out), .out(multiplexer_3_out), .sel(or_150_out));
  Multiplexer #(.enable("false")) multiplexer_4 (
    .in0(OUTPUT[12]), .in1(or_137_out), .out(multiplexer_4_out), .sel(or_150_out));
  Multiplexer #(.enable("false")) multiplexer_5 (
    .in0(OUTPUT[11]), .in1(or_138_out), .out(multiplexer_5_out), .sel(or_150_out));
  Multiplexer #(.enable("false")) multiplexer_6 (
    .in0(OUTPUT[10]), .in1(or_139_out), .out(multiplexer_6_out), .sel(or_150_out));
  Multiplexer #(.enable("false")) multiplexer_7 (
    .in0(OUTPUT[9]), .in1(or_140_out), .out(multiplexer_7_out), .sel(or_150_out));
  Multiplexer #(.enable("false")) multiplexer_8 (
    .in0(OUTPUT[8]), .in1(or_141_out), .out(multiplexer_8_out), .sel(or_150_out));
  Multiplexer #(.enable("false")) multiplexer_9 (
    .in0(OUTPUT[7]), .in1(or_142_out), .out(multiplexer_9_out), .sel(or_150_out));
  Multiplexer #(.enable("false")) multiplexer_10 (
    .in0(OUTPUT[6]), .in1(or_143_out), .out(multiplexer_10_out), .sel(or_150_out));
  Multiplexer #(.enable("false")) multiplexer_11 (
    .in0(OUTPUT[5]), .in1(or_144_out), .out(multiplexer_11_out), .sel(or_150_out));
  Multiplexer #(.enable("false")) multiplexer_12 (
    .in0(OUTPUT[4]), .in1(or_145_out), .out(multiplexer_12_out), .sel(or_150_out));
  Multiplexer #(.enable("false")) multiplexer_13 (
    .in0(OUTPUT[3]), .in1(or_146_out), .out(multiplexer_13_out), .sel(or_150_out));
  Multiplexer #(.enable("false")) multiplexer_14 (
    .in0(OUTPUT[2]), .in1(or_147_out), .out(multiplexer_14_out), .sel(or_150_out));
  Multiplexer #(.enable("false")) multiplexer_15 (
    .in0(OUTPUT[1]), .in1(or_148_out), .out(multiplexer_15_out), .sel(or_150_out));
  Multiplexer #(.enable("false")) multiplexer_16 (
    .in0(OUTPUT[0]), .in1(or_149_out), .out(multiplexer_16_out), .sel(or_150_out));
  D_Flip_Flop d_ff_1 (.clk(CLK), .D(multiplexer_1_out), .Q(OUTPUT[15]));  // open: Qn, preset, en, reset
  D_Flip_Flop d_ff_2 (.clk(CLK), .D(multiplexer_2_out), .Q(OUTPUT[14]));  // open: Qn, preset, en, reset
  D_Flip_Flop d_ff_3 (.clk(CLK), .D(multiplexer_3_out), .Q(OUTPUT[13]));  // open: Qn, preset, en, reset
  D_Flip_Flop d_ff_4 (.clk(CLK), .D(multiplexer_4_out), .Q(OUTPUT[12]));  // open: Qn, preset, en, reset
  D_Flip_Flop d_ff_5 (.clk(CLK), .D(multiplexer_5_out), .Q(OUTPUT[11]));  // open: Qn, preset, en, reset
  D_Flip_Flop d_ff_6 (.clk(CLK), .D(multiplexer_6_out), .Q(OUTPUT[10]));  // open: Qn, preset, en, reset
  D_Flip_Flop d_ff_7 (.clk(CLK), .D(multiplexer_7_out), .Q(OUTPUT[9]));  // open: Qn, preset, en, reset
  D_Flip_Flop d_ff_8 (.clk(CLK), .D(multiplexer_8_out), .Q(OUTPUT[8]));  // open: Qn, preset, en, reset
  D_Flip_Flop d_ff_9 (.clk(CLK), .D(multiplexer_9_out), .Q(OUTPUT[7]));  // open: Qn, preset, en, reset
  D_Flip_Flop d_ff_10 (.clk(CLK), .D(multiplexer_10_out), .Q(OUTPUT[6]));  // open: Qn, preset, en, reset
  D_Flip_Flop d_ff_11 (.clk(CLK), .D(multiplexer_11_out), .Q(OUTPUT[5]));  // open: Qn, preset, en, reset
  D_Flip_Flop d_ff_12 (.clk(CLK), .D(multiplexer_12_out), .Q(OUTPUT[4]));  // open: Qn, preset, en, reset
  D_Flip_Flop d_ff_13 (.clk(CLK), .D(multiplexer_13_out), .Q(OUTPUT[3]));  // open: Qn, preset, en, reset
  D_Flip_Flop d_ff_14 (.clk(CLK), .D(multiplexer_14_out), .Q(OUTPUT[2]));  // open: Qn, preset, en, reset
  D_Flip_Flop d_ff_15 (.clk(CLK), .D(multiplexer_15_out), .Q(OUTPUT[1]));  // open: Qn, preset, en, reset
  D_Flip_Flop d_ff_16 (.clk(CLK), .D(multiplexer_16_out), .Q(OUTPUT[0]));  // open: Qn, preset, en, reset
endmodule

module SPECIAL_PURPOSE (
  input  [15:0] INPUT,
  input  CLK,
  input  INC,
  input  LD,
  output [15:0] OUTPUT
);

  wire and_1_out, and_2_out, and_3_out, and_4_out, and_5_out, and_6_out, and_7_out, and_8_out, and_9_out,
       and_10_out, and_11_out, and_12_out, and_13_out, and_14_out, and_15_out, and_16_out, and_17_out,
       and_18_out, and_19_out, and_20_out, and_21_out, and_22_out, and_23_out, and_24_out, and_25_out,
       and_26_out, and_27_out, and_28_out, and_29_out, and_30_out, and_31_out, and_32_out, and_33_out,
       and_34_out, and_35_out, and_36_out, and_37_out, and_38_out, and_39_out, and_40_out, and_41_out,
       and_42_out, and_43_out, and_44_out, and_45_out, and_46_out, multiplexer_1_out, multiplexer_2_out,
       multiplexer_3_out, multiplexer_4_out, multiplexer_5_out, multiplexer_6_out, multiplexer_7_out,
       multiplexer_8_out, multiplexer_9_out, multiplexer_10_out, multiplexer_11_out, multiplexer_12_out,
       multiplexer_13_out, multiplexer_14_out, multiplexer_15_out, multiplexer_16_out, not_1_out, or_1_out,
       or_2_out, or_3_out, or_4_out, or_5_out, or_6_out, or_7_out, or_8_out, or_9_out, or_10_out, or_11_out,
       or_12_out, or_13_out, or_14_out, or_15_out, or_16_out, or_17_out, xor_1_out, xor_2_out, xor_3_out,
       xor_4_out, xor_5_out, xor_6_out, xor_7_out, xor_8_out, xor_9_out, xor_10_out, xor_11_out, xor_12_out,
       xor_13_out, xor_14_out, xor_15_out;

  and and_1 (and_1_out, and_2_out, OUTPUT[14]);
  and and_2 (and_2_out, OUTPUT[13], and_3_out);
  and and_3 (and_3_out, and_4_out, OUTPUT[12]);
  and and_4 (and_4_out, OUTPUT[11], and_5_out);
  and and_5 (and_5_out, and_6_out, OUTPUT[10]);
  and and_6 (and_6_out, OUTPUT[9], and_7_out);
  and and_7 (and_7_out, and_8_out, OUTPUT[8]);
  and and_8 (and_8_out, OUTPUT[7], and_9_out);
  and and_9 (and_9_out, and_10_out, OUTPUT[6]);
  and and_10 (and_10_out, OUTPUT[5], and_11_out);
  and and_11 (and_11_out, and_12_out, OUTPUT[4]);
  and and_12 (and_12_out, OUTPUT[3], and_13_out);
  and and_13 (and_13_out, and_14_out, OUTPUT[2]);
  and and_14 (and_14_out, OUTPUT[0], OUTPUT[1]);
  xor xor_1 (xor_1_out, OUTPUT[15], and_1_out);
  and and_15 (and_15_out, xor_1_out, INC);
  xor xor_2 (xor_2_out, OUTPUT[14], and_2_out);
  and and_16 (and_16_out, xor_2_out, INC);
  xor xor_3 (xor_3_out, OUTPUT[13], and_3_out);
  and and_17 (and_17_out, xor_3_out, INC);
  xor xor_4 (xor_4_out, OUTPUT[12], and_4_out);
  and and_18 (and_18_out, xor_4_out, INC);
  xor xor_5 (xor_5_out, OUTPUT[11], and_5_out);
  and and_19 (and_19_out, xor_5_out, INC);
  xor xor_6 (xor_6_out, OUTPUT[10], and_6_out);
  and and_20 (and_20_out, xor_6_out, INC);
  xor xor_7 (xor_7_out, OUTPUT[9], and_7_out);
  and and_21 (and_21_out, xor_7_out, INC);
  xor xor_8 (xor_8_out, OUTPUT[8], and_8_out);
  and and_22 (and_22_out, xor_8_out, INC);
  xor xor_9 (xor_9_out, OUTPUT[7], and_9_out);
  and and_23 (and_23_out, xor_9_out, INC);
  xor xor_10 (xor_10_out, OUTPUT[6], and_10_out);
  and and_24 (and_24_out, xor_10_out, INC);
  xor xor_11 (xor_11_out, OUTPUT[5], and_11_out);
  and and_25 (and_25_out, xor_11_out, INC);
  xor xor_12 (xor_12_out, OUTPUT[4], and_12_out);
  and and_26 (and_26_out, xor_12_out, INC);
  xor xor_13 (xor_13_out, OUTPUT[3], and_13_out);
  and and_27 (and_27_out, xor_13_out, INC);
  xor xor_14 (xor_14_out, OUTPUT[2], and_14_out);
  and and_28 (and_28_out, xor_14_out, INC);
  xor xor_15 (xor_15_out, OUTPUT[1], OUTPUT[0]);
  and and_29 (and_29_out, xor_15_out, INC);
  not not_1 (not_1_out, OUTPUT[0]);
  and and_30 (and_30_out, not_1_out, INC);
  and and_31 (and_31_out, INPUT[15], LD);
  and and_32 (and_32_out, INPUT[14], LD);
  and and_33 (and_33_out, INPUT[13], LD);
  and and_34 (and_34_out, INPUT[12], LD);
  and and_35 (and_35_out, INPUT[11], LD);
  and and_36 (and_36_out, INPUT[10], LD);
  and and_37 (and_37_out, INPUT[9], LD);
  and and_38 (and_38_out, INPUT[8], LD);
  and and_39 (and_39_out, INPUT[7], LD);
  and and_40 (and_40_out, INPUT[6], LD);
  and and_41 (and_41_out, INPUT[5], LD);
  and and_42 (and_42_out, INPUT[4], LD);
  and and_43 (and_43_out, INPUT[3], LD);
  and and_44 (and_44_out, INPUT[2], LD);
  and and_45 (and_45_out, INPUT[1], LD);
  and and_46 (and_46_out, INPUT[0], LD);
  or or_1 (or_1_out, INC, LD);
  or or_2 (or_2_out, and_15_out, and_31_out);
  or or_3 (or_3_out, and_16_out, and_32_out);
  or or_4 (or_4_out, and_17_out, and_33_out);
  or or_5 (or_5_out, and_18_out, and_34_out);
  or or_6 (or_6_out, and_19_out, and_35_out);
  or or_7 (or_7_out, and_20_out, and_36_out);
  or or_8 (or_8_out, and_21_out, and_37_out);
  or or_9 (or_9_out, and_22_out, and_38_out);
  or or_10 (or_10_out, and_23_out, and_39_out);
  or or_11 (or_11_out, and_24_out, and_40_out);
  or or_12 (or_12_out, and_25_out, and_41_out);
  or or_13 (or_13_out, and_26_out, and_42_out);
  or or_14 (or_14_out, and_27_out, and_43_out);
  or or_15 (or_15_out, and_28_out, and_44_out);
  or or_16 (or_16_out, and_29_out, and_45_out);
  or or_17 (or_17_out, and_30_out, and_46_out);
  Multiplexer #(.enable("false")) multiplexer_1 (
    .in0(OUTPUT[15]), .in1(or_2_out), .out(multiplexer_1_out), .sel(or_1_out));
  Multiplexer #(.enable("false")) multiplexer_2 (
    .in0(OUTPUT[14]), .in1(or_3_out), .out(multiplexer_2_out), .sel(or_1_out));
  Multiplexer #(.enable("false")) multiplexer_3 (
    .in0(OUTPUT[13]), .in1(or_4_out), .out(multiplexer_3_out), .sel(or_1_out));
  Multiplexer #(.enable("false")) multiplexer_4 (
    .in0(OUTPUT[12]), .in1(or_5_out), .out(multiplexer_4_out), .sel(or_1_out));
  Multiplexer #(.enable("false")) multiplexer_5 (
    .in0(OUTPUT[11]), .in1(or_6_out), .out(multiplexer_5_out), .sel(or_1_out));
  Multiplexer #(.enable("false")) multiplexer_6 (
    .in0(OUTPUT[10]), .in1(or_7_out), .out(multiplexer_6_out), .sel(or_1_out));
  Multiplexer #(.enable("false")) multiplexer_7 (
    .in0(OUTPUT[9]), .in1(or_8_out), .out(multiplexer_7_out), .sel(or_1_out));
  Multiplexer #(.enable("false")) multiplexer_8 (
    .in0(OUTPUT[8]), .in1(or_9_out), .out(multiplexer_8_out), .sel(or_1_out));
  Multiplexer #(.enable("false")) multiplexer_9 (
    .in0(OUTPUT[7]), .in1(or_10_out), .out(multiplexer_9_out), .sel(or_1_out));
  Multiplexer #(.enable("false")) multiplexer_10 (
    .in0(OUTPUT[6]), .in1(or_11_out), .out(multiplexer_10_out), .sel(or_1_out));
  Multiplexer #(.enable("false")) multiplexer_11 (
    .in0(OUTPUT[5]), .in1(or_12_out), .out(multiplexer_11_out), .sel(or_1_out));
  Multiplexer #(.enable("false")) multiplexer_12 (
    .in0(OUTPUT[4]), .in1(or_13_out), .out(multiplexer_12_out), .sel(or_1_out));
  Multiplexer #(.enable("false")) multiplexer_13 (
    .in0(OUTPUT[3]), .in1(or_14_out), .out(multiplexer_13_out), .sel(or_1_out));
  Multiplexer #(.enable("false")) multiplexer_14 (
    .in0(OUTPUT[2]), .in1(or_15_out), .out(multiplexer_14_out), .sel(or_1_out));
  Multiplexer #(.enable("false")) multiplexer_15 (
    .in0(OUTPUT[1]), .in1(or_16_out), .out(multiplexer_15_out), .sel(or_1_out));
  Multiplexer #(.enable("false")) multiplexer_16 (
    .in0(OUTPUT[0]), .in1(or_17_out), .out(multiplexer_16_out), .sel(or_1_out));
  D_Flip_Flop d_ff_1 (.clk(CLK), .D(multiplexer_1_out), .Q(OUTPUT[15]));  // open: Qn, preset, en, reset
  D_Flip_Flop d_ff_2 (.clk(CLK), .D(multiplexer_2_out), .Q(OUTPUT[14]));  // open: Qn, preset, en, reset
  D_Flip_Flop d_ff_3 (.clk(CLK), .D(multiplexer_3_out), .Q(OUTPUT[13]));  // open: Qn, preset, en, reset
  D_Flip_Flop d_ff_4 (.clk(CLK), .D(multiplexer_4_out), .Q(OUTPUT[12]));  // open: Qn, preset, en, reset
  D_Flip_Flop d_ff_5 (.clk(CLK), .D(multiplexer_5_out), .Q(OUTPUT[11]));  // open: Qn, preset, en, reset
  D_Flip_Flop d_ff_6 (.clk(CLK), .D(multiplexer_6_out), .Q(OUTPUT[10]));  // open: Qn, preset, en, reset
  D_Flip_Flop d_ff_7 (.clk(CLK), .D(multiplexer_7_out), .Q(OUTPUT[9]));  // open: Qn, preset, en, reset
  D_Flip_Flop d_ff_8 (.clk(CLK), .D(multiplexer_8_out), .Q(OUTPUT[8]));  // open: Qn, preset, en, reset
  D_Flip_Flop d_ff_9 (.clk(CLK), .D(multiplexer_9_out), .Q(OUTPUT[7]));  // open: Qn, preset, en, reset
  D_Flip_Flop d_ff_10 (.clk(CLK), .D(multiplexer_10_out), .Q(OUTPUT[6]));  // open: Qn, preset, en, reset
  D_Flip_Flop d_ff_11 (.clk(CLK), .D(multiplexer_11_out), .Q(OUTPUT[5]));  // open: Qn, preset, en, reset
  D_Flip_Flop d_ff_12 (.clk(CLK), .D(multiplexer_12_out), .Q(OUTPUT[4]));  // open: Qn, preset, en, reset
  D_Flip_Flop d_ff_13 (.clk(CLK), .D(multiplexer_13_out), .Q(OUTPUT[3]));  // open: Qn, preset, en, reset
  D_Flip_Flop d_ff_14 (.clk(CLK), .D(multiplexer_14_out), .Q(OUTPUT[2]));  // open: Qn, preset, en, reset
  D_Flip_Flop d_ff_15 (.clk(CLK), .D(multiplexer_15_out), .Q(OUTPUT[1]));  // open: Qn, preset, en, reset
  D_Flip_Flop d_ff_16 (.clk(CLK), .D(multiplexer_16_out), .Q(OUTPUT[0]));  // open: Qn, preset, en, reset
endmodule

module INSTRUCTION_REGISTER (
  input  [23:0] INPUT,
  input  LOAD,
  input  CLK,
  output [23:0] OUTPUT
);

  wire multiplexer_1_out, multiplexer_2_out, multiplexer_3_out, multiplexer_4_out, multiplexer_5_out,
       multiplexer_6_out, multiplexer_7_out, multiplexer_8_out, multiplexer_9_out, multiplexer_10_out,
       multiplexer_11_out, multiplexer_12_out, multiplexer_13_out, multiplexer_14_out, multiplexer_15_out,
       multiplexer_16_out, multiplexer_17_out, multiplexer_18_out, multiplexer_19_out, multiplexer_20_out,
       multiplexer_21_out, multiplexer_22_out, multiplexer_23_out, multiplexer_24_out;

  Multiplexer #(.enable("false")) multiplexer_1 (
    .in0(OUTPUT[23]), .in1(INPUT[23]), .out(multiplexer_1_out), .sel(LOAD));
  Multiplexer #(.enable("false")) multiplexer_2 (
    .in0(OUTPUT[22]), .in1(INPUT[22]), .out(multiplexer_2_out), .sel(LOAD));
  Multiplexer #(.enable("false")) multiplexer_3 (
    .in0(OUTPUT[21]), .in1(INPUT[21]), .out(multiplexer_3_out), .sel(LOAD));
  Multiplexer #(.enable("false")) multiplexer_4 (
    .in0(OUTPUT[20]), .in1(INPUT[20]), .out(multiplexer_4_out), .sel(LOAD));
  Multiplexer #(.enable("false")) multiplexer_5 (
    .in0(OUTPUT[19]), .in1(INPUT[19]), .out(multiplexer_5_out), .sel(LOAD));
  Multiplexer #(.enable("false")) multiplexer_6 (
    .in0(OUTPUT[18]), .in1(INPUT[18]), .out(multiplexer_6_out), .sel(LOAD));
  Multiplexer #(.enable("false")) multiplexer_7 (
    .in0(OUTPUT[17]), .in1(INPUT[17]), .out(multiplexer_7_out), .sel(LOAD));
  Multiplexer #(.enable("false")) multiplexer_8 (
    .in0(OUTPUT[16]), .in1(INPUT[16]), .out(multiplexer_8_out), .sel(LOAD));
  Multiplexer #(.enable("false")) multiplexer_9 (
    .in0(OUTPUT[15]), .in1(INPUT[15]), .out(multiplexer_9_out), .sel(LOAD));
  Multiplexer #(.enable("false")) multiplexer_10 (
    .in0(OUTPUT[14]), .in1(INPUT[14]), .out(multiplexer_10_out), .sel(LOAD));
  Multiplexer #(.enable("false")) multiplexer_11 (
    .in0(OUTPUT[13]), .in1(INPUT[13]), .out(multiplexer_11_out), .sel(LOAD));
  Multiplexer #(.enable("false")) multiplexer_12 (
    .in0(OUTPUT[12]), .in1(INPUT[12]), .out(multiplexer_12_out), .sel(LOAD));
  Multiplexer #(.enable("false")) multiplexer_13 (
    .in0(OUTPUT[11]), .in1(INPUT[11]), .out(multiplexer_13_out), .sel(LOAD));
  Multiplexer #(.enable("false")) multiplexer_14 (
    .in0(OUTPUT[10]), .in1(INPUT[10]), .out(multiplexer_14_out), .sel(LOAD));
  Multiplexer #(.enable("false")) multiplexer_15 (
    .in0(OUTPUT[9]), .in1(INPUT[9]), .out(multiplexer_15_out), .sel(LOAD));
  Multiplexer #(.enable("false")) multiplexer_16 (
    .in0(OUTPUT[8]), .in1(INPUT[8]), .out(multiplexer_16_out), .sel(LOAD));
  Multiplexer #(.enable("false")) multiplexer_17 (
    .in0(OUTPUT[7]), .in1(INPUT[7]), .out(multiplexer_17_out), .sel(LOAD));
  Multiplexer #(.enable("false")) multiplexer_18 (
    .in0(OUTPUT[6]), .in1(INPUT[6]), .out(multiplexer_18_out), .sel(LOAD));
  Multiplexer #(.enable("false")) multiplexer_19 (
    .in0(OUTPUT[5]), .in1(INPUT[5]), .out(multiplexer_19_out), .sel(LOAD));
  Multiplexer #(.enable("false")) multiplexer_20 (
    .in0(OUTPUT[4]), .in1(INPUT[4]), .out(multiplexer_20_out), .sel(LOAD));
  Multiplexer #(.enable("false")) multiplexer_21 (
    .in0(OUTPUT[3]), .in1(INPUT[3]), .out(multiplexer_21_out), .sel(LOAD));
  Multiplexer #(.enable("false")) multiplexer_22 (
    .in0(OUTPUT[2]), .in1(INPUT[2]), .out(multiplexer_22_out), .sel(LOAD));
  Multiplexer #(.enable("false")) multiplexer_23 (
    .in0(OUTPUT[1]), .in1(INPUT[1]), .out(multiplexer_23_out), .sel(LOAD));
  Multiplexer #(.enable("false")) multiplexer_24 (
    .in0(OUTPUT[0]), .in1(INPUT[0]), .out(multiplexer_24_out), .sel(LOAD));
  D_Flip_Flop d_ff_1 (.clk(CLK), .D(multiplexer_1_out), .Q(OUTPUT[23]));  // open: Qn, preset, en, reset
  D_Flip_Flop d_ff_2 (.clk(CLK), .D(multiplexer_2_out), .Q(OUTPUT[22]));  // open: Qn, preset, en, reset
  D_Flip_Flop d_ff_3 (.clk(CLK), .D(multiplexer_3_out), .Q(OUTPUT[21]));  // open: Qn, preset, en, reset
  D_Flip_Flop d_ff_4 (.clk(CLK), .D(multiplexer_4_out), .Q(OUTPUT[20]));  // open: Qn, preset, en, reset
  D_Flip_Flop d_ff_5 (.clk(CLK), .D(multiplexer_5_out), .Q(OUTPUT[19]));  // open: Qn, preset, en, reset
  D_Flip_Flop d_ff_6 (.clk(CLK), .D(multiplexer_6_out), .Q(OUTPUT[18]));  // open: Qn, preset, en, reset
  D_Flip_Flop d_ff_7 (.clk(CLK), .D(multiplexer_7_out), .Q(OUTPUT[17]));  // open: Qn, preset, en, reset
  D_Flip_Flop d_ff_8 (.clk(CLK), .D(multiplexer_8_out), .Q(OUTPUT[16]));  // open: Qn, preset, en, reset
  D_Flip_Flop d_ff_9 (.clk(CLK), .D(multiplexer_9_out), .Q(OUTPUT[15]));  // open: Qn, preset, en, reset
  D_Flip_Flop d_ff_10 (.clk(CLK), .D(multiplexer_10_out), .Q(OUTPUT[14]));  // open: Qn, preset, en, reset
  D_Flip_Flop d_ff_11 (.clk(CLK), .D(multiplexer_11_out), .Q(OUTPUT[13]));  // open: Qn, preset, en, reset
  D_Flip_Flop d_ff_12 (.clk(CLK), .D(multiplexer_12_out), .Q(OUTPUT[12]));  // open: Qn, preset, en, reset
  D_Flip_Flop d_ff_13 (.clk(CLK), .D(multiplexer_13_out), .Q(OUTPUT[11]));  // open: Qn, preset, en, reset
  D_Flip_Flop d_ff_14 (.clk(CLK), .D(multiplexer_14_out), .Q(OUTPUT[10]));  // open: Qn, preset, en, reset
  D_Flip_Flop d_ff_15 (.clk(CLK), .D(multiplexer_15_out), .Q(OUTPUT[9]));  // open: Qn, preset, en, reset
  D_Flip_Flop d_ff_16 (.clk(CLK), .D(multiplexer_16_out), .Q(OUTPUT[8]));  // open: Qn, preset, en, reset
  D_Flip_Flop d_ff_17 (.clk(CLK), .D(multiplexer_17_out), .Q(OUTPUT[7]));  // open: Qn, preset, en, reset
  D_Flip_Flop d_ff_18 (.clk(CLK), .D(multiplexer_18_out), .Q(OUTPUT[6]));  // open: Qn, preset, en, reset
  D_Flip_Flop d_ff_19 (.clk(CLK), .D(multiplexer_19_out), .Q(OUTPUT[5]));  // open: Qn, preset, en, reset
  D_Flip_Flop d_ff_20 (.clk(CLK), .D(multiplexer_20_out), .Q(OUTPUT[4]));  // open: Qn, preset, en, reset
  D_Flip_Flop d_ff_21 (.clk(CLK), .D(multiplexer_21_out), .Q(OUTPUT[3]));  // open: Qn, preset, en, reset
  D_Flip_Flop d_ff_22 (.clk(CLK), .D(multiplexer_22_out), .Q(OUTPUT[2]));  // open: Qn, preset, en, reset
  D_Flip_Flop d_ff_23 (.clk(CLK), .D(multiplexer_23_out), .Q(OUTPUT[1]));  // open: Qn, preset, en, reset
  D_Flip_Flop d_ff_24 (.clk(CLK), .D(multiplexer_24_out), .Q(OUTPUT[0]));  // open: Qn, preset, en, reset
endmodule
